# Fritzing sketch adder (saved by Fritzing 0.9.3b)
circuit board: 7.00084cm x 6.97166cm
breadboards: 1

parts:
  power = female pin header, 2 pins [form="♀ (female)"]
  carry_in = female pin header, 1 pin [form="♀ (female)"]
  carry_out = female pin header, 1 pin [form="♀ (female)"]
  74283_H = IC, DIP package, 16 pins [chip_label=IC]
  74283_L = IC, DIP package, 16 pins [chip_label=IC]
  input_b = female pin header, 8 pins [form="♀ (female)"]
  input_a = female pin header, 8 pins [form="♀ (female)"]
  enable_add = female pin header, 1 pin [form="♀ (female)"]
  74LS245 = IC, DIP package, 20 pins [chip_label=IC]
  nonzero = female pin header, 1 pin [form="♀ (female)"]
  74HC125 = IC, DIP package, 14 pins [chip_label=IC]
  nz = female pin header, 1 pin [form="♀ (female)"]
  co = female pin header, 1 pin [form="♀ (female)"]
  en = female pin header, 1 pin [form="♀ (female)"]
  C1 = Ceramic Capacitor [capacitance=100nF package="100 mil [THT, multilayer]"]
  s1 = female pin header, 8 pins [form="♀ (female)"]
  output1 = female pin header, 8 pins [form="♀ (female)"]
  en9 = female pin header, 1 pin [form="♀ (female)"]
  op4 = female pin header, 1 pin [form="♀ (female)"]
  en10 = female pin header, 1 pin [form="♀ (female)"]
  op5 = female pin header, 1 pin [form="♀ (female)"]
  op6 = female pin header, 1 pin [form="♀ (female)"]
  op7 = female pin header, 1 pin [form="♀ (female)"]
  enable_not1 = female pin header, 1 pin [form="♀ (female)"]
  enable_ror1 = female pin header, 1 pin [form="♀ (female)"]
  en11 = female pin header, 1 pin [form="♀ (female)"]
  en12 = female pin header, 1 pin [form="♀ (female)"]
  en13 = female pin header, 1 pin [form="♀ (female)"]
  enable_rol1 = female pin header, 1 pin [form="♀ (female)"]
  en14 = female pin header, 1 pin [form="♀ (female)"]
  enable_xor1 = female pin header, 1 pin [form="♀ (female)"]
  en15 = female pin header, 1 pin [form="♀ (female)"]
  enable_or1 = female pin header, 1 pin [form="♀ (female)"]
  en16 = female pin header, 1 pin [form="♀ (female)"]
  enable_and1 = female pin header, 1 pin [form="♀ (female)"]
  power2 = female pin header, 2 pins [form="♀ (female)"]
  carry_in2 = female pin header, 1 pin [form="♀ (female)"]
  input_b2 = female pin header, 8 pins [form="♀ (female)"]
  input_a2 = female pin header, 8 pins [form="♀ (female)"]

nets:
  N1: power.pin1, 74283_H.pin16, 74283_L.pin16, 74LS245.pin20, 74HC125.pin14, C1.0, power2.pin1
  N2: power.pin2, 74283_H.pin8, 74283_L.pin8, 74LS245.pin1, 74LS245.pin10, 74HC125.pin7, C1.1, power2.pin2
  N3: carry_in.pin1, 74283_L.pin7, carry_in2.pin1
  N4: carry_out.pin1, 74HC125.pin3, co.pin1
  N5: 74283_H.pin1, 74LS245.pin16
  N6: 74283_H.pin2, input_a.pin3, input_a2.pin3
  N7: 74283_H.pin3, input_b.pin3, input_b2.pin3
  N8: 74283_H.pin4, 74LS245.pin15
  N9: 74283_H.pin5, input_b.pin4, input_b2.pin4
  N10: 74283_H.pin6, input_a.pin4, input_a2.pin4
  N11: 74283_H.pin7, 74283_L.pin9
  N12: 74283_H.pin9, 74HC125.pin2
  N13: 74283_H.pin10, 74LS245.pin18
  N14: 74283_H.pin11, input_a.pin1, input_a2.pin1
  N15: 74283_H.pin12, input_b.pin1, input_b2.pin1
  N16: 74283_H.pin13, 74LS245.pin17
  N17: 74283_H.pin14, input_b.pin2, input_b2.pin2
  N18: 74283_H.pin15, input_a.pin2, input_a2.pin2
  N19: 74283_L.pin1, 74LS245.pin12
  N20: 74283_L.pin2, input_a.pin7, input_a2.pin7
  N21: 74283_L.pin3, input_b.pin7, input_b2.pin7
  N22: 74283_L.pin4, 74LS245.pin11
  N23: 74283_L.pin5, input_b.pin8, input_b2.pin8
  N24: 74283_L.pin6, input_a.pin8, input_a2.pin8
  N25: 74283_L.pin10, 74LS245.pin14
  N26: 74283_L.pin11, input_a.pin5, input_a2.pin5
  N27: 74283_L.pin12, input_b.pin5, input_b2.pin5
  N28: 74283_L.pin13, 74LS245.pin13
  N29: 74283_L.pin14, input_b.pin6, input_b2.pin6
  N30: 74283_L.pin15, input_a.pin6, input_a2.pin6
  N31: enable_add.pin1, 74LS245.pin19, 74HC125.pin1, en.pin1
  N32: 74LS245.pin2, s1.pin1, output1.pin1
  N33: 74LS245.pin3, s1.pin2, output1.pin2
  N34: 74LS245.pin4, s1.pin3, output1.pin3
  N35: 74LS245.pin5, s1.pin4, output1.pin4
  N36: 74LS245.pin6, s1.pin5, output1.pin5
  N37: 74LS245.pin7, s1.pin6, output1.pin6
  N38: 74LS245.pin8, s1.pin7, output1.pin7
  N39: 74LS245.pin9, s1.pin8, output1.pin8
  N40: nonzero.pin1, nz.pin1
  N41: en9.pin1, op4.pin1
  N42: en10.pin1, op5.pin1
  N43: op6.pin1, op7.pin1
  N44: enable_not1.pin1, en11.pin1
  N45: enable_ror1.pin1, en12.pin1
  N46: en13.pin1, enable_rol1.pin1
  N47: en14.pin1, enable_xor1.pin1
  N48: en15.pin1, enable_or1.pin1
  N49: en16.pin1, enable_and1.pin1
