# Fritzing sketch aluctrl (saved by Fritzing 0.9.3b)
circuit board: 7.00084cm x 6.97166cm
breadboards: 1

parts:
  power = female pin header, 2 pins [form="♀ (female)"]
  carry_in = female pin header, 1 pin [form="♀ (female)"]
  carry_out = female pin header, 1 pin [form="♀ (female)"]
  input_b = female pin header, 8 pins [form="♀ (female)"]
  input_a = female pin header, 8 pins [form="♀ (female)"]
  output = female pin header, 8 pins [form="♀ (female)"]
  enable_add = female pin header, 1 pin [form="♀ (female)"]
  nonzero = female pin header, 1 pin [form="♀ (female)"]
  nz = female pin header, 1 pin [form="♀ (female)"]
  co = female pin header, 1 pin [form="♀ (female)"]
  s = female pin header, 8 pins [form="♀ (female)"]
  en = female pin header, 1 pin [form="♀ (female)"]
  enable_and = female pin header, 1 pin [form="♀ (female)"]
  en1 = female pin header, 1 pin [form="♀ (female)"]
  enable_or = female pin header, 1 pin [form="♀ (female)"]
  en2 = female pin header, 1 pin [form="♀ (female)"]
  enable_xor = female pin header, 1 pin [form="♀ (female)"]
  en3 = female pin header, 1 pin [form="♀ (female)"]
  enable_rol = female pin header, 1 pin [form="♀ (female)"]
  en4 = female pin header, 1 pin [form="♀ (female)"]
  en5 = female pin header, 1 pin [form="♀ (female)"]
  enable_ror = female pin header, 1 pin [form="♀ (female)"]
  carry_in1 = female pin header, 1 pin [form="♀ (female)"]
  input_b1 = female pin header, 8 pins [form="♀ (female)"]
  input_a1 = female pin header, 8 pins [form="♀ (female)"]
  en6 = female pin header, 1 pin [form="♀ (female)"]
  op0 = female pin header, 1 pin [form="♀ (female)"]
  en7 = female pin header, 1 pin [form="♀ (female)"]
  op1 = female pin header, 1 pin [form="♀ (female)"]
  op2 = female pin header, 1 pin [form="♀ (female)"]
  op3 = female pin header, 1 pin [form="♀ (female)"]
  74ls139 = IC, DIP package, 16 pins [chip_label=IC]
  LED2 = LED - 3mm [color="Red (633nm)" package="3 mm [THT]"]
  LED3 = LED - 3mm [color="Red (633nm)" package="3 mm [THT]"]
  LED4 = LED - 3mm [color="Red (633nm)" package="3 mm [THT]"]
  LED5 = LED - 3mm [color="Red (633nm)" package="3 mm [THT]"]
  LED7 = LED - 3mm [color="Red (633nm)" package="3 mm [THT]"]
  LED9 = LED - 3mm [color="Red (633nm)" package="3 mm [THT]"]
  LED8 = LED - 3mm [color="Red (633nm)" package="3 mm [THT]"]
  LED6 = LED - 3mm [color="Red (633nm)" package="3 mm [THT]"]
  R1 = Resistor [tolerance=±5% resistance=220 package="1206 [SMD]"]
  R2 = Resistor [tolerance=±5% resistance=220 package="1206 [SMD]"]
  R3 = Resistor [tolerance=±5% resistance=220 package="1206 [SMD]"]
  R4 = Resistor [tolerance=±5% resistance=220 package="1206 [SMD]"]
  R5 = Resistor [tolerance=±5% resistance=220 package="1206 [SMD]"]
  R6 = Resistor [tolerance=±5% resistance=220 package="1206 [SMD]"]
  R7 = Resistor [tolerance=±5% resistance=220 package="1206 [SMD]"]
  R8 = Resistor [tolerance=±5% resistance=220 package="1206 [SMD]"]
  LED10 = LED - 3mm [color="Red (633nm)" package="3 mm [THT]"]
  LED11 = LED - 3mm [color="Red (633nm)" package="3 mm [THT]"]
  LED12 = LED - 3mm [color="Red (633nm)" package="3 mm [THT]"]
  LED13 = LED - 3mm [color="Red (633nm)" package="3 mm [THT]"]
  LED14 = LED - 3mm [color="Red (633nm)" package="3 mm [THT]"]
  LED15 = LED - 3mm [color="Red (633nm)" package="3 mm [THT]"]
  LED16 = LED - 3mm [color="Red (633nm)" package="3 mm [THT]"]
  LED17 = LED - 3mm [color="Red (633nm)" package="3 mm [THT]"]
  LED18 = LED - 3mm [color="Red (633nm)" package="3 mm [THT]"]
  LED19 = LED - 3mm [color="Red (633nm)" package="3 mm [THT]"]
  LED20 = LED - 3mm [color="Red (633nm)" package="3 mm [THT]"]
  LED21 = LED - 3mm [color="Red (633nm)" package="3 mm [THT]"]
  LED22 = LED - 3mm [color="Red (633nm)" package="3 mm [THT]"]
  LED23 = LED - 3mm [color="Red (633nm)" package="3 mm [THT]"]
  LED24 = LED - 3mm [color="Red (633nm)" package="3 mm [THT]"]
  LED25 = LED - 3mm [color="Red (633nm)" package="3 mm [THT]"]
  LED26 = LED - 3mm [color="Red (633nm)" package="3 mm [THT]"]
  LED27 = LED - 3mm [color="Red (633nm)" package="3 mm [THT]"]
  LED28 = LED - 3mm [color="Red (633nm)" package="3 mm [THT]"]
  LED29 = LED - 3mm [color="Red (633nm)" package="3 mm [THT]"]
  LED30 = LED - 3mm [color="Red (633nm)" package="3 mm [THT]"]
  LED31 = LED - 3mm [color="Red (633nm)" package="3 mm [THT]"]
  R9 = Resistor [tolerance=±5% resistance=220 package="1206 [SMD]"]
  R10 = Resistor [tolerance=±5% resistance=220 package="1206 [SMD]"]
  R11 = Resistor [tolerance=±5% resistance=220 package="1206 [SMD]"]
  R12 = Resistor [tolerance=±5% resistance=220 package="1206 [SMD]"]
  R13 = Resistor [tolerance=±5% resistance=220 package="1206 [SMD]"]
  R14 = Resistor [tolerance=±5% resistance=220 package="1206 [SMD]"]
  R15 = Resistor [tolerance=±5% resistance=220 package="1206 [SMD]"]
  R16 = Resistor [tolerance=±5% resistance=220 package="1206 [SMD]"]
  R17 = Resistor [tolerance=±5% resistance=220 package="1206 [SMD]"]
  R18 = Resistor [tolerance=±5% resistance=220 package="1206 [SMD]"]
  R19 = Resistor [tolerance=±5% resistance=220 package="1206 [SMD]"]
  R20 = Resistor [tolerance=±5% resistance=220 package="1206 [SMD]"]
  R21 = Resistor [tolerance=±5% resistance=220 package="1206 [SMD]"]
  R22 = Resistor [tolerance=±5% resistance=220 package="1206 [SMD]"]
  R23 = Resistor [tolerance=±5% resistance=220 package="1206 [SMD]"]
  R24 = Resistor [tolerance=±5% resistance=220 package="1206 [SMD]"]
  R25 = Resistor [tolerance=±5% resistance=220 package="1206 [SMD]"]
  R26 = Resistor [tolerance=±5% resistance=220 package="1206 [SMD]"]
  R27 = Resistor [tolerance=±5% resistance=220 package="1206 [SMD]"]
  R28 = Resistor [tolerance=±5% resistance=220 package="1206 [SMD]"]
  R29 = Resistor [tolerance=±5% resistance=220 package="1206 [SMD]"]
  R30 = Resistor [tolerance=±5% resistance=220 package="1206 [SMD]"]
  enable_not = female pin header, 1 pin [form="♀ (female)"]
  en8 = female pin header, 1 pin [form="♀ (female)"]
  LED32 = LED - 3mm [color="Red (633nm)" package="3 mm [THT]"]
  R31 = Resistor [tolerance=±5% resistance=220 package="1206 [SMD]"]
  7404 = IC, DIP package, 14 pins [chip_label=IC]
  LED33 = LED - 3mm [color="Red (633nm)" package="3 mm [THT]"]
  LED34 = LED - 3mm [color="Red (633nm)" package="3 mm [THT]"]
  R32 = Resistor [tolerance=±5% resistance=220 package="1206 [SMD]"]
  R33 = Resistor [tolerance=±5% resistance=220 package="1206 [SMD]"]
  LED35 = LED - 3mm [color="Red (633nm)" package="3 mm [THT]"]
  R34 = Resistor [tolerance=±5% resistance=220 package="1206 [SMD]"]
  C1 = Ceramic Capacitor [capacitance=100nF package="100 mil [THT, multilayer]"]

nets:
  N1: power.pin1, 74ls139.pin16, R9.Pin_0, R10.Pin_0, R11.Pin_0, R12.Pin_0, R13.Pin_0, R14.Pin_0, R31.Pin_0, 7404.pin14, C1.0
  N2: power.pin2, 74ls139.pin8, R1.Pin_0, R2.Pin_0, R3.Pin_0, R4.Pin_0, R5.Pin_0, R6.Pin_0, R7.Pin_0, R8.Pin_0, R15.Pin_1, R16.Pin_1, R17.Pin_1, R18.Pin_1, R19.Pin_1, R20.Pin_1, R21.Pin_1, R22.Pin_1, R23.Pin_1, R24.Pin_1, R25.Pin_1, R26.Pin_1, R27.Pin_1, R28.Pin_1, R29.Pin_1, R30.Pin_1, 7404.pin7, R32.Pin_0, R33.Pin_0, R34.Pin_1, C1.1
  N3: carry_in.pin1, carry_in1.pin1, LED35.anode
  N4: carry_out.pin1, co.pin1, LED33.anode
  N5: input_b.pin1, input_b1.pin1, LED25.anode
  N6: input_b.pin2, input_b1.pin2, LED23.anode
  N7: input_b.pin3, input_b1.pin3, LED19.anode
  N8: input_b.pin4, input_b1.pin4, LED18.anode
  N9: input_b.pin5, input_b1.pin5, LED24.anode
  N10: input_b.pin6, input_b1.pin6, LED20.anode
  N11: input_b.pin7, input_b1.pin7, LED22.anode
  N12: input_b.pin8, input_b1.pin8, LED21.anode
  N13: input_a.pin1, input_a1.pin1, LED17.anode
  N14: input_a.pin2, input_a1.pin2, LED11.anode
  N15: input_a.pin3, input_a1.pin3, LED10.anode
  N16: input_a.pin4, input_a1.pin4, LED13.anode
  N17: input_a.pin5, input_a1.pin5, LED12.anode
  N18: input_a.pin6, input_a1.pin6, LED16.anode
  N19: input_a.pin7, input_a1.pin7, LED14.anode
  N20: input_a.pin8, input_a1.pin8, LED15.anode
  N21: output.pin1, s.pin1, LED2.anode
  N22: output.pin2, s.pin2, LED3.anode
  N23: output.pin3, s.pin3, LED4.anode
  N24: output.pin4, s.pin4, LED5.anode
  N25: output.pin5, s.pin5, LED7.anode
  N26: output.pin6, s.pin6, LED6.anode
  N27: output.pin7, s.pin7, LED9.anode
  N28: output.pin8, s.pin8, LED8.anode
  N29: enable_add.pin1, en.pin1, 74ls139.pin4, LED30.anode
  N30: nonzero.pin1, nz.pin1, LED34.anode
  N31: enable_and.pin1, en1.pin1, 74ls139.pin5, LED31.anode
  N32: enable_or.pin1, en2.pin1, 74ls139.pin6, LED29.anode
  N33: enable_xor.pin1, en3.pin1, 74ls139.pin7, LED27.anode
  N34: enable_rol.pin1, en4.pin1, 74ls139.pin12, LED28.anode
  N35: en5.pin1, enable_ror.pin1, 74ls139.pin11, LED26.anode
  N36: en6.pin1, op0.pin1, 74ls139.pin1, 7404.pin1
  N37: en7.pin1, op1.pin1, 74ls139.pin3, 74ls139.pin13
  N38: op2.pin1, op3.pin1, 74ls139.pin2, 74ls139.pin14
  N39: 74ls139.pin10, enable_not.pin1, en8.pin1, LED32.anode
  N40: 74ls139.pin15, 7404.pin2
  N41: LED2.cathode, R1.Pin_1
  N42: LED3.cathode, R2.Pin_1
  N43: LED4.cathode, R3.Pin_1
  N44: LED5.cathode, R4.Pin_1
  N45: LED7.cathode, R5.Pin_1
  N46: LED9.cathode, R6.Pin_1
  N47: LED8.cathode, R8.Pin_1
  N48: LED6.cathode, R7.Pin_1
  N49: LED10.cathode, R15.Pin_0
  N50: LED11.cathode, R16.Pin_0
  N51: LED12.cathode, R17.Pin_0
  N52: LED13.cathode, R20.Pin_0
  N53: LED14.cathode, R22.Pin_0
  N54: LED15.cathode, R21.Pin_0
  N55: LED16.cathode, R18.Pin_0
  N56: LED17.cathode, R19.Pin_0
  N57: LED18.cathode, R24.Pin_0
  N58: LED19.cathode, R30.Pin_0
  N59: LED20.cathode, R27.Pin_0
  N60: LED21.cathode, R25.Pin_0
  N61: LED22.cathode, R29.Pin_0
  N62: LED23.cathode, R26.Pin_0
  N63: LED24.cathode, R23.Pin_0
  N64: LED25.cathode, R28.Pin_0
  N65: LED26.cathode, R11.Pin_1
  N66: LED27.cathode, R13.Pin_1
  N67: LED28.cathode, R14.Pin_1
  N68: LED29.cathode, R10.Pin_1
  N69: LED30.cathode, R9.Pin_1
  N70: LED31.cathode, R12.Pin_1
  N71: LED32.cathode, R31.Pin_1
  N72: LED33.cathode, R32.Pin_1
  N73: LED34.cathode, R33.Pin_1
  N74: LED35.cathode, R34.Pin_0
