# Fritzing sketch aluregs (saved by Fritzing 0.9.3b)
circuit board: 13.8542cm x 7.81278cm
breadboards: 1

parts:
  BUS = female pin header, 8 pins [form="♀ (female)"]
  74LS173_A-HIGH = IC, DIP package, 16 pins [chip_label=IC]
  74LS173_A-LOW = IC, DIP package, 16 pins [chip_label=IC]
  74LS173_B-LOW = IC, DIP package, 16 pins [chip_label=IC]
  74LS173_B-HIGH = IC, DIP package, 16 pins [chip_label=IC]
  CLK = female pin header, 1 pin [form="♀ (female)"]
  RESET-A = female pin header, 1 pin [form="♀ (female)"]
  LOAD-A = female pin header, 1 pin [form="♀ (female)"]
  LOAD-B = female pin header, 1 pin [form="♀ (female)"]
  RESET-B = female pin header, 1 pin [form="♀ (female)"]
  LED1 = LED - 5mm [color="Red (633nm)" package="5 mm [THT]"]
  LED2 = LED - 5mm [color="Red (633nm)" package="5 mm [THT]"]
  OUTPUT_A = female pin header, 8 pins [form="♀ (female)"]
  LED3 = LED - 5mm [color="Red (633nm)" package="5 mm [THT]"]
  LED4 = LED - 5mm [color="Red (633nm)" package="5 mm [THT]"]
  LED5 = LED - 5mm [color="Red (633nm)" package="5 mm [THT]"]
  LED6 = LED - 5mm [color="Red (633nm)" package="5 mm [THT]"]
  LED7 = LED - 5mm [color="Red (633nm)" package="5 mm [THT]"]
  LED8 = LED - 5mm [color="Red (633nm)" package="5 mm [THT]"]
  LED9 = LED - 5mm [color="Red (633nm)" package="5 mm [THT]"]
  LED10 = LED - 5mm [color="Red (633nm)" package="5 mm [THT]"]
  LED11 = LED - 5mm [color="Red (633nm)" package="5 mm [THT]"]
  LED12 = LED - 5mm [color="Red (633nm)" package="5 mm [THT]"]
  LED13 = LED - 5mm [color="Red (633nm)" package="5 mm [THT]"]
  LED14 = LED - 5mm [color="Red (633nm)" package="5 mm [THT]"]
  LED15 = LED - 5mm [color="Red (633nm)" package="5 mm [THT]"]
  LED16 = LED - 5mm [color="Red (633nm)" package="5 mm [THT]"]
  OUTPUT_B = female pin header, 8 pins [form="♀ (female)"]
  74LS86 = IC, DIP package, 14 pins [chip_label=IC]
  74LS86_2 = IC, DIP package, 14 pins [chip_label=IC]
  J2 = female pin header, 2 pins [form="♀ (female)"]
  C1 = Ceramic Capacitor [capacitance=100nF package="100 mil [THT, multilayer]"]
  LED17 = LED - 5mm [color="Red (633nm)" package="5 mm [THT]"]
  INVERT-B = female pin header, 1 pin [form="♀ (female)"]
  R2 = Resistor [tolerance=±5% resistance=220 package="1206 [SMD]"]
  R3 = Resistor [tolerance=±5% resistance=220 package="1206 [SMD]"]
  R4 = Resistor [tolerance=±5% resistance=220 package="1206 [SMD]"]
  R5 = Resistor [tolerance=±5% resistance=220 package="1206 [SMD]"]
  R6 = Resistor [tolerance=±5% resistance=220 package="1206 [SMD]"]
  R7 = Resistor [tolerance=±5% resistance=220 package="1206 [SMD]"]
  R8 = Resistor [tolerance=±5% resistance=220 package="1206 [SMD]"]
  R9 = Resistor [tolerance=±5% resistance=220 package="1206 [SMD]"]
  R10 = Resistor [tolerance=±5% resistance=220 package="1206 [SMD]"]
  R11 = Resistor [tolerance=±5% resistance=220 package="1206 [SMD]"]
  R12 = Resistor [tolerance=±5% resistance=220 package="1206 [SMD]"]
  R13 = Resistor [tolerance=±5% resistance=220 package="1206 [SMD]"]
  R14 = Resistor [tolerance=±5% resistance=220 package="1206 [SMD]"]
  R15 = Resistor [tolerance=±5% resistance=220 package="1206 [SMD]"]
  R16 = Resistor [tolerance=±5% resistance=220 package="1206 [SMD]"]
  R17 = Resistor [tolerance=±5% resistance=220 package="1206 [SMD]"]
  R18 = Resistor [tolerance=±5% resistance=220 package="1206 [SMD]"]
  C2 = Ceramic Capacitor [capacitance=100nF package="100 mil [THT, multilayer]"]
  J3 = female pin header, 1 pin [form="♀ (female)"]
  J4 = female pin header, 1 pin [form="♀ (female)"]
  J5 = female pin header, 2 pins [form="♀ (female)"]
  J6 = female pin header, 2 pins [form="♀ (female)"]
  J7 = female pin header, 1 pin [form="♀ (female)"]
  J8 = female pin header, 1 pin [form="♀ (female)"]
  CLK1 = female pin header, 1 pin [form="♀ (female)"]
  CLK2 = female pin header, 1 pin [form="♀ (female)"]

nets:
  N1: BUS.pin1, 74LS173_A-LOW.pin11, 74LS173_B-LOW.pin11
  N2: BUS.pin2, 74LS173_A-LOW.pin12, 74LS173_B-LOW.pin12
  N3: BUS.pin3, 74LS173_A-LOW.pin13, 74LS173_B-LOW.pin13
  N4: BUS.pin4, 74LS173_A-LOW.pin14, 74LS173_B-LOW.pin14
  N5: BUS.pin5, 74LS173_A-HIGH.pin11, 74LS173_B-HIGH.pin11
  N6: BUS.pin6, 74LS173_A-HIGH.pin12, 74LS173_B-HIGH.pin12
  N7: BUS.pin7, 74LS173_A-HIGH.pin13, 74LS173_B-HIGH.pin13
  N8: BUS.pin8, 74LS173_A-HIGH.pin14, 74LS173_B-HIGH.pin14
  N9: 74LS173_A-HIGH.pin1, 74LS173_A-HIGH.pin2, 74LS173_A-HIGH.pin8, 74LS173_A-LOW.pin1, 74LS173_A-LOW.pin2, 74LS173_A-LOW.pin8, 74LS173_B-LOW.pin1, 74LS173_B-LOW.pin2, 74LS173_B-LOW.pin8, 74LS173_B-HIGH.pin1, 74LS173_B-HIGH.pin2, 74LS173_B-HIGH.pin8, 74LS86.pin7, 74LS86_2.pin7, J2.pin2, C1.0, R2.Pin_1, R3.Pin_1, R4.Pin_1, R5.Pin_1, R6.Pin_1, R7.Pin_1, R8.Pin_1, R9.Pin_1, R10.Pin_1, R11.Pin_1, R12.Pin_1, R13.Pin_1, R14.Pin_1, R15.Pin_1, R16.Pin_1, R17.Pin_1, R18.Pin_1, C2.0, J4.pin1, J5.pin2, J6.pin2, J8.pin1
  N10: 74LS173_A-HIGH.pin3, LED1.anode, OUTPUT_A.pin1
  N11: 74LS173_A-HIGH.pin4, LED2.anode, OUTPUT_A.pin2
  N12: 74LS173_A-HIGH.pin5, OUTPUT_A.pin3, LED4.anode
  N13: 74LS173_A-HIGH.pin6, OUTPUT_A.pin4, LED3.anode
  N14: 74LS173_A-HIGH.pin7, 74LS173_A-LOW.pin7, 74LS173_B-LOW.pin7, 74LS173_B-HIGH.pin7, CLK.pin1, CLK1.pin1, CLK2.pin1
  N15: 74LS173_A-HIGH.pin9, 74LS173_A-HIGH.pin10, 74LS173_A-LOW.pin9, 74LS173_A-LOW.pin10, LOAD-A.pin1
  N16: 74LS173_A-HIGH.pin15, 74LS173_A-LOW.pin15, RESET-A.pin1
  N17: 74LS173_A-HIGH.pin16, 74LS173_A-LOW.pin16, 74LS173_B-LOW.pin16, 74LS173_B-HIGH.pin16, 74LS86.pin14, 74LS86_2.pin14, J2.pin1, C1.1, C2.1, J3.pin1, J5.pin1, J6.pin1, J7.pin1
  N18: 74LS173_A-LOW.pin3, OUTPUT_A.pin5, LED6.anode
  N19: 74LS173_A-LOW.pin4, OUTPUT_A.pin6, LED7.anode
  N20: 74LS173_A-LOW.pin5, OUTPUT_A.pin7, LED8.anode
  N21: 74LS173_A-LOW.pin6, OUTPUT_A.pin8, LED5.anode
  N22: 74LS173_B-LOW.pin3, LED9.anode, 74LS86_2.pin1
  N23: 74LS173_B-LOW.pin4, LED10.anode, 74LS86_2.pin12
  N24: 74LS173_B-LOW.pin5, LED11.anode, 74LS86_2.pin9
  N25: 74LS173_B-LOW.pin6, LED13.anode, 74LS86_2.pin5
  N26: 74LS173_B-LOW.pin9, 74LS173_B-LOW.pin10, 74LS173_B-HIGH.pin9, 74LS173_B-HIGH.pin10, LOAD-B.pin1
  N27: 74LS173_B-LOW.pin15, 74LS173_B-HIGH.pin15, RESET-B.pin1
  N28: 74LS173_B-HIGH.pin3, LED14.anode, 74LS86.pin1
  N29: 74LS173_B-HIGH.pin4, LED15.anode, 74LS86.pin12
  N30: 74LS173_B-HIGH.pin5, LED12.anode, 74LS86.pin9
  N31: 74LS173_B-HIGH.pin6, LED16.anode, 74LS86.pin5
  N32: LED1.cathode, R2.Pin_0
  N33: LED2.cathode, R3.Pin_0
  N34: LED3.cathode, R5.Pin_0
  N35: LED4.cathode, R4.Pin_0
  N36: LED5.cathode, R9.Pin_0
  N37: LED6.cathode, R6.Pin_0
  N38: LED7.cathode, R8.Pin_0
  N39: LED8.cathode, R7.Pin_0
  N40: LED9.cathode, R17.Pin_0
  N41: LED10.cathode, R11.Pin_0
  N42: LED11.cathode, R16.Pin_0
  N43: LED12.cathode, R12.Pin_0
  N44: LED13.cathode, R13.Pin_0
  N45: LED14.cathode, R10.Pin_0
  N46: LED15.cathode, R14.Pin_0
  N47: LED16.cathode, R15.Pin_0
  N48: OUTPUT_B.pin1, 74LS86.pin3
  N49: OUTPUT_B.pin2, 74LS86.pin11
  N50: OUTPUT_B.pin3, 74LS86.pin8
  N51: OUTPUT_B.pin4, 74LS86.pin6
  N52: OUTPUT_B.pin5, 74LS86_2.pin3
  N53: OUTPUT_B.pin6, 74LS86_2.pin11
  N54: OUTPUT_B.pin7, 74LS86_2.pin8
  N55: OUTPUT_B.pin8, 74LS86_2.pin6
  N56: 74LS86.pin2, 74LS86.pin4, 74LS86.pin10, 74LS86.pin13, 74LS86_2.pin2, 74LS86_2.pin4, 74LS86_2.pin10, 74LS86_2.pin13, LED17.anode, INVERT-B.pin1
  N57: LED17.cathode, R18.Pin_0

notes:
  VCC
  GND
