# Fritzing sketch andorxor (saved by Fritzing 0.9.3b)
circuit board: 7.00084cm x 6.97166cm
breadboards: 1

parts:
  power = female pin header, 2 pins [form="♀ (female)"]
  carry_in = female pin header, 1 pin [form="♀ (female)"]
  carry_out = female pin header, 1 pin [form="♀ (female)"]
  input_b = female pin header, 8 pins [form="♀ (female)"]
  input_a = female pin header, 8 pins [form="♀ (female)"]
  output = female pin header, 8 pins [form="♀ (female)"]
  enable_add = female pin header, 1 pin [form="♀ (female)"]
  74LS245_ROR = IC, DIP package, 20 pins [chip_label=IC]
  nonzero = female pin header, 1 pin [form="♀ (female)"]
  nz = female pin header, 1 pin [form="♀ (female)"]
  co = female pin header, 1 pin [form="♀ (female)"]
  s = female pin header, 8 pins [form="♀ (female)"]
  en = female pin header, 1 pin [form="♀ (female)"]
  enable_and = female pin header, 1 pin [form="♀ (female)"]
  en1 = female pin header, 1 pin [form="♀ (female)"]
  enable_or = female pin header, 1 pin [form="♀ (female)"]
  en2 = female pin header, 1 pin [form="♀ (female)"]
  enable_xor = female pin header, 1 pin [form="♀ (female)"]
  en3 = female pin header, 1 pin [form="♀ (female)"]
  enable_rol = female pin header, 1 pin [form="♀ (female)"]
  en4 = female pin header, 1 pin [form="♀ (female)"]
  en5 = female pin header, 1 pin [form="♀ (female)"]
  enable_ror = female pin header, 1 pin [form="♀ (female)"]
  carry_in1 = female pin header, 1 pin [form="♀ (female)"]
  input_b1 = female pin header, 8 pins [form="♀ (female)"]
  input_a1 = female pin header, 8 pins [form="♀ (female)"]
  en6 = female pin header, 1 pin [form="♀ (female)"]
  op0 = female pin header, 1 pin [form="♀ (female)"]
  en7 = female pin header, 1 pin [form="♀ (female)"]
  op1 = female pin header, 1 pin [form="♀ (female)"]
  op2 = female pin header, 1 pin [form="♀ (female)"]
  op3 = female pin header, 1 pin [form="♀ (female)"]
  power1 = female pin header, 2 pins [form="♀ (female)"]
  enable_xor1 = female pin header, 1 pin [form="♀ (female)"]
  enable_or1 = female pin header, 1 pin [form="♀ (female)"]
  enable_and1 = female pin header, 1 pin [form="♀ (female)"]
  enable_xor2 = female pin header, 1 pin [form="♀ (female)"]
  enable_or2 = female pin header, 1 pin [form="♀ (female)"]
  enable_and2 = female pin header, 1 pin [form="♀ (female)"]
  Logic_Low_4bit = IC, DIP package, 14 pins [chip_label=IC]
  Logic_High_4bit = IC, DIP package, 14 pins [chip_label=IC]
  C1 = Ceramic Capacitor [capacitance=100nF package="100 mil [THT, multilayer]"]
  enable_not = female pin header, 1 pin [form="♀ (female)"]
  en8 = female pin header, 1 pin [form="♀ (female)"]

nets:
  N1: power.pin1, 74LS245_ROR.pin20, power1.pin1, Logic_Low_4bit.pin14, Logic_High_4bit.pin14, C1.1
  N2: power.pin2, 74LS245_ROR.pin1, 74LS245_ROR.pin10, power1.pin2, Logic_Low_4bit.pin7, Logic_High_4bit.pin7, C1.0
  N3: carry_in.pin1, carry_in1.pin1
  N4: carry_out.pin1, co.pin1
  N5: input_b.pin1, input_b1.pin1, Logic_High_4bit.pin2
  N6: input_b.pin2, input_b1.pin2, Logic_High_4bit.pin5
  N7: input_b.pin3, input_b1.pin3, Logic_High_4bit.pin12
  N8: input_b.pin4, input_b1.pin4, Logic_High_4bit.pin9
  N9: input_b.pin5, input_b1.pin5, Logic_Low_4bit.pin2
  N10: input_b.pin6, input_b1.pin6, Logic_Low_4bit.pin5
  N11: input_b.pin7, input_b1.pin7, Logic_Low_4bit.pin12
  N12: input_b.pin8, input_b1.pin8, Logic_Low_4bit.pin9
  N13: input_a.pin1, input_a1.pin1, Logic_High_4bit.pin1
  N14: input_a.pin2, input_a1.pin2, Logic_High_4bit.pin4
  N15: input_a.pin3, input_a1.pin3, Logic_High_4bit.pin13
  N16: input_a.pin4, input_a1.pin4, Logic_High_4bit.pin10
  N17: input_a.pin5, input_a1.pin5, Logic_Low_4bit.pin1
  N18: input_a.pin6, input_a1.pin6, Logic_Low_4bit.pin4
  N19: input_a.pin7, input_a1.pin7, Logic_Low_4bit.pin13
  N20: input_a.pin8, input_a1.pin8, Logic_Low_4bit.pin10
  N21: output.pin1, 74LS245_ROR.pin2, s.pin1
  N22: output.pin2, 74LS245_ROR.pin3, s.pin2
  N23: output.pin3, 74LS245_ROR.pin4, s.pin3
  N24: output.pin4, 74LS245_ROR.pin5, s.pin4
  N25: output.pin5, 74LS245_ROR.pin6, s.pin5
  N26: output.pin6, 74LS245_ROR.pin7, s.pin6
  N27: output.pin7, 74LS245_ROR.pin8, s.pin7
  N28: output.pin8, 74LS245_ROR.pin9, s.pin8
  N29: enable_add.pin1, en.pin1
  N30: 74LS245_ROR.pin11, Logic_Low_4bit.pin8
  N31: 74LS245_ROR.pin12, Logic_Low_4bit.pin11
  N32: 74LS245_ROR.pin13, Logic_Low_4bit.pin6
  N33: 74LS245_ROR.pin14, Logic_Low_4bit.pin3
  N34: 74LS245_ROR.pin15, Logic_High_4bit.pin8
  N35: 74LS245_ROR.pin16, Logic_High_4bit.pin11
  N36: 74LS245_ROR.pin17, Logic_High_4bit.pin6
  N37: 74LS245_ROR.pin18, Logic_High_4bit.pin3
  N38: 74LS245_ROR.pin19, enable_xor2.pin1, enable_or2.pin1, enable_and2.pin1
  N39: nonzero.pin1, nz.pin1
  N40: enable_and.pin1, en1.pin1, enable_and1.pin1
  N41: enable_or.pin1, en2.pin1, enable_or1.pin1
  N42: enable_xor.pin1, en3.pin1, enable_xor1.pin1
  N43: enable_rol.pin1, en4.pin1
  N44: en5.pin1, enable_ror.pin1
  N45: en6.pin1, op0.pin1
  N46: en7.pin1, op1.pin1
  N47: op2.pin1, op3.pin1
  N48: enable_not.pin1, en8.pin1
