# Fritzing sketch flags (saved by Fritzing 0.9.3b)
circuit board: 11.22cm x 9.94912cm
breadboards: 1

parts:
  74LS32-3 = IC, DIP package, 14 pins [chip_label=IC]
  74LS32-4 = IC, DIP package, 14 pins [chip_label=IC]
  C2 = Ceramic Capacitor [capacitance=100nF package="100 mil [THT, multilayer]"]
  7408 = IC, DIP package, 14 pins [chip_label=IC]
  74hc126 = IC, DIP package, 14 pins [chip_label=IC]
  zerocarry_out1 = LED - 3mm [color="Red (633nm)" package="3 mm [THT]"]
  R5 = Resistor [tolerance=±5% resistance=220 package="1206 [SMD]"]
  enable_not1 = female pin header, 1 pin [form="♀ (female)"]
  enable_ror1 = female pin header, 1 pin [form="♀ (female)"]  # not connected
  enable_rol1 = female pin header, 1 pin [form="♀ (female)"]  # not connected
  op4 = female pin header, 1 pin [form="♀ (female)"]
  enable_xor1 = female pin header, 1 pin [form="♀ (female)"]
  op5 = female pin header, 1 pin [form="♀ (female)"]
  enable_or1 = female pin header, 1 pin [form="♀ (female)"]
  op7 = female pin header, 1 pin [form="♀ (female)"]
  enable_and1 = female pin header, 1 pin [form="♀ (female)"]
  enable_add1 = female pin header, 1 pin [form="♀ (female)"]  # not connected
  nonzero1 = female pin header, 1 pin [form="♀ (female)"]
  carry_out1 = female pin header, 1 pin [form="♀ (female)"]
  carry_in2 = female pin header, 1 pin [form="♀ (female)"]
  carry_in3 = female pin header, 1 pin [form="♀ (female)"]
  input_b2 = female pin header, 8 pins [form="♀ (female)"]
  input_b3 = female pin header, 8 pins [form="♀ (female)"]
  input_a2 = female pin header, 8 pins [form="♀ (female)"]
  input_a3 = female pin header, 8 pins [form="♀ (female)"]
  output1 = female pin header, 8 pins [form="♀ (female)"]
  power3 = female pin header, 2 pins [form="♀ (female)"]
  IC2 = IC, DIP package, 20 pins [chip_label=IC]
  alu_write = female alternating pin header, 1 pin [form="♀ (female)"]
  alu2bus1 = female pin header, 8 pins [form="♀ (female)"]
  C3 = Ceramic Capacitor [capacitance=100nF package="100 mil [THT, multilayer]"]
  flag_output1 = female pin header, 3 pins [form="♀ (female)"]
  NZ/NEG = female pin header, 2 pins [form="♀ (female)"]
  74ls74_nzneglatch1 = IC, DIP package, 14 pins [chip_label=IC]
  74ls74_carrylatch1 = IC, DIP package, 14 pins [chip_label=IC]
  7408_2 = IC, DIP package, 14 pins [chip_label=IC]
  Flag_update = female pin header, 2 pins [form="♀ (female)"]
  J1 = female pin header, 3 pins [form="♀ (female)"]
  power4 = female pin header, 2 pins [form="♀ (female)"]
  C4 = Ceramic Capacitor [capacitance=100nF package="100 mil [THT, multilayer]"]
  J2 = female pin header, 2 pins [form="♀ (female)"]

nets:
  N1: 74LS32-3.pin1, output1.pin1, IC2.pin11, 74ls74_nzneglatch1.pin12
  N2: 74LS32-3.pin2, output1.pin2, IC2.pin12
  N3: 74LS32-3.pin3, 74LS32-3.pin10
  N4: 74LS32-3.pin4, 74LS32-4.pin11
  N5: 74LS32-3.pin5, 74LS32-4.pin8
  N6: 74LS32-3.pin6, 74LS32-3.pin9
  N7: 74LS32-3.pin7, 74LS32-4.pin7, C2.1, 7408.pin7, 74hc126.pin2, 74hc126.pin7, R5.Pin_1, power3.pin2, IC2.pin1, IC2.pin10, C3.0, 74ls74_nzneglatch1.pin7, 74ls74_carrylatch1.pin7, 7408_2.pin7, power4.pin1, C4.0, J2.pin2
  N8: 74LS32-3.pin8, 74LS32-3.pin12
  N9: 74LS32-3.pin11, nonzero1.pin1, 74ls74_nzneglatch1.pin2
  N10: 74LS32-3.pin13, 74hc126.pin3, carry_out1.pin1, 74ls74_carrylatch1.pin12
  N11: 74LS32-3.pin14, 74LS32-4.pin14, C2.0, 7408.pin14, 74hc126.pin14, power3.pin1, IC2.pin20, C3.1, 74ls74_nzneglatch1.pin1, 74ls74_nzneglatch1.pin4, 74ls74_nzneglatch1.pin10, 74ls74_nzneglatch1.pin13, 74ls74_nzneglatch1.pin14, 74ls74_carrylatch1.pin14, 7408_2.pin14, power4.pin2, C4.1, J2.pin1
  N12: 74LS32-4.pin1, output1.pin6, IC2.pin16
  N13: 74LS32-4.pin2, output1.pin5, IC2.pin15
  N14: 74LS32-4.pin3, 74LS32-4.pin10
  N15: 74LS32-4.pin4, output1.pin7, IC2.pin17
  N16: 74LS32-4.pin5, output1.pin8, IC2.pin18
  N17: 74LS32-4.pin6, 74LS32-4.pin9
  N18: 74LS32-4.pin12, output1.pin4, IC2.pin14
  N19: 74LS32-4.pin13, output1.pin3, IC2.pin13
  N20: 7408.pin1, enable_and1.pin1
  N21: 7408.pin2, enable_or1.pin1
  N22: 7408.pin3, 7408.pin10
  N23: 7408.pin4, enable_xor1.pin1
  N24: 7408.pin5, enable_not1.pin1
  N25: 7408.pin6, 7408.pin9
  N26: 7408.pin8, 74hc126.pin1, zerocarry_out1.anode
  N27: zerocarry_out1.cathode, R5.Pin_0
  N28: op4.pin1, J1.pin3
  N29: op5.pin1, J1.pin2
  N30: op7.pin1, J1.pin1
  N31: carry_in2.pin1, carry_in3.pin1, flag_output1.pin3, 74ls74_carrylatch1.pin9
  N32: input_b2.pin1, input_b3.pin1
  N33: input_b2.pin2, input_b3.pin2
  N34: input_b2.pin3, input_b3.pin3
  N35: input_b2.pin4, input_b3.pin4
  N36: input_b2.pin5, input_b3.pin5
  N37: input_b2.pin6, input_b3.pin6
  N38: input_b2.pin7, input_b3.pin7
  N39: input_b2.pin8, input_b3.pin8
  N40: input_a2.pin1, input_a3.pin1
  N41: input_a2.pin2, input_a3.pin2
  N42: input_a2.pin3, input_a3.pin3
  N43: input_a2.pin4, input_a3.pin4
  N44: input_a2.pin5, input_a3.pin5
  N45: input_a2.pin6, input_a3.pin6
  N46: input_a2.pin7, input_a3.pin7
  N47: input_a2.pin8, input_a3.pin8
  N48: IC2.pin2, alu2bus1.pin1
  N49: IC2.pin3, alu2bus1.pin2
  N50: IC2.pin4, alu2bus1.pin3
  N51: IC2.pin5, alu2bus1.pin4
  N52: IC2.pin6, alu2bus1.pin5
  N53: IC2.pin7, alu2bus1.pin6
  N54: IC2.pin8, alu2bus1.pin7
  N55: IC2.pin9, alu2bus1.pin8
  N56: IC2.pin19, alu_write.pin1
  N57: flag_output1.pin1, 74ls74_carrylatch1.pin13
  N58: flag_output1.pin2, 74ls74_carrylatch1.pin10
  N59: NZ/NEG.pin1, 74ls74_nzneglatch1.pin9
  N60: NZ/NEG.pin2, 74ls74_nzneglatch1.pin5
  N61: 74ls74_nzneglatch1.pin3, 74ls74_nzneglatch1.pin11, 74ls74_carrylatch1.pin11, 7408_2.pin3
  N62: 7408_2.pin1, Flag_update.pin2
  N63: 7408_2.pin2, Flag_update.pin1

notes:
  NZF
  CF
  NEGF
  CLK
  FLAGW
  CC
  CS
