# Fritzing sketch rolror (saved by Fritzing 0.9.3b)
circuit board: 7.00084cm x 6.97166cm
breadboards: 1

parts:
  power = female pin header, 2 pins [form="♀ (female)"]
  carry_in = female pin header, 1 pin [form="♀ (female)"]
  carry_out = female pin header, 1 pin [form="♀ (female)"]
  input_b = female pin header, 8 pins [form="♀ (female)"]
  input_a = female pin header, 8 pins [form="♀ (female)"]
  output = female pin header, 8 pins [form="♀ (female)"]
  enable_add = female pin header, 1 pin [form="♀ (female)"]
  74LS245_ROR = IC, DIP package, 20 pins [chip_label=IC]
  nonzero = female pin header, 1 pin [form="♀ (female)"]
  74HC125 = IC, DIP package, 14 pins [chip_label=IC]
  nz = female pin header, 1 pin [form="♀ (female)"]
  co = female pin header, 1 pin [form="♀ (female)"]
  s = female pin header, 8 pins [form="♀ (female)"]
  en = female pin header, 1 pin [form="♀ (female)"]
  enable_and = female pin header, 1 pin [form="♀ (female)"]
  en1 = female pin header, 1 pin [form="♀ (female)"]
  enable_or = female pin header, 1 pin [form="♀ (female)"]
  en2 = female pin header, 1 pin [form="♀ (female)"]
  enable_xor = female pin header, 1 pin [form="♀ (female)"]
  en3 = female pin header, 1 pin [form="♀ (female)"]
  enable_rol = female pin header, 1 pin [form="♀ (female)"]
  en4 = female pin header, 1 pin [form="♀ (female)"]
  en5 = female pin header, 1 pin [form="♀ (female)"]
  enable_ror = female pin header, 1 pin [form="♀ (female)"]
  carry_in1 = female pin header, 1 pin [form="♀ (female)"]
  input_b1 = female pin header, 8 pins [form="♀ (female)"]
  input_a1 = female pin header, 8 pins [form="♀ (female)"]
  en6 = female pin header, 1 pin [form="♀ (female)"]
  op0 = female pin header, 1 pin [form="♀ (female)"]
  en7 = female pin header, 1 pin [form="♀ (female)"]
  op1 = female pin header, 1 pin [form="♀ (female)"]
  op2 = female pin header, 1 pin [form="♀ (female)"]
  op3 = female pin header, 1 pin [form="♀ (female)"]
  power1 = female pin header, 2 pins [form="♀ (female)"]
  74LS245-ROL = IC, DIP package, 20 pins [chip_label=IC]
  C1 = Ceramic Capacitor [capacitance=100nF package="100 mil [THT, multilayer]"]
  enable_not = female pin header, 1 pin [form="♀ (female)"]
  en8 = female pin header, 1 pin [form="♀ (female)"]

nets:
  N1: power.pin1, 74LS245_ROR.pin20, 74HC125.pin14, power1.pin1, 74LS245-ROL.pin20, C1.1
  N2: power.pin2, 74LS245_ROR.pin1, 74LS245_ROR.pin10, 74HC125.pin7, power1.pin2, 74LS245-ROL.pin1, 74LS245-ROL.pin10, C1.0
  N3: carry_in.pin1, 74LS245_ROR.pin18, carry_in1.pin1, 74LS245-ROL.pin11
  N4: carry_out.pin1, 74HC125.pin3, 74HC125.pin6, co.pin1
  N5: input_b.pin1, 74LS245_ROR.pin17, input_b1.pin1
  N6: input_b.pin2, 74LS245_ROR.pin16, input_b1.pin2
  N7: input_b.pin3, 74LS245_ROR.pin15, input_b1.pin3
  N8: input_b.pin4, 74LS245_ROR.pin14, input_b1.pin4
  N9: input_b.pin5, 74LS245_ROR.pin13, input_b1.pin5
  N10: input_b.pin6, 74LS245_ROR.pin12, input_b1.pin6
  N11: input_b.pin7, 74LS245_ROR.pin11, input_b1.pin7
  N12: input_b.pin8, 74HC125.pin5, input_b1.pin8
  N13: input_a.pin1, 74HC125.pin2, input_a1.pin1
  N14: input_a.pin2, input_a1.pin2, 74LS245-ROL.pin18
  N15: input_a.pin3, input_a1.pin3, 74LS245-ROL.pin17
  N16: input_a.pin4, input_a1.pin4, 74LS245-ROL.pin16
  N17: input_a.pin5, input_a1.pin5, 74LS245-ROL.pin15
  N18: input_a.pin6, input_a1.pin6, 74LS245-ROL.pin14
  N19: input_a.pin7, input_a1.pin7, 74LS245-ROL.pin13
  N20: input_a.pin8, input_a1.pin8, 74LS245-ROL.pin12
  N21: output.pin1, 74LS245_ROR.pin2, s.pin1, 74LS245-ROL.pin2
  N22: output.pin2, 74LS245_ROR.pin3, s.pin2, 74LS245-ROL.pin3
  N23: output.pin3, 74LS245_ROR.pin4, s.pin3, 74LS245-ROL.pin4
  N24: output.pin4, 74LS245_ROR.pin5, s.pin4, 74LS245-ROL.pin5
  N25: output.pin5, 74LS245_ROR.pin6, s.pin5, 74LS245-ROL.pin6
  N26: output.pin6, 74LS245_ROR.pin7, s.pin6, 74LS245-ROL.pin7
  N27: output.pin7, 74LS245_ROR.pin8, s.pin7, 74LS245-ROL.pin8
  N28: output.pin8, 74LS245_ROR.pin9, s.pin8, 74LS245-ROL.pin9
  N29: enable_add.pin1, en.pin1
  N30: 74LS245_ROR.pin19, 74HC125.pin4, en5.pin1, enable_ror.pin1
  N31: nonzero.pin1, nz.pin1
  N32: 74HC125.pin1, enable_rol.pin1, en4.pin1, 74LS245-ROL.pin19
  N33: enable_and.pin1, en1.pin1
  N34: enable_or.pin1, en2.pin1
  N35: enable_xor.pin1, en3.pin1
  N36: en6.pin1, op0.pin1
  N37: en7.pin1, op1.pin1
  N38: op2.pin1, op3.pin1
  N39: enable_not.pin1, en8.pin1
