# Fritzing sketch bus (saved by Fritzing 0.9.3b)
circuit board: 15.5324cm x 3.34904cm
circuit board: 14.5cm x 2.74696cm
breadboards: 1

parts:
  J1 = female pin header, 8 pins [form="♀ (female)"]
  J2 = female pin header, 8 pins [form="♀ (female)"]
  J3 = female pin header, 8 pins [form="♀ (female)"]
  J4 = female pin header, 8 pins [form="♀ (female)"]
  J5 = female pin header, 8 pins [form="♀ (female)"]
  J6 = female pin header, 8 pins [form="♀ (female)"]
  J7 = female pin header, 8 pins [form="♀ (female)"]
  J8 = female pin header, 8 pins [form="♀ (female)"]
  J9 = female pin header, 8 pins [form="♀ (female)"]
  J10 = female pin header, 8 pins [form="♀ (female)"]
  J11 = female pin header, 8 pins [form="♀ (female)"]
  J12 = female pin header, 8 pins [form="♀ (female)"]
  J13 = female pin header, 8 pins [form="♀ (female)"]
  J14 = female pin header, 8 pins [form="♀ (female)"]
  MAR_PWR = female pin header, 2 pins [form="♀ (female)"]
  RAM_PWR = female pin header, 2 pins [form="♀ (female)"]
  MAR_SIG = female pin header, 3 pins [form="♀ (female)"]
  J15 = female pin header, 10 pins [form="♀ (female)"]
  Z_SIG = female pin header, 4 pins [form="♀ (female)"]
  Y_SIG = female pin header, 4 pins [form="♀ (female)"]
  X_SIG = female pin header, 4 pins [form="♀ (female)"]
  J17 = female pin header, 2 pins [form="♀ (female)"]
  J16 = female pin header, 4 pins [form="♀ (female)"]

nets:
  N1: J1.pin1, J2.pin1, J3.pin1, J4.pin8, J5.pin1, J6.pin8, J7.pin1, J8.pin8, J9.pin8, J10.pin1, J11.pin1, J12.pin8, J13.pin8, J14.pin1
  N2: J1.pin2, J2.pin2, J3.pin2, J4.pin7, J5.pin2, J6.pin7, J7.pin2, J8.pin7, J9.pin7, J10.pin2, J11.pin2, J12.pin7, J13.pin7, J14.pin2
  N3: J1.pin3, J2.pin3, J3.pin3, J4.pin6, J5.pin3, J6.pin6, J7.pin3, J8.pin6, J9.pin6, J10.pin3, J11.pin3, J12.pin6, J13.pin6, J14.pin3
  N4: J1.pin4, J2.pin4, J3.pin4, J4.pin5, J5.pin4, J6.pin5, J7.pin4, J8.pin5, J9.pin5, J10.pin4, J11.pin4, J12.pin5, J13.pin5, J14.pin4
  N5: J1.pin5, J2.pin5, J3.pin5, J4.pin4, J5.pin5, J6.pin4, J7.pin5, J8.pin4, J9.pin4, J10.pin5, J11.pin5, J12.pin4, J13.pin4, J14.pin5
  N6: J1.pin6, J2.pin6, J3.pin6, J4.pin3, J5.pin6, J7.pin6, J9.pin3, J10.pin6, J11.pin6, J14.pin6
  N7: J1.pin7, J2.pin7, J4.pin2, J5.pin7, J6.pin2, J7.pin7, J8.pin2, J9.pin2, J10.pin7, J12.pin2, J13.pin2, J14.pin7
  N8: J1.pin8, J2.pin8, J3.pin8, J4.pin1, J5.pin8, J6.pin1, J7.pin8, J8.pin1, J9.pin1, J10.pin8, J11.pin8, J12.pin1, J13.pin1, J14.pin8
  N9: J3.pin7, J11.pin7
  N10: J6.pin3, J13.pin3
  N11: J8.pin3, J12.pin3
  N12: MAR_PWR.pin1, RAM_PWR.pin1, J15.pin6, J16.pin3
  N13: MAR_PWR.pin2, RAM_PWR.pin2, J15.pin5, J16.pin2
  N14: MAR_SIG.pin1, J17.pin2
  N15: MAR_SIG.pin2, J17.pin1
  N16: MAR_SIG.pin3, J15.pin1, Z_SIG.pin4, Y_SIG.pin4, X_SIG.pin4, J16.pin1
  N17: J15.pin2, X_SIG.pin1
  N18: J15.pin3, Y_SIG.pin1
  N19: J15.pin4, Z_SIG.pin1
  N20: J15.pin7, Z_SIG.pin2, Y_SIG.pin2, X_SIG.pin2, J16.pin4
  N21: J15.pin8, X_SIG.pin3
  N22: J15.pin9, Y_SIG.pin3
  N23: J15.pin10, Z_SIG.pin3

notes:
  5V
  GND
