# Fritzing sketch bus2 (saved by Fritzing 0.9.3b)
circuit board: 9.88943cm x 3.36494cm
breadboards: 1

parts:
  J1 = female pin header, 8 pins [form="♀ (female)"]
  J2 = female pin header, 8 pins [form="♀ (female)"]
  J3 = female pin header, 8 pins [form="♀ (female)"]
  J11 = female pin header, 8 pins [form="♀ (female)"]
  J12 = female pin header, 8 pins [form="♀ (female)"]
  J13 = female pin header, 8 pins [form="♀ (female)"]
  J14 = female pin header, 8 pins [form="♀ (female)"]
  J15 = female pin header, 8 pins [form="♀ (female)"]
  J16 = female pin header, 8 pins [form="♀ (female)"]
  J17 = female pin header, 8 pins [form="♀ (female)"]

nets:
  N1: J1.pin1, J2.pin1, J3.pin1, J11.pin1, J12.pin1, J13.pin1, J14.pin1, J15.pin1, J16.pin1, J17.pin1
  N2: J1.pin2, J2.pin2, J3.pin2, J11.pin2, J12.pin2, J13.pin2, J14.pin2, J15.pin2, J16.pin2, J17.pin2
  N3: J1.pin3, J2.pin3, J3.pin3, J11.pin3, J12.pin3, J13.pin3, J14.pin3, J15.pin3, J16.pin3, J17.pin3
  N4: J1.pin4, J2.pin4, J3.pin4, J11.pin4, J12.pin4, J13.pin4, J14.pin4, J15.pin4, J16.pin4, J17.pin4
  N5: J1.pin5, J2.pin5, J3.pin5, J11.pin5, J12.pin5, J13.pin5, J14.pin5, J15.pin5, J16.pin5, J17.pin5
  N6: J1.pin6, J2.pin6, J3.pin6, J11.pin6, J12.pin6, J13.pin6, J14.pin6, J15.pin6, J16.pin6, J17.pin6
  N7: J1.pin7, J2.pin7, J3.pin7, J11.pin7, J12.pin7, J13.pin7, J14.pin7, J15.pin7, J16.pin7, J17.pin7
  N8: J1.pin8, J2.pin8, J3.pin8, J11.pin8, J12.pin8, J13.pin8, J14.pin8, J15.pin8, J16.pin8, J17.pin8

notes:
  7 6 5 4 3 2 1 0
  0 1 2 3 4 5 6 7
