# Fritzing sketch clock (saved by Fritzing 0.9.3b)
circuit board: 9.59196cm x 6.6843cm
breadboards: 1

parts:
  power = female pin header, 2 pins [form="♀ (female)"]
  555 = 555 Timer [package="DIP8 [THT]"]
  C1 = Ceramic Capacitor [capacitance=100nF package="100 mil [THT, multilayer]"]
  C2 = Electrolytic Capacitor [capacitance=1µF package="100 mil [THT, electrolytic]"]
  C3 = Ceramic Capacitor [capacitance=100nF package="100 mil [THT, multilayer]"]
  555_2 = 555 Timer [package="DIP8 [THT]"]
  manual_clock = Pushbutton [package="[THT]"]
  C4 = Ceramic Capacitor [capacitance=100nF package="100 mil [THT, multilayer]"]
  C5 = Electrolytic Capacitor [capacitance=1µF package="100 mil [THT, electrolytic]"]
  555_3 = 555 Timer [package="DIP8 [THT]"]
  speed_sel3 = Toggle Switch [package=THT]
  clock_select = Toggle Switch [package=THT]  # not connected
  C6 = Ceramic Capacitor [capacitance=100nF package="100 mil [THT, multilayer]"]
  74LS157 = IC, DIP package, 16 pins [chip_label=IC]
  C7 = Ceramic Capacitor [capacitance=100nF package="100 mil [THT, multilayer]"]
  HLT = female pin header, 1 pin [form="♀ (female)"]
  clk_out = female pin header, 6 pins [form="♀ (female)"]
  LED1 = LED - 5mm [color="Red (633nm)" package="5 mm [THT]"]
  R1 = Resistor [tolerance=±5% resistance=680 package=THT]
  R6 = Resistor [tolerance=±5% resistance=220 package=THT]
  R2 = Resistor [tolerance=±5% resistance=1k package=THT]
  R3 = Resistor [tolerance=±5% resistance=20k package=THT]
  R4 = Resistor [tolerance=±5% resistance=10k package=THT]
  R5 = Resistor [tolerance=±5% resistance=10k package=THT]
  R7 = Resistor [tolerance=±5% resistance=10k package=THT]
  J2 = female pin header, 2 pins [form="♀ (female)"]
  J3 = female pin header, 2 pins [form="♀ (female)"]
  R8 = Resistor [tolerance=±5% resistance=1k package=THT]

nets:
  N1: power.pin1, 555.Reset, 555.Vcc_Supply_Voltage, 555_2.Reset, 555_2.Vcc_Supply_Voltage, 555_3.Vcc_Supply_Voltage, 74LS157.pin16, C7.0, R1.Pin_1, R2.Pin_0, R3.Pin_1, R4.Pin_0, R5.Pin_0
  N2: power.pin2, 555.Ground, C1.1, C2.-, C3.0, 555_2.Ground, manual_clock.Pin_3, manual_clock.Pin_4, C4.1, C5.-, 555_3.Ground, 555_3.Threshold, speed_sel3.L1, C6.1, 74LS157.pin8, C7.1, R6.Pin_0, R7.Pin_1
  N3: 555.Trigger, 555.Threshold, J2.pin1, J2.pin2
  N4: 555.Output, 74LS157.pin14
  N5: 555.Control_Voltage, C1.0
  N6: 555.Discharge, R1.Pin_0, R8.Pin_1
  N7: C2.+, J3.pin2
  N8: C3.1, J3.pin1
  N9: 555_2.Trigger, manual_clock.Pin_1, manual_clock.Pin_2, R2.Pin_1
  N10: 555_2.Output, 74LS157.pin13
  N11: 555_2.Control_Voltage, C4.0
  N12: 555_2.Threshold, 555_2.Discharge, C5.+, R3.Pin_0
  N13: 555_3.Trigger, speed_sel3.COM, R4.Pin_1
  N14: 555_3.Output, 74LS157.pin1
  N15: 555_3.Reset, speed_sel3.L2, R5.Pin_1
  N16: 555_3.Control_Voltage, C6.0
  N17: 74LS157.pin12, clk_out.pin1, clk_out.pin2, clk_out.pin3, clk_out.pin4, clk_out.pin5, clk_out.pin6, LED1.anode
  N18: 74LS157.pin15, HLT.pin1, R7.Pin_0
  N19: LED1.cathode, R6.Pin_1
