# Fritzing sketch connectboard (saved by Fritzing 0.9.3b)
circuit board: 12.609cm x 16.0012cm
breadboards: 1

parts:
  SP = female pin header, 6 pins [form="♀ (female)"]  # not connected
  X = female pin header, 4 pins [form="♀ (female)"]  # not connected
  Y = female pin header, 4 pins [form="♀ (female)"]  # not connected
  Z = female pin header, 4 pins [form="♀ (female)"]  # not connected
  TMP = female pin header, 4 pins [form="♀ (female)"]  # not connected
  PC_COND = female pin header, 4 pins [form="♀ (female)"]  # not connected
  PC_JMP = female pin header, 7 pins [form="♀ (female)"]  # not connected
  RAM = female pin header, 3 pins [form="♀ (female)"]  # not connected
  MAR = female pin header, 4 pins [form="♀ (female)"]  # not connected
  INST = female pin header, 2 pins [form="♀ (female)"]  # not connected
  BUSREAD = female pin header, 16 pins [form="♀ (female)"]
  BUSWRITE = female pin header, 16 pins [form="♀ (female)"]
  dec1 = female pin header, 8 pins [form="♀ (female)"]
  dec2 = female pin header, 8 pins [form="♀ (female)"]
  dec3 = female pin header, 8 pins [form="♀ (female)"]
  ALU = female pin header, 8 pins [form="♀ (female)"]  # not connected
  OE = female pin header, 1 pin [form="♀ (female)"]
  SC = female pin header, 1 pin [form="♀ (female)"]
  CC = female pin header, 1 pin [form="♀ (female)"]
  CLK = female pin header, 1 pin [form="♀ (female)"]
  OP0 = female pin header, 1 pin [form="♀ (female)"]
  OP2 = female pin header, 1 pin [form="♀ (female)"]
  OP1 = female pin header, 1 pin [form="♀ (female)"]
  FLAGW = female pin header, 1 pin [form="♀ (female)"]
  INVB = female pin header, 1 pin [form="♀ (female)"]
  RESET_B = female pin header, 1 pin [form="♀ (female)"]
  RESET_A = female pin header, 1 pin [form="♀ (female)"]
  LOAD_B = female pin header, 1 pin [form="♀ (female)"]
  LOAD_A = female pin header, 1 pin [form="♀ (female)"]
  CLK_2 = female pin header, 1 pin [form="♀ (female)"]
  RESET = female pin header, 1 pin [form="♀ (female)"]
  LOAD = female pin header, 1 pin [form="♀ (female)"]
  OE_2 = female pin header, 1 pin [form="♀ (female)"]
  RESET_2 = female pin header, 1 pin [form="♀ (female)"]
  OE_3 = female pin header, 1 pin [form="♀ (female)"]
  LOAD_2 = female pin header, 1 pin [form="♀ (female)"]
  CLK_3 = female pin header, 1 pin [form="♀ (female)"]
  LOAD_3 = female pin header, 1 pin [form="♀ (female)"]
  CLK_4 = female pin header, 1 pin [form="♀ (female)"]
  OE_4 = female pin header, 1 pin [form="♀ (female)"]
  RESET_3 = female pin header, 1 pin [form="♀ (female)"]
  CLK_5 = female pin header, 1 pin [form="♀ (female)"]
  OE_5 = female pin header, 1 pin [form="♀ (female)"]
  LOAD_4 = female pin header, 1 pin [form="♀ (female)"]
  RESET_4 = female pin header, 1 pin [form="♀ (female)"]
  CNT = female pin header, 1 pin [form="♀ (female)"]
  CLK_6 = female pin header, 1 pin [form="♀ (female)"]
  RESET_5 = female pin header, 1 pin [form="♀ (female)"]
  HIGHOUT = female pin header, 1 pin [form="♀ (female)"]
  OE_6 = female pin header, 1 pin [form="♀ (female)"]
  DIRUP = female pin header, 1 pin [form="♀ (female)"]
  CLK_7 = female pin header, 1 pin [form="♀ (female)"]
  LOAD_5 = female pin header, 1 pin [form="♀ (female)"]
  OE_7 = female pin header, 1 pin [form="♀ (female)"]
  LOAD_H = female pin header, 1 pin [form="♀ (female)"]
  CLK_8 = female pin header, 1 pin [form="♀ (female)"]
  LOAD_L = female pin header, 1 pin [form="♀ (female)"]
  LOAD_6 = female pin header, 1 pin [form="♀ (female)"]
  CONT = female pin header, 1 pin [form="♀ (female)"]
  INC = female pin header, 1 pin [form="♀ (female)"]
  COND2 = female pin header, 1 pin [form="♀ (female)"]
  COND0 = female pin header, 1 pin [form="♀ (female)"]
  COND1 = female pin header, 1 pin [form="♀ (female)"]
  COND3 = female pin header, 1 pin [form="♀ (female)"]
  LOAD_H_2 = female pin header, 1 pin [form="♀ (female)"]
  LOAD_L_2 = female pin header, 1 pin [form="♀ (female)"]
  CLK_9 = female pin header, 1 pin [form="♀ (female)"]
  OE_8 = female pin header, 1 pin [form="♀ (female)"]
  LOW_OUT = female pin header, 1 pin [form="♀ (female)"]
  INC_2 = female pin header, 1 pin [form="♀ (female)"]
  ALUREGS = female pin header, 6 pins [form="♀ (female)"]  # not connected
  CLK_10 = female pin header, 1 pin [form="♀ (female)"]
  CLK_11 = female pin header, 2 pins [form="♀ (female)"]
  GND = female pin header, 2 pins [form="♀ (female)"]
  J34 = female pin header, 4 pins [form="♀ (female)"]
  J35 = female pin header, 8 pins [form="♀ (female)"]
  J36 = female pin header, 2 pins [form="♀ (female)"]
  J37 = female pin header, 1 pin [form="♀ (female)"]
  J38 = female pin header, 1 pin [form="♀ (female)"]
  J39 = female pin header, 1 pin [form="♀ (female)"]

nets:
  N1: BUSREAD.pin1, J34.pin1
  N2: BUSREAD.pin2, J34.pin2
  N3: BUSREAD.pin3, J34.pin3
  N4: BUSREAD.pin4, J34.pin4
  N5: BUSREAD.pin5, LOAD_6.pin1
  N6: BUSREAD.pin6, LOAD_5.pin1
  N7: BUSREAD.pin7, LOAD_L.pin1
  N8: BUSREAD.pin8, LOAD_H.pin1
  N9: BUSREAD.pin9, LOAD_L_2.pin1
  N10: BUSREAD.pin10, LOAD_H_2.pin1
  N11: BUSREAD.pin11, LOAD_B.pin1
  N12: BUSREAD.pin12, LOAD_A.pin1
  N13: BUSREAD.pin13, LOAD.pin1
  N14: BUSREAD.pin14, LOAD_2.pin1
  N15: BUSREAD.pin15, LOAD_3.pin1
  N16: BUSREAD.pin16, LOAD_4.pin1
  N17: BUSWRITE.pin1, J35.pin1
  N18: BUSWRITE.pin2, J35.pin2
  N19: BUSWRITE.pin3, J35.pin3
  N20: BUSWRITE.pin4, J35.pin4
  N21: BUSWRITE.pin5, J35.pin5
  N22: BUSWRITE.pin6, J35.pin6
  N23: BUSWRITE.pin7, J35.pin7
  N24: BUSWRITE.pin8, J35.pin8
  N25: BUSWRITE.pin9, OE_2.pin1
  N26: BUSWRITE.pin10, OE_3.pin1
  N27: BUSWRITE.pin11, OE_4.pin1
  N28: BUSWRITE.pin12, OE_5.pin1
  N29: BUSWRITE.pin13, OE_7.pin1
  N30: BUSWRITE.pin14, OE_6.pin1
  N31: BUSWRITE.pin15, OE_8.pin1
  N32: BUSWRITE.pin16, OE.pin1
  N33: dec1.pin1, COND3.pin1
  N34: dec1.pin2, COND2.pin1
  N35: dec1.pin3, COND1.pin1
  N36: dec1.pin4, COND0.pin1
  N37: dec1.pin5, J38.pin1
  N38: dec1.pin6, OP0.pin1
  N39: dec1.pin7, OP1.pin1
  N40: dec1.pin8, OP2.pin1
  N41: dec2.pin1, CONT.pin1
  N42: dec2.pin2, RESET_5.pin1
  N43: dec2.pin3, CNT.pin1
  N44: dec2.pin4, DIRUP.pin1
  N45: dec2.pin5, J37.pin1
  N46: dec2.pin6, LOW_OUT.pin1
  N47: dec2.pin7, J36.pin1
  N48: dec2.pin8, J36.pin2
  N49: dec3.pin1, INC_2.pin1
  N50: dec3.pin2, INC.pin1
  N51: dec3.pin3, HIGHOUT.pin1
  N52: dec3.pin4, J39.pin1
  N53: dec3.pin5, CC.pin1
  N54: dec3.pin6, SC.pin1
  N55: dec3.pin7, INVB.pin1
  N56: dec3.pin8, FLAGW.pin1
  N57: CLK.pin1, CLK_2.pin1, CLK_3.pin1, CLK_4.pin1, CLK_5.pin1, CLK_6.pin1, CLK_7.pin1, CLK_8.pin1, CLK_9.pin1, CLK_10.pin1, CLK_11.pin2
  N58: RESET_B.pin1, RESET_A.pin1, RESET.pin1, RESET_2.pin1, RESET_3.pin1, RESET_4.pin1, GND.pin2
