# Fritzing sketch decoder_10x10cm (saved by Fritzing 0.9.3b)
circuit board: 9.95544cm x 9.65561cm
breadboards: 1

parts:
  J5 = female pin header, 4 pins [form="♀ (female)"]  # not connected
  J6 = female pin header, 4 pins [form="♀ (female)"]  # not connected
  J7 = female pin header, 4 pins [form="♀ (female)"]  # not connected
  J8 = female pin header, 4 pins [form="♀ (female)"]  # not connected
  J9 = female pin header, 11 pins [form="♀ (female)"]
  J10 = female pin header, 2 pins [form="♀ (female)"]
  C1 = Ceramic Capacitor [capacitance=100nF package="100 mil [THT, multilayer]"]
  J11 = female pin header, 11 pins [form="♀ (female)"]
  J12 = female pin header, 2 pins [form="♀ (female)"]
  LED1 = smd LED [color="Red (633nm)" package="1206 [SMD]"]
  R1 = Resistor [tolerance=±5% resistance=220 package="1206 [SMD]"]
  LED2 = smd LED [color="Red (633nm)" package="1206 [SMD]"]
  R2 = Resistor [tolerance=±5% resistance=220 package="1206 [SMD]"]
  LED3 = smd LED [color="Red (633nm)" package="1206 [SMD]"]
  R3 = Resistor [tolerance=±5% resistance=220 package="1206 [SMD]"]
  LED4 = smd LED [color="Red (633nm)" package="1206 [SMD]"]
  R4 = Resistor [tolerance=±5% resistance=220 package="1206 [SMD]"]
  LED5 = smd LED [color="Red (633nm)" package="1206 [SMD]"]
  R5 = Resistor [tolerance=±5% resistance=220 package="1206 [SMD]"]
  LED6 = smd LED [color="Red (633nm)" package="1206 [SMD]"]
  R6 = Resistor [tolerance=±5% resistance=220 package="1206 [SMD]"]
  LED7 = smd LED [color="Red (633nm)" package="1206 [SMD]"]
  R7 = Resistor [tolerance=±5% resistance=220 package="1206 [SMD]"]
  LED8 = smd LED [color="Red (633nm)" package="1206 [SMD]"]
  R8 = Resistor [tolerance=±5% resistance=220 package="1206 [SMD]"]
  LED9 = smd LED [color="Red (633nm)" package="1206 [SMD]"]
  R9 = Resistor [tolerance=±5% resistance=220 package="1206 [SMD]"]
  LED10 = smd LED [color="Red (633nm)" package="1206 [SMD]"]
  R10 = Resistor [tolerance=±5% resistance=220 package="1206 [SMD]"]
  LED11 = smd LED [color="Red (633nm)" package="1206 [SMD]"]
  R11 = Resistor [tolerance=±5% resistance=220 package="1206 [SMD]"]
  LED12 = smd LED [color="Red (633nm)" package="1206 [SMD]"]
  R12 = Resistor [tolerance=±5% resistance=220 package="1206 [SMD]"]
  LED13 = smd LED [color="Red (633nm)" package="1206 [SMD]"]
  R13 = Resistor [tolerance=±5% resistance=220 package="1206 [SMD]"]
  LED14 = smd LED [color="Red (633nm)" package="1206 [SMD]"]
  R14 = Resistor [tolerance=±5% resistance=220 package="1206 [SMD]"]
  LED15 = smd LED [color="Red (633nm)" package="1206 [SMD]"]
  R15 = Resistor [tolerance=±5% resistance=220 package="1206 [SMD]"]
  LED16 = smd LED [color="Red (633nm)" package="1206 [SMD]"]
  R16 = Resistor [tolerance=±5% resistance=220 package="1206 [SMD]"]
  J14 = female pin header, 12 pins [form="♀ (female)"]
  J15 = female pin header, 12 pins [form="♀ (female)"]
  J16 = female pin header, 12 pins [form="♀ (female)"]
  J17 = female pin header, 12 pins [form="♀ (female)"]

nets:
  N1: J9.pin1, J11.pin1, J15.pin5, J16.pin5
  N2: J9.pin2, J11.pin2, J15.pin6, J16.pin6
  N3: J9.pin3, J11.pin3, J15.pin7, J16.pin7
  N4: J9.pin4, J11.pin4, J15.pin8, J16.pin8
  N5: J9.pin5, J11.pin5, J15.pin9, J16.pin9
  N6: J9.pin6, J11.pin6, J15.pin10, J16.pin10
  N7: J9.pin7, J11.pin7, J15.pin11, J16.pin11
  N8: J9.pin8, J11.pin8, J15.pin12, J16.pin12
  N9: J9.pin9, J11.pin9, J14.pin11, J17.pin11
  N10: J9.pin10, J11.pin10, J14.pin10, J17.pin10
  N11: J9.pin11, J11.pin11, J14.pin7, J17.pin7
  N12: J10.pin1, C1.0, J12.pin1, R1.Pin_1, R2.Pin_1, R3.Pin_1, R4.Pin_1, R5.Pin_1, R6.Pin_1, R7.Pin_1, R8.Pin_1, R9.Pin_1, R10.Pin_1, R11.Pin_1, R12.Pin_1, R13.Pin_1, R14.Pin_1, R15.Pin_1, R16.Pin_1, J14.pin9, J14.pin12, J17.pin9, J17.pin12
  N13: J10.pin2, C1.1, J12.pin2, J14.pin6, J14.pin8, J15.pin1, J17.pin6, J17.pin8
  N14: LED1.anode, R1.Pin_0
  N15: LED2.anode, R2.Pin_0
  N16: LED3.anode, R3.Pin_0
  N17: LED4.anode, R4.Pin_0
  N18: LED5.anode, R5.Pin_0
  N19: LED6.anode, R6.Pin_0
  N20: LED7.anode, R7.Pin_0
  N21: LED8.anode, R8.Pin_0
  N22: LED9.anode, R9.Pin_0
  N23: LED10.anode, R10.Pin_0
  N24: LED11.anode, R11.Pin_0
  N25: LED12.anode, R12.Pin_0
  N26: LED13.anode, R13.Pin_0
  N27: LED14.anode, R14.Pin_0
  N28: LED15.anode, R15.Pin_0
  N29: LED16.anode, R16.Pin_0
