# Fritzing sketch decoderfloor (saved by Fritzing 0.9.3b)
circuit board: 7.52675cm x 7.1323cm
breadboards: 1

parts:
  J6 = female pin header, 4 pins [form="♀ (female)"]
  J8 = female pin header, 4 pins [form="♀ (female)"]
  J9 = female pin header, 11 pins [form="♀ (female)"]
  J10 = female pin header, 2 pins [form="♀ (female)"]
  C1 = Ceramic Capacitor [capacitance=100nF package="100 mil [THT, multilayer]"]
  LED1 = smd LED [color="Red (633nm)" package="1206 [SMD]"]
  R1 = Resistor [tolerance=±5% resistance=220 package="1206 [SMD]"]
  LED2 = smd LED [color="Red (633nm)" package="1206 [SMD]"]
  R2 = Resistor [tolerance=±5% resistance=220 package="1206 [SMD]"]
  LED3 = smd LED [color="Red (633nm)" package="1206 [SMD]"]
  R3 = Resistor [tolerance=±5% resistance=220 package="1206 [SMD]"]
  LED4 = smd LED [color="Red (633nm)" package="1206 [SMD]"]
  R4 = Resistor [tolerance=±5% resistance=220 package="1206 [SMD]"]
  LED5 = smd LED [color="Red (633nm)" package="1206 [SMD]"]
  R5 = Resistor [tolerance=±5% resistance=220 package="1206 [SMD]"]
  LED6 = smd LED [color="Red (633nm)" package="1206 [SMD]"]
  R6 = Resistor [tolerance=±5% resistance=220 package="1206 [SMD]"]
  LED7 = smd LED [color="Red (633nm)" package="1206 [SMD]"]
  R7 = Resistor [tolerance=±5% resistance=220 package="1206 [SMD]"]
  LED8 = smd LED [color="Red (633nm)" package="1206 [SMD]"]
  R8 = Resistor [tolerance=±5% resistance=220 package="1206 [SMD]"]
  J14 = female pin header, 12 pins [form="♀ (female)"]
  J15 = female pin header, 12 pins [form="♀ (female)"]
  J16 = female pin header, 11 pins [form="♀ (female)"]
  J17 = female pin header, 2 pins [form="♀ (female)"]
  J18 = female pin header, 1 pin [form="♀ (female)"]
  J19 = female pin header, 1 pin [form="♀ (female)"]
  J20 = female pin header, 1 pin [form="♀ (female)"]
  J21 = female pin header, 1 pin [form="♀ (female)"]

nets:
  N1: J6.pin1, LED5.cathode, J14.pin1
  N2: J6.pin2, LED6.cathode, J15.pin2
  N3: J6.pin3, LED7.cathode, J15.pin3
  N4: J6.pin4, LED8.cathode, J15.pin4
  N5: J8.pin1, LED1.cathode, J14.pin5
  N6: J8.pin2, LED2.cathode, J14.pin4
  N7: J8.pin3, LED3.cathode, J14.pin3
  N8: J8.pin4, LED4.cathode, J14.pin2
  N9: J9.pin1, J15.pin5, J16.pin1
  N10: J9.pin2, J15.pin6, J16.pin2
  N11: J9.pin3, J15.pin7, J16.pin3
  N12: J9.pin4, J15.pin8, J16.pin4
  N13: J9.pin5, J15.pin9, J16.pin5
  N14: J9.pin6, J15.pin10, J16.pin6
  N15: J9.pin7, J15.pin11, J16.pin7
  N16: J9.pin8, J15.pin12, J16.pin8
  N17: J9.pin9, J14.pin11, J16.pin9
  N18: J9.pin10, J14.pin10, J16.pin10
  N19: J9.pin11, J14.pin7, J16.pin11
  N20: J10.pin1, C1.0, J14.pin9, J14.pin12, J17.pin1, J18.pin1
  N21: J10.pin2, C1.1, J14.pin6, J14.pin8, J15.pin1, J17.pin2, J19.pin1
  N22: LED1.anode, R1.Pin_0
  N23: R1.Pin_1, R2.Pin_1, R3.Pin_1, R4.Pin_1, R5.Pin_1, R6.Pin_1, R7.Pin_1, R8.Pin_1, J20.pin1, J21.pin1
  N24: LED2.anode, R2.Pin_0
  N25: LED3.anode, R3.Pin_0
  N26: LED4.anode, R4.Pin_0
  N27: LED5.anode, R5.Pin_0
  N28: LED6.anode, R6.Pin_0
  N29: LED7.anode, R7.Pin_0
  N30: LED8.anode, R8.Pin_0
