# Fritzing sketch instreg (saved by Fritzing 0.9.3b)
circuit board: 9.99277cm x 10.0003cm

parts:
  74163 = IC, DIP package, 16 pins [chip_label=IC]
  74LS173 = IC, DIP package, 16 pins [chip_label=IC]
  74LS173_2 = IC, DIP package, 16 pins [chip_label=IC]
  src_sel = female pin header, 1 pin [form="♀ (female)"]
  7404 = IC, DIP package, 14 pins [chip_label=IC]
  74LS245 = IC, DIP package, 20 pins [chip_label=IC]
  74LS245_2 = IC, DIP package, 20 pins [chip_label=IC]
  74LS245_3 = IC, DIP package, 20 pins [chip_label=IC]
  74LS245_4 = IC, DIP package, 20 pins [chip_label=IC]
  inst_out = female pin header, 11 pins [form="♀ (female)"]
  clk_in = female pin header, 1 pin [form="♀ (female)"]
  load_instr_(AL) = female pin header, 1 pin [form="♀ (female)"]
  programmer_in = female pin header, 11 pins [form="♀ (female)"]
  ard_clk = female pin header, 1 pin [form="♀ (female)"]
  bus = female pin header, 8 pins [form="♀ (female)"]
  cont_(AL) = female pin header, 1 pin [form="♀ (female)"]
  power_out = female pin header, 2 pins [form="♀ (female)"]
  C1 = Ceramic Capacitor [capacitance=100nF package="100 mil [THT, multilayer]"]
  pow = female pin header, 2 pins [form="♀ (female)"]
  C2 = Ceramic Capacitor [capacitance=100nF package="100 mil [THT, multilayer]"]
  clk_out = female pin header, 15 pins [form="♀ (female)"]
  LED3 = smd LED [color="Red (633nm)" package="1206 [SMD]"]
  LED4 = smd LED [color="Red (633nm)" package="1206 [SMD]"]
  R3 = Resistor [tolerance=±5% resistance=220 package="1206 [SMD]"]
  R4 = Resistor [tolerance=±5% resistance=220 package="1206 [SMD]"]
  LED5 = smd LED [color="Red (633nm)" package="1206 [SMD]"]
  LED6 = smd LED [color="Red (633nm)" package="1206 [SMD]"]
  R5 = Resistor [tolerance=±5% resistance=220 package="1206 [SMD]"]
  R6 = Resistor [tolerance=±5% resistance=220 package="1206 [SMD]"]
  LED7 = smd LED [color="Red (633nm)" package="1206 [SMD]"]
  LED8 = smd LED [color="Red (633nm)" package="1206 [SMD]"]
  LED9 = smd LED [color="Red (633nm)" package="1206 [SMD]"]
  R7 = Resistor [tolerance=±5% resistance=220 package="1206 [SMD]"]
  R9 = Resistor [tolerance=±5% resistance=220 package="1206 [SMD]"]
  R10 = Resistor [tolerance=±5% resistance=220 package="1206 [SMD]"]
  LED11 = smd LED [color="Red (633nm)" package="1206 [SMD]"]
  LED12 = smd LED [color="Red (633nm)" package="1206 [SMD]"]
  LED13 = smd LED [color="Red (633nm)" package="1206 [SMD]"]
  LED14 = smd LED [color="Red (633nm)" package="1206 [SMD]"]
  R11 = Resistor [tolerance=±5% resistance=220 package="1206 [SMD]"]
  R12 = Resistor [tolerance=±5% resistance=220 package="1206 [SMD]"]
  R13 = Resistor [tolerance=±5% resistance=220 package="1206 [SMD]"]
  R14 = Resistor [tolerance=±5% resistance=220 package="1206 [SMD]"]
  C3 = Ceramic Capacitor [capacitance=100nF package="100 mil [THT, multilayer]"]
  R21 = Resistor [tolerance=±5% resistance=220 package="1206 [SMD]"]
  R22 = Resistor [tolerance=±5% resistance=220 package="1206 [SMD]"]
  R23 = Resistor [tolerance=±5% resistance=220 package="1206 [SMD]"]
  R24 = Resistor [tolerance=±5% resistance=220 package="1206 [SMD]"]
  R25 = Resistor [tolerance=±5% resistance=220 package="1206 [SMD]"]
  R26 = Resistor [tolerance=±5% resistance=220 package="1206 [SMD]"]
  R27 = Resistor [tolerance=±5% resistance=220 package="1206 [SMD]"]
  R28 = Resistor [tolerance=±5% resistance=220 package="1206 [SMD]"]
  pow1 = female pin header, 1 pin [form="♀ (female)"]
  pow2 = female pin header, 1 pin [form="♀ (female)"]
  bus_2 = female pin header, 8 pins [form="♀ (female)"]
  src_sel1 = female pin header, 1 pin [form="♀ (female)"]
  src_sel2 = female pin header, 1 pin [form="♀ (female)"]
  clk_pull = female pin header, 1 pin [form="♀ (female)"]
  clk_gnd = female pin header, 1 pin [form="♀ (female)"]

nets:
  N1: 74163.pin1, cont_(AL).pin1
  N2: 74163.pin2, 74LS173.pin7, 74LS173_2.pin7, 7404.pin4
  N3: 74163.pin3, 74163.pin4, 74163.pin5, 74163.pin6, 74163.pin7, 74163.pin9, 74163.pin10, 74163.pin16, 74LS173.pin16, 74LS173_2.pin16, 7404.pin5, 7404.pin9, 7404.pin11, 7404.pin13, 7404.pin14, 74LS245.pin20, 74LS245_2.pin11, 74LS245_2.pin12, 74LS245_2.pin13, 74LS245_2.pin14, 74LS245_2.pin20, 74LS245_3.pin20, 74LS245_4.pin11, 74LS245_4.pin12, 74LS245_4.pin13, 74LS245_4.pin14, 74LS245_4.pin20, power_out.pin1, C1.1, pow.pin2, C2.1, C3.1, pow1.pin1, src_sel2.pin1
  N4: 74163.pin8, 74LS173.pin1, 74LS173.pin2, 74LS173.pin8, 74LS173.pin15, 74LS173_2.pin1, 74LS173_2.pin2, 74LS173_2.pin8, 74LS173_2.pin15, 7404.pin7, 74LS245.pin1, 74LS245.pin10, 74LS245_2.pin1, 74LS245_2.pin10, 74LS245_3.pin1, 74LS245_3.pin10, 74LS245_4.pin1, 74LS245_4.pin10, power_out.pin2, C1.0, pow.pin1, C2.0, R3.Pin_1, R4.Pin_1, R5.Pin_1, R6.Pin_1, R7.Pin_1, R9.Pin_1, R10.Pin_1, R11.Pin_1, R12.Pin_1, R13.Pin_1, R14.Pin_1, C3.0, R21.Pin_1, R22.Pin_1, R23.Pin_1, R24.Pin_1, R25.Pin_1, R26.Pin_1, R27.Pin_1, R28.Pin_1, pow2.pin1, clk_gnd.pin1
  N5: 74163.pin11, 74LS245_4.pin18
  N6: 74163.pin12, 74LS245_4.pin17
  N7: 74163.pin13, 74LS245_4.pin16
  N8: 74163.pin14, 74LS245_4.pin15
  N9: 74LS173.pin3, 74LS245_3.pin14
  N10: 74LS173.pin4, 74LS245_3.pin13
  N11: 74LS173.pin5, 74LS245_3.pin12
  N12: 74LS173.pin6, 74LS245_3.pin11
  N13: 74LS173.pin9, 74LS173.pin10, 74LS173_2.pin9, 74LS173_2.pin10, load_instr_(AL).pin1
  N14: 74LS173.pin11, bus.pin1, R28.Pin_0, bus_2.pin1
  N15: 74LS173.pin12, bus.pin2, R27.Pin_0, bus_2.pin2
  N16: 74LS173.pin13, bus.pin3, R26.Pin_0, bus_2.pin3
  N17: 74LS173.pin14, bus.pin4, R25.Pin_0, bus_2.pin4
  N18: 74LS173_2.pin4, 74LS245_3.pin17
  N19: 74LS173_2.pin5, 74LS245_3.pin16
  N20: 74LS173_2.pin6, 74LS245_3.pin15
  N21: 74LS173_2.pin11, bus.pin5, R24.Pin_0, bus_2.pin5
  N22: 74LS173_2.pin12, bus.pin6, R23.Pin_0, bus_2.pin6
  N23: 74LS173_2.pin13, bus.pin7, R22.Pin_0, bus_2.pin7
  N24: 74LS173_2.pin14, bus.pin8, R21.Pin_0, bus_2.pin8
  N25: src_sel.pin1, 7404.pin1, 74LS245.pin19, 74LS245_2.pin19, src_sel1.pin1
  N26: 7404.pin2, 74LS245_3.pin19, 74LS245_4.pin19
  N27: 7404.pin3, 74LS245.pin2, 74LS245_3.pin2, clk_out.pin1, clk_out.pin2, clk_out.pin3, clk_out.pin4, clk_out.pin5, clk_out.pin6, clk_out.pin7, clk_out.pin8, clk_out.pin9, clk_out.pin10, clk_out.pin11, clk_out.pin12, clk_out.pin13, clk_out.pin14, clk_out.pin15
  N28: 74LS245.pin3, 74LS245_3.pin3, inst_out.pin1, LED11.cathode
  N29: 74LS245.pin4, 74LS245_3.pin4, inst_out.pin2, LED13.cathode
  N30: 74LS245.pin5, 74LS245_3.pin5, inst_out.pin3, LED12.cathode
  N31: 74LS245.pin6, 74LS245_3.pin6, inst_out.pin4, LED14.cathode
  N32: 74LS245.pin7, 74LS245_3.pin7, inst_out.pin5, LED5.cathode
  N33: 74LS245.pin8, 74LS245_3.pin8, inst_out.pin6, LED6.cathode
  N34: 74LS245.pin9, 74LS245_3.pin9, inst_out.pin7, LED3.cathode
  N35: 74LS245.pin11, programmer_in.pin5
  N36: 74LS245.pin12, programmer_in.pin6
  N37: 74LS245.pin13, programmer_in.pin7
  N38: 74LS245.pin14, programmer_in.pin8
  N39: 74LS245.pin15, programmer_in.pin9
  N40: 74LS245.pin16, programmer_in.pin10
  N41: 74LS245.pin17, programmer_in.pin11
  N42: 74LS245.pin18, ard_clk.pin1
  N43: 74LS245_2.pin2, 74LS245_4.pin2, inst_out.pin8, LED4.cathode
  N44: 74LS245_2.pin3, 74LS245_4.pin3, inst_out.pin9, LED9.cathode
  N45: 74LS245_2.pin4, 74LS245_4.pin4, inst_out.pin10, LED8.cathode
  N46: 74LS245_2.pin5, 74LS245_4.pin5, inst_out.pin11, LED7.cathode
  N47: 74LS245_2.pin15, programmer_in.pin1
  N48: 74LS245_2.pin16, programmer_in.pin2
  N49: 74LS245_2.pin17, programmer_in.pin3
  N50: 74LS245_2.pin18, programmer_in.pin4
  N51: 74LS245_3.pin18, clk_in.pin1, clk_pull.pin1
  N52: LED3.anode, R3.Pin_0
  N53: LED4.anode, R4.Pin_0
  N54: LED5.anode, R5.Pin_0
  N55: LED6.anode, R6.Pin_0
  N56: LED7.anode, R7.Pin_0
  N57: LED8.anode, R9.Pin_0
  N58: LED9.anode, R10.Pin_0
  N59: LED11.anode, R13.Pin_0
  N60: LED12.anode, R11.Pin_0
  N61: LED13.anode, R12.Pin_0
  N62: LED14.anode, R14.Pin_0

notes:
  Instruction Register
  {
  instruction
  step
  +
  load
  cont
  -
  krabz 2018
  msb
