# Fritzing sketch outreg_display (saved by Fritzing 0.9.3b)
circuit board: 8.99614cm x 7.99737cm
breadboards: 2

parts:
  555 = 555 Timer [package="DIP8 [THT]"]
  1k = Resistor [tolerance=±5% resistance=1k package=THT]
  46k = Resistor [tolerance=±5% resistance=46k package=THT]
  104 = Ceramic Capacitor [capacitance=100nF package="100 mil [THT, multilayer]"]
  104_2 = Ceramic Capacitor [capacitance=100nF package="100 mil [THT, multilayer]"]
  161(counter) = IC, DIP package, 16 pins [chip_label=IC]
  139(mux) = IC, DIP package, 16 pins [chip_label=IC]
  7404(6xnot) = IC, DIP package, 14 pins [chip_label=IC]
  seg1000 = 7-Segment LED Display [package=THT]
  seg100 = 7-Segment LED Display [package=THT]
  seg10 = 7-Segment LED Display [package=THT]
  seg1 = 7-Segment LED Display [package=THT]
  J1 = female pin header, 12 pins [form="♀ (female)"]
  J2 = female pin header, 12 pins [form="♀ (female)"]
  data = female pin header, 8 pins [form="♀ (female)"]
  J3 = female pin header, 3 pins [form="♀ (female)"]
  20uF = Electrolytic Capacitor [capacitance=1µF package="100 mil [THT, electrolytic]"]
  power = female pin header, 2 pins [form="♀ (female)"]

nets:
  N1: 555.Ground, 104.1, 104_2.1, 161(counter).pin8, 139(mux).pin1, 139(mux).pin8, 7404(6xnot).pin7, J1.pin5, J1.pin7, J2.pin12, J3.pin3, 20uF.-, power.pin2
  N2: 555.Trigger, 555.Threshold, 46k.Pin_1, 104_2.0
  N3: 555.Output, 161(counter).pin2
  N4: 555.Control_Voltage, 104.0
  N5: 555.Discharge, 1k.Pin_1, 46k.Pin_0
  N6: 555.Vcc_Supply_Voltage, 1k.Pin_0, 161(counter).pin1, 161(counter).pin7, 161(counter).pin9, 161(counter).pin10, 161(counter).pin16, 139(mux).pin16, 7404(6xnot).pin14, J1.pin1, J1.pin4, J3.pin1, 20uF.+, power.pin1
  N7: 161(counter).pin13, 139(mux).pin3, J1.pin3
  N8: 161(counter).pin14, 139(mux).pin2, J1.pin2
  N9: 139(mux).pin4, 7404(6xnot).pin1
  N10: 139(mux).pin5, 7404(6xnot).pin3
  N11: 139(mux).pin6, 7404(6xnot).pin5
  N12: 139(mux).pin7, 7404(6xnot).pin9
  N13: 7404(6xnot).pin2, seg1000.commAnode#7
  N14: 7404(6xnot).pin4, seg100.commAnode#7
  N15: 7404(6xnot).pin6, seg10.commAnode#7
  N16: 7404(6xnot).pin8, seg1.commAnode#7
  N17: seg1000.cathodeE, seg100.cathodeE, seg10.cathodeE, seg1.cathodeE, J1.pin11
  N18: seg1000.cathodeD, seg100.cathodeD, seg10.cathodeD, seg1.cathodeD, J1.pin12
  N19: seg1000.cathodeC, seg100.cathodeC, seg10.cathodeC, seg1.cathodeC, J2.pin11
  N20: seg1000.cathodeDP, seg100.cathodeDP, seg10.cathodeDP, seg1.cathodeDP, J1.pin8
  N21: seg1000.cathodeB, seg100.cathodeB, seg10.cathodeB, seg1.cathodeB, J2.pin10
  N22: seg1000.cathodeA, seg100.cathodeA, seg10.cathodeA, seg1.cathodeA, J2.pin9
  N23: seg1000.cathodeF, seg100.cathodeF, seg10.cathodeF, seg1.cathodeF, J1.pin10
  N24: seg1000.cathodeG, seg100.cathodeG, seg10.cathodeG, seg1.cathodeG, J1.pin9
  N25: J1.pin6, J3.pin2
  N26: J2.pin1, data.pin1
  N27: J2.pin2, data.pin2
  N28: J2.pin3, data.pin3
  N29: J2.pin4, data.pin4
  N30: J2.pin5, data.pin5
  N31: J2.pin6, data.pin6
  N32: J2.pin7, data.pin7
  N33: J2.pin8, data.pin8
