# Fritzing sketch outregx3_v2_registers (saved by Fritzing 0.9.3b)
circuit board: 11.4613cm x 14.4225cm
breadboards: 2

parts:
  power = female pin header, 3 pins [form="♀ (female)"]
  J10 = female pin header, 8 pins [form="♀ (female)"]
  J11 = female pin header, 8 pins [form="♀ (female)"]
  J12 = female pin header, 8 pins [form="♀ (female)"]
  J13 = female pin header, 8 pins [form="♀ (female)"]
  J14 = female pin header, 8 pins [form="♀ (female)"]
  J15 = female pin header, 8 pins [form="♀ (female)"]
  power1 = female pin header, 3 pins [form="♀ (female)"]
  IC1 = IC, DIP package, 16 pins [chip_label=IC]
  IC2 = IC, DIP package, 16 pins [chip_label=IC]
  IC3 = IC, DIP package, 16 pins [chip_label=IC]
  IC4 = IC, DIP package, 16 pins [chip_label=IC]
  IC5 = IC, DIP package, 16 pins [chip_label=IC]
  IC6 = IC, DIP package, 16 pins [chip_label=IC]
  J16 = female pin header, 8 pins [form="♀ (female)"]
  J17 = female pin header, 4 pins [form="♀ (female)"]
  C1 = Ceramic Capacitor [capacitance=100nF package="100 mil [THT, multilayer]"]

nets:
  N1: power.pin1, power1.pin1, IC1.pin16, IC2.pin16, IC3.pin16, IC4.pin16, IC5.pin16, IC6.pin16, C1.1
  N2: power.pin3, power1.pin3, IC1.pin1, IC1.pin2, IC1.pin8, IC1.pin15, IC2.pin1, IC2.pin2, IC2.pin8, IC2.pin15, IC3.pin1, IC3.pin2, IC3.pin8, IC3.pin15, IC4.pin1, IC4.pin2, IC4.pin8, IC4.pin15, IC5.pin1, IC5.pin2, IC5.pin8, IC5.pin15, IC6.pin1, IC6.pin2, IC6.pin8, IC6.pin15, C1.0
  N3: J10.pin1, J11.pin1, IC1.pin3
  N4: J10.pin2, J11.pin2, IC1.pin4
  N5: J10.pin3, J11.pin3, IC1.pin5
  N6: J10.pin4, J11.pin4, IC1.pin6
  N7: J10.pin5, J11.pin5, IC2.pin3
  N8: J10.pin6, J11.pin6, IC2.pin4
  N9: J10.pin7, J11.pin7, IC2.pin5
  N10: J10.pin8, J11.pin8, IC2.pin6
  N11: J12.pin1, J13.pin1, IC3.pin3
  N12: J12.pin2, J13.pin2, IC3.pin4
  N13: J12.pin3, J13.pin3, IC3.pin5
  N14: J12.pin4, J13.pin4, IC3.pin6
  N15: J12.pin5, J13.pin5, IC4.pin3
  N16: J12.pin6, J13.pin6, IC4.pin4
  N17: J12.pin7, J13.pin7, IC4.pin5
  N18: J12.pin8, J13.pin8, IC4.pin6
  N19: J14.pin1, J15.pin1, IC6.pin3
  N20: J14.pin2, J15.pin2, IC6.pin4
  N21: J14.pin3, J15.pin3, IC6.pin5
  N22: J14.pin4, J15.pin4, IC6.pin6
  N23: J14.pin5, J15.pin5, IC5.pin3
  N24: J14.pin6, J15.pin6, IC5.pin4
  N25: J14.pin7, J15.pin7, IC5.pin5
  N26: J14.pin8, J15.pin8, IC5.pin6
  N27: IC1.pin7, IC2.pin7, IC3.pin7, IC4.pin7, IC5.pin7, IC6.pin7, J17.pin4
  N28: IC1.pin9, IC1.pin10, IC2.pin9, IC2.pin10, J17.pin1
  N29: IC1.pin11, IC3.pin11, IC6.pin11, J16.pin4
  N30: IC1.pin12, IC3.pin12, IC6.pin12, J16.pin3
  N31: IC1.pin13, IC3.pin13, IC6.pin13, J16.pin2
  N32: IC1.pin14, IC3.pin14, IC6.pin14, J16.pin1
  N33: IC2.pin11, IC4.pin11, IC5.pin11, J16.pin8
  N34: IC2.pin12, IC4.pin12, IC5.pin12, J16.pin7
  N35: IC2.pin13, IC4.pin13, IC5.pin13, J16.pin6
  N36: IC2.pin14, IC4.pin14, IC5.pin14, J16.pin5
  N37: IC3.pin9, IC3.pin10, IC4.pin9, IC4.pin10, J17.pin2
  N38: IC5.pin9, IC5.pin10, IC6.pin9, IC6.pin10, J17.pin3
