# Fritzing sketch programmer (saved by Fritzing 0.9.3b)
circuit board: 10.2026cm x 6.20225cm
breadboards: 1

parts:
  MAS_CLK = female pin header, 1 pin [form="♀ (female)"]
  inst = female pin header, 7 pins [form="♀ (female)"]
  step = female pin header, 4 pins [form="♀ (female)"]
  U1 = 74HC595 [package="DIP16 [THT]"]
  U2 = 74HC595 [package="DIP16 [THT]"]
  R1 = Resistor [tolerance=±5% resistance=220 package="1206 [SMD]"]
  LED1 = smd LED [color="Red (633nm)" package="1206 [SMD]"]
  R2 = Resistor [tolerance=±5% resistance=220 package="1206 [SMD]"]
  LED2 = smd LED [color="Red (633nm)" package="1206 [SMD]"]
  R3 = Resistor [tolerance=±5% resistance=220 package="1206 [SMD]"]
  R4 = Resistor [tolerance=±5% resistance=220 package="1206 [SMD]"]
  LED3 = smd LED [color="Red (633nm)" package="1206 [SMD]"]
  LED4 = smd LED [color="Red (633nm)" package="1206 [SMD]"]
  R5 = Resistor [tolerance=±5% resistance=220 package="1206 [SMD]"]
  R6 = Resistor [tolerance=±5% resistance=220 package="1206 [SMD]"]
  LED5 = smd LED [color="Red (633nm)" package="1206 [SMD]"]
  LED6 = smd LED [color="Red (633nm)" package="1206 [SMD]"]
  R7 = Resistor [tolerance=±5% resistance=220 package="1206 [SMD]"]
  R8 = Resistor [tolerance=±5% resistance=220 package="1206 [SMD]"]
  LED7 = smd LED [color="Red (633nm)" package="1206 [SMD]"]
  LED8 = smd LED [color="Red (633nm)" package="1206 [SMD]"]
  R9 = Resistor [tolerance=±5% resistance=220 package="1206 [SMD]"]
  R10 = Resistor [tolerance=±5% resistance=220 package="1206 [SMD]"]
  LED9 = smd LED [color="Red (633nm)" package="1206 [SMD]"]
  LED10 = smd LED [color="Red (633nm)" package="1206 [SMD]"]
  R11 = Resistor [tolerance=±5% resistance=220 package="1206 [SMD]"]
  LED12 = smd LED [color="Red (633nm)" package="1206 [SMD]"]
  R12 = Resistor [tolerance=±5% resistance=220 package="1206 [SMD]"]
  LED13 = smd LED [color="Red (633nm)" package="1206 [SMD]"]
  C1 = Ceramic Capacitor [capacitance=100nF package="100 mil [THT, multilayer]"]
  C2 = Ceramic Capacitor [capacitance=100nF package="100 mil [THT, multilayer]"]
  C3 = Ceramic Capacitor [capacitance=100nF package="100 mil [THT, multilayer]"]
  U3 = 74HC595 [package="DIP16 [THT]"]
  R13 = Resistor [tolerance=±5% resistance=220 package="1206 [SMD]"]
  LED14 = smd LED [color="Red (633nm)" package="1206 [SMD]"]
  R14 = Resistor [tolerance=±5% resistance=220 package="1206 [SMD]"]
  LED15 = smd LED [color="Red (633nm)" package="1206 [SMD]"]
  R15 = Resistor [tolerance=±5% resistance=220 package="1206 [SMD]"]
  LED16 = smd LED [color="Red (633nm)" package="1206 [SMD]"]
  R16 = Resistor [tolerance=±5% resistance=220 package="1206 [SMD]"]
  LED17 = smd LED [color="Red (633nm)" package="1206 [SMD]"]
  R17 = Resistor [tolerance=±5% resistance=220 package="1206 [SMD]"]
  LED18 = smd LED [color="Red (633nm)" package="1206 [SMD]"]
  R18 = Resistor [tolerance=±5% resistance=220 package="1206 [SMD]"]
  LED19 = smd LED [color="Red (633nm)" package="1206 [SMD]"]
  R19 = Resistor [tolerance=±5% resistance=220 package="1206 [SMD]"]
  LED20 = smd LED [color="Red (633nm)" package="1206 [SMD]"]
  R20 = Resistor [tolerance=±5% resistance=220 package="1206 [SMD]"]
  LED21 = smd LED [color="Red (633nm)" package="1206 [SMD]"]
  data = female pin header, 8 pins [form="♀ (female)"]
  Part1 = Arduino Nano (Rev3.0)
  SRC_SEL = female pin header, 1 pin [form="♀ (female)"]
  CLK = female pin header, 1 pin [form="♀ (female)"]
  C4 = Ceramic Capacitor [capacitance=100nF package="100 mil [THT, multilayer]"]
  R21 = Resistor [tolerance=±5% resistance=220 package="1206 [SMD]"]
  LED22 = smd LED [color="Red (633nm)" package="1206 [SMD]"]
  GND = female pin header, 4 pins [form="♀ (female)"]
  VCC = female pin header, 4 pins [form="♀ (female)"]
  R22 = Resistor [tolerance=±5% resistance=220 package="1206 [SMD]"]
  LED23 = smd LED [color="Red (633nm)" package="1206 [SMD]"]
  R23 = Resistor [tolerance=±5% resistance=220 package="1206 [SMD]"]
  LED24 = smd LED [color="Red (633nm)" package="1206 [SMD]"]
  C5 = Electrolytic Capacitor [capacitance=1µF package="100 mil [THT, electrolytic]"]
  DATA_OUT = female pin header, 1 pin [form="♀ (female)"]
  data1 = female pin header, 8 pins [form="♀ (female)"]
  data2 = female pin header, 8 pins [form="♀ (female)"]

nets:
  N1: MAS_CLK.pin1, R12.Pin_0, Part1.D12/MISO
  N2: inst.pin1, U1.Q1, R1.Pin_0
  N3: inst.pin2, U1.Q2, R2.Pin_0
  N4: inst.pin3, U1.Q3, R3.Pin_0
  N5: inst.pin4, U1.Q4, R4.Pin_0
  N6: inst.pin5, U1.Q5, R5.Pin_0
  N7: inst.pin6, U1.Q6, R6.Pin_0
  N8: inst.pin7, U1.Q7, R7.Pin_0
  N9: step.pin1, U2.Q1, R8.Pin_0
  N10: step.pin2, U2.Q2, R10.Pin_0
  N11: step.pin3, U2.Q3, R9.Pin_0
  N12: step.pin4, U2.Q4, R11.Pin_0
  GND: U1.GND, U1.OE, U2.GND, U2.OE, LED1.anode, LED2.anode, LED3.anode, LED4.anode, LED5.anode, LED6.anode, LED7.anode, LED8.anode, LED9.anode, LED10.anode, LED12.anode, LED13.anode, C1.0, C2.0, C3.0, U3.GND, LED14.anode, LED15.anode, LED16.anode, LED17.anode, LED18.anode, LED19.anode, LED20.anode, LED21.anode, Part1.GND, C4.1, GND.pin1, GND.pin2, GND.pin3, GND.pin4, LED23.anode, LED24.anode, C5.-
  N13: U1.Q7', U2.DS
  VCC: U1.MR, U1.VCC, U2.MR, U2.VCC, C1.1, C2.1, C3.1, U3.MR, U3.VCC, Part1.5V, C4.0, R21.Pin_1, VCC.pin1, VCC.pin2, VCC.pin3, VCC.pin4, C5.+
  N14: U1.SH_CP, U2.SH_CP, Part1.A2
  N15: U1.ST_CP, U2.ST_CP, Part1.A1
  N16: U1.DS, Part1.A0
  N17: R1.Pin_1, LED1.cathode
  N18: R2.Pin_1, LED2.cathode
  N19: R3.Pin_1, LED3.cathode
  N20: R4.Pin_1, LED4.cathode
  N21: R5.Pin_1, LED5.cathode
  N22: R6.Pin_1, LED6.cathode
  N23: R7.Pin_1, LED8.cathode
  N24: R8.Pin_1, LED7.cathode
  N25: R9.Pin_1, LED10.cathode
  N26: R10.Pin_1, LED9.cathode
  N27: R11.Pin_1, LED12.cathode
  N28: R12.Pin_1, LED13.cathode
  N29: U3.Q1, R18.Pin_0, data.pin2, data1.pin2, data2.pin2
  N30: U3.Q2, R17.Pin_0, data.pin3, data1.pin3, data2.pin3
  N31: U3.Q3, R16.Pin_0, data.pin4, data1.pin4, data2.pin4
  N32: U3.Q4, R15.Pin_0, data.pin5, data1.pin5, data2.pin5
  N33: U3.Q5, R14.Pin_0, data.pin6, data1.pin6, data2.pin6
  N34: U3.Q6, R13.Pin_0, data.pin7, data1.pin7, data2.pin7
  N35: U3.Q7, R20.Pin_0, data.pin8, data1.pin8, data2.pin8
  N36: U3.SH_CP, Part1.D4
  N37: U3.ST_CP, Part1.D3
  N38: U3.OE, Part1.D5, LED22.cathode, DATA_OUT.pin1
  N39: U3.DS, Part1.D6
  N40: U3.Q0, R19.Pin_0, data.pin1, data1.pin1, data2.pin1
  N41: R13.Pin_1, LED14.cathode
  N42: R14.Pin_1, LED15.cathode
  N43: R15.Pin_1, LED16.cathode
  N44: R16.Pin_1, LED17.cathode
  N45: R17.Pin_1, LED18.cathode
  N46: R18.Pin_1, LED19.cathode
  N47: R19.Pin_1, LED20.cathode
  N48: R20.Pin_1, LED21.cathode
  N49: Part1.A4, SRC_SEL.pin1, R22.Pin_0
  N50: Part1.A3, CLK.pin1, R23.Pin_0
  N51: R21.Pin_0, LED22.anode
  N52: R22.Pin_1, LED23.cathode
  N53: R23.Pin_1, LED24.cathode
