# Fritzing sketch ramv3_mar (saved by Fritzing 0.9.3b)
circuit board: 12.3776cm x 7.79631cm
circuit board: 12.3934cm x 9.06819cm
breadboards: 2

parts:
  power = female pin header, 2 pins [form="♀ (female)"]
  bus = female pin header, 8 pins [form="♀ (female)"]
  74245 = IC, DIP package, 20 pins [chip_label=IC]
  74LS173-H = IC, DIP package, 16 pins [chip_label=IC]
  74LS173-L = IC, DIP package, 16 pins [chip_label=IC]
  IS61C256AH = IC, DIP package, 28 pins [chip_label=IC]
  J27 = female pin header, 15 pins [form="♀ (female)"]
  C1 = Ceramic Capacitor [capacitance=100nF package="100 mil [THT, multilayer]"]
  bus-to-ram_(active_low) = female pin header, 1 pin [form="♀ (female)"]
  ram-to-bus_(active_low) = female pin header, 1 pin [form="♀ (female)"]
  CLK = female pin header, 1 pin [form="♀ (female)"]
  74LS74 = IC, DIP package, 14 pins [chip_label=IC]
  C2 = Ceramic Capacitor [capacitance=100nF package="100 mil [THT, multilayer]"]
  C3 = Ceramic Capacitor [capacitance=100nF package="100 mil [THT, multilayer]"]
  J28 = female pin header, 2 pins [form="♀ (female)"]
  C4 = Ceramic Capacitor [capacitance=100nF package="100 mil [THT, multilayer]"]
  C6 = Ceramic Capacitor [capacitance=100nF package="100 mil [THT, multilayer]"]
  J29 = female pin header, 1 pin [form="♀ (female)"]
  J30 = female pin header, 8 pins [form="♀ (female)"]
  74LS161_B-HIGH1 = IC, DIP package, 16 pins [chip_label=IC]
  74LS161_B-LOW1 = IC, DIP package, 16 pins [chip_label=IC]
  74LS161_A-LOW1 = IC, DIP package, 16 pins [chip_label=IC]
  74LS161_A-HIGH1 = IC, DIP package, 16 pins [chip_label=IC]
  LOAD-L = female pin header, 1 pin [form="♀ (female)"]
  LED17 = LED - 5mm [color="Red (633nm)" package="5 mm [THT]"]
  LED18 = LED - 5mm [color="Red (633nm)" package="5 mm [THT]"]
  LED19 = LED - 5mm [color="Red (633nm)" package="5 mm [THT]"]
  LED20 = LED - 5mm [color="Red (633nm)" package="5 mm [THT]"]
  LED21 = LED - 5mm [color="Red (633nm)" package="5 mm [THT]"]
  LED22 = LED - 5mm [color="Red (633nm)" package="5 mm [THT]"]
  LED23 = LED - 5mm [color="Red (633nm)" package="5 mm [THT]"]
  LED24 = LED - 5mm [color="Red (633nm)" package="5 mm [THT]"]
  LED25 = LED - 5mm [color="Red (633nm)" package="5 mm [THT]"]
  LED26 = LED - 5mm [color="Red (633nm)" package="5 mm [THT]"]
  LED27 = LED - 5mm [color="Red (633nm)" package="5 mm [THT]"]
  LED28 = LED - 5mm [color="Red (633nm)" package="5 mm [THT]"]
  LED29 = LED - 5mm [color="Red (633nm)" package="5 mm [THT]"]
  LED30 = LED - 5mm [color="Red (633nm)" package="5 mm [THT]"]
  LED31 = LED - 5mm [color="Red (633nm)" package="5 mm [THT]"]
  LED32 = LED - 5mm [color="Red (633nm)" package="5 mm [THT]"]
  J31 = female pin header, 2 pins [form="♀ (female)"]
  J32 = female pin header, 2 pins [form="♀ (female)"]
  J33 = female pin header, 15 pins [form="♀ (female)"]
  R1 = Resistor [tolerance=±5% resistance=220 package="1206 [SMD]"]
  R2 = Resistor [tolerance=±5% resistance=220 package="1206 [SMD]"]
  R3 = Resistor [tolerance=±5% resistance=220 package="1206 [SMD]"]
  R4 = Resistor [tolerance=±5% resistance=220 package="1206 [SMD]"]
  R5 = Resistor [tolerance=±5% resistance=220 package="1206 [SMD]"]
  R6 = Resistor [tolerance=±5% resistance=220 package="1206 [SMD]"]
  R7 = Resistor [tolerance=±5% resistance=220 package="1206 [SMD]"]
  R8 = Resistor [tolerance=±5% resistance=220 package="1206 [SMD]"]
  R9 = Resistor [tolerance=±5% resistance=220 package="1206 [SMD]"]
  R10 = Resistor [tolerance=±5% resistance=220 package="1206 [SMD]"]
  R11 = Resistor [tolerance=±5% resistance=220 package="1206 [SMD]"]
  R12 = Resistor [tolerance=±5% resistance=220 package="1206 [SMD]"]
  R13 = Resistor [tolerance=±5% resistance=220 package="1206 [SMD]"]
  R14 = Resistor [tolerance=±5% resistance=220 package="1206 [SMD]"]
  R15 = Resistor [tolerance=±5% resistance=220 package="1206 [SMD]"]
  CNT = female pin header, 1 pin [form="♀ (female)"]
  LOAD-H = female pin header, 1 pin [form="♀ (female)"]
  R16 = Resistor [tolerance=±5% resistance=220 package="1206 [SMD]"]
  CLK_2 = female pin header, 1 pin [form="♀ (female)"]
  J34 = female pin header, 1 pin [form="♀ (female)"]
  J35 = female pin header, 1 pin [form="♀ (female)"]
  J36 = female pin header, 1 pin [form="♀ (female)"]
  J37 = female pin header, 1 pin [form="♀ (female)"]
  C7 = Ceramic Capacitor [capacitance=100nF package="100 mil [THT, multilayer]"]
  J38 = female pin header, 2 pins [form="♀ (female)"]

nets:
  N1: power.pin1, 74245.pin1, 74245.pin20, 74LS173-H.pin16, 74LS173-L.pin16, IS61C256AH.pin28, C1.1, 74LS74.pin1, 74LS74.pin10, 74LS74.pin13, 74LS74.pin14, C2.1, C3.0, J28.pin1, C4.0
  N2: power.pin2, 74245.pin10, 74LS173-H.pin8, 74LS173-H.pin15, 74LS173-L.pin8, 74LS173-L.pin15, IS61C256AH.pin14, IS61C256AH.pin20, C1.0, 74LS74.pin7, C2.0, C3.1, J28.pin2, C4.1
  N3: bus.pin1, 74245.pin18, 74LS173-H.pin14
  N4: bus.pin2, 74245.pin17, 74LS173-H.pin13
  N5: bus.pin3, 74245.pin16, 74LS173-H.pin12
  N6: bus.pin4, 74245.pin15, 74LS173-H.pin11
  N7: bus.pin5, 74245.pin14, 74LS173-L.pin14
  N8: bus.pin6, 74245.pin13, 74LS173-L.pin13
  N9: bus.pin7, 74245.pin12, 74LS173-L.pin12
  N10: bus.pin8, 74245.pin11, 74LS173-L.pin11
  N11: 74245.pin2, 74LS173-H.pin3, IS61C256AH.pin19
  N12: 74245.pin3, 74LS173-H.pin4, IS61C256AH.pin18
  N13: 74245.pin4, 74LS173-H.pin5, IS61C256AH.pin17
  N14: 74245.pin5, 74LS173-H.pin6, IS61C256AH.pin16
  N15: 74245.pin6, 74LS173-L.pin3, IS61C256AH.pin15
  N16: 74245.pin7, 74LS173-L.pin4, IS61C256AH.pin13
  N17: 74245.pin8, 74LS173-L.pin5, IS61C256AH.pin12
  N18: 74245.pin9, 74LS173-L.pin6, IS61C256AH.pin11
  N19: 74245.pin19, IS61C256AH.pin22, ram-to-bus_(active_low).pin1
  N20: 74LS173-H.pin1, 74LS173-H.pin2, 74LS173-L.pin1, 74LS173-L.pin2, 74LS74.pin9
  N21: 74LS173-H.pin7, 74LS173-L.pin7, CLK.pin1, 74LS74.pin3, 74LS74.pin4, 74LS74.pin11
  N22: 74LS173-H.pin9, 74LS173-H.pin10, 74LS173-L.pin9, 74LS173-L.pin10, bus-to-ram_(active_low).pin1, 74LS74.pin2, 74LS74.pin12
  N23: IS61C256AH.pin1, J27.pin1
  N24: IS61C256AH.pin2, J27.pin3
  N25: IS61C256AH.pin3, J27.pin8
  N26: IS61C256AH.pin4, J27.pin9
  N27: IS61C256AH.pin5, J27.pin10
  N28: IS61C256AH.pin6, J27.pin11
  N29: IS61C256AH.pin7, J27.pin12
  N30: IS61C256AH.pin8, J27.pin13
  N31: IS61C256AH.pin9, J27.pin14
  N32: IS61C256AH.pin10, J27.pin15
  N33: IS61C256AH.pin21, J27.pin5
  N34: IS61C256AH.pin23, J27.pin4
  N35: IS61C256AH.pin24, J27.pin6
  N36: IS61C256AH.pin25, J27.pin7
  N37: IS61C256AH.pin26, J27.pin2
  N38: IS61C256AH.pin27, 74LS74.pin5
  N39: C6.0, 74LS161_B-HIGH1.pin1, 74LS161_B-HIGH1.pin16, 74LS161_B-LOW1.pin1, 74LS161_B-LOW1.pin16, 74LS161_A-LOW1.pin1, 74LS161_A-LOW1.pin16, 74LS161_A-HIGH1.pin1, 74LS161_A-HIGH1.pin16, J31.pin1, J32.pin2, J35.pin1, J36.pin1, C7.0, J38.pin2
  N40: C6.1, 74LS161_B-HIGH1.pin8, 74LS161_B-LOW1.pin8, 74LS161_A-LOW1.pin8, 74LS161_A-HIGH1.pin8, J31.pin2, J32.pin1, R1.Pin_0, R2.Pin_0, R3.Pin_0, R4.Pin_0, R5.Pin_0, R6.Pin_0, R7.Pin_0, R8.Pin_0, R9.Pin_0, R10.Pin_0, R11.Pin_0, R12.Pin_0, R13.Pin_0, R14.Pin_0, R15.Pin_0, R16.Pin_0, J34.pin1, J37.pin1, C7.1, J38.pin1
  N41: J29.pin1, 74LS161_A-HIGH1.pin11, LED32.anode
  N42: J30.pin1, 74LS161_B-HIGH1.pin6, 74LS161_A-HIGH1.pin6
  N43: J30.pin2, 74LS161_B-HIGH1.pin5, 74LS161_A-HIGH1.pin5
  N44: J30.pin3, 74LS161_B-HIGH1.pin4, 74LS161_A-HIGH1.pin4
  N45: J30.pin4, 74LS161_B-HIGH1.pin3, 74LS161_A-HIGH1.pin3
  N46: J30.pin5, 74LS161_B-LOW1.pin6, 74LS161_A-LOW1.pin6
  N47: J30.pin6, 74LS161_B-LOW1.pin5, 74LS161_A-LOW1.pin5
  N48: J30.pin7, 74LS161_B-LOW1.pin4, 74LS161_A-LOW1.pin4
  N49: J30.pin8, 74LS161_B-LOW1.pin3, 74LS161_A-LOW1.pin3
  N50: 74LS161_B-HIGH1.pin2, 74LS161_B-LOW1.pin2, 74LS161_A-LOW1.pin2, 74LS161_A-HIGH1.pin2, CLK_2.pin1
  N51: 74LS161_B-HIGH1.pin7, 74LS161_B-HIGH1.pin10, 74LS161_B-LOW1.pin15
  N52: 74LS161_B-HIGH1.pin9, 74LS161_B-LOW1.pin9, LOAD-L.pin1
  N53: 74LS161_B-HIGH1.pin11, LED19.anode, J33.pin8
  N54: 74LS161_B-HIGH1.pin12, LED18.anode, J33.pin9
  N55: 74LS161_B-HIGH1.pin13, LED21.anode, J33.pin10
  N56: 74LS161_B-HIGH1.pin14, LED17.anode, J33.pin11
  N57: 74LS161_B-HIGH1.pin15, 74LS161_A-LOW1.pin7, 74LS161_A-LOW1.pin10
  N58: 74LS161_B-LOW1.pin7, 74LS161_B-LOW1.pin10, CNT.pin1
  N59: 74LS161_B-LOW1.pin11, LED24.anode, J33.pin12
  N60: 74LS161_B-LOW1.pin12, LED23.anode, J33.pin13
  N61: 74LS161_B-LOW1.pin13, LED22.anode, J33.pin14
  N62: 74LS161_B-LOW1.pin14, LED20.anode, J33.pin15
  N63: 74LS161_A-LOW1.pin9, 74LS161_A-HIGH1.pin9, LOAD-H.pin1
  N64: 74LS161_A-LOW1.pin11, LED27.anode, J33.pin4
  N65: 74LS161_A-LOW1.pin12, LED26.anode, J33.pin5
  N66: 74LS161_A-LOW1.pin13, LED25.anode, J33.pin6
  N67: 74LS161_A-LOW1.pin14, LED28.anode, J33.pin7
  N68: 74LS161_A-LOW1.pin15, 74LS161_A-HIGH1.pin7, 74LS161_A-HIGH1.pin10
  N69: 74LS161_A-HIGH1.pin12, LED31.anode, J33.pin1
  N70: 74LS161_A-HIGH1.pin13, LED29.anode, J33.pin2
  N71: 74LS161_A-HIGH1.pin14, LED30.anode, J33.pin3
  N72: LED17.cathode, R12.Pin_1
  N73: LED18.cathode, R9.Pin_1
  N74: LED19.cathode, R16.Pin_1
  N75: LED20.cathode, R15.Pin_1
  N76: LED21.cathode, R10.Pin_1
  N77: LED22.cathode, R14.Pin_1
  N78: LED23.cathode, R13.Pin_1
  N79: LED24.cathode, R11.Pin_1
  N80: LED25.cathode, R7.Pin_1
  N81: LED26.cathode, R6.Pin_1
  N82: LED27.cathode, R5.Pin_1
  N83: LED28.cathode, R8.Pin_1
  N84: LED29.cathode, R3.Pin_1
  N85: LED30.cathode, R4.Pin_1
  N86: LED31.cathode, R2.Pin_1
  N87: LED32.cathode, R1.Pin_1
