# Fritzing sketch register_v3 (saved by Fritzing 0.9.3b)
circuit board: 9.05082cm x 5.16249cm
breadboards: 2

parts:
  74ls245 = IC, DIP package, 20 pins [chip_label=IC]
  74ls173-H = IC, DIP package, 16 pins [chip_label=IC]
  74ls173-L = IC, DIP package, 16 pins [chip_label=IC]
  load = female pin header, 1 pin [form="♀ (female)"]
  clk = female pin header, 1 pin [form="♀ (female)"]
  BUS = female pin header, 8 pins [form="♀ (female)"]
  reset = female pin header, 1 pin [form="♀ (female)"]
  LED1 = LED - 5mm [color="Red (633nm)" package="5 mm [THT]"]
  LED2 = LED - 5mm [color="Red (633nm)" package="5 mm [THT]"]
  LED3 = LED - 5mm [color="Red (633nm)" package="5 mm [THT]"]
  LED4 = LED - 5mm [color="Red (633nm)" package="5 mm [THT]"]
  LED5 = LED - 5mm [color="Red (633nm)" package="5 mm [THT]"]
  LED6 = LED - 5mm [color="Red (633nm)" package="5 mm [THT]"]
  LED7 = LED - 5mm [color="Red (633nm)" package="5 mm [THT]"]
  LED8 = LED - 5mm [color="Red (633nm)" package="5 mm [THT]"]
  enable = female pin header, 1 pin [form="♀ (female)"]
  power = female pin header, 2 pins [form="♀ (female)"]
  out = female pin header, 8 pins [form="♀ (female)"]
  clk1 = female pin header, 1 pin [form="♀ (female)"]
  J1 = female pin header, 1 pin [form="♀ (female)"]
  J2 = female pin header, 1 pin [form="♀ (female)"]
  R1 = Resistor [tolerance=±5% resistance=220 package="1206 [SMD]"]
  R2 = Resistor [tolerance=±5% resistance=220 package="1206 [SMD]"]
  R3 = Resistor [tolerance=±5% resistance=220 package="1206 [SMD]"]
  R4 = Resistor [tolerance=±5% resistance=220 package="1206 [SMD]"]
  C1 = Ceramic Capacitor [capacitance=100nF package="100 mil [THT, multilayer]"]
  R5 = Resistor [tolerance=±5% resistance=220 package="1206 [SMD]"]
  R6 = Resistor [tolerance=±5% resistance=220 package="1206 [SMD]"]
  R7 = Resistor [tolerance=±5% resistance=220 package="1206 [SMD]"]
  R8 = Resistor [tolerance=±5% resistance=220 package="1206 [SMD]"]

nets:
  N1: 74ls245.pin1, 74ls245.pin20, 74ls173-H.pin16, 74ls173-L.pin16, power.pin1, J1.pin1, C1.0
  N2: 74ls245.pin2, 74ls173-H.pin3, out.pin1, R1.Pin_0
  N3: 74ls245.pin3, 74ls173-H.pin4, out.pin2, R2.Pin_0
  N4: 74ls245.pin4, 74ls173-H.pin5, out.pin3, R3.Pin_0
  N5: 74ls245.pin5, 74ls173-H.pin6, out.pin4, R4.Pin_0
  N6: 74ls245.pin6, 74ls173-L.pin3, out.pin5, R5.Pin_0
  N7: 74ls245.pin7, 74ls173-L.pin4, out.pin6, R6.Pin_0
  N8: 74ls245.pin8, 74ls173-L.pin5, out.pin7, R7.Pin_0
  N9: 74ls245.pin9, 74ls173-L.pin6, out.pin8, R8.Pin_0
  N10: 74ls245.pin10, 74ls173-H.pin1, 74ls173-H.pin2, 74ls173-H.pin8, 74ls173-L.pin1, 74ls173-L.pin2, 74ls173-L.pin8, LED1.cathode, LED2.cathode, LED3.cathode, LED4.cathode, LED5.cathode, LED6.cathode, LED7.cathode, LED8.cathode, power.pin2, J2.pin1, C1.1
  N11: 74ls245.pin11, 74ls173-L.pin11, BUS.pin8
  N12: 74ls245.pin12, 74ls173-L.pin12, BUS.pin7
  N13: 74ls245.pin13, 74ls173-L.pin13, BUS.pin6
  N14: 74ls245.pin14, 74ls173-L.pin14, BUS.pin5
  N15: 74ls245.pin15, 74ls173-H.pin11, BUS.pin4
  N16: 74ls245.pin16, 74ls173-H.pin12, BUS.pin3
  N17: 74ls245.pin17, 74ls173-H.pin13, BUS.pin2
  N18: 74ls245.pin18, 74ls173-H.pin14, BUS.pin1
  N19: 74ls245.pin19, enable.pin1
  N20: 74ls173-H.pin7, 74ls173-L.pin7, clk.pin1, clk1.pin1
  N21: 74ls173-H.pin9, 74ls173-H.pin10, 74ls173-L.pin9, 74ls173-L.pin10, load.pin1
  N22: 74ls173-H.pin15, 74ls173-L.pin15, reset.pin1
  N23: LED1.anode, R1.Pin_1
  N24: LED2.anode, R2.Pin_1
  N25: LED3.anode, R3.Pin_1
  N26: LED4.anode, R4.Pin_1
  N27: LED5.anode, R5.Pin_1
  N28: LED6.anode, R6.Pin_1
  N29: LED7.anode, R7.Pin_1
  N30: LED8.anode, R8.Pin_1
