# Fritzing sketch sp_adder (saved by Fritzing 0.9.3b)
circuit board: 15.2966cm x 10.5576cm
breadboards: 1

parts:
  74LS173 = IC, DIP package, 16 pins [chip_label=IC]
  74LS283 = IC, DIP package, 16 pins [chip_label=IC]
  L1 = LED - 5mm [color="Red (633nm)" package="5 mm [THT]"]
  R1 = Resistor [tolerance=±5% resistance=220 package="1206 [SMD]"]
  L2 = LED - 5mm [color="Red (633nm)" package="5 mm [THT]"]
  R2 = Resistor [tolerance=±5% resistance=220 package="1206 [SMD]"]
  L3 = LED - 5mm [color="Red (633nm)" package="5 mm [THT]"]
  L4 = LED - 5mm [color="Red (633nm)" package="5 mm [THT]"]
  R4 = Resistor [tolerance=±5% resistance=220 package="1206 [SMD]"]
  R3 = Resistor [tolerance=±5% resistance=220 package="1206 [SMD]"]
  74LS283_2 = IC, DIP package, 16 pins [chip_label=IC]
  74LS173_2 = IC, DIP package, 16 pins [chip_label=IC]
  L5 = LED - 5mm [color="Red (633nm)" package="5 mm [THT]"]
  L6 = LED - 5mm [color="Red (633nm)" package="5 mm [THT]"]
  L7 = LED - 5mm [color="Red (633nm)" package="5 mm [THT]"]
  L8 = LED - 5mm [color="Red (633nm)" package="5 mm [THT]"]
  R5 = Resistor [tolerance=±5% resistance=220 package="1206 [SMD]"]
  R6 = Resistor [tolerance=±5% resistance=220 package="1206 [SMD]"]
  R7 = Resistor [tolerance=±5% resistance=220 package="1206 [SMD]"]
  R8 = Resistor [tolerance=±5% resistance=220 package="1206 [SMD]"]
  C1 = Ceramic Capacitor [capacitance=100nF package="100 mil [THT, multilayer]"]
  bustrans = IC, DIP package, 20 pins [chip_label=IC]
  bustrans1 = IC, DIP package, 20 pins [chip_label=IC]
  74LS173_3 = IC, DIP package, 16 pins [chip_label=IC]
  74LS283_3 = IC, DIP package, 16 pins [chip_label=IC]
  74LS283_4 = IC, DIP package, 16 pins [chip_label=IC]
  74LS173_4 = IC, DIP package, 16 pins [chip_label=IC]
  L9 = LED - 5mm [color="Red (633nm)" package="5 mm [THT]"]
  L10 = LED - 5mm [color="Red (633nm)" package="5 mm [THT]"]
  L11 = LED - 5mm [color="Red (633nm)" package="5 mm [THT]"]
  L12 = LED - 5mm [color="Red (633nm)" package="5 mm [THT]"]
  L13 = LED - 5mm [color="Red (633nm)" package="5 mm [THT]"]
  L14 = LED - 5mm [color="Red (633nm)" package="5 mm [THT]"]
  L15 = LED - 5mm [color="Red (633nm)" package="5 mm [THT]"]
  L16 = LED - 5mm [color="Red (633nm)" package="5 mm [THT]"]
  C2 = Ceramic Capacitor [capacitance=100nF package="100 mil [THT, multilayer]"]
  R9 = Resistor [tolerance=±5% resistance=220 package="1206 [SMD]"]
  R10 = Resistor [tolerance=±5% resistance=220 package="1206 [SMD]"]
  R11 = Resistor [tolerance=±5% resistance=220 package="1206 [SMD]"]
  R12 = Resistor [tolerance=±5% resistance=220 package="1206 [SMD]"]
  R13 = Resistor [tolerance=±5% resistance=220 package="1206 [SMD]"]
  R14 = Resistor [tolerance=±5% resistance=220 package="1206 [SMD]"]
  R15 = Resistor [tolerance=±5% resistance=220 package="1206 [SMD]"]
  R16 = Resistor [tolerance=±5% resistance=220 package="1206 [SMD]"]
  not = IC, DIP package, 14 pins [chip_label=IC]
  J1 = female pin header, 6 pins [form="♀ (female)"]
  and = IC, DIP package, 14 pins [chip_label=IC]
  J2 = female pin header, 8 pins [form="♀ (female)"]
  J3 = female pin header, 2 pins [form="♀ (female)"]
  C3 = Ceramic Capacitor [capacitance=100nF package="100 mil [THT, multilayer]"]
  C4 = Ceramic Capacitor [capacitance=100nF package="100 mil [THT, multilayer]"]
  J4 = female pin header, 2 pins [form="♀ (female)"]

nets:
  N1: 74LS173.pin1, 74LS173.pin2, 74LS173.pin8, 74LS283.pin8, R1.Pin_1, R2.Pin_1, R4.Pin_1, R3.Pin_1, 74LS283_2.pin8, 74LS173_2.pin1, 74LS173_2.pin2, 74LS173_2.pin8, R5.Pin_1, R6.Pin_1, R7.Pin_1, R8.Pin_1, C1.0, bustrans.pin1, bustrans.pin10, bustrans1.pin1, bustrans1.pin10, 74LS173_3.pin1, 74LS173_3.pin2, 74LS173_3.pin8, 74LS283_3.pin8, 74LS283_4.pin8, 74LS173_4.pin1, 74LS173_4.pin2, 74LS173_4.pin8, C2.0, R9.Pin_1, R10.Pin_1, R11.Pin_1, R12.Pin_1, R13.Pin_1, R14.Pin_1, R15.Pin_1, R16.Pin_1, not.pin7, and.pin7, J3.pin2, C3.0, C4.0, J4.pin2
  N2: 74LS173.pin3, 74LS283.pin12, L4.anode, bustrans.pin14
  N3: 74LS173.pin4, 74LS283.pin14, L3.anode, bustrans.pin13
  N4: 74LS173.pin5, 74LS283.pin3, L2.anode, bustrans.pin12
  N5: 74LS173.pin6, 74LS283.pin5, L1.anode, bustrans.pin11
  N6: 74LS173.pin7, 74LS173_2.pin7, 74LS173_3.pin7, 74LS173_4.pin7, J1.pin2, and.pin9
  N7: 74LS173.pin9, 74LS173.pin10, 74LS173_2.pin9, 74LS173_2.pin10, 74LS173_3.pin9, 74LS173_3.pin10, 74LS173_4.pin9, 74LS173_4.pin10, J1.pin1
  N8: 74LS173.pin11, 74LS283.pin4
  N9: 74LS173.pin12, 74LS283.pin1
  N10: 74LS173.pin13, 74LS283.pin13
  N11: 74LS173.pin14, 74LS283.pin10
  N12: 74LS173.pin15, 74LS173_2.pin15, 74LS173_3.pin15, 74LS173_4.pin15, and.pin8
  N13: 74LS173.pin16, 74LS283.pin16, 74LS283_2.pin16, 74LS173_2.pin16, C1.1, bustrans.pin20, bustrans1.pin20, 74LS173_3.pin16, 74LS283_3.pin16, 74LS283_4.pin16, 74LS173_4.pin16, C2.1, not.pin14, and.pin12, and.pin13, and.pin14, J3.pin1, C3.1, C4.1, J4.pin1
  N14: 74LS283.pin2, 74LS283.pin6, 74LS283.pin11, 74LS283.pin15, 74LS283_2.pin2, 74LS283_2.pin6, 74LS283_2.pin11, 74LS283_2.pin15, 74LS283_3.pin2, 74LS283_3.pin6, 74LS283_3.pin11, 74LS283_3.pin15, 74LS283_4.pin2, 74LS283_4.pin6, 74LS283_4.pin11, 74LS283_4.pin15, not.pin1, J1.pin6
  N15: 74LS283.pin7, not.pin2
  N16: 74LS283.pin9, 74LS283_2.pin7
  N17: L1.cathode, R1.Pin_0
  N18: L2.cathode, R2.Pin_0
  N19: L3.cathode, R3.Pin_0
  N20: L4.cathode, R4.Pin_0
  N21: 74LS283_2.pin1, 74LS173_2.pin12
  N22: 74LS283_2.pin3, 74LS173_2.pin5, L8.anode, bustrans.pin16
  N23: 74LS283_2.pin4, 74LS173_2.pin11
  N24: 74LS283_2.pin5, 74LS173_2.pin6, L6.anode, bustrans.pin15
  N25: 74LS283_2.pin9, 74LS283_4.pin7
  N26: 74LS283_2.pin10, 74LS173_2.pin14
  N27: 74LS283_2.pin12, 74LS173_2.pin3, L5.anode, bustrans.pin18
  N28: 74LS283_2.pin13, 74LS173_2.pin13
  N29: 74LS283_2.pin14, 74LS173_2.pin4, L7.anode, bustrans.pin17
  N30: L5.cathode, R5.Pin_0
  N31: L6.cathode, R7.Pin_0
  N32: L7.cathode, R8.Pin_0
  N33: L8.cathode, R6.Pin_0
  N34: bustrans.pin2, bustrans1.pin2, J2.pin1
  N35: bustrans.pin3, bustrans1.pin3, J2.pin2
  N36: bustrans.pin4, bustrans1.pin4, J2.pin3
  N37: bustrans.pin5, bustrans1.pin5, J2.pin4
  N38: bustrans.pin6, bustrans1.pin6, J2.pin5
  N39: bustrans.pin7, bustrans1.pin7, J2.pin6
  N40: bustrans.pin8, bustrans1.pin8, J2.pin7
  N41: bustrans.pin9, bustrans1.pin9, J2.pin8
  N42: bustrans.pin19, not.pin6
  N43: bustrans1.pin11, 74LS283_4.pin5, 74LS173_4.pin6, L16.anode
  N44: bustrans1.pin12, 74LS283_4.pin3, 74LS173_4.pin5, L15.anode
  N45: bustrans1.pin13, 74LS283_4.pin14, 74LS173_4.pin4, L14.anode
  N46: bustrans1.pin14, 74LS283_4.pin12, 74LS173_4.pin3, L13.anode
  N47: bustrans1.pin15, 74LS173_3.pin6, 74LS283_3.pin5, L11.anode
  N48: bustrans1.pin16, 74LS173_3.pin5, 74LS283_3.pin3, L9.anode
  N49: bustrans1.pin17, 74LS173_3.pin4, 74LS283_3.pin14, L10.anode
  N50: bustrans1.pin18, 74LS173_3.pin3, 74LS283_3.pin12, L12.anode
  N51: bustrans1.pin19, not.pin4
  N52: 74LS173_3.pin11, 74LS283_3.pin4
  N53: 74LS173_3.pin12, 74LS283_3.pin1
  N54: 74LS173_3.pin13, 74LS283_3.pin13
  N55: 74LS173_3.pin14, 74LS283_3.pin10
  N56: 74LS283_3.pin7, 74LS283_4.pin9
  N57: 74LS283_4.pin1, 74LS173_4.pin12
  N58: 74LS283_4.pin4, 74LS173_4.pin11
  N59: 74LS283_4.pin10, 74LS173_4.pin14
  N60: 74LS283_4.pin13, 74LS173_4.pin13
  N61: L9.cathode, R11.Pin_0
  N62: L10.cathode, R9.Pin_0
  N63: L11.cathode, R10.Pin_0
  N64: L12.cathode, R12.Pin_0
  N65: L13.cathode, R14.Pin_0
  N66: L14.cathode, R13.Pin_0
  N67: L15.cathode, R15.Pin_0
  N68: L16.cathode, R16.Pin_0
  N69: not.pin3, and.pin3
  N70: not.pin5, and.pin6
  N71: not.pin8, and.pin10
  N72: not.pin9, J1.pin3
  N73: not.pin10, and.pin1, and.pin5
  N74: not.pin11, J1.pin5
  N75: not.pin12, and.pin4
  N76: not.pin13, J1.pin4, and.pin2

notes:
  cnt
  clk
  res
  up
  out
  high
  lsb
