# Fritzing sketch HI_LO_MUX_HAT_BUSWRITE_v2-groundfill (saved by Fritzing 0.9.1b)
circuit board: 9.99058cm x 5.48209cm
breadboards: 2

parts:
  BUS = female pin header, 8 pins [form="♀ (female)"]
  GND = female pin header, 4 pins [form="♀ (female)"]
  VCC = female pin header, 4 pins [form="♀ (female)"]
  J56 = female pin header, 8 pins [form="♀ (female)"]
  J57 = female pin header, 8 pins [form="♀ (female)"]
  GND_2 = female pin header, 4 pins [form="♀ (female)"]
  VCC_2 = female pin header, 4 pins [form="♀ (female)"]
  VCC3 = female pin header, 4 pins [form="♀ (female)"]
  GND3 = female pin header, 4 pins [form="♀ (female)"]
  J59 = female pin header, 8 pins [form="♀ (female)"]
  J60 = female pin header, 8 pins [form="♀ (female)"]
  74LS157-1 = IC, DIP package, 16 pins [chip_label=IC]
  74LS157-2 = IC, DIP package, 16 pins [chip_label=IC]
  C1 = Ceramic Capacitor [capacitance=100nF package="100 mil [THT, multilayer]"]
  C2 = Ceramic Capacitor [capacitance=100nF package="100 mil [THT, multilayer]"]
  SELECT = female pin header, 1 pin [form="♀ (female)"]
  OUT = female pin header, 1 pin [form="♀ (female)"]

nets:
  N1: BUS.pin1, 74LS157-2.pin9
  N2: BUS.pin2, 74LS157-2.pin12
  N3: BUS.pin3, 74LS157-2.pin7
  N4: BUS.pin4, 74LS157-2.pin4
  N5: BUS.pin5, 74LS157-1.pin9
  N6: BUS.pin6, 74LS157-1.pin12
  N7: BUS.pin7, 74LS157-1.pin7
  N8: BUS.pin8, 74LS157-1.pin4
  N9: GND.pin1, GND.pin2, GND.pin3, GND.pin4, GND_2.pin1, GND_2.pin2, GND_2.pin3, GND_2.pin4, GND3.pin1, GND3.pin2, GND3.pin3, GND3.pin4, 74LS157-1.pin8, 74LS157-2.pin8, C1.0, C2.0
  N10: VCC.pin1, VCC.pin2, VCC.pin3, VCC.pin4, VCC_2.pin1, VCC_2.pin2, VCC_2.pin3, VCC_2.pin4, VCC3.pin1, VCC3.pin2, VCC3.pin3, VCC3.pin4, 74LS157-1.pin16, 74LS157-2.pin16, C1.1, C2.1
  N11: J56.pin1, J60.pin1, 74LS157-2.pin11
  N12: J56.pin2, J60.pin2, 74LS157-2.pin14
  N13: J56.pin3, J60.pin3, 74LS157-2.pin5
  N14: J56.pin4, J60.pin4, 74LS157-2.pin2
  N15: J56.pin5, J60.pin5, 74LS157-1.pin11
  N16: J56.pin6, J60.pin6, 74LS157-1.pin14
  N17: J56.pin7, J60.pin7, 74LS157-1.pin5
  N18: J56.pin8, J60.pin8, 74LS157-1.pin2
  N19: J57.pin1, J59.pin1, 74LS157-2.pin10
  N20: J57.pin2, J59.pin2, 74LS157-2.pin13
  N21: J57.pin3, J59.pin3, 74LS157-2.pin6
  N22: J57.pin4, J59.pin4, 74LS157-2.pin3
  N23: J57.pin5, J59.pin5, 74LS157-1.pin10
  N24: J57.pin6, J59.pin6, 74LS157-1.pin13
  N25: J57.pin7, J59.pin7, 74LS157-1.pin6
  N26: J57.pin8, J59.pin8, 74LS157-1.pin3
  N27: 74LS157-1.pin1, 74LS157-2.pin1, SELECT.pin1
  N28: 74LS157-1.pin15, 74LS157-2.pin15, OUT.pin1

notes:
  0
