# Fritzing sketch HI_LO_MUX_v2-groundfill (saved by Fritzing 0.9.1b)
circuit board: 9.99058cm x 5.48209cm
breadboards: 2

parts:
  74LS157-1 = IC, DIP package, 16 pins [chip_label=IC]
  74LS157-2 = IC, DIP package, 16 pins [chip_label=IC]
  J51 = female pin header, 8 pins [form="♀ (female)"]
  J52 = female pin header, 8 pins [form="♀ (female)"]
  GND = female pin header, 4 pins [form="♀ (female)"]
  VCC = female pin header, 4 pins [form="♀ (female)"]
  J54 = female pin header, 8 pins [form="♀ (female)"]
  J56 = female pin header, 8 pins [form="♀ (female)"]
  74LS157-5 = IC, DIP package, 16 pins [chip_label=IC]
  74LS157-6 = IC, DIP package, 16 pins [chip_label=IC]
  J57 = female pin header, 8 pins [form="♀ (female)"]
  J58 = female pin header, 8 pins [form="♀ (female)"]
  GND_2 = female pin header, 4 pins [form="♀ (female)"]
  VCC_2 = female pin header, 4 pins [form="♀ (female)"]
  SELECT = female pin header, 1 pin [form="♀ (female)"]
  C1 = Ceramic Capacitor [capacitance=100nF package="100 mil [THT, multilayer]"]
  C2 = Ceramic Capacitor [capacitance=100nF package="100 mil [THT, multilayer]"]
  C3 = Ceramic Capacitor [capacitance=100nF package="100 mil [THT, multilayer]"]
  VCC3 = female pin header, 4 pins [form="♀ (female)"]
  GND3 = female pin header, 4 pins [form="♀ (female)"]
  J59 = female pin header, 8 pins [form="♀ (female)"]
  J60 = female pin header, 8 pins [form="♀ (female)"]
  R1 = Resistor [tolerance=±5% resistance=220 package="1206 [SMD]"]
  LED1 = LED - 3mm [color="Red (633nm)" package="3 mm [THT]"]
  GND_3 = female pin header, 2 pins [form="♀ (female)"]
  VCC_3 = female pin header, 2 pins [form="♀ (female)"]
  C4 = Electrolytic Capacitor [capacitance=1µF package="100 mil [THT, electrolytic]"]

nets:
  N1: 74LS157-1.pin1, 74LS157-2.pin1, 74LS157-5.pin1, 74LS157-6.pin1, SELECT.pin1, R1.Pin_1
  N2: 74LS157-1.pin2, J51.pin1
  N3: 74LS157-1.pin3, J54.pin8
  N4: 74LS157-1.pin4, J56.pin8, J60.pin8
  N5: 74LS157-1.pin5, J51.pin2
  N6: 74LS157-1.pin6, J54.pin7
  N7: 74LS157-1.pin7, J56.pin7, J60.pin7
  N8: 74LS157-1.pin8, 74LS157-1.pin15, 74LS157-2.pin8, 74LS157-2.pin15, GND.pin1, GND.pin2, GND.pin3, GND.pin4, 74LS157-5.pin8, 74LS157-5.pin15, 74LS157-6.pin8, 74LS157-6.pin15, GND_2.pin1, GND_2.pin2, GND_2.pin3, GND_2.pin4, C1.0, C2.0, C3.0, GND3.pin1, GND3.pin2, GND3.pin3, GND3.pin4, LED1.cathode, GND_3.pin1, GND_3.pin2, C4.-
  N9: 74LS157-1.pin9, J56.pin5, J60.pin5
  N10: 74LS157-1.pin10, J54.pin5
  N11: 74LS157-1.pin11, J51.pin4
  N12: 74LS157-1.pin12, J56.pin6, J60.pin6
  N13: 74LS157-1.pin13, J54.pin6
  N14: 74LS157-1.pin14, J51.pin3
  N15: 74LS157-1.pin16, 74LS157-2.pin16, VCC.pin1, VCC.pin2, VCC.pin3, VCC.pin4, 74LS157-5.pin16, 74LS157-6.pin16, VCC_2.pin1, VCC_2.pin2, VCC_2.pin3, VCC_2.pin4, C1.1, C2.1, C3.1, VCC3.pin1, VCC3.pin2, VCC3.pin3, VCC3.pin4, VCC_3.pin1, VCC_3.pin2, C4.+
  N16: 74LS157-2.pin2, J51.pin5
  N17: 74LS157-2.pin3, J54.pin4
  N18: 74LS157-2.pin4, J56.pin4, J60.pin4
  N19: 74LS157-2.pin5, J51.pin6
  N20: 74LS157-2.pin6, J54.pin3
  N21: 74LS157-2.pin7, J56.pin3, J60.pin3
  N22: 74LS157-2.pin9, J56.pin1, J60.pin1
  N23: 74LS157-2.pin10, J54.pin1
  N24: 74LS157-2.pin11, J51.pin8
  N25: 74LS157-2.pin12, J56.pin2, J60.pin2
  N26: 74LS157-2.pin13, J54.pin2
  N27: 74LS157-2.pin14, J51.pin7
  N28: J52.pin1, 74LS157-6.pin2
  N29: J52.pin2, 74LS157-6.pin5
  N30: J52.pin3, 74LS157-6.pin14
  N31: J52.pin4, 74LS157-6.pin11
  N32: J52.pin5, 74LS157-5.pin2
  N33: J52.pin6, 74LS157-5.pin5
  N34: J52.pin7, 74LS157-5.pin14
  N35: J52.pin8, 74LS157-5.pin11
  N36: 74LS157-5.pin3, J58.pin4
  N37: 74LS157-5.pin4, J57.pin4, J59.pin4
  N38: 74LS157-5.pin6, J58.pin3
  N39: 74LS157-5.pin7, J57.pin3, J59.pin3
  N40: 74LS157-5.pin9, J57.pin1, J59.pin1
  N41: 74LS157-5.pin10, J58.pin1
  N42: 74LS157-5.pin12, J57.pin2, J59.pin2
  N43: 74LS157-5.pin13, J58.pin2
  N44: 74LS157-6.pin3, J58.pin8
  N45: 74LS157-6.pin4, J57.pin8, J59.pin8
  N46: 74LS157-6.pin6, J58.pin7
  N47: 74LS157-6.pin7, J57.pin7, J59.pin7
  N48: 74LS157-6.pin9, J57.pin5, J59.pin5
  N49: 74LS157-6.pin10, J58.pin5
  N50: 74LS157-6.pin12, J57.pin6, J59.pin6
  N51: 74LS157-6.pin13, J58.pin6
  N52: R1.Pin_0, LED1.anode

notes:
  0
  16 BIT MUX
  Marius Krabset 2019
