# Fritzing sketch HI_LO_MUX_v2 (saved by Fritzing 0.9.1b)
circuit board: 9.99058cm x 9.99059cm
breadboards: 2

parts:
  J45 = female pin header, 8 pins [form="♀ (female)"]
  74LS245 = IC, DIP package, 20 pins [chip_label=IC]
  74LS245_2 = IC, DIP package, 20 pins [chip_label=IC]
  C11 = Ceramic Capacitor [capacitance=100nF package="100 mil [THT, multilayer]"]
  C15 = Ceramic Capacitor [capacitance=100nF package="100 mil [THT, multilayer]"]
  J46 = female pin header, 8 pins [form="♀ (female)"]
  J47 = female pin header, 8 pins [form="♀ (female)"]
  GND = female pin header, 4 pins [form="♀ (female)"]
  GND1 = female pin header, 4 pins [form="♀ (female)"]
  J48 = female pin header, 8 pins [form="♀ (female)"]
  J49 = female pin header, 8 pins [form="♀ (female)"]
  VCC = female pin header, 4 pins [form="♀ (female)"]
  GND3 = female pin header, 4 pins [form="♀ (female)"]
  J50 = female pin header, 3 pins [form="♀ (female)"]
  DIR = female pin header, 1 pin [form="♀ (female)"]
  GND4 = female pin header, 4 pins [form="♀ (female)"]
  GND5 = female pin header, 4 pins [form="♀ (female)"]
  7404_NOT = IC, DIP package, 14 pins [chip_label=IC]
  EN = female pin header, 1 pin [form="♀ (female)"]  # not connected
  HI = female pin header, 1 pin [form="♀ (female)"]  # not connected
  AND = IC, DIP package, 14 pins [chip_label=IC]
  C16 = Ceramic Capacitor [capacitance=100nF package="100 mil [THT, multilayer]"]
  C17 = Ceramic Capacitor [capacitance=100nF package="100 mil [THT, multilayer]"]

nets:
  N1: J45.pin1, 74LS245.pin2, 74LS245_2.pin2
  N2: J45.pin2, 74LS245.pin3, 74LS245_2.pin3
  N3: J45.pin3, 74LS245.pin4, 74LS245_2.pin4
  N4: J45.pin4, 74LS245.pin5, 74LS245_2.pin5
  N5: J45.pin5, 74LS245.pin6, 74LS245_2.pin6
  N6: J45.pin6, 74LS245.pin7, 74LS245_2.pin7
  N7: J45.pin7, 74LS245.pin8, 74LS245_2.pin8
  N8: J45.pin8, 74LS245.pin9, 74LS245_2.pin9
  N9: 74LS245.pin1, 74LS245_2.pin1, J50.pin2, DIR.pin1
  N10: 74LS245.pin10, 74LS245_2.pin10, C11.0, C15.0, GND.pin1, GND.pin2, GND.pin3, GND.pin4, GND1.pin1, GND1.pin2, GND1.pin3, GND1.pin4, J50.pin3, 7404_NOT.pin7, AND.pin7, C16.1, C17.1
  N11: 74LS245.pin11, J46.pin1, J49.pin1
  N12: 74LS245.pin12, J46.pin2, J49.pin2
  N13: 74LS245.pin13, J46.pin3, J49.pin3
  N14: 74LS245.pin14, J46.pin4, J49.pin4
  N15: 74LS245.pin15, J46.pin5, J49.pin5
  N16: 74LS245.pin16, J46.pin6, J49.pin6
  N17: 74LS245.pin17, J46.pin7, J49.pin7
  N18: 74LS245.pin18, J46.pin8, J49.pin8
  N19: 74LS245.pin20, 74LS245_2.pin20, C11.1, C15.1, J50.pin1, 7404_NOT.pin14, AND.pin14, C16.0, C17.0
  N20: 74LS245_2.pin11, J47.pin1, J48.pin1
  N21: 74LS245_2.pin12, J47.pin2, J48.pin2
  N22: 74LS245_2.pin13, J47.pin3, J48.pin3
  N23: 74LS245_2.pin14, J47.pin4, J48.pin4
  N24: 74LS245_2.pin15, J47.pin5, J48.pin5
  N25: 74LS245_2.pin16, J47.pin6, J48.pin6
  N26: 74LS245_2.pin17, J47.pin7, J48.pin7
  N27: 74LS245_2.pin18, J47.pin8, J48.pin8
  N28: VCC.pin1, VCC.pin2, VCC.pin3, VCC.pin4, GND3.pin1, GND3.pin2, GND3.pin3, GND3.pin4
  N29: GND4.pin1, GND4.pin2, GND4.pin3, GND4.pin4, GND5.pin1, GND5.pin2, GND5.pin3, GND5.pin4

notes:
  7
  3
  5
  4
  1
  0
  6
  2
  16->8
  8->16
