# Fritzing sketch MAR_display_v2-groundfill (saved by Fritzing 0.9.1b)
circuit board: 9.99058cm x 9.99059cm
breadboards: 1

parts:
  J39 = female pin header, 8 pins [form="♀ (female)"]
  J40 = female pin header, 8 pins [form="♀ (female)"]
  GND = female pin header, 4 pins [form="♀ (female)"]
  VCC = female pin header, 4 pins [form="♀ (female)"]
  555 = 555 Timer [package="DIP8 [THT]"]
  74LS163 = IC, DIP package, 16 pins [chip_label=IC]
  R1 = Resistor [tolerance=±5% resistance=220 package=THT]
  R2 = Resistor [tolerance=±5% resistance=220 package=THT]
  C1 = Ceramic Capacitor [capacitance=100nF package="100 mil [THT, multilayer]"]
  74LS139 = IC, DIP package, 16 pins [chip_label=IC]
  C2 = Ceramic Capacitor [capacitance=100nF package="100 mil [THT, multilayer]"]
  J47 = female pin header, 12 pins [form="♀ (female)"]
  J48 = female pin header, 12 pins [form="♀ (female)"]
  74LS157-4 = IC, DIP package, 16 pins [chip_label=IC]
  74LS157-3 = IC, DIP package, 16 pins [chip_label=IC]
  display-3 = female pin header, 6 pins [form="♀ (female)"]
  display-4 = female pin header, 6 pins [form="♀ (female)"]
  R7 = Resistor [tolerance=±5% resistance=220 package="1206 [SMD]"]
  R8 = Resistor [tolerance=±5% resistance=220 package="1206 [SMD]"]
  R9 = Resistor [tolerance=±5% resistance=220 package="1206 [SMD]"]
  R10 = Resistor [tolerance=±5% resistance=220 package="1206 [SMD]"]
  GND_2 = female pin header, 4 pins [form="♀ (female)"]
  VCC_2 = female pin header, 4 pins [form="♀ (female)"]

nets:
  N1: J39.pin1, 74LS157-3.pin10
  N2: J39.pin2, 74LS157-3.pin13
  N3: J39.pin3, 74LS157-3.pin6
  N4: J39.pin4, 74LS157-3.pin3
  N5: J39.pin5, 74LS157-4.pin10
  N6: J39.pin6, 74LS157-4.pin13
  N7: J39.pin7, 74LS157-4.pin6
  N8: J39.pin8, 74LS157-4.pin3
  N9: J40.pin1, 74LS157-3.pin11
  N10: J40.pin2, 74LS157-3.pin14
  N11: J40.pin3, 74LS157-3.pin5
  N12: J40.pin4, 74LS157-3.pin2
  N13: J40.pin5, 74LS157-4.pin11
  N14: J40.pin6, 74LS157-4.pin14
  N15: J40.pin7, 74LS157-4.pin5
  N16: J40.pin8, 74LS157-4.pin2
  N17: GND.pin1, GND.pin2, GND.pin3, GND.pin4, 555.Ground, 74LS163.pin8, C1.1, 74LS139.pin1, 74LS139.pin8, C2.0, J47.pin5, J47.pin6, J47.pin7, J48.pin12, 74LS157-4.pin8, 74LS157-4.pin15, 74LS157-3.pin8, 74LS157-3.pin15, GND_2.pin1, GND_2.pin2, GND_2.pin3, GND_2.pin4
  N18: VCC.pin1, VCC.pin2, VCC.pin3, VCC.pin4, 555.Vcc_Supply_Voltage, 74LS163.pin1, 74LS163.pin7, 74LS163.pin9, 74LS163.pin10, 74LS163.pin16, R1.Pin_1, 74LS139.pin16, C2.1, J47.pin1, J47.pin3, J47.pin4, 74LS157-4.pin16, 74LS157-3.pin16, VCC_2.pin1, VCC_2.pin2, VCC_2.pin3, VCC_2.pin4
  N19: 555.Trigger, 555.Threshold, R2.Pin_0, C1.0
  N20: 555.Output, 74LS163.pin2
  N21: 555.Discharge, R1.Pin_0, R2.Pin_1
  N22: 74LS163.pin13, 74LS139.pin3, 74LS157-4.pin1, 74LS157-3.pin1
  N23: 74LS163.pin14, 74LS139.pin2, J47.pin2
  N24: 74LS139.pin4, R7.Pin_0
  N25: 74LS139.pin5, R9.Pin_0
  N26: 74LS139.pin6, R8.Pin_0
  N27: 74LS139.pin7, R10.Pin_1
  N28: J47.pin8, display-3.pin3
  N29: J47.pin9, display-3.pin5
  N30: J47.pin10, display-4.pin3
  N31: J47.pin11, display-3.pin1
  N32: J47.pin12, display-3.pin2
  N33: J48.pin1, 74LS157-3.pin9
  N34: J48.pin2, 74LS157-3.pin12
  N35: J48.pin3, 74LS157-3.pin7
  N36: J48.pin4, 74LS157-3.pin4
  N37: J48.pin5, 74LS157-4.pin9
  N38: J48.pin6, 74LS157-4.pin12
  N39: J48.pin7, 74LS157-4.pin7
  N40: J48.pin8, 74LS157-4.pin4
  N41: J48.pin9, display-4.pin2
  N42: J48.pin10, display-4.pin6
  N43: J48.pin11, display-3.pin4
  N44: display-3.pin6, R10.Pin_0
  N45: display-4.pin1, R7.Pin_1
  N46: display-4.pin4, R9.Pin_1
  N47: display-4.pin5, R8.Pin_1

notes:
  Address
  Marius Krabset 2019
  Memory Address Register
