# Fritzing sketch MAR_v2-groundfill (saved by Fritzing 0.9.1b)
circuit board: 9.99058cm x 9.99059cm
breadboards: 2

parts:
  C6 = Ceramic Capacitor [capacitance=100nF package="100 mil [THT, multilayer]"]
  74LS161 = IC, DIP package, 16 pins [chip_label=IC]
  74LS161_2 = IC, DIP package, 16 pins [chip_label=IC]
  74LS161_3 = IC, DIP package, 16 pins [chip_label=IC]
  74LS161_4 = IC, DIP package, 16 pins [chip_label=IC]
  CNT = female pin header, 1 pin [form="♀ (female)"]
  LOAD-H = female pin header, 1 pin [form="♀ (female)"]
  CLK = female pin header, 1 pin [form="♀ (female)"]
  + = female pin header, 1 pin [form="♀ (female)"]
  - = female pin header, 1 pin [form="♀ (female)"]
  J38 = female pin header, 2 pins [form="♀ (female)"]
  330 = Resistor [tolerance=±5% resistance=330 package="1206 [SMD]"]
  J40 = female pin header, 1 pin [form="♀ (female)"]
  J41 = female pin header, 1 pin [form="♀ (female)"]
  J42 = female pin header, 2 pins [form="♀ (female)"]
  C7 = Ceramic Capacitor [capacitance=100nF package="100 mil [THT, multilayer]"]
  LOAD-L = female pin header, 1 pin [form="♀ (female)"]
  74LS173 = IC, DIP package, 16 pins [chip_label=IC]
  74LS173_2 = IC, DIP package, 16 pins [chip_label=IC]
  J44 = female pin header, 8 pins [form="♀ (female)"]
  74LS283 = IC, DIP package, 16 pins [chip_label=IC]
  ADDR = female pin header, 8 pins [form="♀ (female)"]
  ADDR1 = female pin header, 8 pins [form="♀ (female)"]
  74LS283_2 = IC, DIP package, 16 pins [chip_label=IC]
  74LS283_3 = IC, DIP package, 16 pins [chip_label=IC]
  74LS283_4 = IC, DIP package, 16 pins [chip_label=IC]
  ADDR2 = female pin header, 8 pins [form="♀ (female)"]
  ADDR3 = female pin header, 8 pins [form="♀ (female)"]
  C8 = Ceramic Capacitor [capacitance=100nF package="100 mil [THT, multilayer]"]
  C9 = Ceramic Capacitor [capacitance=100nF package="100 mil [THT, multilayer]"]
  C10 = Ceramic Capacitor [capacitance=100nF package="100 mil [THT, multilayer]"]
  LOAD_offset = female pin header, 1 pin [form="♀ (female)"]
  J45 = female pin header, 8 pins [form="♀ (female)"]
  J46 = female pin header, 8 pins [form="♀ (female)"]
  J47 = female pin header, 8 pins [form="♀ (female)"]
  GND = female pin header, 4 pins [form="♀ (female)"]
  VCC = female pin header, 4 pins [form="♀ (female)"]
  VCC1 = female pin header, 4 pins [form="♀ (female)"]
  GND1 = female pin header, 4 pins [form="♀ (female)"]
  CLK1 = female pin header, 1 pin [form="♀ (female)"]
  J48 = female pin header, 4 pins [form="♀ (female)"]
  VCC_2 = female pin header, 4 pins [form="♀ (female)"]
  74LS157 = IC, DIP package, 16 pins [chip_label=IC]
  74LS157_2 = IC, DIP package, 16 pins [chip_label=IC]
  74LS157_3 = IC, DIP package, 16 pins [chip_label=IC]
  74LS157_4 = IC, DIP package, 16 pins [chip_label=IC]
  GND_2 = female pin header, 4 pins [form="♀ (female)"]
  74LS86_XOR = IC, DIP package, 14 pins [chip_label=IC]
  C11 = Ceramic Capacitor [capacitance=100nF package="100 mil [THT, multilayer]"]
  C12 = Ceramic Capacitor [capacitance=100nF package="100 mil [THT, multilayer]"]
  C13 = Ceramic Capacitor [capacitance=100nF package="100 mil [THT, multilayer]"]
  C14 = Ceramic Capacitor [capacitance=100nF package="100 mil [THT, multilayer]"]
  C15 = Ceramic Capacitor [capacitance=100nF package="100 mil [THT, multilayer]"]
  C16 = Ceramic Capacitor [capacitance=100nF package="100 mil [THT, multilayer]"]

nets:
  N1: C6.0, 74LS161.pin1, 74LS161.pin16, 74LS161_2.pin1, 74LS161_2.pin16, 74LS161_3.pin1, 74LS161_3.pin16, 74LS161_4.pin1, 74LS161_4.pin16, +.pin1, J38.pin2, J40.pin1, J42.pin2, C7.0, 74LS173.pin16, 74LS173_2.pin16, 74LS283.pin16, 74LS283_2.pin16, 74LS283_3.pin16, 74LS283_4.pin16, C8.1, C9.1, C10.1, VCC.pin1, VCC.pin2, VCC.pin3, VCC.pin4, GND1.pin1, GND1.pin2, GND1.pin3, GND1.pin4, VCC_2.pin1, VCC_2.pin2, VCC_2.pin3, VCC_2.pin4, 74LS157.pin16, 74LS157_2.pin16, 74LS157_3.pin16, 74LS157_4.pin16, 74LS86_XOR.pin1, 74LS86_XOR.pin2, 74LS86_XOR.pin9, 74LS86_XOR.pin10, 74LS86_XOR.pin12, 74LS86_XOR.pin13, 74LS86_XOR.pin14, C11.1, C12.1, C13.0, C14.1, C15.1, C16.1
  N2: C6.1, 74LS161.pin8, 74LS161_2.pin8, 74LS161_3.pin8, 74LS161_4.pin8, -.pin1, J38.pin1, J41.pin1, J42.pin1, C7.1, 74LS173.pin1, 74LS173.pin2, 74LS173.pin8, 74LS173.pin15, 74LS173_2.pin1, 74LS173_2.pin2, 74LS173_2.pin8, 74LS173_2.pin15, 74LS283.pin7, 74LS283.pin8, 74LS283_2.pin8, 74LS283_3.pin3, 74LS283_3.pin5, 74LS283_3.pin8, 74LS283_3.pin12, 74LS283_3.pin14, 74LS283_4.pin3, 74LS283_4.pin5, 74LS283_4.pin8, 74LS283_4.pin12, 74LS283_4.pin14, C8.0, C9.0, C10.0, GND.pin1, GND.pin2, GND.pin3, GND.pin4, VCC1.pin1, VCC1.pin2, VCC1.pin3, VCC1.pin4, 74LS157.pin8, 74LS157.pin15, 74LS157_2.pin8, 74LS157_2.pin15, 74LS157_3.pin8, 74LS157_3.pin15, 74LS157_4.pin8, 74LS157_4.pin15, GND_2.pin1, GND_2.pin2, GND_2.pin3, GND_2.pin4, 74LS86_XOR.pin7, C11.0, C12.0, C13.1, C14.0, C15.0, C16.0
  N3: 74LS161.pin2, 74LS161_2.pin2, 74LS161_3.pin2, 74LS161_4.pin2, 330.Pin_1, 74LS173.pin7, 74LS173_2.pin7
  N4: 74LS161.pin3, 74LS157_3.pin9
  N5: 74LS161.pin4, 74LS157_3.pin12
  N6: 74LS161.pin5, 74LS157_3.pin7
  N7: 74LS161.pin6, 74LS157_3.pin4
  N8: 74LS161.pin7, 74LS161.pin10, 74LS161_2.pin15
  N9: 74LS161.pin9, 74LS161_2.pin9, LOAD-L.pin1, J48.pin2, 74LS86_XOR.pin5
  N10: 74LS161.pin11, 74LS283_2.pin11
  N11: 74LS161.pin12, 74LS283_2.pin15
  N12: 74LS161.pin13, 74LS283_2.pin2
  N13: 74LS161.pin14, 74LS283_2.pin6
  N14: 74LS161.pin15, 74LS161_3.pin7, 74LS161_3.pin10
  N15: 74LS161_2.pin3, 74LS157_4.pin9
  N16: 74LS161_2.pin4, 74LS157_4.pin12
  N17: 74LS161_2.pin5, 74LS157_4.pin7
  N18: 74LS161_2.pin6, 74LS157_4.pin4
  N19: 74LS161_2.pin7, 74LS161_2.pin10, CNT.pin1, J48.pin3
  N20: 74LS161_2.pin11, 74LS283.pin11
  N21: 74LS161_2.pin12, 74LS283.pin15
  N22: 74LS161_2.pin13, 74LS283.pin2
  N23: 74LS161_2.pin14, 74LS283.pin6
  N24: 74LS161_3.pin3, 74LS157_2.pin9
  N25: 74LS161_3.pin4, 74LS157_2.pin12
  N26: 74LS161_3.pin5, 74LS157_2.pin7
  N27: 74LS161_3.pin6, 74LS157_2.pin4
  N28: 74LS161_3.pin9, 74LS161_4.pin9, LOAD-H.pin1, J48.pin1, 74LS86_XOR.pin4
  N29: 74LS161_3.pin11, 74LS283_4.pin11
  N30: 74LS161_3.pin12, 74LS283_4.pin15
  N31: 74LS161_3.pin13, 74LS283_4.pin2
  N32: 74LS161_3.pin14, 74LS283_4.pin6
  N33: 74LS161_3.pin15, 74LS161_4.pin7, 74LS161_4.pin10
  N34: 74LS161_4.pin3, 74LS157.pin9
  N35: 74LS161_4.pin4, 74LS157.pin12
  N36: 74LS161_4.pin5, 74LS157.pin7
  N37: 74LS161_4.pin6, 74LS157.pin4
  N38: 74LS161_4.pin11, 74LS283_3.pin11
  N39: 74LS161_4.pin12, 74LS283_3.pin15
  N40: 74LS161_4.pin13, 74LS283_3.pin2
  N41: 74LS161_4.pin14, 74LS283_3.pin6
  N42: CLK.pin1, 330.Pin_0, CLK1.pin1
  N43: 74LS173.pin3, 74LS283_2.pin12
  N44: 74LS173.pin4, 74LS283_2.pin14
  N45: 74LS173.pin5, 74LS283_2.pin3
  N46: 74LS173.pin6, 74LS283_2.pin5
  N47: 74LS173.pin9, 74LS173.pin10, 74LS173_2.pin9, 74LS173_2.pin10, LOAD_offset.pin1, J48.pin4
  N48: 74LS173.pin11, J44.pin4
  N49: 74LS173.pin12, J44.pin3
  N50: 74LS173.pin13, J44.pin2
  N51: 74LS173.pin14, J44.pin1
  N52: 74LS173_2.pin3, 74LS283.pin12
  N53: 74LS173_2.pin4, 74LS283.pin14
  N54: 74LS173_2.pin5, 74LS283.pin3
  N55: 74LS173_2.pin6, 74LS283.pin5
  N56: 74LS173_2.pin11, J44.pin8
  N57: 74LS173_2.pin12, J44.pin7
  N58: 74LS173_2.pin13, J44.pin6
  N59: 74LS173_2.pin14, J44.pin5
  N60: 74LS283.pin1, ADDR1.pin7, ADDR3.pin7
  N61: 74LS283.pin4, ADDR1.pin8, ADDR3.pin8
  N62: 74LS283.pin9, 74LS283_2.pin7
  N63: 74LS283.pin10, ADDR1.pin5, ADDR3.pin5
  N64: 74LS283.pin13, ADDR1.pin6, ADDR3.pin6
  N65: ADDR.pin1, 74LS283_3.pin10, ADDR2.pin1
  N66: ADDR.pin2, 74LS283_3.pin13, ADDR2.pin2
  N67: ADDR.pin3, 74LS283_3.pin1, ADDR2.pin3
  N68: ADDR.pin4, 74LS283_3.pin4, ADDR2.pin4
  N69: ADDR.pin5, 74LS283_4.pin10, ADDR2.pin5
  N70: ADDR.pin6, 74LS283_4.pin13, ADDR2.pin6
  N71: ADDR.pin7, 74LS283_4.pin1, ADDR2.pin7
  N72: ADDR.pin8, 74LS283_4.pin4, ADDR2.pin8
  N73: ADDR1.pin1, 74LS283_2.pin10, ADDR3.pin1
  N74: ADDR1.pin2, 74LS283_2.pin13, ADDR3.pin2
  N75: ADDR1.pin3, 74LS283_2.pin1, ADDR3.pin3
  N76: ADDR1.pin4, 74LS283_2.pin4, ADDR3.pin4
  N77: 74LS283_2.pin9, 74LS283_4.pin7
  N78: 74LS283_3.pin7, 74LS283_4.pin9
  N79: J45.pin1, 74LS157.pin3, 74LS157_3.pin3
  N80: J45.pin2, 74LS157.pin6, 74LS157_3.pin6
  N81: J45.pin3, 74LS157.pin13, 74LS157_3.pin13
  N82: J45.pin4, 74LS157.pin10, 74LS157_3.pin10
  N83: J45.pin5, 74LS157_2.pin3, 74LS157_4.pin3
  N84: J45.pin6, 74LS157_2.pin6, 74LS157_4.pin6
  N85: J45.pin7, 74LS157_2.pin13, 74LS157_4.pin13
  N86: J45.pin8, 74LS157_2.pin10, 74LS157_4.pin10
  N87: J46.pin1, 74LS157_2.pin11
  N88: J46.pin2, 74LS157_2.pin14
  N89: J46.pin3, 74LS157_2.pin5
  N90: J46.pin4, 74LS157_2.pin2
  N91: J46.pin5, 74LS157.pin11
  N92: J46.pin6, 74LS157.pin14
  N93: J46.pin7, 74LS157.pin5
  N94: J46.pin8, 74LS157.pin2
  N95: J47.pin1, 74LS157_4.pin11
  N96: J47.pin2, 74LS157_4.pin14
  N97: J47.pin3, 74LS157_4.pin5
  N98: J47.pin4, 74LS157_4.pin2
  N99: J47.pin5, 74LS157_3.pin11
  N100: J47.pin6, 74LS157_3.pin14
  N101: J47.pin7, 74LS157_3.pin5
  N102: J47.pin8, 74LS157_3.pin2
  N103: 74LS157.pin1, 74LS157_2.pin1, 74LS157_3.pin1, 74LS157_4.pin1, 74LS86_XOR.pin6

notes:
  7
  6
  5
  4
  3
  2
  1
  0
  MEMORY ADDRESS REGISTER
  Address out
  Marius Krabset 2019
