# Fritzing sketch MAR_v2 (saved by Fritzing 0.9.1b)
circuit board: 9.99058cm x 9.99059cm
breadboards: 2

parts:
  C6 = Ceramic Capacitor [capacitance=100nF package="100 mil [THT, multilayer]"]
  74LS161_B-HIGH1 = IC, DIP package, 16 pins [chip_label=IC]
  74LS161_B-LOW1 = IC, DIP package, 16 pins [chip_label=IC]
  74LS161_A-LOW1 = IC, DIP package, 16 pins [chip_label=IC]
  74LS161_A-HIGH1 = IC, DIP package, 16 pins [chip_label=IC]
  CNT = female pin header, 1 pin [form="♀ (female)"]
  LOAD-H = female pin header, 1 pin [form="♀ (female)"]
  CLK = female pin header, 1 pin [form="♀ (female)"]
  + = female pin header, 1 pin [form="♀ (female)"]
  - = female pin header, 1 pin [form="♀ (female)"]
  J38 = female pin header, 2 pins [form="♀ (female)"]
  330 = Resistor [tolerance=±5% resistance=330 package="1206 [SMD]"]
  J40 = female pin header, 1 pin [form="♀ (female)"]
  J41 = female pin header, 1 pin [form="♀ (female)"]
  J42 = female pin header, 2 pins [form="♀ (female)"]
  C7 = Ceramic Capacitor [capacitance=100nF package="100 mil [THT, multilayer]"]
  LOAD-L = female pin header, 1 pin [form="♀ (female)"]
  74LS173 = IC, DIP package, 16 pins [chip_label=IC]
  74LS173_2 = IC, DIP package, 16 pins [chip_label=IC]
  J44 = female pin header, 8 pins [form="♀ (female)"]
  74LS283 = IC, DIP package, 16 pins [chip_label=IC]
  ADDR = female pin header, 8 pins [form="♀ (female)"]
  ADDR1 = female pin header, 8 pins [form="♀ (female)"]
  74LS283_2 = IC, DIP package, 16 pins [chip_label=IC]
  74LS285 = IC, DIP package, 16 pins [chip_label=IC]
  74LS286 = IC, DIP package, 16 pins [chip_label=IC]
  ADDR2 = female pin header, 8 pins [form="♀ (female)"]
  ADDR3 = female pin header, 8 pins [form="♀ (female)"]
  C8 = Ceramic Capacitor [capacitance=100nF package="100 mil [THT, multilayer]"]
  C9 = Ceramic Capacitor [capacitance=100nF package="100 mil [THT, multilayer]"]
  C10 = Ceramic Capacitor [capacitance=100nF package="100 mil [THT, multilayer]"]
  LOAD_offset = female pin header, 1 pin [form="♀ (female)"]
  74LS245 = IC, DIP package, 20 pins [chip_label=IC]
  J45 = female pin header, 8 pins [form="♀ (female)"]
  74LS245_2 = IC, DIP package, 20 pins [chip_label=IC]
  74LS245_3 = IC, DIP package, 20 pins [chip_label=IC]
  AND = IC, DIP package, 14 pins [chip_label=IC]
  NOT = IC, DIP package, 14 pins [chip_label=IC]
  C11 = Ceramic Capacitor [capacitance=100nF package="100 mil [THT, multilayer]"]
  C12 = Ceramic Capacitor [capacitance=100nF package="100 mil [THT, multilayer]"]
  C15 = Ceramic Capacitor [capacitance=100nF package="100 mil [THT, multilayer]"]
  J46 = female pin header, 8 pins [form="♀ (female)"]
  J47 = female pin header, 8 pins [form="♀ (female)"]
  VCC = female pin header, 4 pins [form="♀ (female)"]
  GND = female pin header, 4 pins [form="♀ (female)"]
  VCC1 = female pin header, 4 pins [form="♀ (female)"]
  GND1 = female pin header, 4 pins [form="♀ (female)"]
  CLK1 = female pin header, 1 pin [form="♀ (female)"]
  J48 = female pin header, 4 pins [form="♀ (female)"]
  GND_2 = female pin header, 4 pins [form="♀ (female)"]
  VCC_2 = female pin header, 4 pins [form="♀ (female)"]

nets:
  N1: C6.0, 74LS161_B-HIGH1.pin1, 74LS161_B-HIGH1.pin16, 74LS161_B-LOW1.pin1, 74LS161_B-LOW1.pin16, 74LS161_A-LOW1.pin1, 74LS161_A-LOW1.pin16, 74LS161_A-HIGH1.pin1, 74LS161_A-HIGH1.pin16, +.pin1, J38.pin2, J40.pin1, J42.pin2, C7.0, 74LS173.pin16, 74LS173_2.pin16, 74LS283.pin16, 74LS283_2.pin16, 74LS285.pin16, 74LS286.pin16, C8.1, C9.1, C10.1, 74LS245.pin20, 74LS245_2.pin20, 74LS245_3.pin20, AND.pin1, AND.pin2, AND.pin9, AND.pin10, AND.pin12, AND.pin13, AND.pin14, NOT.pin14, C11.1, C12.1, C15.1, VCC.pin1, VCC.pin2, VCC.pin3, VCC.pin4, VCC1.pin1, VCC1.pin2, VCC1.pin3, VCC1.pin4, VCC_2.pin1, VCC_2.pin2, VCC_2.pin3, VCC_2.pin4
  N2: C6.1, 74LS161_B-HIGH1.pin8, 74LS161_B-LOW1.pin8, 74LS161_A-LOW1.pin8, 74LS161_A-HIGH1.pin8, -.pin1, J38.pin1, J41.pin1, J42.pin1, C7.1, 74LS173.pin1, 74LS173.pin2, 74LS173.pin8, 74LS173.pin15, 74LS173_2.pin1, 74LS173_2.pin2, 74LS173_2.pin8, 74LS173_2.pin15, 74LS283.pin7, 74LS283.pin8, 74LS283_2.pin8, 74LS285.pin3, 74LS285.pin5, 74LS285.pin8, 74LS285.pin12, 74LS285.pin14, 74LS286.pin3, 74LS286.pin5, 74LS286.pin8, 74LS286.pin12, 74LS286.pin14, C8.0, C9.0, C10.0, 74LS245.pin1, 74LS245.pin10, 74LS245_2.pin1, 74LS245_2.pin10, 74LS245_3.pin1, 74LS245_3.pin10, AND.pin7, NOT.pin7, NOT.pin9, C11.0, C12.0, C15.0, GND.pin1, GND.pin2, GND.pin3, GND.pin4, GND1.pin1, GND1.pin2, GND1.pin3, GND1.pin4, GND_2.pin1, GND_2.pin2, GND_2.pin3, GND_2.pin4
  N3: 74LS161_B-HIGH1.pin2, 74LS161_B-LOW1.pin2, 74LS161_A-LOW1.pin2, 74LS161_A-HIGH1.pin2, 330.Pin_1, 74LS173.pin7, 74LS173_2.pin7
  N4: 74LS161_B-HIGH1.pin3, 74LS161_A-HIGH1.pin3, 74LS245.pin5, 74LS245_2.pin5, 74LS245_3.pin5
  N5: 74LS161_B-HIGH1.pin4, 74LS161_A-HIGH1.pin4, 74LS245.pin4, 74LS245_2.pin4, 74LS245_3.pin4
  N6: 74LS161_B-HIGH1.pin5, 74LS161_A-HIGH1.pin5, 74LS245.pin3, 74LS245_2.pin3, 74LS245_3.pin3
  N7: 74LS161_B-HIGH1.pin6, 74LS161_A-HIGH1.pin6, 74LS245.pin2, 74LS245_2.pin2, 74LS245_3.pin2
  N8: 74LS161_B-HIGH1.pin7, 74LS161_B-HIGH1.pin10, 74LS161_B-LOW1.pin15
  N9: 74LS161_B-HIGH1.pin9, 74LS161_B-LOW1.pin9, LOAD-L.pin1, NOT.pin5, J48.pin2
  N10: 74LS161_B-HIGH1.pin11, 74LS283_2.pin11
  N11: 74LS161_B-HIGH1.pin12, 74LS283_2.pin15
  N12: 74LS161_B-HIGH1.pin13, 74LS283_2.pin2
  N13: 74LS161_B-HIGH1.pin14, 74LS283_2.pin6
  N14: 74LS161_B-HIGH1.pin15, 74LS161_A-LOW1.pin7, 74LS161_A-LOW1.pin10
  N15: 74LS161_B-LOW1.pin3, 74LS161_A-LOW1.pin3, 74LS245.pin9, 74LS245_2.pin9, 74LS245_3.pin9
  N16: 74LS161_B-LOW1.pin4, 74LS161_A-LOW1.pin4, 74LS245.pin8, 74LS245_2.pin8, 74LS245_3.pin8
  N17: 74LS161_B-LOW1.pin5, 74LS161_A-LOW1.pin5, 74LS245.pin7, 74LS245_2.pin7, 74LS245_3.pin7
  N18: 74LS161_B-LOW1.pin6, 74LS161_A-LOW1.pin6, 74LS245.pin6, 74LS245_2.pin6, 74LS245_3.pin6
  N19: 74LS161_B-LOW1.pin7, 74LS161_B-LOW1.pin10, CNT.pin1, J48.pin3
  N20: 74LS161_B-LOW1.pin11, 74LS283.pin11
  N21: 74LS161_B-LOW1.pin12, 74LS283.pin15
  N22: 74LS161_B-LOW1.pin13, 74LS283.pin2
  N23: 74LS161_B-LOW1.pin14, 74LS283.pin6
  N24: 74LS161_A-LOW1.pin9, 74LS161_A-HIGH1.pin9, LOAD-H.pin1, NOT.pin3, J48.pin1
  N25: 74LS161_A-LOW1.pin11, 74LS286.pin11
  N26: 74LS161_A-LOW1.pin12, 74LS286.pin15
  N27: 74LS161_A-LOW1.pin13, 74LS286.pin2
  N28: 74LS161_A-LOW1.pin14, 74LS286.pin6
  N29: 74LS161_A-LOW1.pin15, 74LS161_A-HIGH1.pin7, 74LS161_A-HIGH1.pin10
  N30: 74LS161_A-HIGH1.pin11, 74LS285.pin11
  N31: 74LS161_A-HIGH1.pin12, 74LS285.pin15
  N32: 74LS161_A-HIGH1.pin13, 74LS285.pin2
  N33: 74LS161_A-HIGH1.pin14, 74LS285.pin6
  N34: CLK.pin1, 330.Pin_0, CLK1.pin1
  N35: 74LS173.pin3, 74LS283_2.pin12
  N36: 74LS173.pin4, 74LS283_2.pin14
  N37: 74LS173.pin5, 74LS283_2.pin3
  N38: 74LS173.pin6, 74LS283_2.pin5
  N39: 74LS173.pin9, 74LS173.pin10, 74LS173_2.pin9, 74LS173_2.pin10, LOAD_offset.pin1, J48.pin4
  N40: 74LS173.pin11, J44.pin4
  N41: 74LS173.pin12, J44.pin3
  N42: 74LS173.pin13, J44.pin2
  N43: 74LS173.pin14, J44.pin1
  N44: 74LS173_2.pin3, 74LS283.pin12
  N45: 74LS173_2.pin4, 74LS283.pin14
  N46: 74LS173_2.pin5, 74LS283.pin3
  N47: 74LS173_2.pin6, 74LS283.pin5
  N48: 74LS173_2.pin11, J44.pin8
  N49: 74LS173_2.pin12, J44.pin7
  N50: 74LS173_2.pin13, J44.pin6
  N51: 74LS173_2.pin14, J44.pin5
  N52: 74LS283.pin1, ADDR1.pin7, ADDR3.pin7
  N53: 74LS283.pin4, ADDR1.pin8, ADDR3.pin8
  N54: 74LS283.pin9, 74LS283_2.pin7
  N55: 74LS283.pin10, ADDR1.pin5, ADDR3.pin5
  N56: 74LS283.pin13, ADDR1.pin6, ADDR3.pin6
  N57: ADDR.pin1, 74LS285.pin10, ADDR2.pin1
  N58: ADDR.pin2, 74LS285.pin13, ADDR2.pin2
  N59: ADDR.pin3, 74LS285.pin1, ADDR2.pin3
  N60: ADDR.pin4, 74LS285.pin4, ADDR2.pin4
  N61: ADDR.pin5, 74LS286.pin10, ADDR2.pin5
  N62: ADDR.pin6, 74LS286.pin13, ADDR2.pin6
  N63: ADDR.pin7, 74LS286.pin1, ADDR2.pin7
  N64: ADDR.pin8, 74LS286.pin4, ADDR2.pin8
  N65: ADDR1.pin1, 74LS283_2.pin10, ADDR3.pin1
  N66: ADDR1.pin2, 74LS283_2.pin13, ADDR3.pin2
  N67: ADDR1.pin3, 74LS283_2.pin1, ADDR3.pin3
  N68: ADDR1.pin4, 74LS283_2.pin4, ADDR3.pin4
  N69: 74LS283_2.pin9, 74LS286.pin7
  N70: 74LS285.pin7, 74LS286.pin9
  N71: 74LS245.pin11, J45.pin8
  N72: 74LS245.pin12, J45.pin7
  N73: 74LS245.pin13, J45.pin6
  N74: 74LS245.pin14, J45.pin5
  N75: 74LS245.pin15, J45.pin4
  N76: 74LS245.pin16, J45.pin3
  N77: 74LS245.pin17, J45.pin2
  N78: 74LS245.pin18, J45.pin1
  N79: 74LS245.pin19, AND.pin6, NOT.pin1, NOT.pin11, NOT.pin13
  N80: 74LS245_2.pin11, J46.pin1
  N81: 74LS245_2.pin12, J46.pin2
  N82: 74LS245_2.pin13, J46.pin3
  N83: 74LS245_2.pin14, J46.pin4
  N84: 74LS245_2.pin15, J46.pin5
  N85: 74LS245_2.pin16, J46.pin6
  N86: 74LS245_2.pin17, J46.pin7
  N87: 74LS245_2.pin18, J46.pin8
  N88: 74LS245_2.pin19, 74LS245_3.pin19, NOT.pin12
  N89: 74LS245_3.pin11, J47.pin1
  N90: 74LS245_3.pin12, J47.pin2
  N91: 74LS245_3.pin13, J47.pin3
  N92: 74LS245_3.pin14, J47.pin4
  N93: 74LS245_3.pin15, J47.pin5
  N94: 74LS245_3.pin16, J47.pin6
  N95: 74LS245_3.pin17, J47.pin7
  N96: 74LS245_3.pin18, J47.pin8
  N97: AND.pin4, NOT.pin6
  N98: AND.pin5, NOT.pin4

notes:
  7
  6
  5
  4
  3
  2
  1
  0
