# Fritzing sketch PC_display_v2-groundfill (saved by Fritzing 0.9.1b)
circuit board: 9.99cm x 9.99cm
breadboards: 1

parts:
  J39 = female pin header, 8 pins [form="♀ (female)"]
  J40 = female pin header, 8 pins [form="♀ (female)"]
  J41 = female pin header, 4 pins [form="♀ (female)"]
  J42 = female pin header, 4 pins [form="♀ (female)"]
  J43 = female pin header, 4 pins [form="♀ (female)"]
  J44 = female pin header, 4 pins [form="♀ (female)"]
  GND = female pin header, 4 pins [form="♀ (female)"]
  VCC = female pin header, 4 pins [form="♀ (female)"]
  555 = 555 Timer [package="DIP8 [THT]"]
  74LS163 = IC, DIP package, 16 pins [chip_label=IC]
  R1 = Resistor [tolerance=±5% resistance=220 package=THT]
  R2 = Resistor [tolerance=±5% resistance=220 package=THT]
  C1 = Ceramic Capacitor [capacitance=100nF package="100 mil [THT, multilayer]"]
  74LS139 = IC, DIP package, 16 pins [chip_label=IC]
  C2 = Ceramic Capacitor [capacitance=100nF package="100 mil [THT, multilayer]"]
  display-1 = female pin header, 6 pins [form="♀ (female)"]
  display-2 = female pin header, 6 pins [form="♀ (female)"]
  74LS157-1 = IC, DIP package, 16 pins [chip_label=IC]
  74LS157-2 = IC, DIP package, 16 pins [chip_label=IC]
  J45 = female pin header, 12 pins [form="♀ (female)"]
  J46 = female pin header, 12 pins [form="♀ (female)"]
  R3 = Resistor [tolerance=±5% resistance=220 package="1206 [SMD]"]
  R4 = Resistor [tolerance=±5% resistance=220 package="1206 [SMD]"]
  R5 = Resistor [tolerance=±5% resistance=220 package="1206 [SMD]"]
  R6 = Resistor [tolerance=±5% resistance=220 package="1206 [SMD]"]
  J47 = female pin header, 12 pins [form="♀ (female)"]
  J48 = female pin header, 12 pins [form="♀ (female)"]
  74LS157-4 = IC, DIP package, 16 pins [chip_label=IC]
  74LS157-3 = IC, DIP package, 16 pins [chip_label=IC]
  display-3 = female pin header, 6 pins [form="♀ (female)"]
  display-4 = female pin header, 6 pins [form="♀ (female)"]
  R7 = Resistor [tolerance=±5% resistance=220 package="1206 [SMD]"]
  R8 = Resistor [tolerance=±5% resistance=220 package="1206 [SMD]"]
  R9 = Resistor [tolerance=±5% resistance=220 package="1206 [SMD]"]
  R10 = Resistor [tolerance=±5% resistance=220 package="1206 [SMD]"]
  J49 = female pin header, 1 pin [form="♀ (female)"]
  R11 = Resistor [tolerance=±5% resistance=220 package="1206 [SMD]"]
  LED1 = LED - 3mm [color="Red (633nm)" package="3 mm [THT]"]

nets:
  N1: J39.pin1, 74LS157-3.pin10
  N2: J39.pin2, 74LS157-3.pin13
  N3: J39.pin3, 74LS157-3.pin6
  N4: J39.pin4, 74LS157-3.pin3
  N5: J39.pin5, 74LS157-4.pin10
  N6: J39.pin6, 74LS157-4.pin13
  N7: J39.pin7, 74LS157-4.pin6
  N8: J39.pin8, 74LS157-4.pin3
  N9: J40.pin1, 74LS157-3.pin11
  N10: J40.pin2, 74LS157-3.pin14
  N11: J40.pin3, 74LS157-3.pin5
  N12: J40.pin4, 74LS157-3.pin2
  N13: J40.pin5, 74LS157-4.pin11
  N14: J40.pin6, 74LS157-4.pin14
  N15: J40.pin7, 74LS157-4.pin5
  N16: J40.pin8, 74LS157-4.pin2
  N17: J41.pin1, 74LS157-2.pin10
  N18: J41.pin2, 74LS157-2.pin13
  N19: J41.pin3, 74LS157-2.pin6
  N20: J41.pin4, 74LS157-2.pin3
  N21: J42.pin1, 74LS157-1.pin10
  N22: J42.pin2, 74LS157-1.pin13
  N23: J42.pin3, 74LS157-1.pin6
  N24: J42.pin4, 74LS157-1.pin3
  N25: J43.pin1, 74LS157-2.pin11
  N26: J43.pin2, 74LS157-2.pin14
  N27: J43.pin3, 74LS157-2.pin5
  N28: J43.pin4, 74LS157-2.pin2
  N29: J44.pin1, 74LS157-1.pin11
  N30: J44.pin2, 74LS157-1.pin14
  N31: J44.pin3, 74LS157-1.pin5
  N32: J44.pin4, 74LS157-1.pin2
  N33: GND.pin1, GND.pin2, GND.pin3, GND.pin4, 555.Ground, 74LS163.pin8, C1.1, 74LS139.pin1, 74LS139.pin8, C2.0, 74LS157-1.pin8, 74LS157-1.pin15, 74LS157-2.pin8, 74LS157-2.pin15, J45.pin12, J46.pin5, J46.pin6, J46.pin7, J47.pin5, J47.pin6, J47.pin7, J48.pin12, 74LS157-4.pin8, 74LS157-4.pin15, 74LS157-3.pin8, 74LS157-3.pin15
  N34: VCC.pin1, VCC.pin2, VCC.pin3, VCC.pin4, 555.Vcc_Supply_Voltage, 74LS163.pin1, 74LS163.pin7, 74LS163.pin9, 74LS163.pin10, 74LS163.pin16, R1.Pin_1, 74LS139.pin16, C2.1, 74LS157-1.pin16, 74LS157-2.pin16, J46.pin1, J46.pin3, J46.pin4, J47.pin1, J47.pin3, J47.pin4, 74LS157-4.pin16, 74LS157-3.pin16, LED1.anode
  N35: 555.Trigger, 555.Threshold, R2.Pin_0, C1.0
  N36: 555.Output, 74LS163.pin2
  N37: 555.Discharge, R1.Pin_0, R2.Pin_1
  N38: 74LS163.pin13, 74LS139.pin3, 74LS157-1.pin1, 74LS157-2.pin1, 74LS157-4.pin1, 74LS157-3.pin1
  N39: 74LS163.pin14, 74LS139.pin2, J46.pin2, J47.pin2
  N40: 74LS139.pin4, R6.Pin_0, R7.Pin_0
  N41: 74LS139.pin5, R4.Pin_0, R9.Pin_0
  N42: 74LS139.pin6, R5.Pin_0, R8.Pin_0
  N43: 74LS139.pin7, R3.Pin_1, R10.Pin_1
  N44: display-1.pin1, R6.Pin_1
  N45: display-1.pin2, J45.pin9
  N46: display-1.pin3, J46.pin10
  N47: display-1.pin4, R4.Pin_1
  N48: display-1.pin5, R5.Pin_1
  N49: display-1.pin6, J45.pin10
  N50: display-2.pin1, J46.pin11
  N51: display-2.pin2, J46.pin12
  N52: display-2.pin3, J46.pin8
  N53: display-2.pin4, J45.pin11
  N54: display-2.pin5, J46.pin9
  N55: display-2.pin6, R3.Pin_0
  N56: 74LS157-1.pin4, J45.pin4
  N57: 74LS157-1.pin7, J45.pin3
  N58: 74LS157-1.pin9, J45.pin1
  N59: 74LS157-1.pin12, J45.pin2
  N60: 74LS157-2.pin4, J45.pin8
  N61: 74LS157-2.pin7, J45.pin7
  N62: 74LS157-2.pin9, J45.pin5
  N63: 74LS157-2.pin12, J45.pin6
  N64: J47.pin8, display-3.pin3
  N65: J47.pin9, display-3.pin5
  N66: J47.pin10, display-4.pin3
  N67: J47.pin11, display-3.pin1
  N68: J47.pin12, display-3.pin2
  N69: J48.pin1, 74LS157-3.pin9
  N70: J48.pin2, 74LS157-3.pin12
  N71: J48.pin3, 74LS157-3.pin7
  N72: J48.pin4, 74LS157-3.pin4
  N73: J48.pin5, 74LS157-4.pin9
  N74: J48.pin6, 74LS157-4.pin12
  N75: J48.pin7, 74LS157-4.pin7
  N76: J48.pin8, 74LS157-4.pin4
  N77: J48.pin9, display-4.pin2
  N78: J48.pin10, display-4.pin6
  N79: J48.pin11, display-3.pin4
  N80: display-3.pin6, R10.Pin_0
  N81: display-4.pin1, R7.Pin_1
  N82: display-4.pin4, R9.Pin_1
  N83: display-4.pin5, R8.Pin_1
  N84: J49.pin1, R11.Pin_0
  N85: R11.Pin_1, LED1.cathode

notes:
  JumpAddress
  ProgramCounter
  JUMP
  Marius Krabset 2019
