# Fritzing sketch PC_display_v2 (saved by Fritzing 0.9.1b)
circuit board: 9.99cm x 9.99cm
breadboards: 1

parts:
  J39 = female pin header, 8 pins [form="♀ (female)"]  # not connected
  J40 = female pin header, 8 pins [form="♀ (female)"]  # not connected
  J41 = female pin header, 4 pins [form="♀ (female)"]
  J42 = female pin header, 4 pins [form="♀ (female)"]
  J43 = female pin header, 4 pins [form="♀ (female)"]
  J44 = female pin header, 4 pins [form="♀ (female)"]
  GND5 = female pin header, 4 pins [form="♀ (female)"]  # not connected
  VCC1 = female pin header, 4 pins [form="♀ (female)"]  # not connected
  flags1 = female pin header, 4 pins [form="♀ (female)"]  # not connected
  jmp_cond1 = female pin header, 4 pins [form="♀ (female)"]  # not connected
  555 = 555 Timer [package="DIP8 [THT]"]
  74LS163 = IC, DIP package, 16 pins [chip_label=IC]
  R1 = Resistor [tolerance=±5% resistance=220 package=THT]
  R2 = Resistor [tolerance=±5% resistance=220 package=THT]
  C1 = Ceramic Capacitor [capacitance=100nF package="100 mil [THT, multilayer]"]
  74LS139 = IC, DIP package, 16 pins [chip_label=IC]
  C2 = Ceramic Capacitor [capacitance=100nF package="100 mil [THT, multilayer]"]
  display-1 = female pin header, 6 pins [form="♀ (female)"]
  display-2 = female pin header, 6 pins [form="♀ (female)"]
  74LS157 = IC, DIP package, 16 pins [chip_label=IC]
  74LS164 = IC, DIP package, 16 pins [chip_label=IC]
  J45 = female pin header, 12 pins [form="♀ (female)"]
  J46 = female pin header, 12 pins [form="♀ (female)"]
  R3 = Resistor [tolerance=±5% resistance=220 package="1206 [SMD]"]
  R4 = Resistor [tolerance=±5% resistance=220 package="1206 [SMD]"]
  R5 = Resistor [tolerance=±5% resistance=220 package="1206 [SMD]"]
  R6 = Resistor [tolerance=±5% resistance=220 package="1206 [SMD]"]

nets:
  N1: J41.pin1, 74LS164.pin10
  N2: J41.pin2, 74LS164.pin13
  N3: J41.pin3, 74LS164.pin6
  N4: J41.pin4, 74LS164.pin3
  N5: J42.pin1, 74LS157.pin10
  N6: J42.pin2, 74LS157.pin13
  N7: J42.pin3, 74LS157.pin6
  N8: J42.pin4, 74LS157.pin3
  N9: J43.pin1, 74LS164.pin11
  N10: J43.pin2, 74LS164.pin14
  N11: J43.pin3, 74LS164.pin5
  N12: J43.pin4, 74LS164.pin2
  N13: J44.pin1, 74LS157.pin11
  N14: J44.pin2, 74LS157.pin14
  N15: J44.pin3, 74LS157.pin5
  N16: J44.pin4, 74LS157.pin2
  N17: 555.Ground, 74LS163.pin8, C1.1, 74LS139.pin1, 74LS139.pin8, C2.0, 74LS157.pin8, 74LS157.pin15, 74LS164.pin8, 74LS164.pin15, J45.pin12, J46.pin5, J46.pin6, J46.pin7
  N18: 555.Trigger, 555.Threshold, R2.Pin_0, C1.0
  N19: 555.Output, 74LS163.pin2
  N20: 555.Discharge, R1.Pin_0, R2.Pin_1
  N21: 555.Vcc_Supply_Voltage, 74LS163.pin1, 74LS163.pin7, 74LS163.pin9, 74LS163.pin10, 74LS163.pin16, R1.Pin_1, 74LS139.pin16, C2.1, 74LS157.pin16, 74LS164.pin16, J46.pin1, J46.pin3, J46.pin4
  N22: 74LS163.pin13, 74LS139.pin3, 74LS157.pin1, 74LS164.pin1
  N23: 74LS163.pin14, 74LS139.pin2, J46.pin2
  N24: 74LS139.pin4, R6.Pin_0
  N25: 74LS139.pin5, R4.Pin_0
  N26: 74LS139.pin6, R5.Pin_0
  N27: 74LS139.pin7, R3.Pin_1
  N28: display-1.pin1, R6.Pin_1
  N29: display-1.pin2, J45.pin9
  N30: display-1.pin3, J46.pin10
  N31: display-1.pin4, R4.Pin_1
  N32: display-1.pin5, R5.Pin_1
  N33: display-1.pin6, J45.pin10
  N34: display-2.pin1, J46.pin11
  N35: display-2.pin2, J46.pin12
  N36: display-2.pin3, J46.pin8
  N37: display-2.pin4, J45.pin11
  N38: display-2.pin5, J46.pin9
  N39: display-2.pin6, R3.Pin_0
  N40: 74LS157.pin4, J45.pin4
  N41: 74LS157.pin7, J45.pin3
  N42: 74LS157.pin9, J45.pin1
  N43: 74LS157.pin12, J45.pin2
  N44: 74LS164.pin4, J45.pin8
  N45: 74LS164.pin7, J45.pin7
  N46: 74LS164.pin9, J45.pin5
  N47: 74LS164.pin12, J45.pin6
