# Fritzing sketch PC_v2 (saved by Fritzing 0.9.1b)
circuit board: 9.99cm x 9.99cm
circuit board: 12.3427cm x 15.5929cm
breadboards: 1

parts:
  74LS173_A-HIGH = IC, DIP package, 16 pins [chip_label=IC]
  74LS173_A-LOW = IC, DIP package, 16 pins [chip_label=IC]
  74LS173_B-LOW = IC, DIP package, 16 pins [chip_label=IC]
  74LS173_B-HIGH = IC, DIP package, 16 pins [chip_label=IC]
  CLK = female pin header, 1 pin [form="♀ (female)"]
  LOAD-A = female pin header, 1 pin [form="♀ (female)"]
  LOAD-B = female pin header, 1 pin [form="♀ (female)"]
  J2 = female pin header, 2 pins [form="♀ (female)"]
  C1 = Ceramic Capacitor [capacitance=100nF package="100 mil [THT, multilayer]"]
  J15 = female pin header, 8 pins [form="♀ (female)"]
  C6 = Ceramic Capacitor [capacitance=100nF package="100 mil [THT, multilayer]"]
  J24 = female pin header, 8 pins [form="♀ (female)"]
  74LS161_B-HIGH1 = IC, DIP package, 16 pins [chip_label=IC]
  74LS161_B-LOW1 = IC, DIP package, 16 pins [chip_label=IC]
  74LS161_A-LOW1 = IC, DIP package, 16 pins [chip_label=IC]
  74LS161_A-HIGH1 = IC, DIP package, 16 pins [chip_label=IC]
  CNT = female pin header, 1 pin [form="♀ (female)"]
  J25 = female pin header, 2 pins [form="♀ (female)"]
  IC1 = IC, DIP package, 20 pins [chip_label=IC]
  IC2 = IC, DIP package, 20 pins [chip_label=IC]
  jmp_cond = female pin header, 4 pins [form="♀ (female)"]
  INV = IC, DIP package, 14 pins [chip_label=IC]
  AND = IC, DIP package, 14 pins [chip_label=IC]
  flags = female pin header, 4 pins [form="♀ (female)"]
  C7 = Ceramic Capacitor [capacitance=100nF package="100 mil [THT, multilayer]"]
  flags2 = female pin header, 12 pins [form="♀ (female)"]
  flags3 = female pin header, 12 pins [form="♀ (female)"]
  C8 = Ceramic Capacitor [capacitance=100nF package="100 mil [THT, multilayer]"]
  jmp = LED - 5mm [color="Red (633nm)" package="5 mm [THT]"]
  R1 = Resistor [tolerance=±5% resistance=220 package=THT]
  GND = female pin header, 1 pin [form="♀ (female)"]
  VCC = female pin header, 1 pin [form="♀ (female)"]
  GND_2 = female pin header, 1 pin [form="♀ (female)"]
  VCC_2 = female pin header, 1 pin [form="♀ (female)"]
  J26 = female pin header, 2 pins [form="♀ (female)"]
  GND1 = female pin header, 1 pin [form="♀ (female)"]
  VCC1 = female pin header, 1 pin [form="♀ (female)"]
  VCC2 = female pin header, 1 pin [form="♀ (female)"]
  GND2 = female pin header, 1 pin [form="♀ (female)"]
  J27 = female pin header, 2 pins [form="♀ (female)"]
  C9 = Ceramic Capacitor [capacitance=100nF package="100 mil [THT, multilayer]"]
  out_ctrl1 = female pin header, 2 pins [form="♀ (female)"]
  V = Resistor [tolerance=±5% resistance=220 package="1206 [SMD]"]
  C = Resistor [tolerance=±5% resistance=220 package="1206 [SMD]"]
  N = Resistor [tolerance=±5% resistance=220 package="1206 [SMD]"]
  Z = Resistor [tolerance=±5% resistance=220 package="1206 [SMD]"]
  LED33 = smd LED [color="Red (633nm)" package="1206 [SMD]"]
  LED34 = smd LED [color="Red (633nm)" package="1206 [SMD]"]
  LED35 = smd LED [color="Red (633nm)" package="1206 [SMD]"]
  LED36 = smd LED [color="Red (633nm)" package="1206 [SMD]"]
  RESET = female pin header, 1 pin [form="♀ (female)"]
  C10 = Ceramic Capacitor [capacitance=100nF package="100 mil [THT, multilayer]"]
  74LS173-1 = IC, DIP package, 16 pins [chip_label=IC]
  74LS173-2 = IC, DIP package, 16 pins [chip_label=IC]
  J28 = female pin header, 8 pins [form="♀ (female)"]
  74LS161-1 = IC, DIP package, 16 pins [chip_label=IC]
  74LS161-2 = IC, DIP package, 16 pins [chip_label=IC]
  74LS173-3 = IC, DIP package, 16 pins [chip_label=IC]
  74LS173-4 = IC, DIP package, 16 pins [chip_label=IC]
  74LS161-3 = IC, DIP package, 16 pins [chip_label=IC]
  74LS161-4 = IC, DIP package, 16 pins [chip_label=IC]
  C11 = Ceramic Capacitor [capacitance=100nF package="100 mil [THT, multilayer]"]
  C12 = Ceramic Capacitor [capacitance=100nF package="100 mil [THT, multilayer]"]
  C13 = Ceramic Capacitor [capacitance=100nF package="100 mil [THT, multilayer]"]
  C14 = Ceramic Capacitor [capacitance=100nF package="100 mil [THT, multilayer]"]
  LOAD-B1 = female pin header, 1 pin [form="♀ (female)"]
  LOAD-A1 = female pin header, 1 pin [form="♀ (female)"]
  CLK1 = female pin header, 1 pin [form="♀ (female)"]
  C15 = Ceramic Capacitor [capacitance=100nF package="100 mil [THT, multilayer]"]
  C16 = Ceramic Capacitor [capacitance=100nF package="100 mil [THT, multilayer]"]
  C17 = Ceramic Capacitor [capacitance=100nF package="100 mil [THT, multilayer]"]
  C18 = Ceramic Capacitor [capacitance=100nF package="100 mil [THT, multilayer]"]
  flags4 = female pin header, 12 pins [form="♀ (female)"]  # not connected
  flags5 = female pin header, 12 pins [form="♀ (female)"]  # not connected
  AND1 = IC, DIP package, 14 pins [chip_label=IC]  # not connected
  INV1 = IC, DIP package, 14 pins [chip_label=IC]  # not connected
  J33 = female pin header, 4 pins [form="♀ (female)"]
  J34 = female pin header, 4 pins [form="♀ (female)"]
  J35 = female pin header, 4 pins [form="♀ (female)"]
  J36 = female pin header, 4 pins [form="♀ (female)"]
  RESET_2 = female pin header, 1 pin [form="♀ (female)"]
  CNT_2 = female pin header, 1 pin [form="♀ (female)"]
  JUMP = female pin header, 1 pin [form="♀ (female)"]

nets:
  N1: 74LS173_A-HIGH.pin1, 74LS173_A-HIGH.pin2, 74LS173_A-HIGH.pin8, 74LS173_A-HIGH.pin15, 74LS173_A-LOW.pin1, 74LS173_A-LOW.pin2, 74LS173_A-LOW.pin8, 74LS173_A-LOW.pin15, 74LS173_B-LOW.pin1, 74LS173_B-LOW.pin2, 74LS173_B-LOW.pin8, 74LS173_B-LOW.pin15, 74LS173_B-HIGH.pin1, 74LS173_B-HIGH.pin2, 74LS173_B-HIGH.pin8, 74LS173_B-HIGH.pin15, J2.pin2, C1.0, C6.1, 74LS161_B-HIGH1.pin8, 74LS161_B-LOW1.pin8, 74LS161_A-LOW1.pin8, 74LS161_A-HIGH1.pin8, J25.pin1, IC1.pin1, IC1.pin10, IC2.pin1, IC2.pin10, INV.pin5, INV.pin7, INV.pin9, AND.pin7, C7.0, flags2.pin1, flags3.pin6, flags3.pin7, flags3.pin8, flags3.pin10, flags3.pin11, C8.1, GND.pin1, GND_2.pin1, J26.pin2, GND1.pin1, GND2.pin1, J27.pin1, C9.1, V.Pin_0, C.Pin_0, N.Pin_0, Z.Pin_0, C10.0
  N2: 74LS173_A-HIGH.pin7, 74LS173_A-LOW.pin7, 74LS173_B-LOW.pin7, 74LS173_B-HIGH.pin7, CLK.pin1, 74LS161_B-HIGH1.pin2, 74LS161_B-LOW1.pin2, 74LS161_A-LOW1.pin2, 74LS161_A-HIGH1.pin2
  N3: 74LS173_A-HIGH.pin9, 74LS173_A-HIGH.pin10, 74LS173_A-LOW.pin9, 74LS173_A-LOW.pin10, LOAD-A.pin1
  N4: 74LS173_A-HIGH.pin11, 74LS173_B-HIGH.pin11, J15.pin4
  N5: 74LS173_A-HIGH.pin12, 74LS173_B-HIGH.pin12, J15.pin3
  N6: 74LS173_A-HIGH.pin13, 74LS173_B-HIGH.pin13, J15.pin2
  N7: 74LS173_A-HIGH.pin14, 74LS173_B-HIGH.pin14, J15.pin1
  N8: 74LS173_A-HIGH.pin16, 74LS173_A-LOW.pin16, 74LS173_B-LOW.pin16, 74LS173_B-HIGH.pin16, J2.pin1, C1.1, C6.0, 74LS161_B-HIGH1.pin16, 74LS161_B-LOW1.pin16, 74LS161_A-LOW1.pin16, 74LS161_A-HIGH1.pin16, J25.pin2, IC1.pin20, IC2.pin20, INV.pin14, AND.pin9, AND.pin10, AND.pin12, AND.pin13, AND.pin14, C7.1, flags3.pin9, flags3.pin12, C8.0, R1.Pin_0, VCC.pin1, VCC_2.pin1, J26.pin1, VCC1.pin1, VCC2.pin1, J27.pin2, C9.0, C10.1
  N9: 74LS173_A-LOW.pin11, 74LS173_B-LOW.pin11, J15.pin8
  N10: 74LS173_A-LOW.pin12, 74LS173_B-LOW.pin12, J15.pin7
  N11: 74LS173_A-LOW.pin13, 74LS173_B-LOW.pin13, J15.pin6
  N12: 74LS173_A-LOW.pin14, 74LS173_B-LOW.pin14, J15.pin5
  N13: 74LS173_B-LOW.pin9, 74LS173_B-LOW.pin10, 74LS173_B-HIGH.pin9, 74LS173_B-HIGH.pin10, LOAD-B.pin1
  N14: J24.pin1, IC1.pin9, IC2.pin9
  N15: J24.pin2, IC1.pin8, IC2.pin8
  N16: J24.pin3, IC1.pin7, IC2.pin7
  N17: J24.pin4, IC1.pin6, IC2.pin6
  N18: J24.pin5, IC1.pin5, IC2.pin5
  N19: J24.pin6, IC1.pin4, IC2.pin4
  N20: J24.pin7, IC1.pin3, IC2.pin3
  N21: J24.pin8, IC1.pin2, IC2.pin2
  N22: 74LS161_B-HIGH1.pin1, 74LS161_B-LOW1.pin1, 74LS161_A-LOW1.pin1, 74LS161_A-HIGH1.pin1, RESET.pin1
  N23: 74LS161_B-HIGH1.pin7, 74LS161_B-HIGH1.pin10, 74LS161_B-LOW1.pin15
  N24: 74LS161_B-HIGH1.pin9, 74LS161_B-LOW1.pin9, 74LS161_A-LOW1.pin9, 74LS161_A-HIGH1.pin9, flags2.pin4, jmp.cathode
  N25: 74LS161_B-HIGH1.pin15, 74LS161_A-LOW1.pin7, 74LS161_A-LOW1.pin10
  N26: 74LS161_B-LOW1.pin7, 74LS161_B-LOW1.pin10, CNT.pin1
  N27: 74LS161_A-LOW1.pin15, 74LS161_A-HIGH1.pin7, 74LS161_A-HIGH1.pin10
  N28: IC1.pin19, INV.pin12
  N29: IC2.pin19, INV.pin10
  N30: jmp_cond.pin1, flags2.pin5
  N31: jmp_cond.pin2, flags2.pin6
  N32: jmp_cond.pin3, flags2.pin7
  N33: jmp_cond.pin4, flags2.pin8
  N34: INV.pin1, out_ctrl1.pin1
  N35: INV.pin2, AND.pin1, AND.pin4
  N36: INV.pin3, AND.pin2, out_ctrl1.pin2
  N37: INV.pin4, AND.pin5
  N38: INV.pin11, AND.pin6
  N39: INV.pin13, AND.pin3
  N40: flags.pin1, flags2.pin9, LED36.anode
  N41: flags.pin2, flags2.pin10, LED35.anode
  N42: flags.pin3, flags2.pin11, LED34.anode
  N43: flags.pin4, flags2.pin12, LED33.anode
  N44: jmp.anode, R1.Pin_1
  N45: V.Pin_1, LED33.cathode
  N46: C.Pin_1, LED34.cathode
  N47: N.Pin_1, LED35.cathode
  N48: Z.Pin_1, LED36.cathode
  N49: 74LS173-1.pin1, 74LS173-1.pin2, 74LS173-1.pin8, 74LS173-1.pin15, 74LS173-2.pin1, 74LS173-2.pin2, 74LS173-2.pin8, 74LS173-2.pin15, 74LS173-3.pin1, 74LS173-3.pin2, 74LS173-3.pin8, 74LS173-3.pin15, 74LS173-4.pin1, 74LS173-4.pin2, 74LS173-4.pin8, 74LS173-4.pin15, C11.0, C12.0, C13.0, C14.0
  N50: 74LS173-1.pin3, 74LS161-1.pin6, J33.pin1
  N51: 74LS173-1.pin4, 74LS161-1.pin5, J33.pin2
  N52: 74LS173-1.pin5, 74LS161-1.pin4, J33.pin3
  N53: 74LS173-1.pin6, 74LS161-1.pin3, J33.pin4
  N54: 74LS173-1.pin7, 74LS173-2.pin7, 74LS161-1.pin2, 74LS161-2.pin2, 74LS173-3.pin7, 74LS173-4.pin7, 74LS161-3.pin2, 74LS161-4.pin2, CLK1.pin1
  N55: 74LS173-1.pin9, 74LS173-1.pin10, 74LS173-2.pin9, 74LS173-2.pin10, LOAD-B1.pin1
  N56: 74LS173-1.pin11, J28.pin4, 74LS173-4.pin11
  N57: 74LS173-1.pin12, J28.pin3, 74LS173-4.pin12
  N58: 74LS173-1.pin13, J28.pin2, 74LS173-4.pin13
  N59: 74LS173-1.pin14, J28.pin1, 74LS173-4.pin14
  N60: 74LS173-1.pin16, 74LS173-2.pin16, 74LS173-3.pin16, 74LS173-4.pin16, C11.1, C12.1, C13.1, C14.1
  N61: 74LS173-2.pin3, 74LS161-2.pin6, J34.pin1
  N62: 74LS173-2.pin4, 74LS161-2.pin5, J34.pin2
  N63: 74LS173-2.pin5, 74LS161-2.pin4, J34.pin3
  N64: 74LS173-2.pin6, 74LS161-2.pin3, J34.pin4
  N65: 74LS173-2.pin11, J28.pin8, 74LS173-3.pin11
  N66: 74LS173-2.pin12, J28.pin7, 74LS173-3.pin12
  N67: 74LS173-2.pin13, J28.pin6, 74LS173-3.pin13
  N68: 74LS173-2.pin14, J28.pin5, 74LS173-3.pin14
  N69: 74LS161-1.pin1, 74LS161-2.pin1, 74LS161-3.pin1, 74LS161-4.pin1, RESET_2.pin1
  N70: 74LS161-1.pin7, 74LS161-1.pin10, 74LS161-2.pin15
  N71: 74LS161-1.pin8, 74LS161-2.pin8, 74LS161-3.pin8, 74LS161-4.pin8, C15.1, C16.1, C17.1, C18.1
  N72: 74LS161-1.pin9, 74LS161-2.pin9, 74LS161-3.pin9, 74LS161-4.pin9, JUMP.pin1
  N73: 74LS161-1.pin16, 74LS161-2.pin16, 74LS161-3.pin16, 74LS161-4.pin16, C15.0, C16.0, C17.0, C18.0
  N74: 74LS161-2.pin7, 74LS161-2.pin10, 74LS161-3.pin15
  N75: 74LS173-3.pin3, 74LS161-4.pin6, J36.pin1
  N76: 74LS173-3.pin4, 74LS161-4.pin5, J36.pin2
  N77: 74LS173-3.pin5, 74LS161-4.pin4, J36.pin3
  N78: 74LS173-3.pin6, 74LS161-4.pin3, J36.pin4
  N79: 74LS173-3.pin9, 74LS173-3.pin10, 74LS173-4.pin9, 74LS173-4.pin10, LOAD-A1.pin1
  N80: 74LS173-4.pin3, 74LS161-3.pin6, J35.pin1
  N81: 74LS173-4.pin4, 74LS161-3.pin5, J35.pin2
  N82: 74LS173-4.pin5, 74LS161-3.pin4, J35.pin3
  N83: 74LS173-4.pin6, 74LS161-3.pin3, J35.pin4
  N84: 74LS161-3.pin7, 74LS161-3.pin10, 74LS161-4.pin15
  N85: 74LS161-4.pin7, 74LS161-4.pin10, CNT_2.pin1

notes:
  HIGH
  OE
  LSB
