# Fritzing sketch RAM_v2-groundfill (saved by Fritzing 0.9.1b)
circuit board: 9.99058cm x 6.84381cm
breadboards: 2

parts:
  VCC = female pin header, 4 pins [form="♀ (female)"]
  GND = female pin header, 4 pins [form="♀ (female)"]
  ADDR8 = female pin header, 8 pins [form="♀ (female)"]
  ADDR9 = female pin header, 8 pins [form="♀ (female)"]
  74245 = IC, DIP package, 20 pins [chip_label=IC]
  74LS173-H = IC, DIP package, 16 pins [chip_label=IC]
  74LS173-L = IC, DIP package, 16 pins [chip_label=IC]
  bus1 = female pin header, 8 pins [form="♀ (female)"]
  C5 = Ceramic Capacitor [capacitance=100nF package="100 mil [THT, multilayer]"]
  IS61C1024 = IC, DIP package, 32 pins [chip_label=IC]
  BANKSEL = female pin header, 3 pins [form="♀ (female)"]
  74LS74 = IC, DIP package, 14 pins [chip_label=IC]
  C6 = Ceramic Capacitor [capacitance=100nF package="100 mil [THT, multilayer]"]
  C7 = Ceramic Capacitor [capacitance=100nF package="100 mil [THT, multilayer]"]
  b2ram = female pin header, 1 pin [form="♀ (female)"]
  CLK = female pin header, 1 pin [form="♀ (female)"]
  ram2b = female pin header, 1 pin [form="♀ (female)"]
  CLK1 = female pin header, 1 pin [form="♀ (female)"]
  ram2b1 = female pin header, 1 pin [form="♀ (female)"]
  b2ram1 = female pin header, 1 pin [form="♀ (female)"]
  R1 = Resistor [tolerance=±5% resistance=220 package="1206 [SMD]"]
  C8 = Ceramic Capacitor [capacitance=100nF package="100 mil [THT, multilayer]"]
  R2 = Resistor [tolerance=±5% resistance=220 package="1206 [SMD]"]
  R3 = Resistor [tolerance=±5% resistance=220 package="1206 [SMD]"]
  R4 = Resistor [tolerance=±5% resistance=220 package="1206 [SMD]"]
  R5 = Resistor [tolerance=±5% resistance=220 package="1206 [SMD]"]
  R6 = Resistor [tolerance=±5% resistance=220 package="1206 [SMD]"]
  R7 = Resistor [tolerance=±5% resistance=220 package="1206 [SMD]"]
  R8 = Resistor [tolerance=±5% resistance=220 package="1206 [SMD]"]
  R9 = Resistor [tolerance=±5% resistance=220 package="1206 [SMD]"]

nets:
  N1: VCC.pin1, VCC.pin2, VCC.pin3, VCC.pin4, 74245.pin1, 74245.pin20, 74LS173-H.pin16, 74LS173-L.pin16, C5.0, IS61C1024.pin30, IS61C1024.pin32, BANKSEL.pin3, 74LS74.pin1, 74LS74.pin10, 74LS74.pin13, 74LS74.pin14, C6.1, C7.1, C8.1
  N2: GND.pin1, GND.pin2, GND.pin3, GND.pin4, 74245.pin10, 74LS173-H.pin8, 74LS173-H.pin15, 74LS173-L.pin8, 74LS173-L.pin15, C5.1, IS61C1024.pin16, IS61C1024.pin22, BANKSEL.pin1, 74LS74.pin7, C6.0, C7.0, C8.0
  N3: ADDR8.pin1, IS61C1024.pin5
  N4: ADDR8.pin2, IS61C1024.pin6
  N5: ADDR8.pin3, IS61C1024.pin7
  N6: ADDR8.pin4, IS61C1024.pin8
  N7: ADDR8.pin5, IS61C1024.pin9
  N8: ADDR8.pin6, IS61C1024.pin10
  N9: ADDR8.pin7, IS61C1024.pin11
  N10: ADDR8.pin8, IS61C1024.pin12
  N11: ADDR9.pin1, IS61C1024.pin31
  N12: ADDR9.pin2, IS61C1024.pin3
  N13: ADDR9.pin3, IS61C1024.pin28
  N14: ADDR9.pin4, IS61C1024.pin4
  N15: ADDR9.pin5, IS61C1024.pin25
  N16: ADDR9.pin6, IS61C1024.pin23
  N17: ADDR9.pin7, IS61C1024.pin26
  N18: ADDR9.pin8, IS61C1024.pin27
  N19: 74245.pin2, 74LS173-H.pin3, IS61C1024.pin21
  N20: 74245.pin3, 74LS173-H.pin4, IS61C1024.pin20
  N21: 74245.pin4, 74LS173-H.pin5, IS61C1024.pin19
  N22: 74245.pin5, 74LS173-H.pin6, IS61C1024.pin18
  N23: 74245.pin6, 74LS173-L.pin3, IS61C1024.pin17
  N24: 74245.pin7, 74LS173-L.pin4, IS61C1024.pin15
  N25: 74245.pin8, 74LS173-L.pin5, IS61C1024.pin14
  N26: 74245.pin9, 74LS173-L.pin6, IS61C1024.pin13
  N27: 74245.pin11, 74LS173-L.pin11, R7.Pin_0
  N28: 74245.pin12, 74LS173-L.pin12, R9.Pin_0
  N29: 74245.pin13, 74LS173-L.pin13, R8.Pin_0
  N30: 74245.pin14, 74LS173-L.pin14, R6.Pin_0
  N31: 74245.pin15, 74LS173-H.pin11, R5.Pin_0
  N32: 74245.pin16, 74LS173-H.pin12, R4.Pin_0
  N33: 74245.pin17, 74LS173-H.pin13, R3.Pin_0
  N34: 74245.pin18, 74LS173-H.pin14, R2.Pin_0
  N35: 74245.pin19, IS61C1024.pin24, ram2b.pin1, ram2b1.pin1
  N36: 74LS173-H.pin1, 74LS173-H.pin2, 74LS173-L.pin1, 74LS173-L.pin2, 74LS74.pin9
  N37: 74LS173-H.pin7, 74LS173-L.pin7, 74LS74.pin3, 74LS74.pin4, 74LS74.pin11, R1.Pin_1
  N38: 74LS173-H.pin9, 74LS173-H.pin10, 74LS173-L.pin9, 74LS173-L.pin10, 74LS74.pin2, 74LS74.pin12, b2ram.pin1, b2ram1.pin1
  N39: bus1.pin1, R2.Pin_1
  N40: bus1.pin2, R3.Pin_1
  N41: bus1.pin3, R4.Pin_1
  N42: bus1.pin4, R5.Pin_1
  N43: bus1.pin5, R6.Pin_1
  N44: bus1.pin6, R8.Pin_1
  N45: bus1.pin7, R9.Pin_1
  N46: bus1.pin8, R7.Pin_1
  N47: IS61C1024.pin2, BANKSEL.pin2
  N48: IS61C1024.pin29, 74LS74.pin5
  N49: CLK.pin1, CLK1.pin1, R1.Pin_0

notes:
  2 x 64 KB MEMORY
  Memory address input
  0
  Marius Krabset 2019
