# Fritzing sketch SP_v2-groundfill (saved by Fritzing 0.9.1b)
circuit board: 9.99cm x 6.96181cm

parts:
  VCC = female pin header, 4 pins [form="♀ (female)"]
  GND = female pin header, 4 pins [form="♀ (female)"]
  OUT-H = female pin header, 8 pins [form="♀ (female)"]
  OUT-L = female pin header, 8 pins [form="♀ (female)"]
  104 = Ceramic Capacitor [capacitance=100nF package="100 mil [THT, multilayer]"]
  104_2 = Ceramic Capacitor [capacitance=100nF package="100 mil [THT, multilayer]"]
  104_3 = Ceramic Capacitor [capacitance=100nF package="100 mil [THT, multilayer]"]
  104_4 = Ceramic Capacitor [capacitance=100nF package="100 mil [THT, multilayer]"]
  CLK = female pin header, 1 pin [form="♀ (female)"]
  CNT = female pin header, 1 pin [form="♀ (female)"]
  RES = female pin header, 1 pin [form="♀ (female)"]
  74ls169-1 = IC, DIP package, 16 pins [chip_label=IC]
  74ls169-2 = IC, DIP package, 16 pins [chip_label=IC]
  74ls169-3 = IC, DIP package, 16 pins [chip_label=IC]
  74ls169-4 = IC, DIP package, 16 pins [chip_label=IC]
  R1 = Resistor [tolerance=±5% resistance=220 package="1206 [SMD]"]
  DIR = female pin header, 1 pin [form="♀ (female)"]
  GND_2 = female pin header, 2 pins [form="♀ (female)"]
  VCC_2 = female pin header, 2 pins [form="♀ (female)"]
  GND1 = female pin header, 4 pins [form="♀ (female)"]
  VCC1 = female pin header, 4 pins [form="♀ (female)"]
  74LS245 = IC, DIP package, 20 pins [chip_label=IC]
  74LS245_2 = IC, DIP package, 20 pins [chip_label=IC]
  LEDS = IC, DIP package, 16 pins [chip_label=IC]
  LEDS_2 = IC, DIP package, 16 pins [chip_label=IC]
  R2 = Resistor [tolerance=±5% resistance=220 package="1206 [SMD]"]
  R3 = Resistor [tolerance=±5% resistance=220 package="1206 [SMD]"]
  R4 = Resistor [tolerance=±5% resistance=220 package="1206 [SMD]"]
  R5 = Resistor [tolerance=±5% resistance=220 package="1206 [SMD]"]
  R6 = Resistor [tolerance=±5% resistance=220 package="1206 [SMD]"]
  R7 = Resistor [tolerance=±5% resistance=220 package="1206 [SMD]"]
  R8 = Resistor [tolerance=±5% resistance=220 package="1206 [SMD]"]
  R9 = Resistor [tolerance=±5% resistance=220 package="1206 [SMD]"]
  R10 = Resistor [tolerance=±5% resistance=220 package="1206 [SMD]"]
  R11 = Resistor [tolerance=±5% resistance=220 package="1206 [SMD]"]
  R13 = Resistor [tolerance=±5% resistance=220 package="1206 [SMD]"]
  R14 = Resistor [tolerance=±5% resistance=220 package="1206 [SMD]"]
  R15 = Resistor [tolerance=±5% resistance=220 package="1206 [SMD]"]
  R16 = Resistor [tolerance=±5% resistance=220 package="1206 [SMD]"]
  R17 = Resistor [tolerance=±5% resistance=220 package="1206 [SMD]"]
  R18 = Resistor [tolerance=±5% resistance=220 package="1206 [SMD]"]

nets:
  N1: VCC.pin1, VCC.pin2, VCC.pin3, VCC.pin4, 104.0, 104_2.0, 104_3.0, 104_4.0, 74ls169-1.pin16, 74ls169-2.pin16, 74ls169-3.pin16, 74ls169-4.pin16, VCC_2.pin1, VCC_2.pin2, VCC1.pin1, VCC1.pin2, VCC1.pin3, VCC1.pin4, 74LS245.pin20, 74LS245_2.pin20
  N2: GND.pin1, GND.pin2, GND.pin3, GND.pin4, 104.1, 104_2.1, 104_3.1, 104_4.1, 74ls169-1.pin3, 74ls169-1.pin4, 74ls169-1.pin5, 74ls169-1.pin6, 74ls169-1.pin8, 74ls169-2.pin3, 74ls169-2.pin4, 74ls169-2.pin5, 74ls169-2.pin6, 74ls169-2.pin8, 74ls169-3.pin3, 74ls169-3.pin4, 74ls169-3.pin5, 74ls169-3.pin6, 74ls169-3.pin8, 74ls169-4.pin3, 74ls169-4.pin4, 74ls169-4.pin5, 74ls169-4.pin6, 74ls169-4.pin8, GND_2.pin1, GND_2.pin2, GND1.pin1, GND1.pin2, GND1.pin3, GND1.pin4, 74LS245.pin1, 74LS245.pin10, 74LS245.pin19, 74LS245_2.pin1, 74LS245_2.pin10, 74LS245_2.pin19, R2.Pin_0, R3.Pin_0, R4.Pin_0, R5.Pin_0, R6.Pin_0, R7.Pin_0, R8.Pin_0, R9.Pin_0, R10.Pin_0, R11.Pin_0, R13.Pin_0, R14.Pin_0, R15.Pin_0, R16.Pin_0, R17.Pin_0, R18.Pin_0
  N3: OUT-H.pin1, 74ls169-1.pin11, 74LS245.pin18
  N4: OUT-H.pin2, 74ls169-1.pin12, 74LS245.pin17
  N5: OUT-H.pin3, 74ls169-1.pin13, 74LS245.pin16
  N6: OUT-H.pin4, 74ls169-1.pin14, 74LS245.pin15
  N7: OUT-H.pin5, 74ls169-2.pin11, 74LS245.pin14
  N8: OUT-H.pin6, 74ls169-2.pin12, 74LS245.pin13
  N9: OUT-H.pin7, 74ls169-2.pin13, 74LS245.pin12
  N10: OUT-H.pin8, 74ls169-2.pin14, 74LS245.pin11
  N11: OUT-L.pin1, 74ls169-3.pin11, 74LS245_2.pin18
  N12: OUT-L.pin2, 74ls169-3.pin12, 74LS245_2.pin17
  N13: OUT-L.pin3, 74ls169-3.pin13, 74LS245_2.pin16
  N14: OUT-L.pin4, 74ls169-3.pin14, 74LS245_2.pin15
  N15: OUT-L.pin5, 74ls169-4.pin11, 74LS245_2.pin14
  N16: OUT-L.pin6, 74ls169-4.pin12, 74LS245_2.pin13
  N17: OUT-L.pin7, 74ls169-4.pin13, 74LS245_2.pin12
  N18: OUT-L.pin8, 74ls169-4.pin14, 74LS245_2.pin11
  N19: CLK.pin1, R1.Pin_0
  N20: CNT.pin1, 74ls169-4.pin7, 74ls169-4.pin10
  N21: RES.pin1, 74ls169-1.pin9, 74ls169-2.pin9, 74ls169-3.pin9, 74ls169-4.pin9
  N22: 74ls169-1.pin1, 74ls169-2.pin1, 74ls169-3.pin1, 74ls169-4.pin1, DIR.pin1
  N23: 74ls169-1.pin2, 74ls169-2.pin2, 74ls169-3.pin2, 74ls169-4.pin2, R1.Pin_1
  N24: 74ls169-1.pin7, 74ls169-1.pin10, 74ls169-2.pin15
  N25: 74ls169-2.pin7, 74ls169-2.pin10, 74ls169-3.pin15
  N26: 74ls169-3.pin7, 74ls169-3.pin10, 74ls169-4.pin15
  N27: 74LS245.pin2, LEDS.pin16
  N28: 74LS245.pin3, LEDS.pin15
  N29: 74LS245.pin4, LEDS.pin14
  N30: 74LS245.pin5, LEDS.pin13
  N31: 74LS245.pin6, LEDS.pin12
  N32: 74LS245.pin7, LEDS.pin11
  N33: 74LS245.pin8, LEDS.pin10
  N34: 74LS245.pin9, LEDS.pin9
  N35: 74LS245_2.pin2, LEDS_2.pin16
  N36: 74LS245_2.pin3, LEDS_2.pin15
  N37: 74LS245_2.pin4, LEDS_2.pin14
  N38: 74LS245_2.pin5, LEDS_2.pin13
  N39: 74LS245_2.pin6, LEDS_2.pin12
  N40: 74LS245_2.pin7, LEDS_2.pin11
  N41: 74LS245_2.pin8, LEDS_2.pin10
  N42: 74LS245_2.pin9, LEDS_2.pin9
  N43: LEDS.pin1, R2.Pin_1
  N44: LEDS.pin2, R3.Pin_1
  N45: LEDS.pin3, R4.Pin_1
  N46: LEDS.pin4, R5.Pin_1
  N47: LEDS.pin5, R6.Pin_1
  N48: LEDS.pin6, R7.Pin_1
  N49: LEDS.pin7, R8.Pin_1
  N50: LEDS.pin8, R9.Pin_1
  N51: LEDS_2.pin1, R10.Pin_1
  N52: LEDS_2.pin2, R11.Pin_1
  N53: LEDS_2.pin3, R13.Pin_1
  N54: LEDS_2.pin4, R14.Pin_1
  N55: LEDS_2.pin5, R15.Pin_1
  N56: LEDS_2.pin6, R16.Pin_1
  N57: LEDS_2.pin7, R17.Pin_1
  N58: LEDS_2.pin8, R18.Pin_1

notes:
  STACK POINTER
  Marius Krabset 2019
