# Fritzing sketch SP_v2 (saved by Fritzing 0.9.1b)
circuit board: 9.99cm x 6.96181cm

parts:
  VCC = female pin header, 4 pins [form="♀ (female)"]
  GND = female pin header, 4 pins [form="♀ (female)"]
  OUT-H = female pin header, 8 pins [form="♀ (female)"]
  OUT-L = female pin header, 8 pins [form="♀ (female)"]
  104 = Ceramic Capacitor [capacitance=100nF package="100 mil [THT, multilayer]"]
  104_2 = Ceramic Capacitor [capacitance=100nF package="100 mil [THT, multilayer]"]
  104_3 = Ceramic Capacitor [capacitance=100nF package="100 mil [THT, multilayer]"]
  104_4 = Ceramic Capacitor [capacitance=100nF package="100 mil [THT, multilayer]"]
  CLK = female pin header, 1 pin [form="♀ (female)"]
  CNT = female pin header, 1 pin [form="♀ (female)"]
  RES = female pin header, 1 pin [form="♀ (female)"]
  OUT-H_2 = female pin header, 8 pins [form="♀ (female)"]
  OUT-L_2 = female pin header, 8 pins [form="♀ (female)"]
  74ls169-1 = IC, DIP package, 16 pins [chip_label=IC]
  74ls169-2 = IC, DIP package, 16 pins [chip_label=IC]
  74ls169-3 = IC, DIP package, 16 pins [chip_label=IC]
  74ls169-4 = IC, DIP package, 16 pins [chip_label=IC]
  R1 = Resistor [tolerance=±5% resistance=220 package="1206 [SMD]"]
  DIR = female pin header, 1 pin [form="♀ (female)"]
  GND_2 = female pin header, 2 pins [form="♀ (female)"]
  VCC_2 = female pin header, 2 pins [form="♀ (female)"]
  OUT-L1 = female pin header, 8 pins [form="♀ (female)"]
  OUT-H1 = female pin header, 8 pins [form="♀ (female)"]
  GND1 = female pin header, 4 pins [form="♀ (female)"]
  VCC1 = female pin header, 4 pins [form="♀ (female)"]

nets:
  N1: VCC.pin1, VCC.pin2, VCC.pin3, VCC.pin4, 104.0, 104_2.0, 104_3.0, 104_4.0, 74ls169-1.pin16, 74ls169-2.pin16, 74ls169-3.pin16, 74ls169-4.pin16, VCC_2.pin1, VCC_2.pin2, VCC1.pin1, VCC1.pin2, VCC1.pin3, VCC1.pin4
  N2: GND.pin1, GND.pin2, GND.pin3, GND.pin4, 104.1, 104_2.1, 104_3.1, 104_4.1, 74ls169-1.pin3, 74ls169-1.pin4, 74ls169-1.pin5, 74ls169-1.pin6, 74ls169-1.pin8, 74ls169-2.pin3, 74ls169-2.pin4, 74ls169-2.pin5, 74ls169-2.pin6, 74ls169-2.pin8, 74ls169-3.pin3, 74ls169-3.pin4, 74ls169-3.pin5, 74ls169-3.pin6, 74ls169-3.pin8, 74ls169-4.pin3, 74ls169-4.pin4, 74ls169-4.pin5, 74ls169-4.pin6, 74ls169-4.pin8, GND_2.pin1, GND_2.pin2, GND1.pin1, GND1.pin2, GND1.pin3, GND1.pin4
  N3: OUT-H.pin1, OUT-H_2.pin1, 74ls169-1.pin11, OUT-H1.pin1
  N4: OUT-H.pin2, OUT-H_2.pin2, 74ls169-1.pin12, OUT-H1.pin2
  N5: OUT-H.pin3, OUT-H_2.pin3, 74ls169-1.pin13, OUT-H1.pin3
  N6: OUT-H.pin4, OUT-H_2.pin4, 74ls169-1.pin14, OUT-H1.pin4
  N7: OUT-H.pin5, OUT-H_2.pin5, 74ls169-2.pin11, OUT-H1.pin5
  N8: OUT-H.pin6, OUT-H_2.pin6, 74ls169-2.pin12, OUT-H1.pin6
  N9: OUT-H.pin7, OUT-H_2.pin7, 74ls169-2.pin13, OUT-H1.pin7
  N10: OUT-H.pin8, OUT-H_2.pin8, 74ls169-2.pin14, OUT-H1.pin8
  N11: OUT-L.pin1, OUT-L_2.pin1, 74ls169-3.pin11, OUT-L1.pin1
  N12: OUT-L.pin2, OUT-L_2.pin2, 74ls169-3.pin12, OUT-L1.pin2
  N13: OUT-L.pin3, OUT-L_2.pin3, 74ls169-3.pin13, OUT-L1.pin3
  N14: OUT-L.pin4, OUT-L_2.pin4, 74ls169-3.pin14, OUT-L1.pin4
  N15: OUT-L.pin5, OUT-L_2.pin5, 74ls169-4.pin11, OUT-L1.pin5
  N16: OUT-L.pin6, OUT-L_2.pin6, 74ls169-4.pin12, OUT-L1.pin6
  N17: OUT-L.pin7, OUT-L_2.pin7, 74ls169-4.pin13, OUT-L1.pin7
  N18: OUT-L.pin8, OUT-L_2.pin8, 74ls169-4.pin14, OUT-L1.pin8
  N19: CLK.pin1, R1.Pin_0
  N20: CNT.pin1, 74ls169-4.pin7, 74ls169-4.pin10
  N21: RES.pin1, 74ls169-1.pin9, 74ls169-2.pin9, 74ls169-3.pin9, 74ls169-4.pin9
  N22: 74ls169-1.pin1, 74ls169-2.pin1, 74ls169-3.pin1, 74ls169-4.pin1, DIR.pin1
  N23: 74ls169-1.pin2, 74ls169-2.pin2, 74ls169-3.pin2, 74ls169-4.pin2, R1.Pin_1
  N24: 74ls169-1.pin7, 74ls169-1.pin10, 74ls169-2.pin15
  N25: 74ls169-2.pin7, 74ls169-2.pin10, 74ls169-3.pin15
  N26: 74ls169-3.pin7, 74ls169-3.pin10, 74ls169-4.pin15

notes:
  STACK POINTER
  Marius Krabset 2019
