# Fritzing sketch alu-1st-floor-v2-groundfill (saved by Fritzing 0.9.1b)
circuit board: 9.99cm x 11.0207cm
breadboards: 1

parts:
  OUTPUT_B2 = female pin header, 8 pins [form="♀ (female)"]
  OUTPUT_A2 = female pin header, 8 pins [form="♀ (female)"]
  J6 = female pin header, 2 pins [form="♀ (female)"]
  J7 = female pin header, 8 pins [form="♀ (female)"]
  J8 = female pin header, 8 pins [form="♀ (female)"]
  J9 = female pin header, 2 pins [form="♀ (female)"]
  74LS283-1 = IC, DIP package, 16 pins [chip_label=IC]
  74LS283-2 = IC, DIP package, 16 pins [chip_label=IC]
  74LS157-1 = IC, DIP package, 16 pins [chip_label=IC]
  74LS157-2 = IC, DIP package, 16 pins [chip_label=IC]
  C1 = Ceramic Capacitor [capacitance=100nF package="100 mil [THT, multilayer]"]
  floor2 = female pin header, 8 pins [form="♀ (female)"]
  result = female pin header, 8 pins [form="♀ (female)"]
  C2 = Ceramic Capacitor [capacitance=100nF package="100 mil [THT, multilayer]"]
  floor = female pin header, 1 pin [form="♀ (female)"]
  OE = female pin header, 1 pin [form="♀ (female)"]
  cin = female pin header, 1 pin [form="♀ (female)"]
  op = female pin header, 2 pins [form="♀ (female)"]
  op_select1 = female pin header, 2 pins [form="♀ (female)"]
  J10 = female pin header, 2 pins [form="♀ (female)"]
  J11 = female pin header, 2 pins [form="♀ (female)"]
  AND = IC, DIP package, 14 pins [chip_label=IC]
  XOR = IC, DIP package, 14 pins [chip_label=IC]
  cout2 = female pin header, 1 pin [form="♀ (female)"]
  74LS157-3 = IC, DIP package, 16 pins [chip_label=IC]
  74LS74 = IC, DIP package, 14 pins [chip_label=IC]
  J12 = female pin header, 4 pins [form="♀ (female)"]
  AND_2 = IC, DIP package, 14 pins [chip_label=IC]
  NOT = IC, DIP package, 14 pins [chip_label=IC]
  OR = IC, DIP package, 14 pins [chip_label=IC]
  OR_2 = IC, DIP package, 14 pins [chip_label=IC]
  74LS74_2 = IC, DIP package, 14 pins [chip_label=IC]
  C3 = Ceramic Capacitor [capacitance=100nF package="100 mil [THT, multilayer]"]
  C4 = Ceramic Capacitor [capacitance=100nF package="100 mil [THT, multilayer]"]
  C5 = Ceramic Capacitor [capacitance=100nF package="100 mil [THT, multilayer]"]
  C6 = Ceramic Capacitor [capacitance=100nF package="100 mil [THT, multilayer]"]
  C7 = Ceramic Capacitor [capacitance=100nF package="100 mil [THT, multilayer]"]
  C8 = Ceramic Capacitor [capacitance=100nF package="100 mil [THT, multilayer]"]
  J13 = female pin header, 1 pin [form="♀ (female)"]
  J14 = female pin header, 1 pin [form="♀ (female)"]
  J15 = female pin header, 4 pins [form="♀ (female)"]
  J19 = female pin header, 4 pins [form="♀ (female)"]
  result1 = female pin header, 8 pins [form="♀ (female)"]
  floor3 = female pin header, 1 pin [form="♀ (female)"]

nets:
  N1: OUTPUT_B2.pin1, J8.pin1, 74LS283-1.pin11, XOR.pin10, XOR.pin12
  N2: OUTPUT_B2.pin2, J8.pin2, 74LS283-1.pin15
  N3: OUTPUT_B2.pin3, J8.pin3, 74LS283-1.pin2
  N4: OUTPUT_B2.pin4, J8.pin4, 74LS283-1.pin6
  N5: OUTPUT_B2.pin5, J8.pin5, 74LS283-2.pin11
  N6: OUTPUT_B2.pin6, J8.pin6, 74LS283-2.pin15
  N7: OUTPUT_B2.pin7, J8.pin7, 74LS283-2.pin2
  N8: OUTPUT_B2.pin8, J8.pin8, 74LS283-2.pin6
  N9: OUTPUT_A2.pin1, J7.pin1, 74LS283-1.pin12, XOR.pin13
  N10: OUTPUT_A2.pin2, J7.pin2, 74LS283-1.pin14
  N11: OUTPUT_A2.pin3, J7.pin3, 74LS283-1.pin3
  N12: OUTPUT_A2.pin4, J7.pin4, 74LS283-1.pin5
  N13: OUTPUT_A2.pin5, J7.pin5, 74LS283-2.pin12
  N14: OUTPUT_A2.pin6, J7.pin6, 74LS283-2.pin14
  N15: OUTPUT_A2.pin7, J7.pin7, 74LS283-2.pin3
  N16: OUTPUT_A2.pin8, J7.pin8, 74LS283-2.pin5
  N17: J6.pin1, J9.pin2, 74LS283-1.pin8, 74LS283-2.pin8, 74LS157-1.pin8, 74LS157-2.pin8, C1.0, C2.0, AND.pin7, XOR.pin7, 74LS157-3.pin2, 74LS157-3.pin3, 74LS157-3.pin8, 74LS157-3.pin10, 74LS157-3.pin11, 74LS157-3.pin13, 74LS157-3.pin14, 74LS157-3.pin15, 74LS74.pin7, AND_2.pin1, AND_2.pin2, AND_2.pin4, AND_2.pin5, AND_2.pin7, NOT.pin7, OR.pin7, OR_2.pin7, 74LS74_2.pin7, C3.0, C4.0, C5.0, C6.0, C7.1, C8.1, J14.pin1, J19.pin1, J19.pin2
  N18: J6.pin2, J9.pin1, 74LS283-1.pin16, 74LS283-2.pin16, 74LS157-1.pin16, 74LS157-2.pin16, C1.1, C2.1, AND.pin4, AND.pin5, AND.pin14, XOR.pin1, XOR.pin4, XOR.pin14, 74LS157-3.pin16, 74LS74.pin1, 74LS74.pin4, 74LS74.pin14, AND_2.pin12, AND_2.pin13, AND_2.pin14, NOT.pin13, NOT.pin14, OR.pin14, OR_2.pin14, 74LS74_2.pin1, 74LS74_2.pin4, 74LS74_2.pin10, 74LS74_2.pin13, 74LS74_2.pin14, C3.1, C4.1, C5.1, C6.1, C7.0, C8.0, J13.pin1, J19.pin3, J19.pin4
  N19: 74LS283-1.pin1, 74LS157-1.pin14
  N20: 74LS283-1.pin4, 74LS157-1.pin11
  N21: 74LS283-1.pin7, 74LS283-2.pin9
  N22: 74LS283-1.pin9, 74LS157-3.pin5
  N23: 74LS283-1.pin10, 74LS157-1.pin2, XOR.pin9
  N24: 74LS283-1.pin13, 74LS157-1.pin5
  N25: 74LS283-2.pin1, 74LS157-2.pin14
  N26: 74LS283-2.pin4, 74LS157-2.pin11
  N27: 74LS283-2.pin7, cin.pin1, 74LS74.pin9, J12.pin1, J15.pin1
  N28: 74LS283-2.pin10, 74LS157-2.pin2
  N29: 74LS283-2.pin13, 74LS157-2.pin5
  N30: 74LS157-1.pin1, 74LS157-2.pin1, floor.pin1, 74LS157-3.pin1, floor3.pin1
  N31: 74LS157-1.pin3, floor2.pin1
  N32: 74LS157-1.pin4, result.pin1, OR.pin9, 74LS74_2.pin2, result1.pin1
  N33: 74LS157-1.pin6, floor2.pin2
  N34: 74LS157-1.pin7, result.pin2, OR.pin10, result1.pin2
  N35: 74LS157-1.pin9, result.pin4, OR.pin12, result1.pin4
  N36: 74LS157-1.pin10, floor2.pin4
  N37: 74LS157-1.pin12, result.pin3, OR.pin13, result1.pin3
  N38: 74LS157-1.pin13, floor2.pin3
  N39: 74LS157-1.pin15, 74LS157-2.pin15, OE.pin1
  N40: 74LS157-2.pin3, floor2.pin5
  N41: 74LS157-2.pin4, result.pin5, OR.pin1, result1.pin5
  N42: 74LS157-2.pin6, floor2.pin6
  N43: 74LS157-2.pin7, result.pin6, OR.pin2, result1.pin6
  N44: 74LS157-2.pin9, result.pin8, OR_2.pin1, result1.pin8
  N45: 74LS157-2.pin10, floor2.pin8
  N46: 74LS157-2.pin12, result.pin7, OR_2.pin2, result1.pin7
  N47: 74LS157-2.pin13, floor2.pin7
  N48: op.pin1, op_select1.pin1
  N49: op.pin2, op_select1.pin2
  N50: J10.pin1, AND.pin13
  N51: J10.pin2, AND.pin9
  N52: J11.pin1, AND.pin1, AND.pin10, AND.pin12
  N53: J11.pin2, AND.pin2
  N54: AND.pin3, 74LS74.pin3, 74LS74.pin11, 74LS74_2.pin3, 74LS74_2.pin11
  N55: AND.pin8, XOR.pin5
  N56: AND.pin11, XOR.pin2
  N57: XOR.pin3, 74LS74.pin10
  N58: XOR.pin6, 74LS74.pin13
  N59: XOR.pin8, AND_2.pin10, NOT.pin3, NOT.pin11
  N60: XOR.pin11, NOT.pin9
  N61: cout2.pin1, 74LS157-3.pin6
  N62: 74LS157-3.pin7, 74LS74.pin12
  N63: 74LS74.pin2, AND_2.pin8
  N64: 74LS74.pin5, J12.pin2, J15.pin2
  N65: J12.pin3, 74LS74_2.pin9, J15.pin3
  N66: J12.pin4, 74LS74_2.pin5, J15.pin4
  N67: AND_2.pin9, NOT.pin5, NOT.pin8
  N68: NOT.pin1, OR_2.pin6
  N69: NOT.pin2, 74LS74_2.pin12
  N70: OR.pin3, OR_2.pin13
  N71: OR.pin4, OR.pin11
  N72: OR.pin5, OR.pin8
  N73: OR.pin6, OR_2.pin9
  N74: OR_2.pin3, OR_2.pin12
  N75: OR_2.pin4, OR_2.pin5, OR_2.pin8
  N76: OR_2.pin10, OR_2.pin11

notes:
  CS
  CC
  FLAGW
  CLK
  carry selector
  carry flag
  carry
  !(a7^b7)&(a7^r7)
  b7
  a7
  r7
  !(a7^b7)
  overflow flag
  (a7^r7)
  overflow
  zero flag
  zero
  neg
  neg flag
  Marius Krabset 2019
  0
