# Fritzing sketch alu-2nd-floor-v2-groundfill (saved by Fritzing 0.9.1b)
circuit board: 9.99cm x 11.0207cm
breadboards: 1

parts:
  OUTPUT_B2 = female pin header, 8 pins [form="♀ (female)"]
  OUTPUT_A2 = female pin header, 8 pins [form="♀ (female)"]
  J6 = female pin header, 2 pins [form="♀ (female)"]
  J7 = female pin header, 8 pins [form="♀ (female)"]
  J8 = female pin header, 8 pins [form="♀ (female)"]
  J9 = female pin header, 2 pins [form="♀ (female)"]
  AND = IC, DIP package, 14 pins [chip_label=IC]
  AND_2 = IC, DIP package, 14 pins [chip_label=IC]
  OR = IC, DIP package, 14 pins [chip_label=IC]
  OR_2 = IC, DIP package, 14 pins [chip_label=IC]
  XOR = IC, DIP package, 14 pins [chip_label=IC]
  XOR_2 = IC, DIP package, 14 pins [chip_label=IC]
  C1 = Ceramic Capacitor [capacitance=100nF package="100 mil [THT, multilayer]"]
  74LS153-8-7 = IC, DIP package, 16 pins [chip_label=IC]
  cout = female pin header, 1 pin [form="♀ (female)"]
  74LS153-6-5 = IC, DIP package, 16 pins [chip_label=IC]
  74LS153-4-3 = IC, DIP package, 16 pins [chip_label=IC]
  74LS153-2-1 = IC, DIP package, 16 pins [chip_label=IC]
  output = female pin header, 8 pins [form="♀ (female)"]
  C2 = Ceramic Capacitor [capacitance=100nF package="100 mil [THT, multilayer]"]
  C3 = Ceramic Capacitor [capacitance=100nF package="100 mil [THT, multilayer]"]
  op_select = female pin header, 2 pins [form="♀ (female)"]
  cin = female pin header, 1 pin [form="♀ (female)"]
  J15 = female pin header, 1 pin [form="♀ (female)"]
  J16 = female pin header, 1 pin [form="♀ (female)"]
  J17 = female pin header, 4 pins [form="♀ (female)"]  # not connected
  C4 = Ceramic Capacitor [capacitance=100nF package="100 mil [THT, multilayer]"]
  J18 = female pin header, 4 pins [form="♀ (female)"]
  result1 = female pin header, 8 pins [form="♀ (female)"]  # not connected
  floor1 = female pin header, 1 pin [form="♀ (female)"]  # not connected

nets:
  N1: OUTPUT_B2.pin1, J8.pin1, AND.pin2, OR_2.pin12, XOR.pin2, 74LS153-8-7.pin13
  N2: OUTPUT_B2.pin2, J8.pin2, AND.pin5, OR_2.pin9, XOR.pin5, 74LS153-6-5.pin3
  N3: OUTPUT_B2.pin3, J8.pin3, AND.pin12, OR_2.pin1, XOR.pin9, 74LS153-6-5.pin13
  N4: OUTPUT_B2.pin4, J8.pin4, AND.pin9, OR_2.pin4, XOR.pin12, 74LS153-4-3.pin3
  N5: OUTPUT_B2.pin5, J8.pin5, AND_2.pin2, OR.pin13, XOR_2.pin5, 74LS153-4-3.pin13
  N6: OUTPUT_B2.pin6, J8.pin6, AND_2.pin5, OR.pin10, XOR_2.pin2, 74LS153-2-1.pin3
  N7: OUTPUT_B2.pin7, J8.pin7, AND_2.pin10, OR.pin4, XOR_2.pin9, 74LS153-2-1.pin13
  N8: OUTPUT_B2.pin8, J8.pin8, AND_2.pin13, OR.pin1, XOR_2.pin12, cout.pin1
  N9: OUTPUT_A2.pin1, J7.pin1, AND.pin1, OR_2.pin13, XOR.pin1
  N10: OUTPUT_A2.pin2, J7.pin2, AND.pin4, OR_2.pin10, XOR.pin4
  N11: OUTPUT_A2.pin3, J7.pin3, AND.pin13, OR_2.pin2, XOR.pin10
  N12: OUTPUT_A2.pin4, J7.pin4, AND.pin10, OR_2.pin5, XOR.pin13
  N13: OUTPUT_A2.pin5, J7.pin5, AND_2.pin1, OR.pin12, XOR_2.pin4
  N14: OUTPUT_A2.pin6, J7.pin6, AND_2.pin4, OR.pin9, XOR_2.pin1
  N15: OUTPUT_A2.pin7, J7.pin7, AND_2.pin9, OR.pin5, XOR_2.pin10
  N16: OUTPUT_A2.pin8, J7.pin8, AND_2.pin12, OR.pin2, XOR_2.pin13
  N17: J6.pin1, J9.pin2, AND.pin7, AND_2.pin7, OR.pin7, OR_2.pin7, XOR.pin7, XOR_2.pin7, C1.0, 74LS153-8-7.pin1, 74LS153-8-7.pin8, 74LS153-8-7.pin15, 74LS153-6-5.pin1, 74LS153-6-5.pin8, 74LS153-6-5.pin15, 74LS153-4-3.pin1, 74LS153-4-3.pin8, 74LS153-4-3.pin15, 74LS153-2-1.pin1, 74LS153-2-1.pin8, 74LS153-2-1.pin15, C2.0, C3.0, J16.pin1, C4.0, J18.pin1, J18.pin2
  N18: J6.pin2, J9.pin1, AND.pin14, AND_2.pin14, OR.pin14, OR_2.pin14, XOR.pin14, XOR_2.pin14, C1.1, 74LS153-8-7.pin16, 74LS153-6-5.pin16, 74LS153-4-3.pin16, 74LS153-2-1.pin16, C2.1, C3.1, J15.pin1, C4.1, J18.pin3, J18.pin4
  N19: AND.pin3, 74LS153-8-7.pin6
  N20: AND.pin6, 74LS153-8-7.pin10
  N21: AND.pin8, 74LS153-6-5.pin10
  N22: AND.pin11, 74LS153-6-5.pin6
  N23: AND_2.pin3, 74LS153-4-3.pin6
  N24: AND_2.pin6, 74LS153-4-3.pin10
  N25: AND_2.pin8, 74LS153-2-1.pin6
  N26: AND_2.pin11, 74LS153-2-1.pin10
  N27: OR.pin3, 74LS153-2-1.pin11
  N28: OR.pin6, 74LS153-2-1.pin5
  N29: OR.pin8, 74LS153-4-3.pin11
  N30: OR.pin11, 74LS153-4-3.pin5
  N31: OR_2.pin3, 74LS153-6-5.pin5
  N32: OR_2.pin6, 74LS153-6-5.pin11
  N33: OR_2.pin8, 74LS153-8-7.pin11
  N34: OR_2.pin11, 74LS153-8-7.pin5
  N35: XOR.pin3, 74LS153-8-7.pin4
  N36: XOR.pin6, 74LS153-8-7.pin12
  N37: XOR.pin8, 74LS153-6-5.pin4
  N38: XOR.pin11, 74LS153-6-5.pin12
  N39: XOR_2.pin3, 74LS153-4-3.pin12
  N40: XOR_2.pin6, 74LS153-4-3.pin4
  N41: XOR_2.pin8, 74LS153-2-1.pin4
  N42: XOR_2.pin11, 74LS153-2-1.pin12
  N43: 74LS153-8-7.pin2, 74LS153-6-5.pin2, 74LS153-4-3.pin2, 74LS153-2-1.pin2, op_select.pin2
  N44: 74LS153-8-7.pin3, cin.pin1
  N45: 74LS153-8-7.pin7, output.pin1
  N46: 74LS153-8-7.pin9, output.pin2
  N47: 74LS153-8-7.pin14, 74LS153-6-5.pin14, 74LS153-4-3.pin14, 74LS153-2-1.pin14, op_select.pin1
  N48: 74LS153-6-5.pin7, output.pin3
  N49: 74LS153-6-5.pin9, output.pin4
  N50: 74LS153-4-3.pin7, output.pin5
  N51: 74LS153-4-3.pin9, output.pin6
  N52: 74LS153-2-1.pin7, output.pin7
  N53: 74LS153-2-1.pin9, output.pin8

notes:
  Marius Krabset 2019
