# Fritzing sketch alu-2nd-floor-v2 (saved by Fritzing 0.9.1b)
circuit board: 9.99cm x 9.98483cm
breadboards: 1

parts:
  OUTPUT_B2 = female pin header, 8 pins [form="♀ (female)"]
  OUTPUT_A2 = female pin header, 8 pins [form="♀ (female)"]
  J6 = female pin header, 2 pins [form="♀ (female)"]
  J7 = female pin header, 8 pins [form="♀ (female)"]
  J8 = female pin header, 8 pins [form="♀ (female)"]
  J9 = female pin header, 2 pins [form="♀ (female)"]
  AND = IC, DIP package, 14 pins [chip_label=IC]
  AND_2 = IC, DIP package, 14 pins [chip_label=IC]
  OR = IC, DIP package, 14 pins [chip_label=IC]
  OR_2 = IC, DIP package, 14 pins [chip_label=IC]
  XOR = IC, DIP package, 14 pins [chip_label=IC]
  XOR_2 = IC, DIP package, 14 pins [chip_label=IC]
  C1 = Ceramic Capacitor [capacitance=100nF package="100 mil [THT, multilayer]"]
  74LS153 = IC, DIP package, 16 pins [chip_label=IC]  # not connected

nets:
  N1: OUTPUT_B2.pin1, J8.pin1, AND.pin2, OR_2.pin12, XOR.pin2
  N2: OUTPUT_B2.pin2, J8.pin2, AND.pin5, OR_2.pin9, XOR.pin5
  N3: OUTPUT_B2.pin3, J8.pin3, AND.pin12, OR_2.pin1, XOR.pin9
  N4: OUTPUT_B2.pin4, J8.pin4, AND.pin9, OR_2.pin4, XOR.pin12
  N5: OUTPUT_B2.pin5, J8.pin5, AND_2.pin2, OR.pin13, XOR_2.pin5
  N6: OUTPUT_B2.pin6, J8.pin6, AND_2.pin5, OR.pin10, XOR_2.pin2
  N7: OUTPUT_B2.pin7, J8.pin7, AND_2.pin10, OR.pin4, XOR_2.pin9
  N8: OUTPUT_B2.pin8, J8.pin8, AND_2.pin13, OR.pin1, XOR_2.pin12
  N9: OUTPUT_A2.pin1, J7.pin1, AND.pin1, OR_2.pin13, XOR.pin1
  N10: OUTPUT_A2.pin2, J7.pin2, AND.pin4, OR_2.pin10, XOR.pin4
  N11: OUTPUT_A2.pin3, J7.pin3, AND.pin13, OR_2.pin2, XOR.pin10
  N12: OUTPUT_A2.pin4, J7.pin4, AND.pin10, OR_2.pin5, XOR.pin13
  N13: OUTPUT_A2.pin5, J7.pin5, AND_2.pin1, OR.pin12, XOR_2.pin4
  N14: OUTPUT_A2.pin6, J7.pin6, AND_2.pin4, OR.pin9, XOR_2.pin1
  N15: OUTPUT_A2.pin7, J7.pin7, AND_2.pin9, OR.pin5, XOR_2.pin10
  N16: OUTPUT_A2.pin8, J7.pin8, AND_2.pin12, OR.pin2, XOR_2.pin13
  N17: J6.pin1, J9.pin2, AND.pin7, AND_2.pin7, OR.pin7, OR_2.pin7, XOR.pin7, XOR_2.pin7, C1.0
  N18: J6.pin2, J9.pin1, AND.pin14, AND_2.pin14, OR.pin14, OR_2.pin14, XOR.pin14, XOR_2.pin14, C1.1
