# Fritzing sketch alu-3nd-floor-display-v2-groundfill (saved by Fritzing 0.9.1b)
circuit board: 9.99cm x 11.0207cm
breadboards: 1

parts:
  OUTPUT_B2 = female pin header, 8 pins [form="♀ (female)"]
  OUTPUT_A2 = female pin header, 8 pins [form="♀ (female)"]
  J6 = female pin header, 2 pins [form="♀ (female)"]
  J7 = female pin header, 8 pins [form="♀ (female)"]
  J8 = female pin header, 8 pins [form="♀ (female)"]
  J9 = female pin header, 2 pins [form="♀ (female)"]
  cout = female pin header, 1 pin [form="♀ (female)"]
  J15 = female pin header, 1 pin [form="♀ (female)"]
  J16 = female pin header, 1 pin [form="♀ (female)"]
  J18 = female pin header, 4 pins [form="♀ (female)"]
  result1 = female pin header, 8 pins [form="♀ (female)"]
  op1 = female pin header, 2 pins [form="♀ (female)"]
  J21 = female pin header, 4 pins [form="♀ (female)"]
  74LS245 = IC, DIP package, 20 pins [chip_label=IC]
  floor1 = female pin header, 1 pin [form="♀ (female)"]
  74LS245_2 = IC, DIP package, 20 pins [chip_label=IC]
  LEDBAR = IC, DIP package, 16 pins [chip_label=IC]
  R1 = Resistor [tolerance=±5% resistance=220 package="1206 [SMD]"]
  R2 = Resistor [tolerance=±5% resistance=220 package="1206 [SMD]"]
  R3 = Resistor [tolerance=±5% resistance=220 package="1206 [SMD]"]
  R4 = Resistor [tolerance=±5% resistance=220 package="1206 [SMD]"]
  R5 = Resistor [tolerance=±5% resistance=220 package="1206 [SMD]"]
  R6 = Resistor [tolerance=±5% resistance=220 package="1206 [SMD]"]
  R7 = Resistor [tolerance=±5% resistance=220 package="1206 [SMD]"]
  R8 = Resistor [tolerance=±5% resistance=220 package="1206 [SMD]"]
  LEDBAR_2 = IC, DIP package, 16 pins [chip_label=IC]
  R9 = Resistor [tolerance=±5% resistance=220 package="1206 [SMD]"]
  R10 = Resistor [tolerance=±5% resistance=220 package="1206 [SMD]"]
  R11 = Resistor [tolerance=±5% resistance=220 package="1206 [SMD]"]
  R12 = Resistor [tolerance=±5% resistance=220 package="1206 [SMD]"]
  R13 = Resistor [tolerance=±5% resistance=220 package="1206 [SMD]"]
  R14 = Resistor [tolerance=±5% resistance=220 package="1206 [SMD]"]
  R15 = Resistor [tolerance=±5% resistance=220 package="1206 [SMD]"]
  R16 = Resistor [tolerance=±5% resistance=220 package="1206 [SMD]"]
  74LS245_3 = IC, DIP package, 20 pins [chip_label=IC]
  LEDBAR1 = IC, DIP package, 16 pins [chip_label=IC]
  R17 = Resistor [tolerance=±5% resistance=220 package="1206 [SMD]"]
  R18 = Resistor [tolerance=±5% resistance=220 package="1206 [SMD]"]
  R19 = Resistor [tolerance=±5% resistance=220 package="1206 [SMD]"]
  R20 = Resistor [tolerance=±5% resistance=220 package="1206 [SMD]"]
  R21 = Resistor [tolerance=±5% resistance=220 package="1206 [SMD]"]
  R22 = Resistor [tolerance=±5% resistance=220 package="1206 [SMD]"]
  R23 = Resistor [tolerance=±5% resistance=220 package="1206 [SMD]"]
  R24 = Resistor [tolerance=±5% resistance=220 package="1206 [SMD]"]
  74LS245_4 = IC, DIP package, 20 pins [chip_label=IC]
  LEDBAR_3 = IC, DIP package, 16 pins [chip_label=IC]
  R25 = Resistor [tolerance=±5% resistance=220 package="1206 [SMD]"]
  R26 = Resistor [tolerance=±5% resistance=220 package="1206 [SMD]"]
  R27 = Resistor [tolerance=±5% resistance=220 package="1206 [SMD]"]
  R28 = Resistor [tolerance=±5% resistance=220 package="1206 [SMD]"]
  R29 = Resistor [tolerance=±5% resistance=220 package="1206 [SMD]"]
  R30 = Resistor [tolerance=±5% resistance=220 package="1206 [SMD]"]
  R31 = Resistor [tolerance=±5% resistance=220 package="1206 [SMD]"]
  R32 = Resistor [tolerance=±5% resistance=220 package="1206 [SMD]"]
  C1 = Electrolytic Capacitor [capacitance=1µF package="100 mil [THT, electrolytic]"]

nets:
  N1: OUTPUT_B2.pin1, J8.pin1, 74LS245_2.pin18
  N2: OUTPUT_B2.pin2, J8.pin2, 74LS245_2.pin17
  N3: OUTPUT_B2.pin3, J8.pin3, 74LS245_2.pin16
  N4: OUTPUT_B2.pin4, J8.pin4, 74LS245_2.pin15
  N5: OUTPUT_B2.pin5, J8.pin5, 74LS245_2.pin14
  N6: OUTPUT_B2.pin6, J8.pin6, 74LS245_2.pin13
  N7: OUTPUT_B2.pin7, J8.pin7, 74LS245_2.pin12
  N8: OUTPUT_B2.pin8, J8.pin8, 74LS245_2.pin11
  N9: OUTPUT_A2.pin1, J7.pin1, 74LS245.pin18
  N10: OUTPUT_A2.pin2, J7.pin2, 74LS245.pin17
  N11: OUTPUT_A2.pin3, J7.pin3, 74LS245.pin16
  N12: OUTPUT_A2.pin4, J7.pin4, 74LS245.pin15
  N13: OUTPUT_A2.pin5, J7.pin5, 74LS245.pin14
  N14: OUTPUT_A2.pin6, J7.pin6, 74LS245.pin13
  N15: OUTPUT_A2.pin7, J7.pin7, 74LS245.pin12
  N16: OUTPUT_A2.pin8, J7.pin8, 74LS245.pin11
  N17: J6.pin1, J9.pin2, J16.pin1, J18.pin1, J18.pin2, 74LS245.pin1, 74LS245.pin10, 74LS245.pin19, 74LS245_2.pin1, 74LS245_2.pin10, 74LS245_2.pin19, R1.Pin_1, R2.Pin_1, R3.Pin_1, R4.Pin_1, R5.Pin_1, R6.Pin_1, R7.Pin_1, R8.Pin_1, R9.Pin_1, R10.Pin_1, R11.Pin_1, R12.Pin_1, R13.Pin_1, R14.Pin_1, R15.Pin_1, R16.Pin_1, 74LS245_3.pin10, 74LS245_3.pin19, R17.Pin_1, R18.Pin_1, R19.Pin_1, R20.Pin_1, R21.Pin_1, R22.Pin_1, R23.Pin_1, R24.Pin_1, 74LS245_4.pin1, 74LS245_4.pin10, 74LS245_4.pin19, R25.Pin_1, R26.Pin_1, R27.Pin_1, R28.Pin_1, R29.Pin_1, R30.Pin_1, R31.Pin_1, R32.Pin_1, C1.-
  N18: J6.pin2, J9.pin1, J15.pin1, J18.pin3, J18.pin4, 74LS245.pin20, 74LS245_2.pin20, 74LS245_3.pin1, 74LS245_3.pin20, 74LS245_4.pin20, C1.+
  N19: cout.pin1, 74LS245_4.pin11
  N20: result1.pin1, 74LS245_3.pin2
  N21: result1.pin2, 74LS245_3.pin3
  N22: result1.pin3, 74LS245_3.pin4
  N23: result1.pin4, 74LS245_3.pin5
  N24: result1.pin5, 74LS245_3.pin6
  N25: result1.pin6, 74LS245_3.pin7
  N26: result1.pin7, 74LS245_3.pin8
  N27: result1.pin8, 74LS245_3.pin9
  N28: op1.pin1, 74LS245_4.pin16
  N29: op1.pin2, 74LS245_4.pin17
  N30: J21.pin1, 74LS245_4.pin12
  N31: J21.pin2, 74LS245_4.pin13
  N32: J21.pin3, 74LS245_4.pin14
  N33: J21.pin4, 74LS245_4.pin15
  N34: 74LS245.pin2, LEDBAR.pin16
  N35: 74LS245.pin3, LEDBAR.pin15
  N36: 74LS245.pin4, LEDBAR.pin14
  N37: 74LS245.pin5, LEDBAR.pin13
  N38: 74LS245.pin6, LEDBAR.pin12
  N39: 74LS245.pin7, LEDBAR.pin11
  N40: 74LS245.pin8, LEDBAR.pin10
  N41: 74LS245.pin9, LEDBAR.pin9
  N42: floor1.pin1, 74LS245_4.pin18
  N43: 74LS245_2.pin2, LEDBAR_2.pin16
  N44: 74LS245_2.pin3, LEDBAR_2.pin15
  N45: 74LS245_2.pin4, LEDBAR_2.pin14
  N46: 74LS245_2.pin5, LEDBAR_2.pin13
  N47: 74LS245_2.pin6, LEDBAR_2.pin12
  N48: 74LS245_2.pin7, LEDBAR_2.pin11
  N49: 74LS245_2.pin8, LEDBAR_2.pin10
  N50: 74LS245_2.pin9, LEDBAR_2.pin9
  N51: LEDBAR.pin1, R1.Pin_0
  N52: LEDBAR.pin2, R2.Pin_0
  N53: LEDBAR.pin3, R3.Pin_0
  N54: LEDBAR.pin4, R4.Pin_0
  N55: LEDBAR.pin5, R5.Pin_0
  N56: LEDBAR.pin6, R6.Pin_0
  N57: LEDBAR.pin7, R7.Pin_0
  N58: LEDBAR.pin8, R8.Pin_0
  N59: LEDBAR_2.pin1, R9.Pin_0
  N60: LEDBAR_2.pin2, R10.Pin_0
  N61: LEDBAR_2.pin3, R16.Pin_0
  N62: LEDBAR_2.pin4, R14.Pin_0
  N63: LEDBAR_2.pin5, R11.Pin_0
  N64: LEDBAR_2.pin6, R13.Pin_0
  N65: LEDBAR_2.pin7, R15.Pin_0
  N66: LEDBAR_2.pin8, R12.Pin_0
  N67: 74LS245_3.pin11, LEDBAR1.pin16
  N68: 74LS245_3.pin12, LEDBAR1.pin15
  N69: 74LS245_3.pin13, LEDBAR1.pin14
  N70: 74LS245_3.pin14, LEDBAR1.pin13
  N71: 74LS245_3.pin15, LEDBAR1.pin12
  N72: 74LS245_3.pin16, LEDBAR1.pin11
  N73: 74LS245_3.pin17, LEDBAR1.pin10
  N74: 74LS245_3.pin18, LEDBAR1.pin9
  N75: LEDBAR1.pin1, R17.Pin_0
  N76: LEDBAR1.pin2, R18.Pin_0
  N77: LEDBAR1.pin3, R24.Pin_0
  N78: LEDBAR1.pin4, R23.Pin_0
  N79: LEDBAR1.pin5, R20.Pin_0
  N80: LEDBAR1.pin6, R22.Pin_0
  N81: LEDBAR1.pin7, R19.Pin_0
  N82: LEDBAR1.pin8, R21.Pin_0
  N83: 74LS245_4.pin2, LEDBAR_3.pin16
  N84: 74LS245_4.pin3, LEDBAR_3.pin15
  N85: 74LS245_4.pin4, LEDBAR_3.pin14
  N86: 74LS245_4.pin5, LEDBAR_3.pin13
  N87: 74LS245_4.pin6, LEDBAR_3.pin12
  N88: 74LS245_4.pin7, LEDBAR_3.pin11
  N89: 74LS245_4.pin8, LEDBAR_3.pin10
  N90: 74LS245_4.pin9, LEDBAR_3.pin9
  N91: LEDBAR_3.pin1, R26.Pin_0
  N92: LEDBAR_3.pin2, R28.Pin_0
  N93: LEDBAR_3.pin3, R27.Pin_0
  N94: LEDBAR_3.pin4, R31.Pin_0
  N95: LEDBAR_3.pin5, R25.Pin_0
  N96: LEDBAR_3.pin6, R29.Pin_0
  N97: LEDBAR_3.pin7, R30.Pin_0
  N98: LEDBAR_3.pin8, R32.Pin_0

notes:
  Marius Krabset 2019
  Operand A
  Operand B
  Result
  carry out
  carry in
  overflow
  zero
  negative
  op 1
  op 2
  logic/ROR
  ALU
  +
  -
