# Fritzing sketch alu-3nd-floor-display-v2 (saved by Fritzing 0.9.1b)
circuit board: 9.99cm x 11.0207cm
breadboards: 1

parts:
  OUTPUT_B2 = female pin header, 8 pins [form="♀ (female)"]
  OUTPUT_A2 = female pin header, 8 pins [form="♀ (female)"]
  J6 = female pin header, 2 pins [form="♀ (female)"]
  J7 = female pin header, 8 pins [form="♀ (female)"]
  J8 = female pin header, 8 pins [form="♀ (female)"]
  J9 = female pin header, 2 pins [form="♀ (female)"]
  cout = female pin header, 1 pin [form="♀ (female)"]  # not connected
  cin = female pin header, 1 pin [form="♀ (female)"]  # not connected
  J15 = female pin header, 1 pin [form="♀ (female)"]
  J16 = female pin header, 1 pin [form="♀ (female)"]
  J18 = female pin header, 4 pins [form="♀ (female)"]
  result1 = female pin header, 8 pins [form="♀ (female)"]  # not connected
  op1 = female pin header, 2 pins [form="♀ (female)"]  # not connected
  J21 = female pin header, 4 pins [form="♀ (female)"]  # not connected
  IC1 = IC, DIP package, 20 pins [chip_label=IC]  # not connected
  floor1 = female pin header, 1 pin [form="♀ (female)"]  # not connected

nets:
  N1: OUTPUT_B2.pin1, J8.pin1
  N2: OUTPUT_B2.pin2, J8.pin2
  N3: OUTPUT_B2.pin3, J8.pin3
  N4: OUTPUT_B2.pin4, J8.pin4
  N5: OUTPUT_B2.pin5, J8.pin5
  N6: OUTPUT_B2.pin6, J8.pin6
  N7: OUTPUT_B2.pin7, J8.pin7
  N8: OUTPUT_B2.pin8, J8.pin8
  N9: OUTPUT_A2.pin1, J7.pin1
  N10: OUTPUT_A2.pin2, J7.pin2
  N11: OUTPUT_A2.pin3, J7.pin3
  N12: OUTPUT_A2.pin4, J7.pin4
  N13: OUTPUT_A2.pin5, J7.pin5
  N14: OUTPUT_A2.pin6, J7.pin6
  N15: OUTPUT_A2.pin7, J7.pin7
  N16: OUTPUT_A2.pin8, J7.pin8
  N17: J6.pin1, J9.pin2, J16.pin1
  N18: J6.pin2, J9.pin1, J15.pin1
  N19: J18.pin1, J18.pin2
  N20: J18.pin3, J18.pin4

notes:
  Marius Krabset 2019
