# Fritzing sketch alu_old_groundfloor (saved by Fritzing 0.9.3b)
circuit board: 11.4387cm x 10.1232cm
breadboards: 1

parts:
  op4 = female pin header, 1 pin [form="♀ (female)"]
  op5 = female pin header, 1 pin [form="♀ (female)"]
  op7 = female pin header, 1 pin [form="♀ (female)"]
  nonzero1 = female pin header, 1 pin [form="♀ (female)"]  # not connected
  carry_out1 = female pin header, 1 pin [form="♀ (female)"]
  carry_in = female pin header, 1 pin [form="♀ (female)"]
  input_b2 = female pin header, 8 pins [form="♀ (female)"]
  input_b = female pin header, 8 pins [form="♀ (female)"]
  input_a2 = female pin header, 8 pins [form="♀ (female)"]
  input_a = female pin header, 8 pins [form="♀ (female)"]
  output1 = female pin header, 8 pins [form="♀ (female)"]
  power3 = female pin header, 2 pins [form="♀ (female)"]
  alu_write = female alternating pin header, 1 pin [form="♀ (female)"]
  alu2bus1 = female pin header, 8 pins [form="♀ (female)"]
  power4 = female pin header, 2 pins [form="♀ (female)"]
  C4 = Ceramic Capacitor [capacitance=100nF package="100 mil [THT, multilayer]"]
  J2 = female pin header, 2 pins [form="♀ (female)"]
  IC2 = IC, DIP package, 20 pins [chip_label=IC]
  C2 = Ceramic Capacitor [capacitance=100nF package="100 mil [THT, multilayer]"]
  74LS32_(OR) = IC, DIP package, 14 pins [chip_label=IC]
  C5 = Ceramic Capacitor [capacitance=100nF package="100 mil [THT, multilayer]"]
  74LS32_(OR)_2 = IC, DIP package, 14 pins [chip_label=IC]
  7408_(AND) = IC, DIP package, 14 pins [chip_label=IC]
  7404_(NOT) = IC, DIP package, 14 pins [chip_label=IC]
  7408_(AND)_2 = IC, DIP package, 14 pins [chip_label=IC]
  C6 = Ceramic Capacitor [capacitance=100nF package="100 mil [THT, multilayer]"]
  J3 = female pin header, 2 pins [form="♀ (female)"]
  74LS74_(FF) = IC, DIP package, 14 pins [chip_label=IC]
  J4 = female pin header, 2 pins [form="♀ (female)"]
  J5 = female pin header, 2 pins [form="♀ (female)"]
  74LS74_(FF)_2 = IC, DIP package, 14 pins [chip_label=IC]
  J6 = female pin header, 2 pins [form="♀ (female)"]
  J7 = female pin header, 3 pins [form="♀ (female)"]

nets:
  N1: op4.pin1, J7.pin3
  N2: op5.pin1, J7.pin2
  N3: op7.pin1, J7.pin1
  N4: carry_out1.pin1, 74LS74_(FF)_2.pin2
  N5: carry_in.pin1, J5.pin1, 74LS74_(FF)_2.pin5
  N6: input_b2.pin1, input_b.pin1, 7408_(AND).pin12, 7404_(NOT).pin11
  N7: input_b2.pin2, input_b.pin2
  N8: input_b2.pin3, input_b.pin3
  N9: input_b2.pin4, input_b.pin4
  N10: input_b2.pin5, input_b.pin5
  N11: input_b2.pin6, input_b.pin6
  N12: input_b2.pin7, input_b.pin7
  N13: input_b2.pin8, input_b.pin8
  N14: input_a2.pin1, input_a.pin1, 7408_(AND).pin13, 7404_(NOT).pin13
  N15: input_a2.pin2, input_a.pin2
  N16: input_a2.pin3, input_a.pin3
  N17: input_a2.pin4, input_a.pin4
  N18: input_a2.pin5, input_a.pin5
  N19: input_a2.pin6, input_a.pin6
  N20: input_a2.pin7, input_a.pin7
  N21: input_a2.pin8, input_a.pin8
  N22: output1.pin1, IC2.pin11, 74LS32_(OR).pin9, 7408_(AND).pin5, 7404_(NOT).pin1, 74LS74_(FF)_2.pin12
  N23: output1.pin2, IC2.pin12, 74LS32_(OR).pin10
  N24: output1.pin3, IC2.pin13, 74LS32_(OR).pin12
  N25: output1.pin4, IC2.pin14, 74LS32_(OR).pin13
  N26: output1.pin5, IC2.pin15, 74LS32_(OR).pin1
  N27: output1.pin6, IC2.pin16, 74LS32_(OR).pin2
  N28: output1.pin7, IC2.pin17, 74LS32_(OR).pin4
  N29: output1.pin8, IC2.pin18, 74LS32_(OR).pin5
  N30: power3.pin1, power4.pin1, C4.0, J2.pin1, IC2.pin20, C2.0, 74LS32_(OR).pin14, C5.1, 74LS32_(OR)_2.pin14, 7408_(AND).pin14, 7404_(NOT).pin14, 7408_(AND)_2.pin12, 7408_(AND)_2.pin13, 7408_(AND)_2.pin14, C6.1, 74LS74_(FF).pin1, 74LS74_(FF).pin4, 74LS74_(FF).pin10, 74LS74_(FF).pin13, 74LS74_(FF).pin14, 74LS74_(FF)_2.pin10, 74LS74_(FF)_2.pin13, 74LS74_(FF)_2.pin14
  N31: power3.pin2, power4.pin2, C4.1, J2.pin2, IC2.pin1, IC2.pin10, C2.1, 74LS32_(OR).pin7, C5.0, 74LS32_(OR)_2.pin7, 7408_(AND).pin7, 7404_(NOT).pin7, 7408_(AND)_2.pin7, C6.0, 74LS74_(FF).pin7, 74LS74_(FF)_2.pin7
  N32: alu_write.pin1, IC2.pin19
  N33: alu2bus1.pin1, IC2.pin2
  N34: alu2bus1.pin2, IC2.pin3
  N35: alu2bus1.pin3, IC2.pin4
  N36: alu2bus1.pin4, IC2.pin5
  N37: alu2bus1.pin5, IC2.pin6
  N38: alu2bus1.pin6, IC2.pin7
  N39: alu2bus1.pin7, IC2.pin8
  N40: alu2bus1.pin8, IC2.pin9
  N41: 74LS32_(OR).pin3, 74LS32_(OR)_2.pin9
  N42: 74LS32_(OR).pin6, 74LS32_(OR)_2.pin10
  N43: 74LS32_(OR).pin8, 74LS32_(OR)_2.pin13
  N44: 74LS32_(OR).pin11, 74LS32_(OR)_2.pin12
  N45: 74LS32_(OR)_2.pin1, 7408_(AND).pin8
  N46: 74LS32_(OR)_2.pin2, 7408_(AND).pin6
  N47: 74LS32_(OR)_2.pin3, 74LS74_(FF).pin2
  N48: 74LS32_(OR)_2.pin4, 74LS32_(OR)_2.pin11
  N49: 74LS32_(OR)_2.pin5, 74LS32_(OR)_2.pin8
  N50: 74LS32_(OR)_2.pin6, 7404_(NOT).pin9
  N51: 7408_(AND).pin1, 7404_(NOT).pin10
  N52: 7408_(AND).pin2, 7404_(NOT).pin12
  N53: 7408_(AND).pin3, 7408_(AND).pin4
  N54: 7408_(AND).pin9, 7404_(NOT).pin2
  N55: 7408_(AND).pin10, 7408_(AND).pin11
  N56: 7404_(NOT).pin3, 7408_(AND)_2.pin3
  N57: 7404_(NOT).pin4, 74LS74_(FF)_2.pin1
  N58: 7404_(NOT).pin5, 7408_(AND)_2.pin8
  N59: 7404_(NOT).pin6, 74LS74_(FF)_2.pin4
  N60: 7404_(NOT).pin8, 74LS74_(FF).pin12
  N61: 7408_(AND)_2.pin1, J6.pin2
  N62: 7408_(AND)_2.pin2, 7408_(AND)_2.pin4, 7408_(AND)_2.pin9, J3.pin1
  N63: 7408_(AND)_2.pin5, J3.pin2
  N64: 7408_(AND)_2.pin6, 74LS74_(FF).pin3, 74LS74_(FF).pin11, 74LS74_(FF)_2.pin3, 74LS74_(FF)_2.pin11
  N65: 7408_(AND)_2.pin10, J6.pin1
  N66: 74LS74_(FF).pin5, J5.pin2
  N67: 74LS74_(FF).pin9, J4.pin1
  N68: J4.pin2, 74LS74_(FF)_2.pin9

notes:
  zero
  carry
  ovf
  CLK
  FLAGW
  CC
  CS
  owerflow
  neg
  lsb
