# Fritzing sketch aluregs_v2-groundfill (saved by Fritzing 0.9.1b)
circuit board: 9.99cm x 7.52526cm
breadboards: 1

parts:
  BUS = female pin header, 8 pins [form="♀ (female)"]
  74LS173-1 = IC, DIP package, 16 pins [chip_label=IC]
  74LS173-2 = IC, DIP package, 16 pins [chip_label=IC]
  74LS173-4 = IC, DIP package, 16 pins [chip_label=IC]
  74LS173-3 = IC, DIP package, 16 pins [chip_label=IC]
  CLK = female pin header, 1 pin [form="♀ (female)"]
  RESET-A = female pin header, 1 pin [form="♀ (female)"]
  LOAD-A = female pin header, 1 pin [form="♀ (female)"]
  LOAD-B = female pin header, 1 pin [form="♀ (female)"]
  RESET-B = female pin header, 1 pin [form="♀ (female)"]
  A = female pin header, 8 pins [form="♀ (female)"]
  B = female pin header, 8 pins [form="♀ (female)"]
  74LS86 = IC, DIP package, 14 pins [chip_label=IC]
  74LS86_2 = IC, DIP package, 14 pins [chip_label=IC]
  INVERT-B = female pin header, 1 pin [form="♀ (female)"]
  C2 = Ceramic Capacitor [capacitance=100nF package="100 mil [THT, multilayer]"]
  J5 = female pin header, 2 pins [form="♀ (female)"]
  J6 = female pin header, 2 pins [form="♀ (female)"]
  J7 = female pin header, 1 pin [form="♀ (female)"]
  J8 = female pin header, 1 pin [form="♀ (female)"]
  CLK_2 = female pin header, 1 pin [form="♀ (female)"]
  CLK2 = female pin header, 1 pin [form="♀ (female)"]
  OUTPUT_B1 = female pin header, 8 pins [form="♀ (female)"]
  OUTPUT_A1 = female pin header, 8 pins [form="♀ (female)"]
  C3 = Ceramic Capacitor [capacitance=100nF package="100 mil [THT, multilayer]"]
  R1 = Resistor [tolerance=±5% resistance=220 package="1206 [SMD]"]

nets:
  N1: BUS.pin1, 74LS173-2.pin11, 74LS173-4.pin11
  N2: BUS.pin2, 74LS173-2.pin12, 74LS173-4.pin12
  N3: BUS.pin3, 74LS173-2.pin13, 74LS173-4.pin13
  N4: BUS.pin4, 74LS173-2.pin14, 74LS173-4.pin14
  N5: BUS.pin5, 74LS173-1.pin11, 74LS173-3.pin11
  N6: BUS.pin6, 74LS173-1.pin12, 74LS173-3.pin12
  N7: BUS.pin7, 74LS173-1.pin13, 74LS173-3.pin13
  N8: BUS.pin8, 74LS173-1.pin14, 74LS173-3.pin14
  N9: 74LS173-1.pin1, 74LS173-1.pin2, 74LS173-1.pin8, 74LS173-2.pin1, 74LS173-2.pin2, 74LS173-2.pin8, 74LS173-4.pin1, 74LS173-4.pin2, 74LS173-4.pin8, 74LS173-3.pin1, 74LS173-3.pin2, 74LS173-3.pin8, 74LS86.pin7, 74LS86_2.pin7, C2.0, J5.pin1, J6.pin2, J8.pin1, C3.0
  N10: 74LS173-1.pin3, A.pin1, OUTPUT_A1.pin1
  N11: 74LS173-1.pin4, A.pin2, OUTPUT_A1.pin2
  N12: 74LS173-1.pin5, A.pin3, OUTPUT_A1.pin3
  N13: 74LS173-1.pin6, A.pin4, OUTPUT_A1.pin4
  N14: 74LS173-1.pin7, 74LS173-2.pin7, 74LS173-4.pin7, 74LS173-3.pin7, R1.Pin_1
  N15: 74LS173-1.pin9, 74LS173-1.pin10, 74LS173-2.pin9, 74LS173-2.pin10, LOAD-A.pin1
  N16: 74LS173-1.pin15, 74LS173-2.pin15, RESET-A.pin1
  N17: 74LS173-1.pin16, 74LS173-2.pin16, 74LS173-4.pin16, 74LS173-3.pin16, 74LS86.pin14, 74LS86_2.pin14, C2.1, J5.pin2, J6.pin1, J7.pin1, C3.1
  N18: 74LS173-2.pin3, A.pin5, OUTPUT_A1.pin5
  N19: 74LS173-2.pin4, A.pin6, OUTPUT_A1.pin6
  N20: 74LS173-2.pin5, A.pin7, OUTPUT_A1.pin7
  N21: 74LS173-2.pin6, A.pin8, OUTPUT_A1.pin8
  N22: 74LS173-4.pin3, 74LS86_2.pin12
  N23: 74LS173-4.pin4, 74LS86_2.pin9
  N24: 74LS173-4.pin5, 74LS86_2.pin1
  N25: 74LS173-4.pin6, 74LS86_2.pin5
  N26: 74LS173-4.pin9, 74LS173-4.pin10, 74LS173-3.pin9, 74LS173-3.pin10, LOAD-B.pin1
  N27: 74LS173-4.pin15, 74LS173-3.pin15, RESET-B.pin1
  N28: 74LS173-3.pin3, 74LS86.pin12
  N29: 74LS173-3.pin4, 74LS86.pin9
  N30: 74LS173-3.pin5, 74LS86.pin1
  N31: 74LS173-3.pin6, 74LS86.pin5
  N32: CLK.pin1, CLK_2.pin1, CLK2.pin1, R1.Pin_0
  N33: B.pin1, 74LS86.pin11, OUTPUT_B1.pin1
  N34: B.pin2, 74LS86.pin8, OUTPUT_B1.pin2
  N35: B.pin3, 74LS86.pin3, OUTPUT_B1.pin3
  N36: B.pin4, 74LS86.pin6, OUTPUT_B1.pin4
  N37: B.pin5, 74LS86_2.pin11, OUTPUT_B1.pin5
  N38: B.pin6, 74LS86_2.pin8, OUTPUT_B1.pin6
  N39: B.pin7, 74LS86_2.pin3, OUTPUT_B1.pin7
  N40: B.pin8, 74LS86_2.pin6, OUTPUT_B1.pin8
  N41: 74LS86.pin2, 74LS86.pin4, 74LS86.pin10, 74LS86.pin13, 74LS86_2.pin2, 74LS86_2.pin4, 74LS86_2.pin10, 74LS86_2.pin13, INVERT-B.pin1

notes:
  +
  -
  0
  ALU Operand Registers
  Marius Krabset 2019
