# Fritzing sketch aluregs_v2 (saved by Fritzing 0.9.1b)
circuit board: 9.99cm x 9.99cm
breadboards: 1

parts:
  BUS = female pin header, 8 pins [form="♀ (female)"]
  74LS173_A-HIGH = IC, DIP package, 16 pins [chip_label=IC]
  74LS173_A-LOW = IC, DIP package, 16 pins [chip_label=IC]
  74LS173_B-LOW = IC, DIP package, 16 pins [chip_label=IC]
  74LS173_B-HIGH = IC, DIP package, 16 pins [chip_label=IC]
  CLK = female pin header, 1 pin [form="♀ (female)"]
  RESET-A = female pin header, 1 pin [form="♀ (female)"]
  LOAD-A = female pin header, 1 pin [form="♀ (female)"]
  LOAD-B = female pin header, 1 pin [form="♀ (female)"]
  RESET-B = female pin header, 1 pin [form="♀ (female)"]  # not connected
  OUTPUT_A = female pin header, 8 pins [form="♀ (female)"]
  OUTPUT_B = female pin header, 8 pins [form="♀ (female)"]
  74LS86 = IC, DIP package, 14 pins [chip_label=IC]
  74LS86_2 = IC, DIP package, 14 pins [chip_label=IC]
  LED17 = LED - 5mm [color="Red (633nm)" package="5 mm [THT]"]
  INVERT-B = female pin header, 1 pin [form="♀ (female)"]
  C2 = Ceramic Capacitor [capacitance=100nF package="100 mil [THT, multilayer]"]
  J5 = female pin header, 2 pins [form="♀ (female)"]
  J6 = female pin header, 2 pins [form="♀ (female)"]
  J7 = female pin header, 1 pin [form="♀ (female)"]
  J8 = female pin header, 1 pin [form="♀ (female)"]
  CLK1 = female pin header, 1 pin [form="♀ (female)"]
  CLK2 = female pin header, 1 pin [form="♀ (female)"]
  OUTPUT_B1 = female pin header, 8 pins [form="♀ (female)"]  # not connected
  OUTPUT_A1 = female pin header, 8 pins [form="♀ (female)"]  # not connected

nets:
  N1: BUS.pin1, 74LS173_A-LOW.pin11
  N2: BUS.pin2, 74LS173_A-LOW.pin12
  N3: BUS.pin3, 74LS173_A-LOW.pin13, 74LS173_B-LOW.pin13
  N4: BUS.pin4, 74LS173_A-LOW.pin14, 74LS173_B-LOW.pin14
  N5: BUS.pin5, 74LS173_A-HIGH.pin11
  N6: BUS.pin6, 74LS173_A-HIGH.pin12
  N7: BUS.pin7, 74LS173_A-HIGH.pin13
  N8: BUS.pin8, 74LS173_A-HIGH.pin14, 74LS173_B-HIGH.pin14
  N9: 74LS173_A-HIGH.pin1, 74LS173_A-HIGH.pin2, C2.0, J6.pin2, J8.pin1
  N10: 74LS173_A-HIGH.pin3, OUTPUT_A.pin1
  N11: 74LS173_A-HIGH.pin4, OUTPUT_A.pin2
  N12: 74LS173_A-HIGH.pin5, OUTPUT_A.pin3
  N13: 74LS173_A-HIGH.pin6, OUTPUT_A.pin4
  N14: 74LS173_A-HIGH.pin7, 74LS173_A-LOW.pin7, 74LS173_B-LOW.pin7, 74LS173_B-HIGH.pin7, CLK.pin1, CLK1.pin1, CLK2.pin1
  N15: 74LS173_A-HIGH.pin8, 74LS173_A-LOW.pin1, 74LS173_A-LOW.pin2, 74LS173_A-LOW.pin8, 74LS173_B-LOW.pin1, 74LS173_B-LOW.pin2, 74LS173_B-LOW.pin8, 74LS173_B-HIGH.pin1, 74LS173_B-HIGH.pin2, 74LS173_B-HIGH.pin8, 74LS86_2.pin7, J5.pin2
  N16: 74LS173_A-HIGH.pin9, 74LS173_A-HIGH.pin10, 74LS173_A-LOW.pin9, 74LS173_A-LOW.pin10, LOAD-A.pin1
  N17: 74LS173_A-HIGH.pin15, 74LS173_A-LOW.pin15, RESET-A.pin1
  N18: 74LS173_A-HIGH.pin16, 74LS173_A-LOW.pin16, 74LS173_B-LOW.pin16, 74LS173_B-HIGH.pin16, C2.1
  N19: 74LS173_A-LOW.pin3, OUTPUT_A.pin5
  N20: 74LS173_A-LOW.pin4, OUTPUT_A.pin6
  N21: 74LS173_A-LOW.pin5, OUTPUT_A.pin7
  N22: 74LS173_A-LOW.pin6, OUTPUT_A.pin8
  N23: 74LS173_B-LOW.pin9, 74LS173_B-LOW.pin10, 74LS173_B-HIGH.pin9, 74LS173_B-HIGH.pin10, LOAD-B.pin1
  N24: 74LS173_B-LOW.pin15, 74LS173_B-HIGH.pin15
  N25: OUTPUT_B.pin1, 74LS86.pin3
  N26: OUTPUT_B.pin3, 74LS86.pin8
  N27: OUTPUT_B.pin5, 74LS86_2.pin3
  N28: OUTPUT_B.pin6, 74LS86_2.pin11
  N29: OUTPUT_B.pin7, 74LS86_2.pin8
  N30: OUTPUT_B.pin8, 74LS86_2.pin6
  N31: 74LS86.pin2, 74LS86.pin4, 74LS86.pin10, 74LS86.pin13, 74LS86_2.pin2, 74LS86_2.pin4, 74LS86_2.pin10, 74LS86_2.pin13, LED17.anode, INVERT-B.pin1
  N32: 74LS86.pin14, 74LS86_2.pin14, J5.pin1
  N33: J6.pin1, J7.pin1

notes:
  VCC
  GND
