# Fritzing sketch bushat (saved by Fritzing 0.9.1b)
circuit board: 9.88943cm x 3.36494cm
breadboards: 1

parts:
  J16 = female pin header, 8 pins [form="♀ (female)"]
  GND = female pin header, 2 pins [form="♀ (female)"]
  VCC = female pin header, 2 pins [form="♀ (female)"]
  74LS245 = IC, DIP package, 20 pins [chip_label=IC]
  Z_OE = female pin header, 2 pins [form="♀ (female)"]
  74LS245_2 = IC, DIP package, 20 pins [chip_label=IC]
  LEDBAR = IC, DIP package, 16 pins [chip_label=IC]
  R1 = Resistor [tolerance=±5% resistance=220 package="1206 [SMD]"]
  R2 = Resistor [tolerance=±5% resistance=220 package="1206 [SMD]"]
  R3 = Resistor [tolerance=±5% resistance=220 package="1206 [SMD]"]
  R4 = Resistor [tolerance=±5% resistance=220 package="1206 [SMD]"]
  R5 = Resistor [tolerance=±5% resistance=220 package="1206 [SMD]"]
  R6 = Resistor [tolerance=±5% resistance=220 package="1206 [SMD]"]
  R7 = Resistor [tolerance=±5% resistance=220 package="1206 [SMD]"]
  R8 = Resistor [tolerance=±5% resistance=220 package="1206 [SMD]"]
  C1 = Electrolytic Capacitor [capacitance=1µF package="100 mil [THT, electrolytic]"]

nets:
  N1: J16.pin1, 74LS245.pin18, 74LS245_2.pin11
  N2: J16.pin2, 74LS245.pin17, 74LS245_2.pin12
  N3: J16.pin3, 74LS245.pin16, 74LS245_2.pin13
  N4: J16.pin4, 74LS245.pin15, 74LS245_2.pin14
  N5: J16.pin5, 74LS245.pin14, 74LS245_2.pin15
  N6: J16.pin6, 74LS245.pin13, 74LS245_2.pin16
  N7: J16.pin7, 74LS245.pin12, 74LS245_2.pin17
  N8: J16.pin8, 74LS245.pin11, 74LS245_2.pin18
  N9: GND.pin1, GND.pin2, 74LS245.pin2, 74LS245.pin3, 74LS245.pin4, 74LS245.pin5, 74LS245.pin6, 74LS245.pin7, 74LS245.pin8, 74LS245.pin9, 74LS245.pin10, 74LS245_2.pin1, 74LS245_2.pin10, 74LS245_2.pin19, R1.Pin_0, R2.Pin_0, R3.Pin_0, R4.Pin_0, R5.Pin_0, R6.Pin_0, R7.Pin_0, R8.Pin_0, C1.-
  N10: VCC.pin1, VCC.pin2, 74LS245.pin1, 74LS245.pin20, 74LS245_2.pin20, C1.+
  N11: 74LS245.pin19, Z_OE.pin1, Z_OE.pin2
  N12: 74LS245_2.pin2, LEDBAR.pin16
  N13: 74LS245_2.pin3, LEDBAR.pin15
  N14: 74LS245_2.pin4, LEDBAR.pin14
  N15: 74LS245_2.pin5, LEDBAR.pin13
  N16: 74LS245_2.pin6, LEDBAR.pin12
  N17: 74LS245_2.pin7, LEDBAR.pin11
  N18: 74LS245_2.pin8, LEDBAR.pin10
  N19: 74LS245_2.pin9, LEDBAR.pin9
  N20: LEDBAR.pin1, R1.Pin_1
  N21: LEDBAR.pin2, R2.Pin_1
  N22: LEDBAR.pin3, R3.Pin_1
  N23: LEDBAR.pin4, R4.Pin_1
  N24: LEDBAR.pin5, R5.Pin_1
  N25: LEDBAR.pin6, R6.Pin_1
  N26: LEDBAR.pin7, R7.Pin_1
  N27: LEDBAR.pin8, R8.Pin_1

notes:
  7 6 5 4 3 2 1 0
