# Fritzing sketch clock (saved by Fritzing 0.9.1b)
circuit board: 9.111cm x 9.30244cm
breadboards: 1

parts:
  power = female pin header, 2 pins [form="♀ (female)"]
  555 = 555 Timer [package="DIP8 [THT]"]
  C1 = Ceramic Capacitor [capacitance=100nF package="100 mil [THT, multilayer]"]
  C2 = Electrolytic Capacitor [capacitance=1µF package="100 mil [THT, electrolytic]"]
  C3 = Ceramic Capacitor [capacitance=100nF package="100 mil [THT, multilayer]"]
  555_2 = 555 Timer [package="DIP8 [THT]"]
  manual = Pushbutton [package="[THT]"]
  C4 = Ceramic Capacitor [capacitance=100nF package="100 mil [THT, multilayer]"]
  C5 = Electrolytic Capacitor [capacitance=1µF package="100 mil [THT, electrolytic]"]
  555_3 = 555 Timer [package="DIP8 [THT]"]
  speed_sel3 = Toggle Switch [package=THT]
  clock_select = Toggle Switch [package=THT]  # not connected
  C6 = Ceramic Capacitor [capacitance=100nF package="100 mil [THT, multilayer]"]
  74LS157 = IC, DIP package, 16 pins [chip_label=IC]
  C7 = Ceramic Capacitor [capacitance=100nF package="100 mil [THT, multilayer]"]
  HLT = female pin header, 1 pin [form="♀ (female)"]
  LED1 = LED - 5mm [color="Red (633nm)" package="5 mm [THT]"]
  R1 = Resistor [tolerance=±5% resistance=680 package=THT]
  R6 = Resistor [tolerance=±5% resistance=220 package=THT]
  R2 = Resistor [tolerance=±5% resistance=1k package=THT]
  R3 = Resistor [tolerance=±5% resistance=20k package=THT]
  R4 = Resistor [tolerance=±5% resistance=10k package=THT]
  R5 = Resistor [tolerance=±5% resistance=10k package=THT]
  R7 = Resistor [tolerance=±5% resistance=10k package=THT]
  J2 = female pin header, 2 pins [form="♀ (female)"]
  J3 = female pin header, 2 pins [form="♀ (female)"]
  R8 = Resistor [tolerance=±5% resistance=1k package=THT]
  instruction = female pin header, 8 pins [form="♀ (female)"]
  step = female pin header, 4 pins [form="♀ (female)"]  # not connected
  GND = female pin header, 1 pin [form="♀ (female)"]  # not connected
  CLK = female pin header, 1 pin [form="♀ (female)"]  # not connected
  SELECT = female pin header, 1 pin [form="♀ (female)"]  # not connected
  BUS = female pin header, 8 pins [form="♀ (female)"]
  instruction1 = female pin header, 8 pins [form="♀ (female)"]
  step1 = female pin header, 4 pins [form="♀ (female)"]  # not connected
  GND1 = female pin header, 1 pin [form="♀ (female)"]  # not connected
  CLK1 = female pin header, 1 pin [form="♀ (female)"]  # not connected
  SELECT1 = female pin header, 1 pin [form="♀ (female)"]  # not connected
  BUS1 = female pin header, 8 pins [form="♀ (female)"]

nets:
  N1: power.pin1, 555.Reset, 555.Vcc_Supply_Voltage, 555_2.Reset, 555_2.Vcc_Supply_Voltage, 555_3.Vcc_Supply_Voltage, 74LS157.pin16, C7.0, R1.Pin_1, R2.Pin_0, R3.Pin_1, R4.Pin_0, R5.Pin_0
  N2: power.pin2, 555.Ground, C1.1, C2.-, C3.0, 555_2.Ground, manual.Pin_3, manual.Pin_4, C4.1, C5.-, 555_3.Ground, 555_3.Threshold, speed_sel3.L1, C6.1, 74LS157.pin8, C7.1, R6.Pin_0, R7.Pin_1
  N3: 555.Trigger, 555.Threshold, J2.pin1, J2.pin2
  N4: 555.Output, 74LS157.pin14
  N5: 555.Control_Voltage, C1.0
  N6: 555.Discharge, R1.Pin_0, R8.Pin_1
  N7: C2.+, J3.pin2
  N8: C3.1, J3.pin1
  N9: 555_2.Trigger, manual.Pin_1, manual.Pin_2, R2.Pin_1
  N10: 555_2.Output, 74LS157.pin13
  N11: 555_2.Control_Voltage, C4.0
  N12: 555_2.Threshold, 555_2.Discharge, C5.+, R3.Pin_0
  N13: 555_3.Trigger, speed_sel3.COM, R4.Pin_1
  N14: 555_3.Output, 74LS157.pin1
  N15: 555_3.Reset, speed_sel3.L2, R5.Pin_1
  N16: 555_3.Control_Voltage, C6.0
  N17: 74LS157.pin12, LED1.anode
  N18: 74LS157.pin15, HLT.pin1, R7.Pin_0
  N19: LED1.cathode, R6.Pin_1
  N20: instruction.pin1, instruction1.pin1
  N21: instruction.pin2, instruction1.pin2
  N22: instruction.pin3, instruction1.pin3
  N23: instruction.pin4, instruction1.pin4
  N24: instruction.pin5, instruction1.pin5
  N25: instruction.pin6, instruction1.pin6
  N26: instruction.pin7, instruction1.pin7
  N27: instruction.pin8, instruction1.pin8
  N28: BUS.pin1, BUS1.pin1
  N29: BUS.pin2, BUS1.pin2
  N30: BUS.pin3, BUS1.pin3
  N31: BUS.pin4, BUS1.pin4
  N32: BUS.pin5, BUS1.pin5
  N33: BUS.pin6, BUS1.pin6
  N34: BUS.pin7, BUS1.pin7
  N35: BUS.pin8, BUS1.pin8
