# Fritzing sketch clockadapter (saved by Fritzing 0.9.1b)
circuit board: 3.60629cm x 9.597cm
breadboards: 1

parts:
  STEP = female pin header, 4 pins [form="♀ (female)"]
  GND = female pin header, 1 pin [form="♀ (female)"]
  CLK = female pin header, 1 pin [form="♀ (female)"]
  SEL = female pin header, 1 pin [form="♀ (female)"]
  BUS = female pin header, 8 pins [form="♀ (female)"]
  step1 = female pin header, 4 pins [form="♀ (female)"]
  GND1 = female pin header, 1 pin [form="♀ (female)"]
  CLK1 = female pin header, 1 pin [form="♀ (female)"]
  SELECT1 = female pin header, 1 pin [form="♀ (female)"]
  BUS1 = female pin header, 8 pins [form="♀ (female)"]
  INSTRUCTION = female pin header, 8 pins [form="♀ (female)"]
  BUS3 = female pin header, 8 pins [form="♀ (female)"]
  J1 = female pin header, 6 pins [form="♀ (female)"]
  GND_2 = female pin header, 1 pin [form="♀ (female)"]
  5V = female pin header, 1 pin [form="♀ (female)"]
  74LS257 = IC, DIP package, 16 pins [chip_label=IC]
  speed_sel4 = Toggle Switch [package=THT]  # not connected
  SRC_SEL = Toggle Switch [package=THT]
  R1 = Resistor [tolerance=±5% resistance=220 package="1206 [SMD]"]

nets:
  N1: STEP.pin1, step1.pin1
  N2: STEP.pin2, step1.pin2
  N3: STEP.pin3, step1.pin3
  N4: STEP.pin4, step1.pin4
  N5: GND.pin1, GND1.pin1, GND_2.pin1, 74LS257.pin8, 74LS257.pin15, R1.Pin_0
  N6: CLK.pin1, 74LS257.pin5
  N7: SEL.pin1, 74LS257.pin2
  N8: BUS.pin1, BUS1.pin1
  N9: BUS.pin2, BUS1.pin2
  N10: BUS.pin3, BUS1.pin3
  N11: BUS.pin4, BUS1.pin4
  N12: BUS.pin5, BUS1.pin5
  N13: BUS.pin6, BUS1.pin6
  N14: BUS.pin7, BUS1.pin7
  N15: BUS.pin8, BUS1.pin8
  N16: CLK1.pin1, 74LS257.pin7
  N17: SELECT1.pin1, 74LS257.pin4
  N18: INSTRUCTION.pin1, BUS3.pin1
  N19: INSTRUCTION.pin2, BUS3.pin2
  N20: INSTRUCTION.pin3, BUS3.pin3
  N21: INSTRUCTION.pin4, BUS3.pin4
  N22: INSTRUCTION.pin5, BUS3.pin5
  N23: INSTRUCTION.pin6, BUS3.pin6
  N24: INSTRUCTION.pin7, BUS3.pin7
  N25: INSTRUCTION.pin8, BUS3.pin8
  N26: J1.pin1, J1.pin2, J1.pin3, J1.pin4, J1.pin5, J1.pin6, 74LS257.pin6
  N27: 5V.pin1, 74LS257.pin3, 74LS257.pin16, SRC_SEL.L2
  N28: 74LS257.pin1, SRC_SEL.L1
  N29: SRC_SEL.COM, R1.Pin_1
