# Fritzing sketch crystalclock (saved by Fritzing 0.9.1b)
circuit board: 12.2564cm x 5.49691cm
breadboards: 1

parts:
  XTAL = female pin header, 1 pin [form="♀ (female)"]
  RESET = female pin header, 1 pin [form="♀ (female)"]
  J6 = female pin header, 4 pins [form="♀ (female)"]
  J7 = female pin header, 4 pins [form="♀ (female)"]
  OUTPUT = female pin header, 1 pin [form="♀ (female)"]
  74LS169 = IC, DIP package, 16 pins [chip_label=IC]
  74LS14 = IC, DIP package, 14 pins [chip_label=IC]
  C4 = Ceramic Capacitor [capacitance=100nF package="100 mil [THT, multilayer]"]
  J8 = female pin header, 1 pin [form="♀ (female)"]
  J9 = female pin header, 1 pin [form="♀ (female)"]
  C5 = Ceramic Capacitor [capacitance=100nF package="100 mil [THT, multilayer]"]
  R1 = Resistor [tolerance=±5% resistance=14k package=THT]
  R2 = Resistor [tolerance=±5% resistance=14k package=THT]
  5161AS = 7 Segment Display
  R5 = Resistor [tolerance=±5% resistance=220 package="1206 [SMD]"]
  R6 = Resistor [tolerance=±5% resistance=220 package="1206 [SMD]"]
  R7 = Resistor [tolerance=±5% resistance=220 package="1206 [SMD]"]
  R9 = Resistor [tolerance=±5% resistance=220 package="1206 [SMD]"]
  MC14495 = IC, DIP package, 16 pins [chip_label=IC]
  R4 = Resistor [tolerance=±5% resistance=220 package="1206 [SMD]"]
  R3 = Resistor [tolerance=±5% resistance=220 package="1206 [SMD]"]
  R10 = Resistor [tolerance=±5% resistance=220 package="1206 [SMD]"]
  AND = IC, DIP package, 14 pins [chip_label=IC]
  speed_sel6 = Toggle Switch [package=THT]
  SEL = Toggle Switch [package=THT]  # not connected
  speed_sel7 = Toggle Switch [package=THT]
  ONOFF = Toggle Switch [package=THT]  # not connected
  C7 = Ceramic Capacitor [capacitance=100nF package="100 mil [THT, multilayer]"]
  R12 = Resistor [tolerance=±5% resistance=220 package="1206 [SMD]"]
  halt = female pin header, 2 pins [form="♀ (female)"]
  OR = IC, DIP package, 14 pins [chip_label=IC]
  CLK_OUT = female pin header, 2 pins [form="♀ (female)"]
  C9 = Ceramic Capacitor [capacitance=100nF package="100 mil [THT, multilayer]"]
  C10 = Ceramic Capacitor [capacitance=100nF package="100 mil [THT, multilayer]"]
  LED1 = LED - 5mm [color="Red (633nm)" package="5 mm [THT]"]
  R14 = Resistor [tolerance=±5% resistance=1k package="1206 [SMD]"]
  VCC = female pin header, 2 pins [form="♀ (female)"]
  GND = female pin header, 2 pins [form="♀ (female)"]
  C11 = Electrolytic Capacitor [capacitance=1µF package="100 mil [THT, electrolytic]"]
  R15 = Resistor [tolerance=±5% resistance=10k package=THT]
  C12 = Ceramic Capacitor [capacitance=100nF package="100 mil [THT, multilayer]"]
  J11 = female pin header, 3 pins [form="♀ (female)"]
  C13 = Ceramic Capacitor [capacitance=100nF package="100 mil [THT, multilayer]"]
  C14 = Ceramic Capacitor [capacitance=100nF package="100 mil [THT, multilayer]"]
  RESET1 = female pin header, 1 pin [form="♀ (female)"]
  J12 = female pin header, 4 pins [form="♀ (female)"]
  J16 = female pin header, 1 pin [form="♀ (female)"]
  J17 = female pin header, 1 pin [form="♀ (female)"]
  J18 = female pin header, 1 pin [form="♀ (female)"]
  J19 = female pin header, 1 pin [form="♀ (female)"]

nets:
  N1: XTAL.pin1, speed_sel6.COM, J17.pin1
  N2: RESET.pin1, RESET1.pin1
  N3: J6.pin1, J6.pin2, 74LS169.pin3, 74LS169.pin4, 74LS169.pin5, 74LS169.pin6, 74LS169.pin7, 74LS169.pin8, 74LS169.pin10, 74LS14.pin3, 74LS14.pin5, 74LS14.pin7, C4.0, J9.pin1, C5.1, 5161AS.common_anode, MC14495.pin7, MC14495.pin8, MC14495.pin11, AND.pin7, speed_sel7.COM, C7.1, OR.pin5, OR.pin7, OR.pin9, OR.pin10, C9.0, C10.0, R14.Pin_0, GND.pin1, GND.pin2, C11.-, C12.1, J11.pin2, C13.0, C14.0, J12.pin1, J12.pin2, J16.pin1
  N4: J6.pin3, J6.pin4, 74LS169.pin9, 74LS169.pin16, 74LS14.pin14, R1.Pin_0, R2.Pin_0, MC14495.pin16, AND.pin1, AND.pin2, AND.pin9, AND.pin10, AND.pin14, speed_sel7.L2, halt.pin1, OR.pin1, OR.pin2, OR.pin14, C9.1, C10.1, VCC.pin1, VCC.pin2, C11.+, R15.Pin_1, C13.1, C14.1, J12.pin3, J12.pin4, J18.pin1, J19.pin1
  N5: J7.pin1, 74LS169.pin11, MC14495.pin10
  N6: J7.pin2, 74LS169.pin12, MC14495.pin9
  N7: J7.pin3, 74LS169.pin13, MC14495.pin6
  N8: J7.pin4, 74LS169.pin14, MC14495.pin5
  N9: OUTPUT.pin1, speed_sel6.L2
  N10: 74LS169.pin1, 74LS14.pin10
  N11: 74LS169.pin2, 74LS14.pin8
  N12: 74LS14.pin1, J8.pin1, R15.Pin_0, C12.0
  N13: 74LS14.pin2, OR.pin12
  N14: 74LS14.pin9, C5.0, R1.Pin_1, J11.pin3
  N15: 74LS14.pin11, C4.1, R2.Pin_1, J11.pin1
  N16: 74LS14.pin12, AND.pin5
  N17: 74LS14.pin13, C7.0, R12.Pin_1
  N18: 5161AS.Segment_E, R7.Pin_0
  N19: 5161AS.Segment_D, R5.Pin_0
  N20: 5161AS.Segment_C, R6.Pin_0
  N21: 5161AS.Segment_B, R3.Pin_1
  N22: 5161AS.Segment_A, R4.Pin_1
  N23: 5161AS.Segment_F, R10.Pin_1
  N24: 5161AS.Segment_G, R9.Pin_1
  N25: R5.Pin_1, MC14495.pin15
  N26: R6.Pin_1, MC14495.pin14
  N27: R7.Pin_1, MC14495.pin1
  N28: R9.Pin_0, MC14495.pin3
  N29: MC14495.pin2, R10.Pin_0
  N30: MC14495.pin12, R4.Pin_0
  N31: MC14495.pin13, R3.Pin_0
  N32: AND.pin4, AND.pin11
  N33: AND.pin6, OR.pin13
  N34: AND.pin12, speed_sel6.L1
  N35: AND.pin13, halt.pin2
  N36: speed_sel7.L1, R12.Pin_0
  N37: OR.pin4, OR.pin11, CLK_OUT.pin1, CLK_OUT.pin2
  N38: OR.pin6, LED1.anode
  N39: LED1.cathode, R14.Pin_1

notes:
  0
  1
  2
  3
  +
  -
