# Fritzing sketch xtal-clock (saved by Fritzing 0.9.1b)
circuit board: 12.2564cm x 5.49691cm
breadboards: 1

parts:
  XTAL = female pin header, 1 pin [form="♀ (female)"]
  RESET = female pin header, 1 pin [form="♀ (female)"]
  74ls161-0 = IC, DIP package, 16 pins [chip_label=IC]
  74ls161-1 = IC, DIP package, 16 pins [chip_label=IC]
  74ls161-2 = IC, DIP package, 16 pins [chip_label=IC]
  74ls161-3 = IC, DIP package, 16 pins [chip_label=IC]
  74ls161-4 = IC, DIP package, 16 pins [chip_label=IC]
  J1 = female pin header, 4 pins [form="♀ (female)"]
  J2 = female pin header, 4 pins [form="♀ (female)"]
  J3 = female pin header, 4 pins [form="♀ (female)"]
  J4 = female pin header, 4 pins [form="♀ (female)"]
  J5 = female pin header, 4 pins [form="♀ (female)"]
  J6 = female pin header, 4 pins [form="♀ (female)"]
  74ls153-1 = IC, DIP package, 16 pins [chip_label=IC]
  74ls153-2 = IC, DIP package, 16 pins [chip_label=IC]
  74ls153-3 = IC, DIP package, 16 pins [chip_label=IC]
  J7 = female pin header, 4 pins [form="♀ (female)"]
  OUTPUT = female pin header, 1 pin [form="♀ (female)"]
  C1 = Ceramic Capacitor [capacitance=100nF package="100 mil [THT, multilayer]"]
  C2 = Ceramic Capacitor [capacitance=100nF package="100 mil [THT, multilayer]"]
  C3 = Ceramic Capacitor [capacitance=100nF package="100 mil [THT, multilayer]"]
  C4 = Ceramic Capacitor [capacitance=100nF package="100 mil [THT, multilayer]"]
  C5 = Ceramic Capacitor [capacitance=100nF package="100 mil [THT, multilayer]"]
  C6 = Ceramic Capacitor [capacitance=100nF package="100 mil [THT, multilayer]"]
  C7 = Ceramic Capacitor [capacitance=100nF package="100 mil [THT, multilayer]"]
  C8 = Electrolytic Capacitor [capacitance=1µF package="100 mil [THT, electrolytic]"]

nets:
  N1: XTAL.pin1, 74ls161-0.pin2, 74ls161-1.pin2, 74ls161-2.pin2, 74ls161-3.pin2, 74ls161-4.pin2
  N2: RESET.pin1, 74ls161-0.pin9, 74ls161-1.pin9, 74ls161-2.pin9, 74ls161-3.pin9, 74ls161-4.pin9
  N3: 74ls161-0.pin1, 74ls161-0.pin7, 74ls161-0.pin10, 74ls161-0.pin16, 74ls161-1.pin1, 74ls161-1.pin16, 74ls161-2.pin1, 74ls161-2.pin16, 74ls161-3.pin1, 74ls161-3.pin16, 74ls161-4.pin1, 74ls161-4.pin16, J6.pin3, J6.pin4, 74ls153-1.pin16, 74ls153-2.pin16, 74ls153-3.pin15, 74ls153-3.pin16, C1.0, C2.0, C3.0, C4.0, C5.0, C6.0, C7.0, C8.+
  N4: 74ls161-0.pin3, 74ls161-0.pin4, 74ls161-0.pin5, 74ls161-0.pin6, 74ls161-0.pin8, 74ls161-1.pin3, 74ls161-1.pin4, 74ls161-1.pin5, 74ls161-1.pin6, 74ls161-1.pin8, 74ls161-2.pin3, 74ls161-2.pin4, 74ls161-2.pin5, 74ls161-2.pin6, 74ls161-2.pin8, 74ls161-3.pin3, 74ls161-3.pin4, 74ls161-3.pin5, 74ls161-3.pin6, 74ls161-3.pin8, 74ls161-4.pin3, 74ls161-4.pin4, 74ls161-4.pin5, 74ls161-4.pin6, 74ls161-4.pin8, J6.pin1, J6.pin2, 74ls153-1.pin1, 74ls153-1.pin8, 74ls153-1.pin15, 74ls153-2.pin1, 74ls153-2.pin8, 74ls153-2.pin15, 74ls153-3.pin1, 74ls153-3.pin8, C1.1, C2.1, C3.1, C4.1, C5.1, C6.1, C7.1, C8.-
  N5: 74ls161-0.pin11, J5.pin1, 74ls153-2.pin10
  N6: 74ls161-0.pin12, J5.pin2, 74ls153-2.pin11
  N7: 74ls161-0.pin13, J5.pin3, 74ls153-2.pin12
  N8: 74ls161-0.pin14, J5.pin4, 74ls153-2.pin13
  N9: 74ls161-0.pin15, 74ls161-1.pin7, 74ls161-1.pin10
  N10: 74ls161-1.pin11, J4.pin1
  N11: 74ls161-1.pin12, J4.pin2, 74ls153-2.pin5
  N12: 74ls161-1.pin13, J4.pin3, 74ls153-2.pin4
  N13: 74ls161-1.pin14, J4.pin4, 74ls153-2.pin3
  N14: 74ls161-1.pin15, 74ls161-2.pin7, 74ls161-2.pin10
  N15: 74ls161-2.pin11, J3.pin1, 74ls153-1.pin13
  N16: 74ls161-2.pin12, J3.pin2
  N17: 74ls161-2.pin13, J3.pin3
  N18: 74ls161-2.pin14, J3.pin4, 74ls153-2.pin6
  N19: 74ls161-2.pin15, 74ls161-4.pin7, 74ls161-4.pin10
  N20: 74ls161-3.pin7, 74ls161-3.pin10, 74ls161-4.pin15
  N21: 74ls161-3.pin11, J1.pin1, 74ls153-1.pin6
  N22: 74ls161-3.pin12, J1.pin2, 74ls153-1.pin5
  N23: 74ls161-3.pin13, J1.pin3, 74ls153-1.pin4
  N24: 74ls161-3.pin14, J1.pin4, 74ls153-1.pin3
  N25: 74ls161-4.pin11, J2.pin1, 74ls153-1.pin10
  N26: 74ls161-4.pin12, J2.pin2, 74ls153-1.pin11
  N27: 74ls161-4.pin13, J2.pin3, 74ls153-1.pin12
  N28: 74ls161-4.pin14, J2.pin4
  N29: 74ls153-1.pin2, 74ls153-2.pin2, J7.pin3
  N30: 74ls153-1.pin7, 74ls153-3.pin6
  N31: 74ls153-1.pin9, 74ls153-3.pin5
  N32: 74ls153-1.pin14, 74ls153-2.pin14, J7.pin4
  N33: 74ls153-2.pin7, 74ls153-3.pin4
  N34: 74ls153-2.pin9, 74ls153-3.pin3
  N35: 74ls153-3.pin2, J7.pin1
  N36: 74ls153-3.pin7, OUTPUT.pin1
  N37: 74ls153-3.pin14, J7.pin2

notes:
  0
  1
  2
  3
  +
  -
  Clock prescaler
