# Fritzing sketch decoder_10x10cm (saved by Fritzing 0.9.3b)
circuit board: 9.95544cm x 9.65561cm
breadboards: 1

parts:
  J5 = female pin header, 4 pins [form="♀ (female)"]
  J6 = female pin header, 4 pins [form="♀ (female)"]
  J7 = female pin header, 4 pins [form="♀ (female)"]
  J8 = female pin header, 4 pins [form="♀ (female)"]
  J9 = female pin header, 11 pins [form="♀ (female)"]
  J10 = female pin header, 2 pins [form="♀ (female)"]
  C1 = Ceramic Capacitor [capacitance=100nF package="100 mil [THT, multilayer]"]
  J11 = female pin header, 11 pins [form="♀ (female)"]
  J12 = female pin header, 2 pins [form="♀ (female)"]
  LED1 = smd LED [color="Red (633nm)" package="1206 [SMD]"]
  R1 = Resistor [tolerance=±5% resistance=220 package="1206 [SMD]"]
  LED2 = smd LED [color="Red (633nm)" package="1206 [SMD]"]
  R2 = Resistor [tolerance=±5% resistance=220 package="1206 [SMD]"]
  LED3 = smd LED [color="Red (633nm)" package="1206 [SMD]"]
  R3 = Resistor [tolerance=±5% resistance=220 package="1206 [SMD]"]
  LED4 = smd LED [color="Red (633nm)" package="1206 [SMD]"]
  R4 = Resistor [tolerance=±5% resistance=220 package="1206 [SMD]"]
  LED5 = smd LED [color="Red (633nm)" package="1206 [SMD]"]
  R5 = Resistor [tolerance=±5% resistance=220 package="1206 [SMD]"]
  LED6 = smd LED [color="Red (633nm)" package="1206 [SMD]"]
  R6 = Resistor [tolerance=±5% resistance=220 package="1206 [SMD]"]
  LED7 = smd LED [color="Red (633nm)" package="1206 [SMD]"]
  R7 = Resistor [tolerance=±5% resistance=220 package="1206 [SMD]"]
  LED8 = smd LED [color="Red (633nm)" package="1206 [SMD]"]
  R8 = Resistor [tolerance=±5% resistance=220 package="1206 [SMD]"]
  LED9 = smd LED [color="Red (633nm)" package="1206 [SMD]"]
  R9 = Resistor [tolerance=±5% resistance=220 package="1206 [SMD]"]
  LED10 = smd LED [color="Red (633nm)" package="1206 [SMD]"]
  R10 = Resistor [tolerance=±5% resistance=220 package="1206 [SMD]"]
  LED11 = smd LED [color="Red (633nm)" package="1206 [SMD]"]
  R11 = Resistor [tolerance=±5% resistance=220 package="1206 [SMD]"]
  LED12 = smd LED [color="Red (633nm)" package="1206 [SMD]"]
  R12 = Resistor [tolerance=±5% resistance=220 package="1206 [SMD]"]
  LED13 = smd LED [color="Red (633nm)" package="1206 [SMD]"]
  R13 = Resistor [tolerance=±5% resistance=220 package="1206 [SMD]"]
  LED14 = smd LED [color="Red (633nm)" package="1206 [SMD]"]
  R14 = Resistor [tolerance=±5% resistance=220 package="1206 [SMD]"]
  LED15 = smd LED [color="Red (633nm)" package="1206 [SMD]"]
  R15 = Resistor [tolerance=±5% resistance=220 package="1206 [SMD]"]
  LED16 = smd LED [color="Red (633nm)" package="1206 [SMD]"]
  R16 = Resistor [tolerance=±5% resistance=220 package="1206 [SMD]"]
  J14 = female pin header, 12 pins [form="♀ (female)"]
  J15 = female pin header, 12 pins [form="♀ (female)"]
  J16 = female pin header, 12 pins [form="♀ (female)"]
  J17 = female pin header, 12 pins [form="♀ (female)"]
  AL = female pin header, 2 pins [form="♀ (female)"]
  AH = female pin header, 2 pins [form="♀ (female)"]
  AL_2 = female pin header, 2 pins [form="♀ (female)"]
  AH_2 = female pin header, 2 pins [form="♀ (female)"]

nets:
  N1: J5.pin1, LED16.cathode, J16.pin4
  N2: J5.pin2, LED15.cathode, J16.pin3
  N3: J5.pin3, LED14.cathode, J16.pin2
  N4: J5.pin4, LED13.cathode, J17.pin1
  N5: J6.pin1, LED5.cathode, J14.pin1
  N6: J6.pin2, LED6.cathode, J15.pin2
  N7: J6.pin3, LED7.cathode, J15.pin3
  N8: J6.pin4, LED8.cathode, J15.pin4
  N9: J7.pin1, LED12.cathode, J17.pin2
  N10: J7.pin2, LED11.cathode, J17.pin3
  N11: J7.pin3, LED10.cathode, J17.pin4
  N12: J7.pin4, LED9.cathode, J17.pin5
  N13: J8.pin1, LED1.cathode, J14.pin5
  N14: J8.pin2, LED2.cathode, J14.pin4
  N15: J8.pin3, LED3.cathode, J14.pin3
  N16: J8.pin4, LED4.cathode, J14.pin2
  N17: J9.pin1, J11.pin1, J15.pin5, J16.pin5
  N18: J9.pin2, J11.pin2, J15.pin6, J16.pin6
  N19: J9.pin3, J11.pin3, J15.pin7, J16.pin7
  N20: J9.pin4, J11.pin4, J15.pin8, J16.pin8
  N21: J9.pin5, J11.pin5, J15.pin9, J16.pin9
  N22: J9.pin6, J11.pin6, J15.pin10, J16.pin10
  N23: J9.pin7, J11.pin7, J15.pin11, J16.pin11
  N24: J9.pin8, J11.pin8, J15.pin12, J16.pin12
  N25: J9.pin9, J11.pin9, J14.pin11, J17.pin11
  N26: J9.pin10, J11.pin10, J14.pin10, J17.pin10
  N27: J9.pin11, J11.pin11, J14.pin7, J17.pin7
  N28: J10.pin1, C1.0, J12.pin1, J14.pin9, J14.pin12, J17.pin9, J17.pin12, AL.pin1, AL_2.pin1
  N29: J10.pin2, C1.1, J12.pin2, J14.pin6, J14.pin8, J15.pin1, J16.pin1, J17.pin6, J17.pin8, AH.pin1, AH_2.pin1
  N30: LED1.anode, R1.Pin_0
  N31: R1.Pin_1, R2.Pin_1, R3.Pin_1, R4.Pin_1, R5.Pin_1, R6.Pin_1, R7.Pin_1, R8.Pin_1, AL.pin2, AH.pin2
  N32: LED2.anode, R2.Pin_0
  N33: LED3.anode, R3.Pin_0
  N34: LED4.anode, R4.Pin_0
  N35: LED5.anode, R5.Pin_0
  N36: LED6.anode, R6.Pin_0
  N37: LED7.anode, R7.Pin_0
  N38: LED8.anode, R8.Pin_0
  N39: LED9.anode, R9.Pin_0
  N40: R9.Pin_1, R10.Pin_1, R11.Pin_1, R12.Pin_1, R13.Pin_1, R14.Pin_1, R15.Pin_1, R16.Pin_1, AL_2.pin2, AH_2.pin2
  N41: LED10.anode, R10.Pin_0
  N42: LED11.anode, R11.Pin_0
  N43: LED12.anode, R12.Pin_0
  N44: LED13.anode, R13.Pin_0
  N45: LED14.anode, R14.Pin_0
  N46: LED15.anode, R15.Pin_0
  N47: LED16.anode, R16.Pin_0

notes:
  +
  -
  Decoder 2x8bit
  krabz 2018
  0 1 2 3 4 5 6 7
  input
