# Fritzing sketch decoder_x3_10x10cm-groundfill (saved by Fritzing 0.9.1b)
circuit board: 9.95544cm x 7.63772cm
breadboards: 1

parts:
  J6 = female pin header, 4 pins [form="♀ (female)"]
  J8 = female pin header, 4 pins [form="♀ (female)"]
  J9 = female pin header, 11 pins [form="♀ (female)"]
  J11 = female pin header, 11 pins [form="♀ (female)"]
  J14 = female pin header, 12 pins [form="♀ (female)"]
  J15 = female pin header, 12 pins [form="♀ (female)"]
  J18 = female pin header, 2 pins [form="♀ (female)"]
  J19 = female pin header, 2 pins [form="♀ (female)"]
  J22 = female pin header, 2 pins [form="♀ (female)"]
  J23 = female pin header, 2 pins [form="♀ (female)"]
  J25 = female pin header, 4 pins [form="♀ (female)"]
  J27 = female pin header, 4 pins [form="♀ (female)"]
  J34 = female pin header, 2 pins [form="♀ (female)"]
  J35 = female pin header, 2 pins [form="♀ (female)"]
  J36 = female pin header, 2 pins [form="♀ (female)"]
  J37 = female pin header, 12 pins [form="♀ (female)"]
  J38 = female pin header, 12 pins [form="♀ (female)"]
  J39 = female pin header, 2 pins [form="♀ (female)"]
  J40 = female pin header, 2 pins [form="♀ (female)"]
  J41 = female pin header, 12 pins [form="♀ (female)"]
  J42 = female pin header, 12 pins [form="♀ (female)"]
  J43 = female pin header, 4 pins [form="♀ (female)"]
  J44 = female pin header, 4 pins [form="♀ (female)"]
  J45 = female pin header, 4 pins [form="♀ (female)"]
  J46 = female pin header, 4 pins [form="♀ (female)"]
  J47 = female pin header, 4 pins [form="♀ (female)"]
  J48 = female pin header, 4 pins [form="♀ (female)"]
  J49 = female pin header, 4 pins [form="♀ (female)"]
  J50 = female pin header, 4 pins [form="♀ (female)"]
  C1 = Ceramic Capacitor [capacitance=100nF package="100 mil [THT, multilayer]"]
  C2 = Ceramic Capacitor [capacitance=100nF package="100 mil [THT, multilayer]"]
  C3 = Ceramic Capacitor [capacitance=100nF package="100 mil [THT, multilayer]"]
  J51 = female pin header, 2 pins [form="♀ (female)"]
  J52 = female pin header, 2 pins [form="♀ (female)"]
  J53 = female pin header, 2 pins [form="♀ (female)"]

nets:
  N1: J6.pin1, J14.pin1, J25.pin1
  N2: J6.pin2, J15.pin2, J25.pin2
  N3: J6.pin3, J15.pin3, J25.pin3
  N4: J6.pin4, J15.pin4, J25.pin4
  N5: J8.pin1, J14.pin5, J27.pin1
  N6: J8.pin2, J14.pin4, J27.pin2
  N7: J8.pin3, J14.pin3, J27.pin3
  N8: J8.pin4, J14.pin2, J27.pin4
  N9: J9.pin1, J11.pin1, J15.pin5, J37.pin5, J41.pin5
  N10: J9.pin2, J11.pin2, J15.pin6, J37.pin6, J41.pin6
  N11: J9.pin3, J11.pin3, J15.pin7, J37.pin7, J41.pin7
  N12: J9.pin4, J11.pin4, J15.pin8, J37.pin8, J41.pin8
  N13: J9.pin5, J11.pin5, J15.pin9, J37.pin9, J41.pin9
  N14: J9.pin6, J11.pin6, J15.pin10, J37.pin10, J41.pin10
  N15: J9.pin7, J11.pin7, J15.pin11, J37.pin11, J41.pin11
  N16: J9.pin8, J11.pin8, J15.pin12, J37.pin12, J41.pin12
  N17: J9.pin9, J11.pin9, J14.pin11, J38.pin11, J42.pin11
  N18: J9.pin10, J11.pin10, J14.pin10, J38.pin10, J42.pin10
  N19: J9.pin11, J11.pin11, J14.pin7, J38.pin7, J42.pin7
  N20: J14.pin6, J14.pin8, J15.pin1, J34.pin2, J37.pin1, J38.pin6, J38.pin8, J41.pin1, J42.pin6, J42.pin8, C1.0, C2.0, C3.0, J51.pin2, J52.pin1, J53.pin1
  N21: J14.pin9, J22.pin1, J23.pin1, J38.pin9, J42.pin9
  N22: J18.pin1, J22.pin2, J23.pin2, J36.pin1, J40.pin1
  N23: J19.pin1, J19.pin2, J34.pin1, J35.pin1, J35.pin2, J39.pin1, J39.pin2, C1.1, C2.1, C3.1, J51.pin1, J52.pin2, J53.pin2
  N24: J37.pin2, J43.pin2, J48.pin2
  N25: J37.pin3, J43.pin3, J48.pin3
  N26: J37.pin4, J43.pin4, J48.pin4
  N27: J38.pin1, J43.pin1, J48.pin1
  N28: J38.pin2, J44.pin4, J50.pin4
  N29: J38.pin3, J44.pin3, J50.pin3
  N30: J38.pin4, J44.pin2, J50.pin2
  N31: J38.pin5, J44.pin1, J50.pin1
  N32: J41.pin2, J45.pin2, J47.pin2
  N33: J41.pin3, J45.pin3, J47.pin3
  N34: J41.pin4, J45.pin4, J47.pin4
  N35: J42.pin1, J45.pin1, J47.pin1
  N36: J42.pin2, J46.pin4, J49.pin4
  N37: J42.pin3, J46.pin3, J49.pin3
  N38: J42.pin4, J46.pin2, J49.pin2
  N39: J42.pin5, J46.pin1, J49.pin1

notes:
  +
  -
  Decoder 3x8bit
  0 1 2 3 4 5 6 7
  input
