# Fritzing sketch eepromwriter-at28c16 (saved by Fritzing 0.9.1b)
circuit board: 9.99619cm x 6.68074cm
breadboards: 1

parts:
  C1 = Ceramic Capacitor [capacitance=100nF package="100 mil [THT, multilayer]"]
  J14 = female pin header, 12 pins [form="♀ (female)"]
  J15 = female pin header, 12 pins [form="♀ (female)"]
  U1 = 74HC595 SMD [package="SO16 [SMD]"]
  U2 = 74HC595 SMD [package="SO16 [SMD]"]
  Part1 = Arduino Nano (Rev3.0)

nets:
  VCC: C1.0, J14.pin12, U1.MR, U1.VCC, U2.MR, U2.VCC, Part1.5V
  GND: C1.1, J15.pin1, U1.GND, U2.GND, Part1.GND
  N1: J14.pin1, Part1.D12/MISO
  N2: J14.pin2, Part1.D11/MOSI
  N3: J14.pin3, Part1.A0
  N4: J14.pin4, Part1.A1
  N5: J14.pin5, Part1.A2
  N6: J14.pin6, Part1.D10
  N7: J14.pin7, U2.Q2
  N8: J14.pin8, Part1.D9
  N9: J14.pin9, Part1.D8
  N10: J14.pin10, U2.Q1
  N11: J14.pin11, U2.Q0
  N12: J15.pin2, Part1.A3
  N13: J15.pin3, Part1.A4
  N14: J15.pin4, Part1.A5
  N15: J15.pin5, U1.Q0
  N16: J15.pin6, U1.Q1
  N17: J15.pin7, U1.Q2
  N18: J15.pin8, U1.Q3
  N19: J15.pin9, U1.Q4
  N20: J15.pin10, U1.Q5
  N21: J15.pin11, U1.Q6
  N22: J15.pin12, U1.Q7
  N23: U1.Q7', U2.DS
  N24: U1.SH_CP, U2.SH_CP, Part1.D3
  N25: U1.ST_CP, U2.ST_CP, Part1.D2
  N26: U1.OE, U2.OE, Part1.D5
  N27: U1.DS, Part1.D4
