# Fritzing sketch eepromwriter-generic (saved by Fritzing 0.9.1b)
circuit board: 9.83391cm x 6.66663cm
breadboards: 1

parts:
  C1 = Ceramic Capacitor [capacitance=100nF package="100 mil [THT, multilayer]"]
  J14 = female pin header, 12 pins [form="♀ (female)"]
  J15 = female pin header, 12 pins [form="♀ (female)"]
  NANO = Arduino Nano (Rev3.0)
  J16 = female pin header, 2 pins [form="♀ (female)"]
  J17 = female pin header, 2 pins [form="♀ (female)"]
  WE = female pin header, 1 pin [form="♀ (female)"]
  WE-16 = female pin header, 1 pin [form="♀ (female)"]
  WE-64 = female pin header, 1 pin [form="♀ (female)"]
  A11 = female pin header, 1 pin [form="♀ (female)"]
  A11_2 = female pin header, 1 pin [form="♀ (female)"]
  74LS595 = CD4048B [part_number=CD4048B package="DIP (Dual Inline) [THT]"]
  74LS595_2 = CD4048B [part_number=CD4048B package="DIP (Dual Inline) [THT]"]
  VCC-64 = female pin header, 1 pin [form="♀ (female)"]
  VCC-16 = female pin header, 1 pin [form="♀ (female)"]
  VCC = female pin header, 1 pin [form="♀ (female)"]
  R1 = Resistor [tolerance=±5% resistance=220 package=THT]
  LED1 = LED - 5mm [color="Red (633nm)" package="5 mm [THT]"]
  LED2 = LED - 5mm [color="Red (633nm)" package="5 mm [THT]"]
  R2 = Resistor [tolerance=±5% resistance=220 package=THT]

nets:
  VDD: C1.0, NANO.5V, 74LS595.Ka, 74LS595.VDD, 74LS595_2.Ka, 74LS595_2.VDD, VCC.pin1
  VSS: C1.1, J15.pin1, NANO.GND, 74LS595.VSS, 74LS595_2.VSS, R1.Pin_0, R2.Pin_0
  N1: J14.pin1, NANO.D12/MISO
  N2: J14.pin2, NANO.D11/MOSI
  N3: J14.pin3, NANO.A0
  N4: J14.pin4, NANO.A1
  N5: J14.pin5, NANO.A2
  N6: J14.pin6, NANO.D10
  N7: J14.pin7, 74LS595_2.Kd
  N8: J14.pin8, NANO.D9
  N9: J14.pin9, WE-16.pin1, A11_2.pin1
  N10: J14.pin10, 74LS595_2.J
  N11: J14.pin11, 74LS595_2.EXPAND
  N12: J14.pin12, VCC-16.pin1
  N13: J15.pin2, NANO.A3
  N14: J15.pin3, NANO.A4
  N15: J15.pin4, NANO.A5
  N16: J15.pin5, 74LS595.EXPAND
  N17: J15.pin6, 74LS595.J
  N18: J15.pin7, 74LS595.Kd
  N19: J15.pin8, 74LS595.H
  N20: J15.pin9, 74LS595.G
  N21: J15.pin10, 74LS595.F
  N22: J15.pin11, 74LS595.E
  N23: J15.pin12, 74LS595.Kb
  N24: NANO.D2, 74LS595.C, 74LS595_2.C
  N25: NANO.D3, 74LS595.D, 74LS595_2.D
  N26: NANO.D4, 74LS595.A
  N27: NANO.D5, 74LS595.B, 74LS595_2.B
  N28: NANO.D6, LED1.anode
  N29: NANO.D7, LED2.anode
  N30: NANO.D8, WE.pin1
  N31: J16.pin1, VCC-64.pin1
  N32: J16.pin2, WE-64.pin1
  N33: J17.pin2, 74LS595_2.G
  N34: A11.pin1, 74LS595_2.H
  N35: 74LS595.Kc, 74LS595_2.A
  N36: R1.Pin_1, LED1.cathode
  N37: LED2.cathode, R2.Pin_1

notes:
  16
  64
  GND
  NOTCH END
  EEPROM PROGRAMMER FOR AT28C16/64
  Marius Krabset 2019
  BUSY
  ERROR
