# Fritzing sketch instreg_display_v2-groundfill (saved by Fritzing 0.9.1b)
circuit board: 9.983cm x 9.98519cm
breadboards: 1

parts:
  555 = 555 Timer [package="DIP8 [THT]"]
  74LS163 = IC, DIP package, 16 pins [chip_label=IC]
  R1 = Resistor [tolerance=±5% resistance=220 package=THT]
  R2 = Resistor [tolerance=±5% resistance=220 package=THT]
  C1 = Ceramic Capacitor [capacitance=100nF package="100 mil [THT, multilayer]"]
  74LS139 = IC, DIP package, 16 pins [chip_label=IC]
  C2 = Ceramic Capacitor [capacitance=100nF package="100 mil [THT, multilayer]"]
  J47 = female pin header, 12 pins [form="♀ (female)"]
  J48 = female pin header, 12 pins [form="♀ (female)"]
  74LS157-4 = IC, DIP package, 16 pins [chip_label=IC]
  74LS157-3 = IC, DIP package, 16 pins [chip_label=IC]
  display-3 = female pin header, 6 pins [form="♀ (female)"]
  display-4 = female pin header, 6 pins [form="♀ (female)"]
  R7 = Resistor [tolerance=±5% resistance=220 package="1206 [SMD]"]
  R8 = Resistor [tolerance=±5% resistance=220 package="1206 [SMD]"]
  R9 = Resistor [tolerance=±5% resistance=220 package="1206 [SMD]"]
  R10 = Resistor [tolerance=±5% resistance=220 package="1206 [SMD]"]
  J49 = female pin header, 2 pins [form="♀ (female)"]
  J50 = female pin header, 13 pins [form="♀ (female)"]
  C3 = Electrolytic Capacitor [capacitance=1µF package="100 mil [THT, electrolytic]"]

nets:
  N1: 555.Ground, 74LS163.pin8, C1.1, 74LS139.pin1, 74LS139.pin8, C2.0, J47.pin5, J47.pin6, J47.pin7, J48.pin12, 74LS157-4.pin8, 74LS157-4.pin15, 74LS157-3.pin3, 74LS157-3.pin6, 74LS157-3.pin8, 74LS157-3.pin10, 74LS157-3.pin13, 74LS157-3.pin15, J49.pin2, C3.-
  N2: 555.Trigger, 555.Threshold, R2.Pin_0, C1.0
  N3: 555.Output, 74LS163.pin2
  N4: 555.Discharge, R1.Pin_0, R2.Pin_1
  N5: 555.Vcc_Supply_Voltage, 74LS163.pin1, 74LS163.pin7, 74LS163.pin9, 74LS163.pin10, 74LS163.pin16, R1.Pin_1, 74LS139.pin16, C2.1, J47.pin1, J47.pin3, J47.pin4, 74LS157-4.pin16, 74LS157-3.pin16, J49.pin1, C3.+
  N6: 74LS163.pin13, 74LS139.pin3, 74LS157-4.pin1, 74LS157-3.pin1
  N7: 74LS163.pin14, 74LS139.pin2, J47.pin2
  N8: 74LS139.pin4, R7.Pin_0
  N9: 74LS139.pin5, R9.Pin_0
  N10: 74LS139.pin6, R8.Pin_0
  N11: 74LS139.pin7, R10.Pin_1
  N12: J47.pin8, display-3.pin3
  N13: J47.pin9, display-3.pin5
  N14: J47.pin10, display-4.pin3
  N15: J47.pin11, display-3.pin1
  N16: J47.pin12, display-3.pin2
  N17: J48.pin1, 74LS157-3.pin9
  N18: J48.pin2, 74LS157-3.pin12
  N19: J48.pin3, 74LS157-3.pin7
  N20: J48.pin4, 74LS157-3.pin4
  N21: J48.pin5, 74LS157-4.pin9
  N22: J48.pin6, 74LS157-4.pin12
  N23: J48.pin7, 74LS157-4.pin7
  N24: J48.pin8, 74LS157-4.pin4
  N25: J48.pin9, display-4.pin2
  N26: J48.pin10, display-4.pin6
  N27: J48.pin11, display-3.pin4
  N28: 74LS157-4.pin2, J50.pin8
  N29: 74LS157-4.pin3, J50.pin12
  N30: 74LS157-4.pin5, J50.pin7
  N31: 74LS157-4.pin6, J50.pin11
  N32: 74LS157-4.pin10, J50.pin9
  N33: 74LS157-4.pin11, J50.pin5
  N34: 74LS157-4.pin13, J50.pin10
  N35: 74LS157-4.pin14, J50.pin6
  N36: 74LS157-3.pin2, J50.pin4
  N37: 74LS157-3.pin5, J50.pin3
  N38: 74LS157-3.pin11, J50.pin1
  N39: 74LS157-3.pin14, J50.pin2
  N40: display-3.pin6, R10.Pin_0
  N41: display-4.pin1, R7.Pin_1
  N42: display-4.pin4, R9.Pin_1
  N43: display-4.pin5, R8.Pin_1

notes:
  INSTR | STEP
  Marius Krabset 2019
  Instruction Register
