# Fritzing sketch instreg_v2-groundfill (saved by Fritzing 0.9.1b)
circuit board: 9.98519cm x 9.983cm
breadboards: 1

parts:
  J31 = female pin header, 2 pins [form="♀ (female)"]
  J32 = female pin header, 11 pins [form="♀ (female)"]
  J33 = female pin header, 2 pins [form="♀ (female)"]
  instruction = female pin header, 8 pins [form="♀ (female)"]
  step = female pin header, 4 pins [form="♀ (female)"]
  SELECT = female pin header, 1 pin [form="♀ (female)"]
  CLK = female pin header, 1 pin [form="♀ (female)"]
  GND = female pin header, 1 pin [form="♀ (female)"]
  74173-1 = IC, DIP package, 16 pins [chip_label=IC]
  BUS = female pin header, 8 pins [form="♀ (female)"]
  74173-2 = IC, DIP package, 16 pins [chip_label=IC]
  BUS_2 = female pin header, 8 pins [form="♀ (female)"]
  cont = female pin header, 1 pin [form="♀ (female)"]
  74163 = IC, DIP package, 16 pins [chip_label=IC]
  load = female pin header, 1 pin [form="♀ (female)"]
  J34 = female pin header, 2 pins [form="♀ (female)"]
  J35 = female pin header, 11 pins [form="♀ (female)"]
  J36 = female pin header, 2 pins [form="♀ (female)"]
  C1 = Ceramic Capacitor [capacitance=100nF package="100 mil [THT, multilayer]"]
  C2 = Ceramic Capacitor [capacitance=100nF package="100 mil [THT, multilayer]"]
  NOT = IC, DIP package, 14 pins [chip_label=IC]
  CLK_2 = female pin header, 6 pins [form="♀ (female)"]
  J37 = female pin header, 4 pins [form="♀ (female)"]
  J38 = female pin header, 4 pins [form="♀ (female)"]
  74LS157-1 = IC, DIP package, 16 pins [chip_label=IC]
  74LS157-2 = IC, DIP package, 16 pins [chip_label=IC]
  74LS157-3 = IC, DIP package, 16 pins [chip_label=IC]
  C3 = Ceramic Capacitor [capacitance=100nF package="100 mil [THT, multilayer]"]
  C4 = Ceramic Capacitor [capacitance=100nF package="100 mil [THT, multilayer]"]
  C5 = Ceramic Capacitor [capacitance=100nF package="100 mil [THT, multilayer]"]
  J39 = female pin header, 3 pins [form="♀ (female)"]
  J40 = female pin header, 3 pins [form="♀ (female)"]
  R1 = Resistor [tolerance=±5% resistance=220 package="1206 [SMD]"]
  R2 = Resistor [tolerance=±5% resistance=220 package="1206 [SMD]"]
  A12 = female pin header, 3 pins [form="♀ (female)"]
  invclk = female pin header, 1 pin [form="♀ (female)"]

nets:
  N1: J31.pin1, J34.pin1, 74LS157-3.pin9
  N2: J31.pin2, J34.pin2, A12.pin2
  N3: J32.pin1, J35.pin1, 74LS157-1.pin4
  N4: J32.pin2, J35.pin2, 74LS157-1.pin7
  N5: J32.pin3, J35.pin3, 74LS157-1.pin12
  N6: J32.pin4, J35.pin4, 74LS157-1.pin9
  N7: J32.pin5, J35.pin5, 74LS157-2.pin4
  N8: J32.pin6, J35.pin6, 74LS157-2.pin7
  N9: J32.pin7, J35.pin7, 74LS157-2.pin12
  N10: J32.pin8, J35.pin8, 74LS157-2.pin9
  N11: J32.pin9, J35.pin9, 74LS157-3.pin4
  N12: J32.pin10, J35.pin10, 74LS157-3.pin7
  N13: J32.pin11, J35.pin11, 74LS157-3.pin12
  N14: J33.pin1, 74173-1.pin16, 74173-2.pin16, 74163.pin3, 74163.pin4, 74163.pin5, 74163.pin6, 74163.pin7, 74163.pin9, 74163.pin10, 74163.pin16, J36.pin1, C1.1, C2.1, NOT.pin3, NOT.pin5, NOT.pin9, NOT.pin11, NOT.pin13, NOT.pin14, J37.pin3, J37.pin4, J38.pin3, J38.pin4, 74LS157-1.pin16, 74LS157-2.pin16, 74LS157-3.pin16, C3.0, C4.1, C5.0, R2.Pin_1, A12.pin1
  N15: J33.pin2, GND.pin1, 74173-1.pin1, 74173-1.pin2, 74173-1.pin8, 74173-1.pin15, 74173-2.pin1, 74173-2.pin2, 74173-2.pin8, 74173-2.pin15, 74163.pin8, J36.pin2, C1.0, C2.0, NOT.pin7, J37.pin1, J37.pin2, J38.pin1, J38.pin2, 74LS157-1.pin8, 74LS157-1.pin15, 74LS157-2.pin8, 74LS157-2.pin15, 74LS157-3.pin8, 74LS157-3.pin15, C3.1, C4.0, C5.1, R1.Pin_1, A12.pin3
  N16: instruction.pin1, 74LS157-1.pin2
  N17: instruction.pin2, 74LS157-1.pin5
  N18: instruction.pin3, 74LS157-1.pin14
  N19: instruction.pin4, 74LS157-1.pin11
  N20: instruction.pin5, 74LS157-2.pin2
  N21: instruction.pin6, 74LS157-2.pin5
  N22: instruction.pin7, 74LS157-2.pin14
  N23: instruction.pin8, 74LS157-2.pin11
  N24: step.pin1, 74LS157-3.pin2
  N25: step.pin2, 74LS157-3.pin5
  N26: step.pin3, 74LS157-3.pin14
  N27: step.pin4, 74LS157-3.pin11
  N28: SELECT.pin1, 74LS157-1.pin1, 74LS157-2.pin1, 74LS157-3.pin1, J39.pin2
  N29: CLK.pin1, NOT.pin1, CLK_2.pin1, CLK_2.pin2, CLK_2.pin3, CLK_2.pin4, CLK_2.pin5, CLK_2.pin6, J40.pin2
  N30: 74173-1.pin3, 74LS157-1.pin3
  N31: 74173-1.pin4, 74LS157-1.pin6
  N32: 74173-1.pin5, 74LS157-1.pin13
  N33: 74173-1.pin6, 74LS157-1.pin10
  N34: 74173-1.pin7, 74173-2.pin7, 74163.pin2, NOT.pin2, invclk.pin1
  N35: 74173-1.pin9, 74173-1.pin10, 74173-2.pin9, 74173-2.pin10, load.pin1
  N36: 74173-1.pin11, BUS.pin5, BUS_2.pin5
  N37: 74173-1.pin12, BUS.pin6, BUS_2.pin6
  N38: 74173-1.pin13, BUS.pin7, BUS_2.pin7
  N39: 74173-1.pin14, BUS.pin8, BUS_2.pin8
  N40: BUS.pin1, 74173-2.pin11, BUS_2.pin1
  N41: BUS.pin2, 74173-2.pin12, BUS_2.pin2
  N42: BUS.pin3, 74173-2.pin13, BUS_2.pin3
  N43: BUS.pin4, 74173-2.pin14, BUS_2.pin4
  N44: 74173-2.pin3, 74LS157-2.pin3
  N45: 74173-2.pin4, 74LS157-2.pin6
  N46: 74173-2.pin5, 74LS157-2.pin13
  N47: 74173-2.pin6, 74LS157-2.pin10
  N48: cont.pin1, 74163.pin1
  N49: 74163.pin11, 74LS157-3.pin3
  N50: 74163.pin12, 74LS157-3.pin6
  N51: 74163.pin13, 74LS157-3.pin13
  N52: 74163.pin14, 74LS157-3.pin10
  N53: J39.pin1, J40.pin1, R1.Pin_0
  N54: J39.pin3, J40.pin3, R2.Pin_0

notes:
  +
  -
  0
  Marius Krabset 2019
  Instruction Register
