# Fritzing sketch instreg_v2 (saved by Fritzing 0.9.1b)
circuit board: 9.98519cm x 9.983cm
breadboards: 1

parts:
  J31 = female pin header, 2 pins [form="♀ (female)"]  # not connected
  J32 = female pin header, 11 pins [form="♀ (female)"]  # not connected
  J33 = female pin header, 2 pins [form="♀ (female)"]  # not connected
  instr = female pin header, 8 pins [form="♀ (female)"]
  step = female pin header, 4 pins [form="♀ (female)"]
  sel = female pin header, 1 pin [form="♀ (female)"]
  clk = female pin header, 1 pin [form="♀ (female)"]
  gnd = female pin header, 1 pin [form="♀ (female)"]
  74173-1 = IC, DIP package, 16 pins [chip_label=IC]
  bus-1 = female pin header, 8 pins [form="♀ (female)"]
  74173-2 = IC, DIP package, 16 pins [chip_label=IC]
  bus-2 = female pin header, 8 pins [form="♀ (female)"]
  cont = female pin header, 1 pin [form="♀ (female)"]
  74163 = IC, DIP package, 16 pins [chip_label=IC]
  load = female pin header, 1 pin [form="♀ (female)"]
  J34 = female pin header, 2 pins [form="♀ (female)"]
  J35 = female pin header, 11 pins [form="♀ (female)"]
  J36 = female pin header, 2 pins [form="♀ (female)"]  # not connected
  C1 = Ceramic Capacitor [capacitance=100nF package="100 mil [THT, multilayer]"]
  C2 = Ceramic Capacitor [capacitance=100nF package="100 mil [THT, multilayer]"]
  NOT = IC, DIP package, 14 pins [chip_label=IC]
  CLK = female pin header, 6 pins [form="♀ (female)"]
  J37 = female pin header, 4 pins [form="♀ (female)"]
  J38 = female pin header, 4 pins [form="♀ (female)"]
  74LS157-1 = IC, DIP package, 16 pins [chip_label=IC]
  74LS157-2 = IC, DIP package, 16 pins [chip_label=IC]
  74LS157-3 = IC, DIP package, 16 pins [chip_label=IC]

nets:
  N1: instr.pin1, 74LS157-1.pin2
  N2: instr.pin2, 74LS157-1.pin5
  N3: instr.pin3, 74LS157-1.pin14
  N4: instr.pin4, 74LS157-1.pin11
  N5: instr.pin5, 74LS157-2.pin2
  N6: instr.pin6, 74LS157-2.pin5
  N7: instr.pin7, 74LS157-2.pin14
  N8: instr.pin8, 74LS157-2.pin11
  N9: step.pin1, 74LS157-3.pin2
  N10: step.pin2, 74LS157-3.pin5
  N11: step.pin3, 74LS157-3.pin14
  N12: step.pin4, 74LS157-3.pin11
  N13: sel.pin1, 74LS157-1.pin1, 74LS157-2.pin1
  N14: clk.pin1, NOT.pin1, CLK.pin1, CLK.pin2, CLK.pin3, CLK.pin4, CLK.pin5, CLK.pin6
  N15: gnd.pin1, 74173-1.pin1, 74173-1.pin2, 74173-1.pin8, 74173-1.pin15, 74173-2.pin1, 74173-2.pin2, 74173-2.pin8, 74173-2.pin15, 74163.pin8, C1.0, C2.0, NOT.pin7, J37.pin1, J37.pin2, J38.pin1, J38.pin2, 74LS157-1.pin8, 74LS157-1.pin15, 74LS157-3.pin8, 74LS157-3.pin15
  N16: 74173-1.pin3, 74LS157-1.pin3
  N17: 74173-1.pin4, 74LS157-1.pin6
  N18: 74173-1.pin5, 74LS157-1.pin13
  N19: 74173-1.pin6, 74LS157-1.pin10
  N20: 74173-1.pin7, 74173-2.pin7, 74163.pin2, NOT.pin2
  N21: 74173-1.pin9, 74173-1.pin10, 74173-2.pin9, 74173-2.pin10, load.pin1
  N22: 74173-1.pin11, bus-1.pin5, bus-2.pin5
  N23: 74173-1.pin12, bus-1.pin6, bus-2.pin6
  N24: 74173-1.pin13, bus-1.pin7, bus-2.pin7
  N25: 74173-1.pin14, bus-1.pin8, bus-2.pin8
  N26: 74173-1.pin16, 74173-2.pin16, 74163.pin3, 74163.pin4, 74163.pin5, 74163.pin6, 74163.pin7, 74163.pin9, 74163.pin10, 74163.pin16, C1.1, C2.1, NOT.pin9, NOT.pin11, NOT.pin13, NOT.pin14, J37.pin3, J37.pin4, J38.pin3, J38.pin4
  N27: bus-1.pin1, 74173-2.pin11, bus-2.pin1
  N28: bus-1.pin2, 74173-2.pin12, bus-2.pin2
  N29: bus-1.pin3, 74173-2.pin13, bus-2.pin3
  N30: bus-1.pin4, 74173-2.pin14, bus-2.pin4
  N31: 74173-2.pin3, 74LS157-2.pin3
  N32: 74173-2.pin4, 74LS157-2.pin6
  N33: 74173-2.pin5, 74LS157-2.pin13
  N34: 74173-2.pin6, 74LS157-2.pin10
  N35: cont.pin1, 74163.pin1
  N36: 74163.pin11, 74LS157-3.pin3
  N37: 74163.pin12, 74LS157-3.pin6
  N38: 74163.pin13, 74LS157-3.pin13
  N39: 74163.pin14, 74LS157-3.pin10
  N40: J34.pin1, 74LS157-3.pin9
  N41: J35.pin1, 74LS157-1.pin4
  N42: J35.pin2, 74LS157-1.pin7
  N43: J35.pin3, 74LS157-1.pin12
  N44: J35.pin4, 74LS157-1.pin9
  N45: J35.pin5, 74LS157-2.pin4
  N46: J35.pin6, 74LS157-2.pin7
  N47: J35.pin7, 74LS157-2.pin12
  N48: J35.pin8, 74LS157-2.pin9
  N49: J35.pin9, 74LS157-3.pin4
  N50: J35.pin10, 74LS157-3.pin7
  N51: J35.pin11, 74LS157-3.pin12
  N52: 74LS157-2.pin8, 74LS157-2.pin15

notes:
  +
  -
