# Fritzing sketch io-decoder_10x10cm-groundfill (saved by Fritzing 0.9.1b)
circuit board: 9.96637cm x 7.62174cm
breadboards: 1

parts:
  74LS139 = IC, DIP package, 16 pins [chip_label=IC]
  J1 = female pin header, 4 pins [form="♀ (female)"]
  74LS139_2 = IC, DIP package, 16 pins [chip_label=IC]
  J3 = female pin header, 4 pins [form="♀ (female)"]
  J4 = female pin header, 4 pins [form="♀ (female)"]
  74LS139_3 = IC, DIP package, 16 pins [chip_label=IC]
  J2 = female pin header, 4 pins [form="♀ (female)"]
  74LS139_4 = IC, DIP package, 16 pins [chip_label=IC]
  74LS139_5 = IC, DIP package, 16 pins [chip_label=IC]
  J5 = female pin header, 4 pins [form="♀ (female)"]
  J6 = female pin header, 4 pins [form="♀ (female)"]
  J7 = female pin header, 4 pins [form="♀ (female)"]
  J8 = female pin header, 4 pins [form="♀ (female)"]
  J9 = female pin header, 11 pins [form="♀ (female)"]
  J10 = female pin header, 2 pins [form="♀ (female)"]
  J11 = female pin header, 11 pins [form="♀ (female)"]
  J12 = female pin header, 2 pins [form="♀ (female)"]
  AT28C64 = female pin header, 12 pins [form="♀ (female)"]
  J15 = female pin header, 12 pins [form="♀ (female)"]
  J17 = female pin header, 2 pins [form="♀ (female)"]
  J18 = female pin header, 2 pins [form="♀ (female)"]
  J19 = female pin header, 2 pins [form="♀ (female)"]
  J20 = female pin header, 2 pins [form="♀ (female)"]
  C1 = Ceramic Capacitor [capacitance=100nF package="100 mil [THT, multilayer]"]
  C2 = Ceramic Capacitor [capacitance=100nF package="100 mil [THT, multilayer]"]
  C3 = Ceramic Capacitor [capacitance=100nF package="100 mil [THT, multilayer]"]
  C4 = Ceramic Capacitor [capacitance=100nF package="100 mil [THT, multilayer]"]
  C5 = Ceramic Capacitor [capacitance=100nF package="100 mil [THT, multilayer]"]
  J21 = female pin header, 4 pins [form="♀ (female)"]
  J22 = female pin header, 4 pins [form="♀ (female)"]
  J23 = female pin header, 4 pins [form="♀ (female)"]
  J24 = female pin header, 4 pins [form="♀ (female)"]
  J25 = female pin header, 4 pins [form="♀ (female)"]
  J26 = female pin header, 4 pins [form="♀ (female)"]
  J27 = female pin header, 4 pins [form="♀ (female)"]
  J28 = female pin header, 4 pins [form="♀ (female)"]
  J29 = female pin header, 2 pins [form="♀ (female)"]
  J30 = female pin header, 2 pins [form="♀ (female)"]

nets:
  N1: 74LS139.pin1, 74LS139_3.pin4
  N2: 74LS139.pin2, 74LS139.pin14, 74LS139_2.pin3, 74LS139_2.pin13, J15.pin4
  N3: 74LS139.pin3, 74LS139.pin13, 74LS139_2.pin2, 74LS139_2.pin14, J15.pin3
  N4: 74LS139.pin4, J1.pin1, J26.pin1
  N5: 74LS139.pin5, J1.pin2, J26.pin2
  N6: 74LS139.pin6, J1.pin3, J26.pin3
  N7: 74LS139.pin7, J1.pin4, J26.pin4
  N8: 74LS139.pin8, 74LS139_2.pin8, 74LS139_3.pin1, 74LS139_3.pin8, 74LS139_3.pin15, 74LS139_4.pin8, 74LS139_5.pin8, J10.pin2, J12.pin2, AT28C64.pin6, AT28C64.pin8, J15.pin1, C1.0, C2.0, C3.0, C4.0, C5.0, J29.pin1, J30.pin1
  N9: 74LS139.pin9, J2.pin4, J28.pin4
  N10: 74LS139.pin10, J2.pin3, J28.pin3
  N11: 74LS139.pin11, J2.pin2, J28.pin2
  N12: 74LS139.pin12, J2.pin1, J28.pin1
  N13: 74LS139.pin15, 74LS139_3.pin5
  N14: 74LS139.pin16, 74LS139_2.pin16, 74LS139_3.pin16, 74LS139_4.pin16, 74LS139_5.pin16, J10.pin1, J12.pin1, J17.pin1, J17.pin2, C1.1, C2.1, C3.1, C4.1, C5.1, J29.pin2, J30.pin2
  N15: 74LS139_2.pin1, 74LS139_3.pin6
  N16: 74LS139_2.pin4, J3.pin1, J25.pin1
  N17: 74LS139_2.pin5, J3.pin2, J25.pin2
  N18: 74LS139_2.pin6, J3.pin3, J25.pin3
  N19: 74LS139_2.pin7, J3.pin4, J25.pin4
  N20: 74LS139_2.pin9, J4.pin4, J24.pin4
  N21: 74LS139_2.pin10, J4.pin3, J24.pin3
  N22: 74LS139_2.pin11, J4.pin2, J24.pin2
  N23: 74LS139_2.pin12, J4.pin1, J24.pin1
  N24: 74LS139_2.pin15, 74LS139_3.pin7
  N25: 74LS139_3.pin2, AT28C64.pin1
  N26: 74LS139_3.pin3, J15.pin2
  N27: 74LS139_3.pin9, 74LS139_5.pin1
  N28: 74LS139_3.pin10, 74LS139_5.pin15
  N29: 74LS139_3.pin11, 74LS139_4.pin1
  N30: 74LS139_3.pin12, 74LS139_4.pin15
  N31: 74LS139_3.pin13, AT28C64.pin3
  N32: 74LS139_3.pin14, AT28C64.pin2
  N33: 74LS139_4.pin2, 74LS139_4.pin14, 74LS139_5.pin3, 74LS139_5.pin13, AT28C64.pin4
  N34: 74LS139_4.pin3, 74LS139_4.pin13, 74LS139_5.pin2, 74LS139_5.pin14, AT28C64.pin5
  N35: 74LS139_4.pin4, J5.pin1, J23.pin1
  N36: 74LS139_4.pin5, J5.pin2, J23.pin2
  N37: 74LS139_4.pin6, J5.pin3, J23.pin3
  N38: 74LS139_4.pin7, J5.pin4, J23.pin4
  N39: 74LS139_4.pin9, J8.pin4, J27.pin4
  N40: 74LS139_4.pin10, J8.pin3, J27.pin3
  N41: 74LS139_4.pin11, J8.pin2, J27.pin2
  N42: 74LS139_4.pin12, J8.pin1, J27.pin1
  N43: 74LS139_5.pin4, J7.pin1, J21.pin1
  N44: 74LS139_5.pin5, J7.pin2, J21.pin2
  N45: 74LS139_5.pin6, J7.pin3, J21.pin3
  N46: 74LS139_5.pin7, J7.pin4, J21.pin4
  N47: 74LS139_5.pin9, J6.pin4, J22.pin4
  N48: 74LS139_5.pin10, J6.pin3, J22.pin3
  N49: 74LS139_5.pin11, J6.pin2, J22.pin2
  N50: 74LS139_5.pin12, J6.pin1, J22.pin1
  N51: J9.pin1, J11.pin1, J15.pin5
  N52: J9.pin2, J11.pin2, J15.pin6
  N53: J9.pin3, J11.pin3, J15.pin7
  N54: J9.pin4, J11.pin4, J15.pin8
  N55: J9.pin5, J11.pin5, J15.pin9
  N56: J9.pin6, J11.pin6, J15.pin10
  N57: J9.pin7, J11.pin7, J15.pin11
  N58: J9.pin8, J11.pin8, J15.pin12
  N59: J9.pin9, J11.pin9, AT28C64.pin11
  N60: J9.pin10, J11.pin10, AT28C64.pin10
  N61: J9.pin11, J11.pin11, AT28C64.pin7
  N62: AT28C64.pin9, J19.pin1, J20.pin1
  N63: J18.pin1, J19.pin2, J20.pin2

notes:
  write-to-bus
  read-from-bus
  BUS I/O Decoder
  0 1 2 3 4 5 6 7 8 9 a b c d e f
  Marius Krabset 2019
  -
  +
