# Fritzing sketch outreg_display_v2 (saved by Fritzing 0.9.1b)
circuit board: 9.99cm x 9.99cm
breadboards: 1

parts:
  555 = 555 Timer [package="DIP8 [THT]"]
  74LS163 = IC, DIP package, 16 pins [chip_label=IC]
  R1 = Resistor [tolerance=±5% resistance=220 package=THT]
  R2 = Resistor [tolerance=±5% resistance=220 package=THT]
  C1 = Ceramic Capacitor [capacitance=100nF package="100 mil [THT, multilayer]"]
  74LS139 = IC, DIP package, 16 pins [chip_label=IC]
  C2 = Ceramic Capacitor [capacitance=100nF package="100 mil [THT, multilayer]"]
  IC1 = TSSOP20 [chip_label=IC package=TSSOP]
  J1 = female pin header, 8 pins [form="♀ (female)"]
  J2 = female pin header, 8 pins [form="♀ (female)"]
  IC2 = TSSOP20 [chip_label=IC package=TSSOP]
  J3 = female pin header, 8 pins [form="♀ (female)"]
  IC3 = TSSOP20 [chip_label=IC package=TSSOP]
  J4 = female pin header, 8 pins [form="♀ (female)"]
  IC4 = TSSOP20 [chip_label=IC package=TSSOP]
  display-3 = female pin header, 6 pins [form="♀ (female)"]  # not connected
  display-4 = female pin header, 6 pins [form="♀ (female)"]  # not connected
  J47 = female pin header, 12 pins [form="♀ (female)"]
  J48 = female pin header, 12 pins [form="♀ (female)"]
  display-5 = female pin header, 6 pins [form="♀ (female)"]  # not connected
  display-6 = female pin header, 6 pins [form="♀ (female)"]  # not connected
  display-7 = female pin header, 6 pins [form="♀ (female)"]  # not connected
  display-8 = female pin header, 6 pins [form="♀ (female)"]  # not connected
  display-9 = female pin header, 6 pins [form="♀ (female)"]  # not connected
  display-10 = female pin header, 6 pins [form="♀ (female)"]  # not connected
  IC5 = TSSOP20 [chip_label=IC package=TSSOP]

nets:
  N1: 555.Ground, 74LS163.pin8, C1.1, 74LS139.pin1, 74LS139.pin8, 74LS139.pin15, C2.0, IC1.10, IC2.10, IC3.10, IC4.10
  N2: 555.Trigger, 555.Threshold, R2.Pin_0, C1.0
  N3: 555.Output, 74LS163.pin2
  N4: 555.Discharge, R1.Pin_0, R2.Pin_1
  N5: 555.Vcc_Supply_Voltage, 74LS163.pin1, 74LS163.pin7, 74LS163.pin9, 74LS163.pin10, 74LS163.pin16, R1.Pin_1, 74LS139.pin16, C2.1, IC1.1, IC1.20, IC2.1, IC2.20, IC3.1, IC3.20, IC4.1, IC4.20
  N6: 74LS163.pin11, 74LS139.pin13
  N7: 74LS163.pin12, 74LS139.pin14
  N8: 74LS163.pin13, 74LS139.pin3
  N9: 74LS163.pin14, 74LS139.pin2
  N10: 74LS139.pin4, IC1.19
  N11: 74LS139.pin5, IC2.19
  N12: 74LS139.pin6, IC3.19
  N13: 74LS139.pin7, IC4.19
  N14: IC1.2, J1.pin1
  N15: IC1.3, J1.pin2
  N16: IC1.4, J1.pin3
  N17: IC1.5, J1.pin4
  N18: IC1.6, J1.pin5
  N19: IC1.7, J1.pin6
  N20: IC1.8, J1.pin7
  N21: IC1.9, J1.pin8
  N22: IC1.11, IC2.11, IC3.11, IC4.11
  N23: IC1.12, IC2.12, IC3.12, IC4.12
  N24: IC1.13, IC2.13, IC3.13, IC4.13
  N25: IC1.14, IC2.14, IC3.14, IC4.14
  N26: IC1.15, IC2.15, IC3.15, IC4.15
  N27: IC1.16, IC2.16, IC3.16, IC4.16
  N28: IC1.17, IC2.17, IC3.17, IC4.17
  N29: IC1.18, IC2.18, IC3.18, IC4.18
  N30: J2.pin1, IC2.2
  N31: J2.pin2, IC2.3
  N32: J2.pin3, IC2.4
  N33: J2.pin4, IC2.5
  N34: J2.pin5, IC2.6
  N35: J2.pin6, IC2.7
  N36: J2.pin7, IC2.8
  N37: J2.pin8, IC2.9
  N38: J3.pin1, IC3.2
  N39: J3.pin2, IC3.3
  N40: J3.pin3, IC3.4
  N41: J3.pin4, IC3.5
  N42: J3.pin5, IC3.6
  N43: J3.pin6, IC3.7
  N44: J3.pin7, IC3.8
  N45: J3.pin8, IC3.9
  N46: J4.pin1, IC4.2
  N47: J4.pin2, IC4.3
  N48: J4.pin3, IC4.4
  N49: J4.pin4, IC4.5
  N50: J4.pin5, IC4.6
  N51: J4.pin6, IC4.7
  N52: J4.pin7, IC4.8
  N53: J4.pin8, IC4.9
  N54: J47.pin7, IC5.10
  N55: J47.pin8, IC5.9
  N56: J47.pin9, IC5.8
  N57: J47.pin10, IC5.7
  N58: J47.pin11, IC5.6
  N59: J47.pin12, IC5.5
  N60: J48.pin9, IC5.2
  N61: J48.pin10, IC5.3
  N62: J48.pin11, IC5.4
