# Fritzing sketch outregdisp_v2_wsop20 (saved by Fritzing 0.9.1b)
circuit board: 9.99cm x 9.99cm
breadboards: 1

parts:
  555 = 555 Timer [package="DIP8 [THT]"]
  74LS163 = IC, DIP package, 16 pins [chip_label=IC]
  C1 = Ceramic Capacitor [capacitance=100nF package="100 mil [THT, multilayer]"]
  74LS139 = IC, DIP package, 16 pins [chip_label=IC]
  C2 = Ceramic Capacitor [capacitance=100nF package="100 mil [THT, multilayer]"]
  display-3 = female pin header, 6 pins [form="♀ (female)"]
  display-4 = female pin header, 6 pins [form="♀ (female)"]
  R2 = Resistor [tolerance=±5% resistance=220 package="1206 [SMD]"]
  R1 = Resistor [tolerance=±5% resistance=220 package="1206 [SMD]"]
  J54 = female pin header, 8 pins [form="♀ (female)"]
  R19 = Resistor [tolerance=±5% resistance=220 package="1206 [SMD]"]
  R20 = Resistor [tolerance=±5% resistance=220 package="1206 [SMD]"]
  R21 = Resistor [tolerance=±5% resistance=220 package="1206 [SMD]"]
  R22 = Resistor [tolerance=±5% resistance=220 package="1206 [SMD]"]
  R23 = Resistor [tolerance=±5% resistance=220 package="1206 [SMD]"]
  R24 = Resistor [tolerance=±5% resistance=220 package="1206 [SMD]"]
  R25 = Resistor [tolerance=±5% resistance=220 package="1206 [SMD]"]
  R26 = Resistor [tolerance=±5% resistance=220 package="1206 [SMD]"]
  IC16 = TSSOP20 [chip_label=IC package=TSSOP]
  J48 = female pin header, 14 pins [form="♀ (female)"]
  J47 = female pin header, 14 pins [form="♀ (female)"]
  R27 = Resistor [tolerance=±5% resistance=220 package="1206 [SMD]"]
  R28 = Resistor [tolerance=±5% resistance=220 package="1206 [SMD]"]
  R29 = Resistor [tolerance=±5% resistance=220 package="1206 [SMD]"]
  R30 = Resistor [tolerance=±5% resistance=220 package="1206 [SMD]"]
  R31 = Resistor [tolerance=±5% resistance=220 package="1206 [SMD]"]
  R32 = Resistor [tolerance=±5% resistance=220 package="1206 [SMD]"]
  R33 = Resistor [tolerance=±5% resistance=220 package="1206 [SMD]"]
  R34 = Resistor [tolerance=±5% resistance=220 package="1206 [SMD]"]
  IC17 = TSSOP20 [chip_label=IC package=TSSOP]
  display-5 = female pin header, 6 pins [form="♀ (female)"]
  display-6 = female pin header, 6 pins [form="♀ (female)"]
  R35 = Resistor [tolerance=±5% resistance=220 package="1206 [SMD]"]
  R36 = Resistor [tolerance=±5% resistance=220 package="1206 [SMD]"]
  R37 = Resistor [tolerance=±5% resistance=220 package="1206 [SMD]"]
  R38 = Resistor [tolerance=±5% resistance=220 package="1206 [SMD]"]
  R39 = Resistor [tolerance=±5% resistance=220 package="1206 [SMD]"]
  R40 = Resistor [tolerance=±5% resistance=220 package="1206 [SMD]"]
  R41 = Resistor [tolerance=±5% resistance=220 package="1206 [SMD]"]
  R42 = Resistor [tolerance=±5% resistance=220 package="1206 [SMD]"]
  display-7 = female pin header, 6 pins [form="♀ (female)"]
  display-8 = female pin header, 6 pins [form="♀ (female)"]
  R43 = Resistor [tolerance=±5% resistance=220 package="1206 [SMD]"]
  R44 = Resistor [tolerance=±5% resistance=220 package="1206 [SMD]"]
  R45 = Resistor [tolerance=±5% resistance=220 package="1206 [SMD]"]
  R46 = Resistor [tolerance=±5% resistance=220 package="1206 [SMD]"]
  R47 = Resistor [tolerance=±5% resistance=220 package="1206 [SMD]"]
  R48 = Resistor [tolerance=±5% resistance=220 package="1206 [SMD]"]
  R49 = Resistor [tolerance=±5% resistance=220 package="1206 [SMD]"]
  R50 = Resistor [tolerance=±5% resistance=220 package="1206 [SMD]"]
  display-9 = female pin header, 6 pins [form="♀ (female)"]
  display-10 = female pin header, 6 pins [form="♀ (female)"]
  R51 = Resistor [tolerance=±5% resistance=220 package="1206 [SMD]"]
  R52 = Resistor [tolerance=±5% resistance=220 package="1206 [SMD]"]
  R53 = Resistor [tolerance=±5% resistance=220 package="1206 [SMD]"]
  R54 = Resistor [tolerance=±5% resistance=220 package="1206 [SMD]"]
  R55 = Resistor [tolerance=±5% resistance=220 package="1206 [SMD]"]
  R56 = Resistor [tolerance=±5% resistance=220 package="1206 [SMD]"]
  R57 = Resistor [tolerance=±5% resistance=220 package="1206 [SMD]"]
  R58 = Resistor [tolerance=±5% resistance=220 package="1206 [SMD]"]
  IC20 = TSSOP20 [chip_label=IC package=TSSOP]
  J56 = female pin header, 8 pins [form="♀ (female)"]
  R59 = Resistor [tolerance=±5% resistance=220 package="1206 [SMD]"]
  R60 = Resistor [tolerance=±5% resistance=220 package="1206 [SMD]"]
  R61 = Resistor [tolerance=±5% resistance=220 package="1206 [SMD]"]
  R62 = Resistor [tolerance=±5% resistance=220 package="1206 [SMD]"]
  R63 = Resistor [tolerance=±5% resistance=220 package="1206 [SMD]"]
  R64 = Resistor [tolerance=±5% resistance=220 package="1206 [SMD]"]
  R65 = Resistor [tolerance=±5% resistance=220 package="1206 [SMD]"]
  R66 = Resistor [tolerance=±5% resistance=220 package="1206 [SMD]"]
  IC21 = TSSOP20 [chip_label=IC package=TSSOP]
  J57 = female pin header, 8 pins [form="♀ (female)"]
  J58 = female pin header, 8 pins [form="♀ (female)"]
  R67 = Resistor [tolerance=±5% resistance=220 package="1206 [SMD]"]
  R68 = Resistor [tolerance=±5% resistance=220 package="1206 [SMD]"]
  R69 = Resistor [tolerance=±5% resistance=220 package="1206 [SMD]"]
  R70 = Resistor [tolerance=±5% resistance=220 package="1206 [SMD]"]
  R71 = Resistor [tolerance=±5% resistance=220 package="1206 [SMD]"]
  R72 = Resistor [tolerance=±5% resistance=220 package="1206 [SMD]"]
  R73 = Resistor [tolerance=±5% resistance=220 package="1206 [SMD]"]
  R74 = Resistor [tolerance=±5% resistance=220 package="1206 [SMD]"]
  R75 = Resistor [tolerance=±5% resistance=220 package="1206 [SMD]"]
  R76 = Resistor [tolerance=±5% resistance=220 package="1206 [SMD]"]
  R77 = Resistor [tolerance=±5% resistance=220 package="1206 [SMD]"]
  R78 = Resistor [tolerance=±5% resistance=220 package="1206 [SMD]"]
  R79 = Resistor [tolerance=±5% resistance=220 package="1206 [SMD]"]
  R80 = Resistor [tolerance=±5% resistance=220 package="1206 [SMD]"]
  R81 = Resistor [tolerance=±5% resistance=220 package="1206 [SMD]"]
  R82 = Resistor [tolerance=±5% resistance=220 package="1206 [SMD]"]
  IC22 = TSSOP20 [chip_label=IC package=TSSOP]
  IC23 = TSSOP20 [chip_label=IC package=TSSOP]
  J59 = female pin header, 3 pins [form="♀ (female)"]
  J60 = female pin header, 3 pins [form="♀ (female)"]
  J61 = female pin header, 3 pins [form="♀ (female)"]
  C3 = Electrolytic Capacitor [capacitance=1µF package="100 mil [THT, electrolytic]"]
  J62 = female pin header, 2 pins [form="♀ (female)"]
  J63 = female pin header, 2 pins [form="♀ (female)"]
  IC24 = SO20W [chip_label=IC package=SO(w)]
  IC25 = SO20W [chip_label=IC package=SO(w)]
  J64 = female pin header, 8 pins [form="♀ (female)"]
  R83 = Resistor [tolerance=±5% resistance=220 package="1206 [SMD]"]
  R84 = Resistor [tolerance=±5% resistance=220 package="1206 [SMD]"]
  R85 = Resistor [tolerance=±5% resistance=220 package="1206 [SMD]"]
  R86 = Resistor [tolerance=±5% resistance=220 package="1206 [SMD]"]
  R87 = Resistor [tolerance=±5% resistance=220 package="1206 [SMD]"]
  R88 = Resistor [tolerance=±5% resistance=220 package="1206 [SMD]"]
  R89 = Resistor [tolerance=±5% resistance=220 package="1206 [SMD]"]
  R90 = Resistor [tolerance=±5% resistance=220 package="1206 [SMD]"]
  IC26 = SO20W [chip_label=IC package=SO(w)]
  J65 = female pin header, 14 pins [form="♀ (female)"]  # not connected
  J66 = female pin header, 14 pins [form="♀ (female)"]  # not connected
  J67 = female pin header, 5 pins [form="♀ (female)"]  # not connected
  IC27 = SO20W [chip_label=IC package=SO(w)]
  display-11 = female pin header, 6 pins [form="♀ (female)"]
  display-12 = female pin header, 6 pins [form="♀ (female)"]
  R91 = Resistor [tolerance=±5% resistance=220 package="1206 [SMD]"]
  R92 = Resistor [tolerance=±5% resistance=220 package="1206 [SMD]"]
  R93 = Resistor [tolerance=±5% resistance=220 package="1206 [SMD]"]
  R94 = Resistor [tolerance=±5% resistance=220 package="1206 [SMD]"]
  R95 = Resistor [tolerance=±5% resistance=220 package="1206 [SMD]"]
  R96 = Resistor [tolerance=±5% resistance=220 package="1206 [SMD]"]
  R97 = Resistor [tolerance=±5% resistance=220 package="1206 [SMD]"]
  R98 = Resistor [tolerance=±5% resistance=220 package="1206 [SMD]"]
  display-13 = female pin header, 6 pins [form="♀ (female)"]
  display-14 = female pin header, 6 pins [form="♀ (female)"]
  IC28 = SO20W [chip_label=IC package=SO(w)]
  R103 = Resistor [tolerance=±5% resistance=220 package="1206 [SMD]"]
  R99 = Resistor [tolerance=±5% resistance=220 package="1206 [SMD]"]
  R104 = Resistor [tolerance=±5% resistance=220 package="1206 [SMD]"]
  R105 = Resistor [tolerance=±5% resistance=220 package="1206 [SMD]"]
  R100 = Resistor [tolerance=±5% resistance=220 package="1206 [SMD]"]
  R102 = Resistor [tolerance=±5% resistance=220 package="1206 [SMD]"]
  R101 = Resistor [tolerance=±5% resistance=220 package="1206 [SMD]"]
  R106 = Resistor [tolerance=±5% resistance=220 package="1206 [SMD]"]

nets:
  N1: 555.Ground, 74LS163.pin8, C1.1, 74LS139.pin1, 74LS139.pin8, 74LS139.pin15, C2.0, IC16.10, J48.pin14, J47.pin7, J47.pin9, IC17.10, IC20.10, IC21.10, IC22.10, IC23.10, J59.pin3, J60.pin3, J61.pin3, C3.-, J62.pin1, J63.pin1, IC24.20, IC25.20
  N2: 555.Trigger, 555.Threshold, C1.0, R2.Pin_0
  N3: 555.Output, 74LS163.pin2
  N4: 555.Discharge, R2.Pin_1, R1.Pin_0
  N5: 555.Vcc_Supply_Voltage, 74LS163.pin1, 74LS163.pin7, 74LS163.pin9, 74LS163.pin10, 74LS163.pin16, 74LS139.pin16, C2.1, R1.Pin_1, IC16.1, IC16.20, J47.pin1, J47.pin2, IC17.1, IC17.20, IC20.1, IC20.20, IC21.1, IC21.20, IC22.1, IC22.20, IC23.1, IC23.20, J59.pin1, J60.pin1, J61.pin1, C3.+, J62.pin2, J63.pin2, IC24.10, IC24.11, IC25.10, IC25.11
  N6: 74LS163.pin11, 74LS139.pin13
  N7: 74LS163.pin12, 74LS139.pin14
  N8: 74LS163.pin13, 74LS139.pin3, J47.pin5
  N9: 74LS163.pin14, 74LS139.pin2, J47.pin4
  N10: 74LS139.pin4, display-4.pin1, display-6.pin1, display-8.pin1, display-10.pin1
  N11: 74LS139.pin5, display-4.pin4, display-6.pin4, display-8.pin4, display-10.pin4
  N12: 74LS139.pin6, display-4.pin5, display-6.pin5, display-8.pin5, display-10.pin5
  N13: 74LS139.pin7, display-3.pin6, display-5.pin6, display-7.pin6, display-9.pin6
  N14: 74LS139.pin9, IC20.19, IC23.19
  N15: 74LS139.pin10, IC22.19, IC25.9
  N16: 74LS139.pin11, IC21.19, IC24.9
  N17: 74LS139.pin12, IC16.19, IC17.19
  N18: display-3.pin1, R30.Pin_1
  N19: display-3.pin2, R31.Pin_1
  N20: display-3.pin3, R29.Pin_1
  N21: display-3.pin4, R32.Pin_1
  N22: display-3.pin5, R27.Pin_1
  N23: display-4.pin2, R34.Pin_1
  N24: display-4.pin3, R28.Pin_1
  N25: display-4.pin6, R33.Pin_1
  N26: J54.pin1, IC16.2
  N27: J54.pin2, IC16.3
  N28: J54.pin3, IC16.4
  N29: J54.pin4, IC16.5
  N30: J54.pin5, IC16.6
  N31: J54.pin6, IC16.7
  N32: J54.pin7, IC16.8
  N33: J54.pin8, IC16.9
  N34: R19.Pin_0, IC16.12
  N35: R19.Pin_1, J48.pin9, R59.Pin_1, R67.Pin_1, R68.Pin_1
  N36: R20.Pin_0, IC16.13
  N37: R20.Pin_1, J48.pin8, R60.Pin_1, R69.Pin_1, R70.Pin_1
  N38: R21.Pin_0, IC16.11
  N39: R21.Pin_1, J48.pin10, R61.Pin_1, R71.Pin_1, R72.Pin_1
  N40: R22.Pin_0, IC16.14
  N41: R22.Pin_1, J48.pin7, R62.Pin_1, R73.Pin_1, R74.Pin_1
  N42: R23.Pin_0, IC16.15
  N43: R23.Pin_1, J48.pin6, R63.Pin_1, R75.Pin_1, R76.Pin_1
  N44: R24.Pin_0, IC16.16
  N45: R24.Pin_1, J48.pin5, R64.Pin_1, R77.Pin_1, R78.Pin_1
  N46: R25.Pin_0, IC16.17
  N47: R25.Pin_1, J48.pin4, R65.Pin_1, R79.Pin_1, R80.Pin_1
  N48: R26.Pin_0, IC16.18
  N49: R26.Pin_1, J48.pin3, R66.Pin_1, R81.Pin_1, R82.Pin_1
  N50: J48.pin2, J59.pin2
  N51: J48.pin11, IC17.2, IC20.2, IC24.12, IC25.12
  N52: J48.pin12, IC17.3, IC20.3, IC24.13, IC25.13
  N53: J48.pin13, IC17.4, IC20.4, IC24.14, IC25.14
  N54: J47.pin6, J61.pin2
  N55: J47.pin8, J60.pin2
  N56: J47.pin10, IC17.9, IC20.9, IC24.19, IC25.19
  N57: J47.pin11, IC17.8, IC20.8, IC24.18, IC25.18
  N58: J47.pin12, IC17.7, IC20.7, IC24.17, IC25.17
  N59: J47.pin13, IC17.6, IC20.6, IC24.16, IC25.16
  N60: J47.pin14, IC17.5, IC20.5, IC24.15, IC25.15
  N61: R27.Pin_0, IC17.12
  N62: R28.Pin_0, IC17.13
  N63: R29.Pin_0, IC17.11
  N64: R30.Pin_0, IC17.14
  N65: R31.Pin_0, IC17.15
  N66: R32.Pin_0, IC17.16
  N67: R33.Pin_0, IC17.17
  N68: R34.Pin_0, IC17.18
  N69: display-5.pin1, R38.Pin_1
  N70: display-5.pin2, R39.Pin_1
  N71: display-5.pin3, R37.Pin_1
  N72: display-5.pin4, R40.Pin_1
  N73: display-5.pin5, R35.Pin_1
  N74: display-6.pin2, R42.Pin_1
  N75: display-6.pin3, R36.Pin_1
  N76: display-6.pin6, R41.Pin_1
  N77: R35.Pin_0, IC24.2
  N78: R36.Pin_0, IC24.3
  N79: R37.Pin_0, IC24.1
  N80: R38.Pin_0, IC24.4
  N81: R39.Pin_0, IC24.5
  N82: R40.Pin_0, IC24.6
  N83: R41.Pin_0, IC24.7
  N84: R42.Pin_0, IC24.8
  N85: display-7.pin1, R46.Pin_1
  N86: display-7.pin2, R47.Pin_1
  N87: display-7.pin3, R45.Pin_1
  N88: display-7.pin4, R48.Pin_1
  N89: display-7.pin5, R43.Pin_1
  N90: display-8.pin2, R50.Pin_1
  N91: display-8.pin3, R44.Pin_1
  N92: display-8.pin6, R49.Pin_1
  N93: R43.Pin_0, IC25.2
  N94: R44.Pin_0, IC25.3
  N95: R45.Pin_0, IC25.1
  N96: R46.Pin_0, IC25.4
  N97: R47.Pin_0, IC25.5
  N98: R48.Pin_0, IC25.6
  N99: R49.Pin_0, IC25.7
  N100: R50.Pin_0, IC25.8
  N101: display-9.pin1, R54.Pin_1
  N102: display-9.pin2, R55.Pin_1
  N103: display-9.pin3, R53.Pin_1
  N104: display-9.pin4, R56.Pin_1
  N105: display-9.pin5, R51.Pin_1
  N106: display-10.pin2, R58.Pin_1
  N107: display-10.pin3, R52.Pin_1
  N108: display-10.pin6, R57.Pin_1
  N109: R51.Pin_0, IC20.12
  N110: R52.Pin_0, IC20.13
  N111: R53.Pin_0, IC20.11
  N112: R54.Pin_0, IC20.14
  N113: R55.Pin_0, IC20.15
  N114: R56.Pin_0, IC20.16
  N115: R57.Pin_0, IC20.17
  N116: R58.Pin_0, IC20.18
  N117: J56.pin1, IC21.2
  N118: J56.pin2, IC21.3
  N119: J56.pin3, IC21.4
  N120: J56.pin4, IC21.5
  N121: J56.pin5, IC21.6
  N122: J56.pin6, IC21.7
  N123: J56.pin7, IC21.8
  N124: J56.pin8, IC21.9
  N125: R59.Pin_0, IC21.12
  N126: R60.Pin_0, IC21.13
  N127: R61.Pin_0, IC21.11
  N128: R62.Pin_0, IC21.14
  N129: R63.Pin_0, IC21.15
  N130: R64.Pin_0, IC21.16
  N131: R65.Pin_0, IC21.17
  N132: R66.Pin_0, IC21.18
  N133: J57.pin1, IC22.2
  N134: J57.pin2, IC22.3
  N135: J57.pin3, IC22.4
  N136: J57.pin4, IC22.5
  N137: J57.pin5, IC22.6
  N138: J57.pin6, IC22.7
  N139: J57.pin7, IC22.8
  N140: J57.pin8, IC22.9
  N141: J58.pin1, IC23.2
  N142: J58.pin2, IC23.3
  N143: J58.pin3, IC23.4
  N144: J58.pin4, IC23.5
  N145: J58.pin5, IC23.6
  N146: J58.pin6, IC23.7
  N147: J58.pin7, IC23.8
  N148: J58.pin8, IC23.9
  N149: R67.Pin_0, IC22.12
  N150: R68.Pin_0, IC23.12
  N151: R69.Pin_0, IC22.13
  N152: R70.Pin_0, IC23.13
  N153: R71.Pin_0, IC22.11
  N154: R72.Pin_0, IC23.11
  N155: R73.Pin_0, IC22.14
  N156: R74.Pin_0, IC23.14
  N157: R75.Pin_0, IC22.15
  N158: R76.Pin_0, IC23.15
  N159: R77.Pin_0, IC22.16
  N160: R78.Pin_0, IC23.16
  N161: R79.Pin_0, IC22.17
  N162: R80.Pin_0, IC23.17
  N163: R81.Pin_0, IC22.18
  N164: R82.Pin_0, IC23.18
  N165: J64.pin1, IC26.2
  N166: J64.pin2, IC26.3
  N167: J64.pin3, IC26.4
  N168: J64.pin4, IC26.5
  N169: J64.pin5, IC26.6
  N170: J64.pin6, IC26.7
  N171: J64.pin7, IC26.8
  N172: J64.pin8, IC26.9
  N173: R83.Pin_0, IC26.12
  N174: R84.Pin_0, IC26.13
  N175: R85.Pin_0, IC26.11
  N176: R86.Pin_0, IC26.14
  N177: R87.Pin_0, IC26.15
  N178: R88.Pin_0, IC26.16
  N179: R89.Pin_0, IC26.17
  N180: R90.Pin_0, IC26.18
  N181: IC26.1, IC26.20
  N182: IC27.1, IC27.20
  N183: IC27.11, R92.Pin_0
  N184: IC27.12, R91.Pin_0
  N185: IC27.13, R94.Pin_0
  N186: IC27.14, R93.Pin_0
  N187: IC27.15, R95.Pin_0
  N188: IC27.16, R96.Pin_1
  N189: IC27.17, R97.Pin_0
  N190: IC27.18, R98.Pin_0
  N191: display-11.pin1, R93.Pin_1
  N192: display-11.pin2, R95.Pin_1
  N193: display-11.pin3, R92.Pin_1
  N194: display-11.pin4, R96.Pin_0
  N195: display-11.pin5, R91.Pin_1
  N196: display-12.pin2, R98.Pin_1
  N197: display-12.pin3, R94.Pin_1
  N198: display-12.pin6, R97.Pin_1
  N199: display-13.pin1, R106.Pin_0
  N200: display-13.pin2, R105.Pin_0
  N201: display-13.pin3, R101.Pin_0
  N202: display-13.pin4, R100.Pin_1
  N203: display-13.pin5, R102.Pin_0
  N204: display-14.pin2, R103.Pin_0
  N205: display-14.pin3, R104.Pin_0
  N206: display-14.pin6, R99.Pin_0
  N207: IC28.1, IC28.10
  N208: IC28.2, R103.Pin_1
  N209: IC28.3, R99.Pin_1
  N210: IC28.4, R100.Pin_0
  N211: IC28.5, R105.Pin_1
  N212: IC28.6, R106.Pin_1
  N213: IC28.7, R104.Pin_1
  N214: IC28.8, R102.Pin_1
  N215: IC28.9, R101.Pin_1

notes:
  OUTPUT REGISTERS
  0
  1
  2
  3
  Marius Krabset 2019
  -
  +
