# Fritzing sketch outregx3_v2 (saved by Fritzing 0.9.3b)
circuit board: 11.4613cm x 14.4225cm
breadboards: 2

parts:
  555 = 555 Timer [package="DIP8 [THT]"]
  1k = Resistor [tolerance=±5% resistance=1k package=THT]
  46k = Resistor [tolerance=±5% resistance=46k package=THT]
  104 = Ceramic Capacitor [capacitance=100nF package="100 mil [THT, multilayer]"]
  104_2 = Ceramic Capacitor [capacitance=100nF package="100 mil [THT, multilayer]"]
  161(counter) = IC, DIP package, 16 pins [chip_label=IC]
  139(mux) = IC, DIP package, 16 pins [chip_label=IC]
  seg1000 = 7-Segment LED Display [package=THT]
  seg100 = 7-Segment LED Display [package=THT]
  seg10 = 7-Segment LED Display [package=THT]
  seg1 = 7-Segment LED Display [package=THT]
  J1 = female pin header, 12 pins [form="♀ (female)"]
  J2 = female pin header, 12 pins [form="♀ (female)"]
  J3 = female pin header, 3 pins [form="♀ (female)"]
  20uF = Electrolytic Capacitor [capacitance=1µF package="100 mil [THT, electrolytic]"]
  power = female pin header, 3 pins [form="♀ (female)"]
  seg1_2 = 7-Segment LED Display [package=THT]
  seg10_2 = 7-Segment LED Display [package=THT]
  seg100_2 = 7-Segment LED Display [package=THT]
  seg1000_2 = 7-Segment LED Display [package=THT]
  J4 = female pin header, 12 pins [form="♀ (female)"]
  J5 = female pin header, 12 pins [form="♀ (female)"]
  J6 = female pin header, 3 pins [form="♀ (female)"]
  J7 = female pin header, 12 pins [form="♀ (female)"]
  J8 = female pin header, 12 pins [form="♀ (female)"]
  J9 = female pin header, 3 pins [form="♀ (female)"]
  J10 = female pin header, 8 pins [form="♀ (female)"]
  J11 = female pin header, 8 pins [form="♀ (female)"]
  J12 = female pin header, 8 pins [form="♀ (female)"]
  J13 = female pin header, 8 pins [form="♀ (female)"]
  J14 = female pin header, 8 pins [form="♀ (female)"]
  J15 = female pin header, 8 pins [form="♀ (female)"]
  7404(6xnot)2 = IC, DIP package, 14 pins [chip_label=IC]
  7404(6xnot)3 = IC, DIP package, 14 pins [chip_label=IC]
  7404(6xnot)4 = IC, DIP package, 14 pins [chip_label=IC]
  seg1001 = 7-Segment LED Display [package=THT]
  seg1002 = 7-Segment LED Display [package=THT]
  seg1003 = 7-Segment LED Display [package=THT]
  seg1004 = 7-Segment LED Display [package=THT]
  power1 = female pin header, 3 pins [form="♀ (female)"]
  C1 = Ceramic Capacitor [capacitance=100nF package="100 mil [THT, multilayer]"]
  C2 = Ceramic Capacitor [capacitance=100nF package="100 mil [THT, multilayer]"]

nets:
  N1: 555.Ground, 104.1, 104_2.1, 161(counter).pin8, 139(mux).pin1, 139(mux).pin8, J1.pin5, J1.pin7, J2.pin12, J3.pin3, 20uF.-, power.pin3, J4.pin12, J5.pin5, J5.pin7, J6.pin3, J7.pin12, J8.pin5, J8.pin7, J9.pin3, 7404(6xnot)2.pin7, 7404(6xnot)3.pin7, 7404(6xnot)4.pin7, power1.pin3, C1.0, C2.0
  N2: 555.Trigger, 555.Threshold, 46k.Pin_1, 104_2.0
  N3: 555.Output, 161(counter).pin2
  N4: 555.Control_Voltage, 104.0
  N5: 555.Discharge, 1k.Pin_1, 46k.Pin_0
  N6: 555.Vcc_Supply_Voltage, 1k.Pin_0, 161(counter).pin1, 161(counter).pin7, 161(counter).pin9, 161(counter).pin10, 161(counter).pin16, 139(mux).pin16, J1.pin1, J1.pin4, J3.pin1, 20uF.+, power.pin1, J5.pin1, J5.pin4, J6.pin1, J8.pin1, J8.pin4, J9.pin1, 7404(6xnot)2.pin14, 7404(6xnot)3.pin14, 7404(6xnot)4.pin14, power1.pin1, C1.1, C2.1
  N7: 161(counter).pin13, 139(mux).pin3, J1.pin3, J5.pin3, J8.pin3
  N8: 161(counter).pin14, 139(mux).pin2, J1.pin2, J5.pin2, J8.pin2
  N9: 139(mux).pin4, 7404(6xnot)2.pin1, 7404(6xnot)3.pin1, 7404(6xnot)4.pin1
  N10: 139(mux).pin5, 7404(6xnot)2.pin3, 7404(6xnot)3.pin3, 7404(6xnot)4.pin3
  N11: 139(mux).pin6, 7404(6xnot)2.pin5, 7404(6xnot)3.pin5, 7404(6xnot)4.pin5
  N12: 139(mux).pin7, 7404(6xnot)2.pin9, 7404(6xnot)3.pin9, 7404(6xnot)4.pin9
  N13: seg1000.cathodeE, seg100.cathodeE, seg10.cathodeE, seg1.cathodeE, J1.pin11
  N14: seg1000.cathodeD, seg100.cathodeD, seg10.cathodeD, seg1.cathodeD, J1.pin12
  N15: seg1000.commAnode, 7404(6xnot)2.pin2
  N16: seg1000.cathodeC, seg100.cathodeC, seg10.cathodeC, seg1.cathodeC, J2.pin11
  N17: seg1000.cathodeDP, seg100.cathodeDP, seg10.cathodeDP, seg1.cathodeDP, J1.pin8
  N18: seg1000.cathodeB, seg100.cathodeB, seg10.cathodeB, seg1.cathodeB, J2.pin10
  N19: seg1000.cathodeA, seg100.cathodeA, seg10.cathodeA, seg1.cathodeA, J2.pin9
  N20: seg1000.cathodeF, seg100.cathodeF, seg10.cathodeF, seg1.cathodeF, J1.pin10
  N21: seg1000.cathodeG, seg100.cathodeG, seg10.cathodeG, seg1.cathodeG, J1.pin9
  N22: seg100.commAnode, 7404(6xnot)2.pin4
  N23: seg10.commAnode, 7404(6xnot)2.pin6
  N24: seg1.commAnode, 7404(6xnot)2.pin8
  N25: J1.pin6, J3.pin2
  N26: J2.pin1, J10.pin1, J11.pin1
  N27: J2.pin2, J10.pin2, J11.pin2
  N28: J2.pin3, J10.pin3, J11.pin3
  N29: J2.pin4, J10.pin4, J11.pin4
  N30: J2.pin5, J10.pin5, J11.pin5
  N31: J2.pin6, J10.pin6, J11.pin6
  N32: J2.pin7, J10.pin7, J11.pin7
  N33: J2.pin8, J10.pin8, J11.pin8
  N34: seg1_2.cathodeE, seg10_2.cathodeE, seg100_2.cathodeE, seg1000_2.cathodeE, J5.pin11
  N35: seg1_2.cathodeD, seg10_2.cathodeD, seg100_2.cathodeD, seg1000_2.cathodeD, J5.pin12
  N36: seg1_2.commAnode, 7404(6xnot)3.pin8
  N37: seg1_2.cathodeC, seg10_2.cathodeC, seg100_2.cathodeC, seg1000_2.cathodeC, J4.pin11
  N38: seg1_2.cathodeDP, seg10_2.cathodeDP, seg100_2.cathodeDP, seg1000_2.cathodeDP, J5.pin8
  N39: seg1_2.cathodeB, seg10_2.cathodeB, seg100_2.cathodeB, seg1000_2.cathodeB, J4.pin10
  N40: seg1_2.cathodeA, seg10_2.cathodeA, seg100_2.cathodeA, seg1000_2.cathodeA, J4.pin9
  N41: seg1_2.cathodeF, seg10_2.cathodeF, seg100_2.cathodeF, seg1000_2.cathodeF, J5.pin10
  N42: seg1_2.cathodeG, seg10_2.cathodeG, seg100_2.cathodeG, seg1000_2.cathodeG, J5.pin9
  N43: seg10_2.commAnode, 7404(6xnot)3.pin6
  N44: seg100_2.commAnode, 7404(6xnot)3.pin4
  N45: seg1000_2.commAnode, 7404(6xnot)3.pin2
  N46: J4.pin1, J12.pin1, J13.pin1
  N47: J4.pin2, J12.pin2, J13.pin2
  N48: J4.pin3, J12.pin3, J13.pin3
  N49: J4.pin4, J12.pin4, J13.pin4
  N50: J4.pin5, J12.pin5, J13.pin5
  N51: J4.pin6, J12.pin6, J13.pin6
  N52: J4.pin7, J12.pin7, J13.pin7
  N53: J4.pin8, J12.pin8, J13.pin8
  N54: J5.pin6, J6.pin2
  N55: J7.pin1, J14.pin1, J15.pin1
  N56: J7.pin2, J14.pin2, J15.pin2
  N57: J7.pin3, J14.pin3, J15.pin3
  N58: J7.pin4, J14.pin4, J15.pin4
  N59: J7.pin5, J14.pin5, J15.pin5
  N60: J7.pin6, J14.pin6, J15.pin6
  N61: J7.pin7, J14.pin7, J15.pin7
  N62: J7.pin8, J14.pin8, J15.pin8
  N63: J7.pin9, seg1001.cathodeA, seg1002.cathodeA, seg1003.cathodeA, seg1004.cathodeA
  N64: J7.pin10, seg1001.cathodeB, seg1002.cathodeB, seg1003.cathodeB, seg1004.cathodeB
  N65: J7.pin11, seg1001.cathodeC, seg1002.cathodeC, seg1003.cathodeC, seg1004.cathodeC
  N66: J8.pin6, J9.pin2
  N67: J8.pin8, seg1001.cathodeDP, seg1002.cathodeDP, seg1003.cathodeDP, seg1004.cathodeDP
  N68: J8.pin9, seg1001.cathodeG, seg1002.cathodeG, seg1003.cathodeG, seg1004.cathodeG
  N69: J8.pin10, seg1001.cathodeF, seg1002.cathodeF, seg1003.cathodeF, seg1004.cathodeF
  N70: J8.pin11, seg1001.cathodeE, seg1002.cathodeE, seg1003.cathodeE, seg1004.cathodeE
  N71: J8.pin12, seg1001.cathodeD, seg1002.cathodeD, seg1003.cathodeD, seg1004.cathodeD
  N72: 7404(6xnot)4.pin2, seg1004.commAnode
  N73: 7404(6xnot)4.pin4, seg1003.commAnode
  N74: 7404(6xnot)4.pin6, seg1002.commAnode
  N75: 7404(6xnot)4.pin8, seg1001.commAnode
