# Fritzing sketch outregx4_v2_registers-groundfill (saved by Fritzing 0.9.1b)
circuit board: 9.99cm x 9.99cm
breadboards: 2

parts:
  J64 = female pin header, 2 pins [form="♀ (female)"]
  J65 = female pin header, 2 pins [form="♀ (female)"]
  J66 = female pin header, 8 pins [form="♀ (female)"]
  J67 = female pin header, 8 pins [form="♀ (female)"]
  J68 = female pin header, 8 pins [form="♀ (female)"]
  J69 = female pin header, 8 pins [form="♀ (female)"]
  IC7 = IC, DIP package, 16 pins [chip_label=IC]
  IC8 = IC, DIP package, 16 pins [chip_label=IC]
  IC9 = IC, DIP package, 16 pins [chip_label=IC]
  IC10 = IC, DIP package, 16 pins [chip_label=IC]
  IC11 = IC, DIP package, 16 pins [chip_label=IC]
  IC12 = IC, DIP package, 16 pins [chip_label=IC]
  IC13 = IC, DIP package, 16 pins [chip_label=IC]
  IC14 = IC, DIP package, 16 pins [chip_label=IC]
  J70 = female pin header, 8 pins [form="♀ (female)"]
  J71 = female pin header, 8 pins [form="♀ (female)"]
  J72 = female pin header, 8 pins [form="♀ (female)"]
  J73 = female pin header, 8 pins [form="♀ (female)"]
  J74 = female pin header, 8 pins [form="♀ (female)"]
  0_1_2_3 = female pin header, 4 pins [form="♀ (female)"]
  CLK = female pin header, 1 pin [form="♀ (female)"]
  J75 = female pin header, 4 pins [form="♀ (female)"]
  C2 = Ceramic Capacitor [capacitance=100nF package="100 mil [THT, multilayer]"]
  C3 = Ceramic Capacitor [capacitance=100nF package="100 mil [THT, multilayer]"]
  C4 = Ceramic Capacitor [capacitance=100nF package="100 mil [THT, multilayer]"]
  C5 = Ceramic Capacitor [capacitance=100nF package="100 mil [THT, multilayer]"]
  C6 = Ceramic Capacitor [capacitance=100nF package="100 mil [THT, multilayer]"]

nets:
  N1: J64.pin1, J65.pin1, IC7.pin1, IC7.pin2, IC7.pin8, IC7.pin15, IC8.pin1, IC8.pin2, IC8.pin8, IC8.pin15, IC9.pin1, IC9.pin2, IC9.pin8, IC9.pin15, IC10.pin1, IC10.pin2, IC10.pin8, IC10.pin15, IC11.pin1, IC11.pin2, IC11.pin8, IC11.pin15, IC12.pin1, IC12.pin2, IC12.pin8, IC12.pin15, IC13.pin1, IC13.pin2, IC13.pin8, IC13.pin15, IC14.pin1, IC14.pin2, IC14.pin8, IC14.pin15, J75.pin3, J75.pin4, C2.0, C3.0, C4.0, C5.0, C6.0
  N2: J64.pin2, J65.pin2, IC7.pin16, IC8.pin16, IC9.pin16, IC10.pin16, IC11.pin16, IC12.pin16, IC13.pin16, IC14.pin16, J75.pin1, J75.pin2, C2.1, C3.1, C4.1, C5.1, C6.1
  N3: J66.pin1, IC11.pin3, J74.pin1
  N4: J66.pin2, IC11.pin4, J74.pin2
  N5: J66.pin3, IC11.pin5, J74.pin3
  N6: J66.pin4, IC11.pin6, J74.pin4
  N7: J66.pin5, IC13.pin3, J74.pin5
  N8: J66.pin6, IC13.pin4, J74.pin6
  N9: J66.pin7, IC13.pin5, J74.pin7
  N10: J66.pin8, IC13.pin6, J74.pin8
  N11: J67.pin1, IC12.pin3, J73.pin1
  N12: J67.pin2, IC12.pin4, J73.pin2
  N13: J67.pin3, IC12.pin5, J73.pin3
  N14: J67.pin4, IC12.pin6, J73.pin4
  N15: J67.pin5, IC14.pin3, J73.pin5
  N16: J67.pin6, IC14.pin4, J73.pin6
  N17: J67.pin7, IC14.pin5, J73.pin7
  N18: J67.pin8, IC14.pin6, J73.pin8
  N19: J68.pin1, IC10.pin3, J72.pin1
  N20: J68.pin2, IC10.pin4, J72.pin2
  N21: J68.pin3, IC10.pin5, J72.pin3
  N22: J68.pin4, IC10.pin6, J72.pin4
  N23: J68.pin5, IC9.pin3, J72.pin5
  N24: J68.pin6, IC9.pin4, J72.pin6
  N25: J68.pin7, IC9.pin5, J72.pin7
  N26: J68.pin8, IC9.pin6, J72.pin8
  N27: J69.pin1, IC7.pin3, J71.pin1
  N28: J69.pin2, IC7.pin4, J71.pin2
  N29: J69.pin3, IC7.pin5, J71.pin3
  N30: J69.pin4, IC7.pin6, J71.pin4
  N31: J69.pin5, IC8.pin3, J71.pin5
  N32: J69.pin6, IC8.pin4, J71.pin6
  N33: J69.pin7, IC8.pin5, J71.pin7
  N34: J69.pin8, IC8.pin6, J71.pin8
  N35: IC7.pin7, IC8.pin7, IC9.pin7, IC10.pin7, IC11.pin7, IC12.pin7, IC13.pin7, IC14.pin7, CLK.pin1
  N36: IC7.pin9, IC7.pin10, IC8.pin9, IC8.pin10, 0_1_2_3.pin1
  N37: IC7.pin11, IC10.pin11, IC11.pin11, IC12.pin11, J70.pin4
  N38: IC7.pin12, IC10.pin12, IC11.pin12, IC12.pin12, J70.pin3
  N39: IC7.pin13, IC10.pin13, IC11.pin13, IC12.pin13, J70.pin2
  N40: IC7.pin14, IC10.pin14, IC11.pin14, IC12.pin14, J70.pin1
  N41: IC8.pin11, IC9.pin11, IC13.pin11, IC14.pin11, J70.pin8
  N42: IC8.pin12, IC9.pin12, IC13.pin12, IC14.pin12, J70.pin7
  N43: IC8.pin13, IC9.pin13, IC13.pin13, IC14.pin13, J70.pin6
  N44: IC8.pin14, IC9.pin14, IC13.pin14, IC14.pin14, J70.pin5
  N45: IC9.pin9, IC9.pin10, IC10.pin9, IC10.pin10, 0_1_2_3.pin2
  N46: IC11.pin9, IC11.pin10, IC13.pin9, IC13.pin10, 0_1_2_3.pin4
  N47: IC12.pin9, IC12.pin10, IC14.pin9, IC14.pin10, 0_1_2_3.pin3

notes:
  +
  -
  Marius Krabset 2019
  Output Registers
