# Fritzing sketch pc_old (saved by Fritzing 0.9.2b)
circuit board: 12.3427cm x 15.5929cm
breadboards: 1

parts:
  74LS173_A-HIGH = IC, DIP package, 16 pins [chip_label=IC]
  74LS173_A-LOW = IC, DIP package, 16 pins [chip_label=IC]
  74LS173_B-LOW = IC, DIP package, 16 pins [chip_label=IC]
  74LS173_B-HIGH = IC, DIP package, 16 pins [chip_label=IC]
  CLK = female pin header, 1 pin [form="♀ (female)"]
  LOAD-A = female pin header, 1 pin [form="♀ (female)"]
  LOAD-B = female pin header, 1 pin [form="♀ (female)"]
  LED1 = LED - 5mm [color="Red (633nm)" package="5 mm [THT]"]
  LED2 = LED - 5mm [color="Red (633nm)" package="5 mm [THT]"]
  LED3 = LED - 5mm [color="Red (633nm)" package="5 mm [THT]"]
  LED4 = LED - 5mm [color="Red (633nm)" package="5 mm [THT]"]
  LED5 = LED - 5mm [color="Red (633nm)" package="5 mm [THT]"]
  LED6 = LED - 5mm [color="Red (633nm)" package="5 mm [THT]"]
  LED7 = LED - 5mm [color="Red (633nm)" package="5 mm [THT]"]
  LED8 = LED - 5mm [color="Red (633nm)" package="5 mm [THT]"]
  LED9 = LED - 5mm [color="Red (633nm)" package="5 mm [THT]"]
  LED10 = LED - 5mm [color="Red (633nm)" package="5 mm [THT]"]
  LED11 = LED - 5mm [color="Red (633nm)" package="5 mm [THT]"]
  LED12 = LED - 5mm [color="Red (633nm)" package="5 mm [THT]"]
  LED13 = LED - 5mm [color="Red (633nm)" package="5 mm [THT]"]
  LED14 = LED - 5mm [color="Red (633nm)" package="5 mm [THT]"]
  LED15 = LED - 5mm [color="Red (633nm)" package="5 mm [THT]"]
  LED16 = LED - 5mm [color="Red (633nm)" package="5 mm [THT]"]
  J2 = female pin header, 2 pins [form="♀ (female)"]
  C1 = Ceramic Capacitor [capacitance=100nF package="100 mil [THT, multilayer]"]
  J15 = female pin header, 8 pins [form="♀ (female)"]
  C6 = Ceramic Capacitor [capacitance=100nF package="100 mil [THT, multilayer]"]
  J24 = female pin header, 8 pins [form="♀ (female)"]
  74LS161_B-HIGH1 = IC, DIP package, 16 pins [chip_label=IC]
  74LS161_B-LOW1 = IC, DIP package, 16 pins [chip_label=IC]
  74LS161_A-LOW1 = IC, DIP package, 16 pins [chip_label=IC]
  74LS161_A-HIGH1 = IC, DIP package, 16 pins [chip_label=IC]
  CNT = female pin header, 1 pin [form="♀ (female)"]
  LED17 = LED - 5mm [color="Red (633nm)" package="5 mm [THT]"]
  LED18 = LED - 5mm [color="Red (633nm)" package="5 mm [THT]"]
  LED19 = LED - 5mm [color="Red (633nm)" package="5 mm [THT]"]
  LED20 = LED - 5mm [color="Red (633nm)" package="5 mm [THT]"]
  LED21 = LED - 5mm [color="Red (633nm)" package="5 mm [THT]"]
  LED22 = LED - 5mm [color="Red (633nm)" package="5 mm [THT]"]
  LED23 = LED - 5mm [color="Red (633nm)" package="5 mm [THT]"]
  LED24 = LED - 5mm [color="Red (633nm)" package="5 mm [THT]"]
  LED25 = LED - 5mm [color="Red (633nm)" package="5 mm [THT]"]
  LED26 = LED - 5mm [color="Red (633nm)" package="5 mm [THT]"]
  LED27 = LED - 5mm [color="Red (633nm)" package="5 mm [THT]"]
  LED28 = LED - 5mm [color="Red (633nm)" package="5 mm [THT]"]
  LED29 = LED - 5mm [color="Red (633nm)" package="5 mm [THT]"]
  LED30 = LED - 5mm [color="Red (633nm)" package="5 mm [THT]"]
  LED31 = LED - 5mm [color="Red (633nm)" package="5 mm [THT]"]
  LED32 = LED - 5mm [color="Red (633nm)" package="5 mm [THT]"]
  J25 = female pin header, 2 pins [form="♀ (female)"]
  IC1 = IC, DIP package, 20 pins [chip_label=IC]
  IC2 = IC, DIP package, 20 pins [chip_label=IC]
  jmp_cond = female pin header, 4 pins [form="♀ (female)"]
  INV = IC, DIP package, 14 pins [chip_label=IC]
  AND = IC, DIP package, 14 pins [chip_label=IC]
  flags = female pin header, 4 pins [form="♀ (female)"]
  C7 = Ceramic Capacitor [capacitance=100nF package="100 mil [THT, multilayer]"]
  flags2 = female pin header, 12 pins [form="♀ (female)"]
  flags3 = female pin header, 12 pins [form="♀ (female)"]
  C8 = Ceramic Capacitor [capacitance=100nF package="100 mil [THT, multilayer]"]
  jmp = LED - 5mm [color="Red (633nm)" package="5 mm [THT]"]
  R1 = Resistor [tolerance=±5% resistance=220 package=THT]
  R2 = Resistor [tolerance=±5% resistance=220 package="1206 [SMD]"]
  R3 = Resistor [tolerance=±5% resistance=220 package="1206 [SMD]"]
  R4 = Resistor [tolerance=±5% resistance=220 package="1206 [SMD]"]
  R5 = Resistor [tolerance=±5% resistance=220 package="1206 [SMD]"]
  R6 = Resistor [tolerance=±5% resistance=220 package="1206 [SMD]"]
  R7 = Resistor [tolerance=±5% resistance=220 package="1206 [SMD]"]
  R8 = Resistor [tolerance=±5% resistance=220 package="1206 [SMD]"]
  R9 = Resistor [tolerance=±5% resistance=220 package="1206 [SMD]"]
  R10 = Resistor [tolerance=±5% resistance=220 package="1206 [SMD]"]
  R11 = Resistor [tolerance=±5% resistance=220 package="1206 [SMD]"]
  R12 = Resistor [tolerance=±5% resistance=220 package="1206 [SMD]"]
  R13 = Resistor [tolerance=±5% resistance=220 package="1206 [SMD]"]
  R14 = Resistor [tolerance=±5% resistance=220 package="1206 [SMD]"]
  R15 = Resistor [tolerance=±5% resistance=220 package="1206 [SMD]"]
  R16 = Resistor [tolerance=±5% resistance=220 package="1206 [SMD]"]
  R17 = Resistor [tolerance=±5% resistance=220 package="1206 [SMD]"]
  GND = female pin header, 1 pin [form="♀ (female)"]
  VCC = female pin header, 1 pin [form="♀ (female)"]
  R18 = Resistor [tolerance=±5% resistance=220 package="1206 [SMD]"]
  R19 = Resistor [tolerance=±5% resistance=220 package="1206 [SMD]"]
  R20 = Resistor [tolerance=±5% resistance=220 package="1206 [SMD]"]
  R21 = Resistor [tolerance=±5% resistance=220 package="1206 [SMD]"]
  R22 = Resistor [tolerance=±5% resistance=220 package="1206 [SMD]"]
  R23 = Resistor [tolerance=±5% resistance=220 package="1206 [SMD]"]
  R24 = Resistor [tolerance=±5% resistance=220 package="1206 [SMD]"]
  R25 = Resistor [tolerance=±5% resistance=220 package="1206 [SMD]"]
  R26 = Resistor [tolerance=±5% resistance=220 package="1206 [SMD]"]
  R27 = Resistor [tolerance=±5% resistance=220 package="1206 [SMD]"]
  R28 = Resistor [tolerance=±5% resistance=220 package="1206 [SMD]"]
  R29 = Resistor [tolerance=±5% resistance=220 package="1206 [SMD]"]
  R30 = Resistor [tolerance=±5% resistance=220 package="1206 [SMD]"]
  R31 = Resistor [tolerance=±5% resistance=220 package="1206 [SMD]"]
  R32 = Resistor [tolerance=±5% resistance=220 package="1206 [SMD]"]
  R33 = Resistor [tolerance=±5% resistance=220 package="1206 [SMD]"]
  GND_2 = female pin header, 1 pin [form="♀ (female)"]
  VCC_2 = female pin header, 1 pin [form="♀ (female)"]
  CLK_2 = female pin header, 8 pins [form="♀ (female)"]
  J26 = female pin header, 2 pins [form="♀ (female)"]
  GND1 = female pin header, 1 pin [form="♀ (female)"]
  VCC1 = female pin header, 1 pin [form="♀ (female)"]
  VCC2 = female pin header, 1 pin [form="♀ (female)"]
  GND2 = female pin header, 1 pin [form="♀ (female)"]
  J27 = female pin header, 2 pins [form="♀ (female)"]
  C9 = Ceramic Capacitor [capacitance=100nF package="100 mil [THT, multilayer]"]
  out_ctrl1 = female pin header, 2 pins [form="♀ (female)"]
  V = Resistor [tolerance=±5% resistance=220 package="1206 [SMD]"]
  C = Resistor [tolerance=±5% resistance=220 package="1206 [SMD]"]
  N = Resistor [tolerance=±5% resistance=220 package="1206 [SMD]"]
  Z = Resistor [tolerance=±5% resistance=220 package="1206 [SMD]"]
  LED33 = smd LED [color="Red (633nm)" package="1206 [SMD]"]
  LED34 = smd LED [color="Red (633nm)" package="1206 [SMD]"]
  LED35 = smd LED [color="Red (633nm)" package="1206 [SMD]"]
  LED36 = smd LED [color="Red (633nm)" package="1206 [SMD]"]
  RESET = female pin header, 1 pin [form="♀ (female)"]
  RESET_2 = Pushbutton [package="[THT]"]
  R34 = Resistor [tolerance=±5% resistance=220 package=THT]
  C10 = Ceramic Capacitor [capacitance=100nF package="100 mil [THT, multilayer]"]

nets:
  N1: 74LS173_A-HIGH.pin1, 74LS173_A-HIGH.pin2, 74LS173_A-HIGH.pin8, 74LS173_A-HIGH.pin15, 74LS173_A-LOW.pin1, 74LS173_A-LOW.pin2, 74LS173_A-LOW.pin8, 74LS173_A-LOW.pin15, 74LS173_B-LOW.pin1, 74LS173_B-LOW.pin2, 74LS173_B-LOW.pin8, 74LS173_B-LOW.pin15, 74LS173_B-HIGH.pin1, 74LS173_B-HIGH.pin2, 74LS173_B-HIGH.pin8, 74LS173_B-HIGH.pin15, J2.pin2, C1.0, C6.1, 74LS161_B-HIGH1.pin8, 74LS161_B-LOW1.pin8, 74LS161_A-LOW1.pin8, 74LS161_A-HIGH1.pin8, J25.pin1, IC1.pin1, IC1.pin10, IC2.pin1, IC2.pin10, INV.pin5, INV.pin7, INV.pin9, AND.pin7, C7.0, flags2.pin1, flags3.pin6, flags3.pin7, flags3.pin8, flags3.pin10, flags3.pin11, C8.1, R2.Pin_1, R3.Pin_1, R4.Pin_1, R5.Pin_1, R6.Pin_1, R7.Pin_1, R8.Pin_1, R9.Pin_1, R10.Pin_1, R11.Pin_1, R12.Pin_1, R13.Pin_1, R14.Pin_1, R15.Pin_1, R16.Pin_1, R17.Pin_1, GND.pin1, R18.Pin_1, R19.Pin_1, R20.Pin_1, R21.Pin_1, R22.Pin_1, R23.Pin_1, R24.Pin_1, R25.Pin_1, R26.Pin_1, R27.Pin_1, R28.Pin_1, R29.Pin_1, R30.Pin_1, R31.Pin_1, R32.Pin_1, R33.Pin_1, GND_2.pin1, J26.pin2, GND1.pin1, GND2.pin1, J27.pin1, C9.1, V.Pin_0, C.Pin_0, N.Pin_0, Z.Pin_0, RESET_2.Pin_1, RESET_2.Pin_2, C10.0
  N2: 74LS173_A-HIGH.pin3, LED1.anode, 74LS161_A-HIGH1.pin6
  N3: 74LS173_A-HIGH.pin4, LED2.anode, 74LS161_A-HIGH1.pin5
  N4: 74LS173_A-HIGH.pin5, LED4.anode, 74LS161_A-HIGH1.pin4
  N5: 74LS173_A-HIGH.pin6, LED3.anode, 74LS161_A-HIGH1.pin3
  N6: 74LS173_A-HIGH.pin7, 74LS173_A-LOW.pin7, 74LS173_B-LOW.pin7, 74LS173_B-HIGH.pin7, CLK.pin1, 74LS161_B-HIGH1.pin2, 74LS161_B-LOW1.pin2, 74LS161_A-LOW1.pin2, 74LS161_A-HIGH1.pin2, CLK_2.pin1, CLK_2.pin2, CLK_2.pin3, CLK_2.pin4, CLK_2.pin5, CLK_2.pin6, CLK_2.pin7, CLK_2.pin8
  N7: 74LS173_A-HIGH.pin9, 74LS173_A-HIGH.pin10, 74LS173_A-LOW.pin9, 74LS173_A-LOW.pin10, LOAD-A.pin1
  N8: 74LS173_A-HIGH.pin11, 74LS173_B-HIGH.pin11, J15.pin4
  N9: 74LS173_A-HIGH.pin12, 74LS173_B-HIGH.pin12, J15.pin3
  N10: 74LS173_A-HIGH.pin13, 74LS173_B-HIGH.pin13, J15.pin2
  N11: 74LS173_A-HIGH.pin14, 74LS173_B-HIGH.pin14, J15.pin1
  N12: 74LS173_A-HIGH.pin16, 74LS173_A-LOW.pin16, 74LS173_B-LOW.pin16, 74LS173_B-HIGH.pin16, J2.pin1, C1.1, C6.0, 74LS161_B-HIGH1.pin16, 74LS161_B-LOW1.pin16, 74LS161_A-LOW1.pin16, 74LS161_A-HIGH1.pin16, J25.pin2, IC1.pin20, IC2.pin20, INV.pin14, AND.pin9, AND.pin10, AND.pin12, AND.pin13, AND.pin14, C7.1, flags3.pin9, flags3.pin12, C8.0, R1.Pin_0, VCC.pin1, VCC_2.pin1, J26.pin1, VCC1.pin1, VCC2.pin1, J27.pin2, C9.0, C10.1
  N13: 74LS173_A-LOW.pin3, LED6.anode, 74LS161_A-LOW1.pin6
  N14: 74LS173_A-LOW.pin4, LED7.anode, 74LS161_A-LOW1.pin5
  N15: 74LS173_A-LOW.pin5, LED8.anode, 74LS161_A-LOW1.pin4
  N16: 74LS173_A-LOW.pin6, LED5.anode, 74LS161_A-LOW1.pin3
  N17: 74LS173_A-LOW.pin11, 74LS173_B-LOW.pin11, J15.pin8
  N18: 74LS173_A-LOW.pin12, 74LS173_B-LOW.pin12, J15.pin7
  N19: 74LS173_A-LOW.pin13, 74LS173_B-LOW.pin13, J15.pin6
  N20: 74LS173_A-LOW.pin14, 74LS173_B-LOW.pin14, J15.pin5
  N21: 74LS173_B-LOW.pin3, LED9.anode, 74LS161_B-LOW1.pin6
  N22: 74LS173_B-LOW.pin4, LED10.anode, 74LS161_B-LOW1.pin5
  N23: 74LS173_B-LOW.pin5, LED11.anode, 74LS161_B-LOW1.pin4
  N24: 74LS173_B-LOW.pin6, LED13.anode, 74LS161_B-LOW1.pin3
  N25: 74LS173_B-LOW.pin9, 74LS173_B-LOW.pin10, 74LS173_B-HIGH.pin9, 74LS173_B-HIGH.pin10, LOAD-B.pin1
  N26: 74LS173_B-HIGH.pin3, LED14.anode, 74LS161_B-HIGH1.pin6
  N27: 74LS173_B-HIGH.pin4, LED15.anode, 74LS161_B-HIGH1.pin5
  N28: 74LS173_B-HIGH.pin5, LED12.anode, 74LS161_B-HIGH1.pin4
  N29: 74LS173_B-HIGH.pin6, LED16.anode, 74LS161_B-HIGH1.pin3
  N30: LED1.cathode, R25.Pin_0
  N31: LED2.cathode, R24.Pin_0
  N32: LED3.cathode, R22.Pin_0
  N33: LED4.cathode, R23.Pin_0
  N34: LED5.cathode, R18.Pin_0
  N35: LED6.cathode, R21.Pin_0
  N36: LED7.cathode, R20.Pin_0
  N37: LED8.cathode, R19.Pin_0
  N38: LED9.cathode, R29.Pin_0
  N39: LED10.cathode, R28.Pin_0
  N40: LED11.cathode, R27.Pin_0
  N41: LED12.cathode, R31.Pin_0
  N42: LED13.cathode, R26.Pin_0
  N43: LED14.cathode, R33.Pin_0
  N44: LED15.cathode, R32.Pin_0
  N45: LED16.cathode, R30.Pin_0
  N46: J24.pin1, IC1.pin9, IC2.pin9
  N47: J24.pin2, IC1.pin8, IC2.pin8
  N48: J24.pin3, IC1.pin7, IC2.pin7
  N49: J24.pin4, IC1.pin6, IC2.pin6
  N50: J24.pin5, IC1.pin5, IC2.pin5
  N51: J24.pin6, IC1.pin4, IC2.pin4
  N52: J24.pin7, IC1.pin3, IC2.pin3
  N53: J24.pin8, IC1.pin2, IC2.pin2
  N54: 74LS161_B-HIGH1.pin1, 74LS161_B-LOW1.pin1, 74LS161_A-LOW1.pin1, 74LS161_A-HIGH1.pin1, RESET_2.Pin_3, RESET_2.Pin_4, R34.Pin_1
  N55: 74LS161_B-HIGH1.pin7, 74LS161_B-HIGH1.pin10, 74LS161_B-LOW1.pin15
  N56: 74LS161_B-HIGH1.pin9, 74LS161_B-LOW1.pin9, 74LS161_A-LOW1.pin9, 74LS161_A-HIGH1.pin9, flags2.pin4, jmp.cathode
  N57: 74LS161_B-HIGH1.pin11, LED19.anode, IC2.pin18
  N58: 74LS161_B-HIGH1.pin12, LED18.anode, IC2.pin17
  N59: 74LS161_B-HIGH1.pin13, LED21.anode, IC2.pin16
  N60: 74LS161_B-HIGH1.pin14, LED17.anode, IC2.pin15
  N61: 74LS161_B-HIGH1.pin15, 74LS161_A-LOW1.pin7, 74LS161_A-LOW1.pin10
  N62: 74LS161_B-LOW1.pin7, 74LS161_B-LOW1.pin10, CNT.pin1
  N63: 74LS161_B-LOW1.pin11, LED24.anode, IC2.pin14
  N64: 74LS161_B-LOW1.pin12, LED23.anode, IC2.pin13
  N65: 74LS161_B-LOW1.pin13, LED22.anode, IC2.pin12
  N66: 74LS161_B-LOW1.pin14, LED20.anode, IC2.pin11
  N67: 74LS161_A-LOW1.pin11, LED27.anode, IC1.pin14
  N68: 74LS161_A-LOW1.pin12, LED26.anode, IC1.pin13
  N69: 74LS161_A-LOW1.pin13, LED25.anode, IC1.pin12
  N70: 74LS161_A-LOW1.pin14, LED28.anode, IC1.pin11
  N71: 74LS161_A-LOW1.pin15, 74LS161_A-HIGH1.pin7, 74LS161_A-HIGH1.pin10
  N72: 74LS161_A-HIGH1.pin11, LED32.anode, IC1.pin18
  N73: 74LS161_A-HIGH1.pin12, LED31.anode, IC1.pin17
  N74: 74LS161_A-HIGH1.pin13, LED29.anode, IC1.pin16
  N75: 74LS161_A-HIGH1.pin14, LED30.anode, IC1.pin15
  N76: LED17.cathode, R14.Pin_0
  N77: LED18.cathode, R17.Pin_0
  N78: LED19.cathode, R10.Pin_0
  N79: LED20.cathode, R11.Pin_0
  N80: LED21.cathode, R12.Pin_0
  N81: LED22.cathode, R16.Pin_0
  N82: LED23.cathode, R13.Pin_0
  N83: LED24.cathode, R15.Pin_0
  N84: LED25.cathode, R8.Pin_0
  N85: LED26.cathode, R7.Pin_0
  N86: LED27.cathode, R6.Pin_0
  N87: LED28.cathode, R9.Pin_0
  N88: LED29.cathode, R4.Pin_0
  N89: LED30.cathode, R5.Pin_0
  N90: LED31.cathode, R3.Pin_0
  N91: LED32.cathode, R2.Pin_0
  N92: IC1.pin19, INV.pin12
  N93: IC2.pin19, INV.pin10
  N94: jmp_cond.pin1, flags2.pin5
  N95: jmp_cond.pin2, flags2.pin6
  N96: jmp_cond.pin3, flags2.pin7
  N97: jmp_cond.pin4, flags2.pin8
  N98: INV.pin1, out_ctrl1.pin1
  N99: INV.pin2, AND.pin1, AND.pin4
  N100: INV.pin3, AND.pin2, out_ctrl1.pin2
  N101: INV.pin4, AND.pin5
  N102: INV.pin11, AND.pin6
  N103: INV.pin13, AND.pin3
  N104: flags.pin1, flags2.pin9, LED36.anode
  N105: flags.pin2, flags2.pin10, LED35.anode
  N106: flags.pin3, flags2.pin11, LED34.anode
  N107: flags.pin4, flags2.pin12, LED33.anode
  N108: jmp.anode, R1.Pin_1
  N109: V.Pin_1, LED33.cathode
  N110: C.Pin_1, LED34.cathode
  N111: N.Pin_1, LED35.cathode
  N112: Z.Pin_1, LED36.cathode
  N113: RESET.pin1, R34.Pin_0

notes:
  HIGH
  OE
  LSB
