# Fritzing sketch programmer_v2 (saved by Fritzing 0.9.1b)
circuit board: 9.81457cm x 5.09453cm
breadboards: 1

parts:
  step = female pin header, 4 pins [form="♀ (female)"]
  U1 = 74HC595 [package="DIP16 [THT]"]
  U2 = 74HC595 [package="DIP16 [THT]"]
  C1 = Ceramic Capacitor [capacitance=100nF package="100 mil [THT, multilayer]"]
  C2 = Ceramic Capacitor [capacitance=100nF package="100 mil [THT, multilayer]"]
  C3 = Ceramic Capacitor [capacitance=100nF package="100 mil [THT, multilayer]"]
  U3 = 74HC595 [package="DIP16 [THT]"]
  Part1 = Arduino Nano (Rev3.0)
  SRC_SEL = female pin header, 1 pin [form="♀ (female)"]
  CLK = female pin header, 1 pin [form="♀ (female)"]
  C4 = Ceramic Capacitor [capacitance=100nF package="100 mil [THT, multilayer]"]
  data2 = female pin header, 8 pins [form="♀ (female)"]
  inst = female pin header, 8 pins [form="♀ (female)"]
  GND = female pin header, 1 pin [form="♀ (female)"]

nets:
  N1: step.pin1, U2.Q1
  N2: step.pin2, U2.Q2
  N3: step.pin3, U2.Q3
  N4: step.pin4, U2.Q4
  N5: U1.Q1, inst.pin2
  N6: U1.Q2, inst.pin3
  N7: U1.Q3, inst.pin4
  N8: U1.Q4, inst.pin5
  N9: U1.Q5, inst.pin6
  N10: U1.Q6, inst.pin7
  N11: U1.Q7, inst.pin8
  GND: U1.GND, U1.OE, U2.GND, U2.OE, C1.0, C2.0, C3.0, U3.GND, Part1.GND, C4.1, GND.pin1
  N12: U1.Q7', U2.DS
  VCC: U1.MR, U1.VCC, U2.MR, U2.VCC, C1.1, C2.1, C3.1, U3.MR, U3.VCC, Part1.5V, C4.0
  N13: U1.SH_CP, U2.SH_CP, Part1.A2
  N14: U1.ST_CP, U2.ST_CP, Part1.A1
  N15: U1.DS, Part1.A0
  N16: U1.Q0, inst.pin1
  N17: U3.Q1, data2.pin7
  N18: U3.Q2, data2.pin6
  N19: U3.Q3, data2.pin5
  N20: U3.Q4, data2.pin4
  N21: U3.Q5, data2.pin3
  N22: U3.Q6, data2.pin2
  N23: U3.Q7, data2.pin1
  N24: U3.SH_CP, Part1.D4
  N25: U3.ST_CP, Part1.D3
  N26: U3.OE, Part1.D5
  N27: U3.DS, Part1.D6
  N28: U3.Q0, data2.pin8
  N29: Part1.A4, SRC_SEL.pin1
  N30: Part1.A3, CLK.pin1
