# Fritzing sketch programmer_v3 (saved by Fritzing 0.9.1b)
circuit board: 9.77879cm x 6.00615cm
breadboards: 1

parts:
  step = female pin header, 4 pins [form="♀ (female)"]
  U1 = 74HC595 [package="DIP16 [THT]"]
  U2 = 74HC595 [package="DIP16 [THT]"]
  C1 = Ceramic Capacitor [capacitance=100nF package="100 mil [THT, multilayer]"]
  C2 = Ceramic Capacitor [capacitance=100nF package="100 mil [THT, multilayer]"]
  Part1 = Arduino Nano (Rev3.0)
  SRC_SEL = female pin header, 1 pin [form="♀ (female)"]
  CLK = female pin header, 1 pin [form="♀ (female)"]
  C4 = Ceramic Capacitor [capacitance=100nF package="100 mil [THT, multilayer]"]
  data2 = female pin header, 8 pins [form="♀ (female)"]
  inst = female pin header, 8 pins [form="♀ (female)"]
  GND = female pin header, 1 pin [form="♀ (female)"]
  R1 = Resistor [tolerance=±5% resistance=220 package="1206 [SMD]"]
  R2 = Resistor [tolerance=±5% resistance=220 package="1206 [SMD]"]
  R3 = Resistor [tolerance=±5% resistance=220 package="1206 [SMD]"]
  R4 = Resistor [tolerance=±5% resistance=220 package="1206 [SMD]"]
  R5 = Resistor [tolerance=±5% resistance=220 package="1206 [SMD]"]
  R6 = Resistor [tolerance=±5% resistance=220 package="1206 [SMD]"]
  R7 = Resistor [tolerance=±5% resistance=220 package="1206 [SMD]"]
  R8 = Resistor [tolerance=±5% resistance=220 package="1206 [SMD]"]
  74LS245 = IC, DIP package, 20 pins [chip_label=IC]
  R9 = Resistor [tolerance=±5% resistance=220 package="1206 [SMD]"]
  R10 = Resistor [tolerance=±5% resistance=220 package="1206 [SMD]"]
  R11 = Resistor [tolerance=±5% resistance=220 package="1206 [SMD]"]
  R12 = Resistor [tolerance=±5% resistance=220 package="1206 [SMD]"]
  R13 = Resistor [tolerance=±5% resistance=220 package="1206 [SMD]"]
  R14 = Resistor [tolerance=±5% resistance=220 package="1206 [SMD]"]
  R15 = Resistor [tolerance=±5% resistance=220 package="1206 [SMD]"]
  R16 = Resistor [tolerance=±5% resistance=220 package="1206 [SMD]"]
  R17 = Resistor [tolerance=±5% resistance=220 package="1206 [SMD]"]
  J1 = female pin header, 4 pins [form="♀ (female)"]
  C5 = Electrolytic Capacitor [capacitance=1µF package="100 mil [THT, electrolytic]"]
  LED1 = smd LED [color="Red (633nm)" package="1206 [SMD]"]
  R18 = Resistor [tolerance=±5% resistance=220 package="1206 [SMD]"]
  J2 = female pin header, 2 pins [form="♀ (female)"]
  R19 = Resistor [tolerance=±5% resistance=220 package="1206 [SMD]"]
  LED2 = smd LED [color="Red (633nm)" package="1206 [SMD]"]
  R20 = Resistor [tolerance=±5% resistance=220 package="1206 [SMD]"]
  LED3 = smd LED [color="Red (633nm)" package="1206 [SMD]"]
  J3 = female pin header, 1 pin [form="♀ (female)"]

nets (from the pcb view):
  N1: step.pin1, U2.Q1
  N2: step.pin2, U2.Q2
  N3: step.pin3, U2.Q3
  N4: step.pin4, U2.Q4
  N5: U1.Q1, inst.pin2
  N6: U1.Q2, inst.pin3
  N7: U1.Q3, inst.pin4
  N8: U1.Q4, inst.pin5
  N9: U1.Q5, inst.pin6
  N10: U1.Q6, inst.pin7
  N11: U1.Q7, inst.pin8
  GND: U1.GND, U1.OE, U2.GND, U2.OE, C1.0, C2.0, Part1.GND, C4.1, GND.pin1, 74LS245.pin10, J1.pin3, J1.pin4, C5.-, LED2.cathode, LED3.cathode
  N12: U1.Q7', U2.DS
  VCC: U1.MR, U1.VCC, U2.MR, U2.VCC, C1.1, C2.1, C4.0, 74LS245.pin20, J1.pin1, J1.pin2, C5.+, R18.Pin_1, J2.pin2
  N13: U1.SH_CP, U2.SH_CP, Part1.A2
  N14: U1.ST_CP, U2.ST_CP, Part1.A1
  N15: U1.DS, Part1.A0
  N16: U1.Q0, inst.pin1
  N17: Part1.D3, R17.Pin_1
  N18: Part1.D4, R16.Pin_1
  N19: Part1.D5, R15.Pin_1
  N20: Part1.D6, R14.Pin_1
  N21: Part1.D7, R9.Pin_1
  N22: Part1.D8, R10.Pin_1
  N23: Part1.D9, R11.Pin_1
  N24: Part1.D10, R12.Pin_1
  N25: Part1.D11/MOSI, R13.Pin_1
  N26: Part1.D12/MISO, 74LS245.pin1, LED1.cathode
  N27: Part1.5V, J2.pin1
  N28: Part1.A4, SRC_SEL.pin1, R20.Pin_1
  N29: Part1.A3, CLK.pin1, R19.Pin_1, J3.pin1
  N30: data2.pin1, R8.Pin_0
  N31: data2.pin2, R7.Pin_0
  N32: data2.pin3, R6.Pin_0
  N33: data2.pin4, R5.Pin_0
  N34: data2.pin5, R4.Pin_0
  N35: data2.pin6, R3.Pin_0
  N36: data2.pin7, R2.Pin_0
  N37: data2.pin8, R1.Pin_0
  N38: R1.Pin_1, 74LS245.pin2
  N39: R2.Pin_1, 74LS245.pin3
  N40: R3.Pin_1, 74LS245.pin4
  N41: R4.Pin_1, 74LS245.pin5
  N42: R5.Pin_1, 74LS245.pin6
  N43: R6.Pin_1, 74LS245.pin7
  N44: R7.Pin_1, 74LS245.pin8
  N45: R8.Pin_1, 74LS245.pin9
  N46: 74LS245.pin11, R17.Pin_0
  N47: 74LS245.pin12, R16.Pin_0
  N48: 74LS245.pin13, R15.Pin_0
  N49: 74LS245.pin14, R14.Pin_0
  N50: 74LS245.pin15, R13.Pin_0
  N51: 74LS245.pin16, R12.Pin_0
  N52: 74LS245.pin17, R11.Pin_0
  N53: 74LS245.pin18, R10.Pin_0
  N54: 74LS245.pin19, R9.Pin_0
  N55: LED1.anode, R18.Pin_0
  N56: R19.Pin_0, LED2.anode
  N57: R20.Pin_0, LED3.anode

notes:
  +
  -
