# Fritzing sketch register (saved by Fritzing 0.9.1b)
circuit board: 9.95628cm x 5.35792cm
breadboards: 2

parts:
  74LS245 = IC, DIP package, 20 pins [chip_label=IC]
  74LS173 = IC, DIP package, 16 pins [chip_label=IC]
  74LS173_2 = IC, DIP package, 16 pins [chip_label=IC]
  LOAD = female pin header, 1 pin [form="♀ (female)"]
  CLK = female pin header, 1 pin [form="♀ (female)"]
  BUS = female pin header, 8 pins [form="♀ (female)"]
  LED1 = LED - 5mm [color="Red (633nm)" package="5 mm [THT]"]
  LED2 = LED - 5mm [color="Red (633nm)" package="5 mm [THT]"]
  LED3 = LED - 5mm [color="Red (633nm)" package="5 mm [THT]"]
  LED4 = LED - 5mm [color="Red (633nm)" package="5 mm [THT]"]
  LED5 = LED - 5mm [color="Red (633nm)" package="5 mm [THT]"]
  LED6 = LED - 5mm [color="Red (633nm)" package="5 mm [THT]"]
  LED7 = LED - 5mm [color="Red (633nm)" package="5 mm [THT]"]
  LED8 = LED - 5mm [color="Red (633nm)" package="5 mm [THT]"]
  EN = female pin header, 1 pin [form="♀ (female)"]
  POWER = female pin header, 2 pins [form="♀ (female)"]
  out = female pin header, 8 pins [form="♀ (female)"]
  clk1 = female pin header, 1 pin [form="♀ (female)"]
  J1 = female pin header, 1 pin [form="♀ (female)"]
  J2 = female pin header, 1 pin [form="♀ (female)"]
  R1 = Resistor [tolerance=±5% resistance=220 package="1206 [SMD]"]
  R2 = Resistor [tolerance=±5% resistance=220 package="1206 [SMD]"]
  R3 = Resistor [tolerance=±5% resistance=220 package="1206 [SMD]"]
  R4 = Resistor [tolerance=±5% resistance=220 package="1206 [SMD]"]
  R5 = Resistor [tolerance=±5% resistance=220 package="1206 [SMD]"]
  R6 = Resistor [tolerance=±5% resistance=220 package="1206 [SMD]"]
  R7 = Resistor [tolerance=±5% resistance=220 package="1206 [SMD]"]
  R8 = Resistor [tolerance=±5% resistance=220 package="1206 [SMD]"]
  clk2 = female pin header, 1 pin [form="♀ (female)"]
  clk3 = female pin header, 1 pin [form="♀ (female)"]
  BUS1 = female pin header, 8 pins [form="♀ (female)"]
  C1 = Ceramic Capacitor [capacitance=100nF package="100 mil [THT, multilayer]"]
  J3 = female pin header, 1 pin [form="♀ (female)"]
  J4 = female pin header, 1 pin [form="♀ (female)"]
  POW1 = female pin header, 2 pins [form="♀ (female)"]
  POW2 = female pin header, 2 pins [form="♀ (female)"]
  POW3 = female pin header, 2 pins [form="♀ (female)"]

nets:
  N1: 74LS245.pin1, 74LS245.pin20, 74LS173.pin16, 74LS173_2.pin16, POWER.pin1, J1.pin1, C1.0, J3.pin1, POW1.pin1, POW2.pin1, POW3.pin1
  N2: 74LS245.pin2, 74LS173.pin3, out.pin1, R1.Pin_0
  N3: 74LS245.pin3, 74LS173.pin4, out.pin2, R2.Pin_0
  N4: 74LS245.pin4, 74LS173.pin5, out.pin3, R3.Pin_0
  N5: 74LS245.pin5, 74LS173.pin6, out.pin4, R4.Pin_0
  N6: 74LS245.pin6, 74LS173_2.pin3, out.pin5, R5.Pin_0
  N7: 74LS245.pin7, 74LS173_2.pin4, out.pin6, R6.Pin_0
  N8: 74LS245.pin8, 74LS173_2.pin5, out.pin7, R7.Pin_0
  N9: 74LS245.pin9, 74LS173_2.pin6, out.pin8, R8.Pin_0
  N10: 74LS245.pin10, 74LS173.pin1, 74LS173.pin2, 74LS173.pin8, 74LS173.pin15, 74LS173_2.pin1, 74LS173_2.pin2, 74LS173_2.pin8, 74LS173_2.pin15, LED1.cathode, LED2.cathode, LED3.cathode, LED4.cathode, LED5.cathode, LED6.cathode, LED7.cathode, LED8.cathode, POWER.pin2, J2.pin1, C1.1, J4.pin1, POW1.pin2, POW2.pin2, POW3.pin2
  N11: 74LS245.pin11, 74LS173_2.pin11, BUS.pin8, BUS1.pin8
  N12: 74LS245.pin12, 74LS173_2.pin12, BUS.pin7, BUS1.pin7
  N13: 74LS245.pin13, 74LS173_2.pin13, BUS.pin6, BUS1.pin6
  N14: 74LS245.pin14, 74LS173_2.pin14, BUS.pin5, BUS1.pin5
  N15: 74LS245.pin15, 74LS173.pin11, BUS.pin4, BUS1.pin4
  N16: 74LS245.pin16, 74LS173.pin12, BUS.pin3, BUS1.pin3
  N17: 74LS245.pin17, 74LS173.pin13, BUS.pin2, BUS1.pin2
  N18: 74LS245.pin18, 74LS173.pin14, BUS.pin1, BUS1.pin1
  N19: 74LS245.pin19, EN.pin1
  N20: 74LS173.pin7, 74LS173_2.pin7, CLK.pin1, clk1.pin1, clk2.pin1, clk3.pin1
  N21: 74LS173.pin9, 74LS173.pin10, 74LS173_2.pin9, 74LS173_2.pin10, LOAD.pin1
  N22: LED1.anode, R1.Pin_1
  N23: LED2.anode, R2.Pin_1
  N24: LED3.anode, R3.Pin_1
  N25: LED4.anode, R4.Pin_1
  N26: LED5.anode, R5.Pin_1
  N27: LED6.anode, R6.Pin_1
  N28: LED7.anode, R7.Pin_1
  N29: LED8.anode, R8.Pin_1

notes:
  +
  -
  8-Bit Register
  krabz 2018
