# Fritzing sketch register_v2 (saved by Fritzing 0.9.1b)
circuit board: 9.91577cm x 6.96494cm
breadboards: 2

parts:
  74LS245 = IC, DIP package, 20 pins [chip_label=IC]
  74LS173 = IC, DIP package, 16 pins [chip_label=IC]
  74LS173_2 = IC, DIP package, 16 pins [chip_label=IC]
  LOAD = female pin header, 1 pin [form="♀ (female)"]
  CLK = female pin header, 1 pin [form="♀ (female)"]
  BUS = female pin header, 8 pins [form="♀ (female)"]
  LED8 = LED - 5mm [color="Red (633nm)" package="5 mm [THT]"]
  EN = female pin header, 1 pin [form="♀ (female)"]
  POWER = female pin header, 2 pins [form="♀ (female)"]
  clk1 = female pin header, 1 pin [form="♀ (female)"]
  J1 = female pin header, 1 pin [form="♀ (female)"]
  J2 = female pin header, 1 pin [form="♀ (female)"]
  clk2 = female pin header, 1 pin [form="♀ (female)"]
  clk3 = female pin header, 1 pin [form="♀ (female)"]
  BUS1 = female pin header, 8 pins [form="♀ (female)"]
  C1 = Ceramic Capacitor [capacitance=100nF package="100 mil [THT, multilayer]"]
  J3 = female pin header, 1 pin [form="♀ (female)"]
  J4 = female pin header, 1 pin [form="♀ (female)"]
  POW1 = female pin header, 2 pins [form="♀ (female)"]
  POW2 = female pin header, 2 pins [form="♀ (female)"]
  POW3 = female pin header, 2 pins [form="♀ (female)"]
  R9 = Resistor [tolerance=±5% resistance=220 package="1206 [SMD]"]
  R10 = Resistor [tolerance=±5% resistance=220 package="1206 [SMD]"]
  R11 = Resistor [tolerance=±5% resistance=220 package="1206 [SMD]"]
  R12 = Resistor [tolerance=±5% resistance=220 package="1206 [SMD]"]
  R13 = Resistor [tolerance=±5% resistance=220 package="1206 [SMD]"]
  R14 = Resistor [tolerance=±5% resistance=220 package="1206 [SMD]"]
  R15 = Resistor [tolerance=±5% resistance=220 package="1206 [SMD]"]
  R16 = Resistor [tolerance=±5% resistance=220 package="1206 [SMD]"]
  74LS245_2 = IC, DIP package, 20 pins [chip_label=IC]
  R17 = Resistor [tolerance=±5% resistance=220 package="1206 [SMD]"]
  R18 = Resistor [tolerance=±5% resistance=220 package="1206 [SMD]"]
  LED9 = LED - 5mm [color="Red (633nm)" package="5 mm [THT]"]
  R19 = Resistor [tolerance=±5% resistance=220 package="1206 [SMD]"]
  LED10 = LED - 5mm [color="Red (633nm)" package="5 mm [THT]"]
  R20 = Resistor [tolerance=±5% resistance=220 package="1206 [SMD]"]
  LED11 = LED - 5mm [color="Red (633nm)" package="5 mm [THT]"]
  R21 = Resistor [tolerance=±5% resistance=220 package="1206 [SMD]"]
  LED12 = LED - 5mm [color="Red (633nm)" package="5 mm [THT]"]
  R22 = Resistor [tolerance=±5% resistance=220 package="1206 [SMD]"]
  LED13 = LED - 5mm [color="Red (633nm)" package="5 mm [THT]"]
  R23 = Resistor [tolerance=±5% resistance=220 package="1206 [SMD]"]
  LED14 = LED - 5mm [color="Red (633nm)" package="5 mm [THT]"]
  R24 = Resistor [tolerance=±5% resistance=220 package="1206 [SMD]"]
  LED15 = LED - 5mm [color="Red (633nm)" package="5 mm [THT]"]
  R25 = Resistor [tolerance=±5% resistance=220 package="1206 [SMD]"]
  C2 = Ceramic Capacitor [capacitance=100nF package="100 mil [THT, multilayer]"]

nets (from the pcb view):
  N1: 74LS245.pin1, 74LS245.pin20, 74LS173.pin16, 74LS173_2.pin16, POWER.pin1, J1.pin1, C1.0, J3.pin1, POW1.pin1, POW2.pin1, POW3.pin1, 74LS245_2.pin20, C2.1
  N2: 74LS245.pin2, 74LS173.pin3, 74LS245_2.pin18
  N3: 74LS245.pin3, 74LS173.pin4, 74LS245_2.pin17
  N4: 74LS245.pin4, 74LS173.pin5, 74LS245_2.pin16
  N5: 74LS245.pin5, 74LS173.pin6, 74LS245_2.pin15
  N6: 74LS245.pin6, 74LS173_2.pin3, 74LS245_2.pin14
  N7: 74LS245.pin7, 74LS173_2.pin4, 74LS245_2.pin13
  N8: 74LS245.pin8, 74LS173_2.pin5, 74LS245_2.pin12
  N9: 74LS245.pin9, 74LS173_2.pin6, 74LS245_2.pin11
  N10: 74LS245.pin10, 74LS173.pin1, 74LS173.pin2, 74LS173.pin8, 74LS173.pin15, 74LS173_2.pin1, 74LS173_2.pin2, 74LS173_2.pin8, 74LS173_2.pin15, LED8.cathode, POWER.pin2, J2.pin1, C1.1, J4.pin1, POW1.pin2, POW2.pin2, POW3.pin2, 74LS245_2.pin1, 74LS245_2.pin10, 74LS245_2.pin19, LED9.cathode, LED10.cathode, LED11.cathode, LED12.cathode, LED13.cathode, LED14.cathode, LED15.cathode, C2.0
  N11: 74LS245.pin11, R16.Pin_0
  N12: 74LS245.pin12, R15.Pin_0
  N13: 74LS245.pin13, R14.Pin_0
  N14: 74LS245.pin14, R13.Pin_0
  N15: 74LS245.pin15, R12.Pin_0
  N16: 74LS245.pin16, R11.Pin_0
  N17: 74LS245.pin17, R10.Pin_0
  N18: 74LS245.pin18, R9.Pin_0
  N19: 74LS245.pin19, EN.pin1
  N20: 74LS173.pin7, 74LS173_2.pin7, R17.Pin_1
  N21: 74LS173.pin9, 74LS173.pin10, 74LS173_2.pin9, 74LS173_2.pin10, LOAD.pin1
  N22: 74LS173.pin11, BUS.pin4, BUS1.pin4, R12.Pin_1
  N23: 74LS173.pin12, BUS.pin3, BUS1.pin3, R11.Pin_1
  N24: 74LS173.pin13, BUS.pin2, BUS1.pin2, R10.Pin_1
  N25: 74LS173.pin14, BUS.pin1, BUS1.pin1, R9.Pin_1
  N26: 74LS173_2.pin11, BUS.pin8, BUS1.pin8, R16.Pin_1
  N27: 74LS173_2.pin12, BUS.pin7, BUS1.pin7, R15.Pin_1
  N28: 74LS173_2.pin13, BUS.pin6, BUS1.pin6, R14.Pin_1
  N29: 74LS173_2.pin14, BUS.pin5, BUS1.pin5, R13.Pin_1
  N30: CLK.pin1, clk1.pin1, clk2.pin1, clk3.pin1, R17.Pin_0
  N31: LED8.anode, R18.Pin_0
  N32: 74LS245_2.pin2, R25.Pin_1
  N33: 74LS245_2.pin3, R24.Pin_1
  N34: 74LS245_2.pin4, R23.Pin_1
  N35: 74LS245_2.pin5, R22.Pin_1
  N36: 74LS245_2.pin6, R21.Pin_1
  N37: 74LS245_2.pin7, R20.Pin_1
  N38: 74LS245_2.pin8, R19.Pin_1
  N39: 74LS245_2.pin9, R18.Pin_1
  N40: LED9.anode, R19.Pin_0
  N41: LED10.anode, R20.Pin_0
  N42: LED11.anode, R21.Pin_0
  N43: LED12.anode, R22.Pin_0
  N44: LED13.anode, R23.Pin_0
  N45: LED14.anode, R24.Pin_0
  N46: LED15.anode, R25.Pin_0

notes:
  +
  -
  8-Bit Register
  krabz 2018
