# Fritzing sketch registers_2x_v2-groundfill (saved by Fritzing 0.9.1b)
circuit board: 10.0001cm x 7.50754cm
breadboards: 1

parts:
  74LS173 = IC, DIP package, 16 pins [chip_label=IC]
  74LS173_2 = IC, DIP package, 16 pins [chip_label=IC]
  J13 = female pin header, 8 pins [form="♀ (female)"]
  J14 = female pin header, 8 pins [form="♀ (female)"]
  J15 = female pin header, 8 pins [form="♀ (female)"]
  J16 = female pin header, 8 pins [form="♀ (female)"]
  J17 = female pin header, 8 pins [form="♀ (female)"]
  J18 = female pin header, 8 pins [form="♀ (female)"]
  74LS245 = IC, DIP package, 20 pins [chip_label=IC]
  J1 = female pin header, 8 pins [form="♀ (female)"]
  74LS173_3 = IC, DIP package, 16 pins [chip_label=IC]
  74LS173_4 = IC, DIP package, 16 pins [chip_label=IC]
  74LS245_2 = IC, DIP package, 20 pins [chip_label=IC]
  J19 = female pin header, 8 pins [form="♀ (female)"]
  J20 = female pin header, 8 pins [form="♀ (female)"]
  J21 = female pin header, 8 pins [form="♀ (female)"]
  J22 = female pin header, 8 pins [form="♀ (female)"]
  J23 = female pin header, 8 pins [form="♀ (female)"]
  J24 = female pin header, 8 pins [form="♀ (female)"]
  J25 = female pin header, 2 pins [form="♀ (female)"]
  J27 = female pin header, 8 pins [form="♀ (female)"]
  CLK = female pin header, 1 pin [form="♀ (female)"]
  J28 = female pin header, 1 pin [form="♀ (female)"]
  C1 = Ceramic Capacitor [capacitance=100nF package="100 mil [THT, multilayer]"]
  C2 = Ceramic Capacitor [capacitance=100nF package="100 mil [THT, multilayer]"]
  J29 = female pin header, 4 pins [form="♀ (female)"]
  J30 = female pin header, 4 pins [form="♀ (female)"]
  J31 = female pin header, 2 pins [form="♀ (female)"]

nets:
  N1: 74LS173.pin1, 74LS173.pin2, 74LS173.pin8, 74LS173.pin15, 74LS173_2.pin1, 74LS173_2.pin2, 74LS173_2.pin8, 74LS173_2.pin15, 74LS245.pin10, 74LS173_3.pin1, 74LS173_3.pin2, 74LS173_3.pin8, 74LS173_3.pin15, 74LS173_4.pin1, 74LS173_4.pin2, 74LS173_4.pin8, 74LS173_4.pin15, 74LS245_2.pin10, C1.0, C2.0, J29.pin3, J29.pin4, J30.pin3, J30.pin4
  N2: 74LS173.pin3, J15.pin1, J17.pin1, 74LS245.pin9
  N3: 74LS173.pin4, J15.pin2, J17.pin2, 74LS245.pin8
  N4: 74LS173.pin5, J15.pin3, J17.pin3, 74LS245.pin7
  N5: 74LS173.pin6, J15.pin4, J17.pin4, 74LS245.pin6
  N6: 74LS173.pin7, 74LS173_2.pin7, 74LS173_3.pin7, 74LS173_4.pin7, CLK.pin1, J28.pin1
  N7: 74LS173.pin9, 74LS173.pin10, 74LS173_2.pin9, 74LS173_2.pin10, J31.pin2
  N8: 74LS173.pin11, 74LS245.pin14, J1.pin4, 74LS173_3.pin11, 74LS245_2.pin14, J27.pin4
  N9: 74LS173.pin12, 74LS245.pin13, J1.pin3, 74LS173_3.pin12, 74LS245_2.pin13, J27.pin3
  N10: 74LS173.pin13, 74LS245.pin12, J1.pin2, 74LS173_3.pin13, 74LS245_2.pin12, J27.pin2
  N11: 74LS173.pin14, 74LS245.pin11, J1.pin1, 74LS173_3.pin14, 74LS245_2.pin11, J27.pin1
  N12: 74LS173.pin16, 74LS173_2.pin16, 74LS245.pin1, 74LS245.pin20, 74LS173_3.pin16, 74LS173_4.pin16, 74LS245_2.pin1, 74LS245_2.pin20, C1.1, C2.1, J29.pin1, J29.pin2, J30.pin1, J30.pin2
  N13: 74LS173_2.pin3, J15.pin5, J17.pin5, 74LS245.pin5
  N14: 74LS173_2.pin4, J15.pin6, J17.pin6, 74LS245.pin4
  N15: 74LS173_2.pin5, J15.pin7, J17.pin7, 74LS245.pin3
  N16: 74LS173_2.pin6, J15.pin8, J17.pin8, 74LS245.pin2
  N17: 74LS173_2.pin11, 74LS245.pin18, J1.pin8, 74LS173_4.pin11, 74LS245_2.pin18, J27.pin8
  N18: 74LS173_2.pin12, 74LS245.pin17, J1.pin7, 74LS173_4.pin12, 74LS245_2.pin17, J27.pin7
  N19: 74LS173_2.pin13, 74LS245.pin16, J1.pin6, 74LS173_4.pin13, 74LS245_2.pin16, J27.pin6
  N20: 74LS173_2.pin14, 74LS245.pin15, J1.pin5, 74LS173_4.pin14, 74LS245_2.pin15, J27.pin5
  N21: J13.pin1, J18.pin1
  N22: J13.pin2, J18.pin2
  N23: J13.pin3, J18.pin3
  N24: J13.pin4, J18.pin4
  N25: J13.pin5, J18.pin5
  N26: J13.pin6, J18.pin6
  N27: J13.pin7, J18.pin7
  N28: J13.pin8, J18.pin8
  N29: J14.pin1, J16.pin1
  N30: J14.pin2, J16.pin2
  N31: J14.pin3, J16.pin3
  N32: J14.pin4, J16.pin4
  N33: J14.pin5, J16.pin5
  N34: J14.pin6, J16.pin6
  N35: J14.pin7, J16.pin7
  N36: J14.pin8, J16.pin8
  N37: 74LS245.pin19, J25.pin2
  N38: 74LS173_3.pin3, 74LS245_2.pin9, J20.pin1, J23.pin1
  N39: 74LS173_3.pin4, 74LS245_2.pin8, J20.pin2, J23.pin2
  N40: 74LS173_3.pin5, 74LS245_2.pin7, J20.pin3, J23.pin3
  N41: 74LS173_3.pin6, 74LS245_2.pin6, J20.pin4, J23.pin4
  N42: 74LS173_3.pin9, 74LS173_3.pin10, 74LS173_4.pin9, 74LS173_4.pin10, J31.pin1
  N43: 74LS173_4.pin3, 74LS245_2.pin5, J20.pin5, J23.pin5
  N44: 74LS173_4.pin4, 74LS245_2.pin4, J20.pin6, J23.pin6
  N45: 74LS173_4.pin5, 74LS245_2.pin3, J20.pin7, J23.pin7
  N46: 74LS173_4.pin6, 74LS245_2.pin2, J20.pin8, J23.pin8
  N47: 74LS245_2.pin19, J25.pin1
  N48: J19.pin1, J21.pin1
  N49: J19.pin2, J21.pin2
  N50: J19.pin3, J21.pin3
  N51: J19.pin4, J21.pin4
  N52: J19.pin5, J21.pin5
  N53: J19.pin6, J21.pin6
  N54: J19.pin7, J21.pin7
  N55: J19.pin8, J21.pin8
  N56: J22.pin1, J24.pin1
  N57: J22.pin2, J24.pin2
  N58: J22.pin3, J24.pin3
  N59: J22.pin4, J24.pin4
  N60: J22.pin5, J24.pin5
  N61: J22.pin6, J24.pin6
  N62: J22.pin7, J24.pin7
  N63: J22.pin8, J24.pin8

notes:
  OE 1
  OE 2
  LOAD 2
  LOAD 1
  -
  +
