# Fritzing sketch regtest (saved by Fritzing 0.9.1b)
circuit board: 9.99067cm x 7.12184cm
breadboards: 1

parts:
  IC3 = IC, DIP package, 16 pins [chip_label=IC]
  IC4 = IC, DIP package, 16 pins [chip_label=IC]
  J13 = female pin header, 8 pins [form="♀ (female)"]
  J14 = female pin header, 8 pins [form="♀ (female)"]
  J15 = female pin header, 8 pins [form="♀ (female)"]
  J16 = female pin header, 8 pins [form="♀ (female)"]
  J17 = female pin header, 8 pins [form="♀ (female)"]
  J18 = female pin header, 8 pins [form="♀ (female)"]
  IC5 = IC, DIP package, 20 pins [chip_label=IC]
  J1 = female pin header, 8 pins [form="♀ (female)"]
  IC6 = IC, DIP package, 16 pins [chip_label=IC]
  IC7 = IC, DIP package, 16 pins [chip_label=IC]
  IC8 = IC, DIP package, 20 pins [chip_label=IC]
  J19 = female pin header, 8 pins [form="♀ (female)"]
  J20 = female pin header, 8 pins [form="♀ (female)"]
  J21 = female pin header, 8 pins [form="♀ (female)"]
  J22 = female pin header, 8 pins [form="♀ (female)"]
  J23 = female pin header, 8 pins [form="♀ (female)"]
  J24 = female pin header, 8 pins [form="♀ (female)"]
  J25 = female pin header, 2 pins [form="♀ (female)"]
  J27 = female pin header, 8 pins [form="♀ (female)"]
  J26 = female pin header, 1 pin [form="♀ (female)"]
  J28 = female pin header, 1 pin [form="♀ (female)"]
  C1 = Ceramic Capacitor [capacitance=100nF package="100 mil [THT, multilayer]"]
  C2 = Ceramic Capacitor [capacitance=100nF package="100 mil [THT, multilayer]"]
  J29 = female pin header, 4 pins [form="♀ (female)"]
  J30 = female pin header, 4 pins [form="♀ (female)"]
  J31 = female pin header, 2 pins [form="♀ (female)"]

nets:
  N1: IC3.pin1, IC3.pin2, IC3.pin8, IC3.pin15, IC4.pin1, IC4.pin2, IC4.pin8, IC4.pin15, IC5.pin10, IC6.pin1, IC6.pin2, IC6.pin8, IC6.pin15, IC7.pin1, IC7.pin2, IC7.pin8, IC7.pin15, IC8.pin10, C1.0, C2.0, J29.pin3, J29.pin4, J30.pin3, J30.pin4
  N2: IC3.pin3, J15.pin1, J17.pin1, IC5.pin9
  N3: IC3.pin4, J15.pin2, J17.pin2, IC5.pin8
  N4: IC3.pin5, J15.pin3, J17.pin3, IC5.pin7
  N5: IC3.pin6, J15.pin4, J17.pin4, IC5.pin6
  N6: IC3.pin7, IC4.pin7, IC6.pin7, IC7.pin7, J26.pin1, J28.pin1
  N7: IC3.pin9, IC3.pin10, IC4.pin9, IC4.pin10, J31.pin2
  N8: IC3.pin11, IC5.pin14, J1.pin4, IC6.pin11, IC8.pin14, J27.pin4
  N9: IC3.pin12, IC5.pin13, J1.pin3, IC6.pin12, IC8.pin13, J27.pin3
  N10: IC3.pin13, IC5.pin12, J1.pin2, IC6.pin13, IC8.pin12, J27.pin2
  N11: IC3.pin14, IC5.pin11, J1.pin1, IC6.pin14, IC8.pin11, J27.pin1
  N12: IC3.pin16, IC4.pin16, IC5.pin1, IC5.pin20, IC6.pin16, IC7.pin16, IC8.pin1, IC8.pin20, C1.1, C2.1, J29.pin1, J29.pin2, J30.pin1, J30.pin2
  N13: IC4.pin3, J15.pin5, J17.pin5, IC5.pin5
  N14: IC4.pin4, J15.pin6, J17.pin6, IC5.pin4
  N15: IC4.pin5, J15.pin7, J17.pin7, IC5.pin3
  N16: IC4.pin6, J15.pin8, J17.pin8, IC5.pin2
  N17: IC4.pin11, IC5.pin18, J1.pin8, IC7.pin11, IC8.pin18, J27.pin8
  N18: IC4.pin12, IC5.pin17, J1.pin7, IC7.pin12, IC8.pin17, J27.pin7
  N19: IC4.pin13, IC5.pin16, J1.pin6, IC7.pin13, IC8.pin16, J27.pin6
  N20: IC4.pin14, IC5.pin15, J1.pin5, IC7.pin14, IC8.pin15, J27.pin5
  N21: J13.pin1, J18.pin1
  N22: J13.pin2, J18.pin2
  N23: J13.pin3, J18.pin3
  N24: J13.pin4, J18.pin4
  N25: J13.pin5, J18.pin5
  N26: J13.pin6, J18.pin6
  N27: J13.pin7, J18.pin7
  N28: J13.pin8, J18.pin8
  N29: J14.pin1, J16.pin1
  N30: J14.pin2, J16.pin2
  N31: J14.pin3, J16.pin3
  N32: J14.pin4, J16.pin4
  N33: J14.pin5, J16.pin5
  N34: J14.pin6, J16.pin6
  N35: J14.pin7, J16.pin7
  N36: J14.pin8, J16.pin8
  N37: IC5.pin19, J25.pin2
  N38: IC6.pin3, IC8.pin9, J20.pin1, J23.pin1
  N39: IC6.pin4, IC8.pin8, J20.pin2, J23.pin2
  N40: IC6.pin5, IC8.pin7, J20.pin3, J23.pin3
  N41: IC6.pin6, IC8.pin6, J20.pin4, J23.pin4
  N42: IC6.pin9, IC6.pin10, IC7.pin9, IC7.pin10, J31.pin1
  N43: IC7.pin3, IC8.pin5, J20.pin5, J23.pin5
  N44: IC7.pin4, IC8.pin4, J20.pin6, J23.pin6
  N45: IC7.pin5, IC8.pin3, J20.pin7, J23.pin7
  N46: IC7.pin6, IC8.pin2, J20.pin8, J23.pin8
  N47: IC8.pin19, J25.pin1
  N48: J19.pin1, J21.pin1
  N49: J19.pin2, J21.pin2
  N50: J19.pin3, J21.pin3
  N51: J19.pin4, J21.pin4
  N52: J19.pin5, J21.pin5
  N53: J19.pin6, J21.pin6
  N54: J19.pin7, J21.pin7
  N55: J19.pin8, J21.pin8
  N56: J22.pin1, J24.pin1
  N57: J22.pin2, J24.pin2
  N58: J22.pin3, J24.pin3
  N59: J22.pin4, J24.pin4
  N60: J22.pin5, J24.pin5
  N61: J22.pin6, J24.pin6
  N62: J22.pin7, J24.pin7
  N63: J22.pin8, J24.pin8

notes:
  OE 1
  OE 2
  LOAD 2
  LOAD 1
