# Fritzing sketch sigdisplay (saved by Fritzing 0.9.1b)
circuit board: 9.95544cm x 7.63772cm
breadboards: 1

parts:
  IC1 = IC, DIP package, 20 pins [chip_label=IC]
  IC2 = IC, DIP package, 20 pins [chip_label=IC]
  IC3 = IC, DIP package, 20 pins [chip_label=IC]
  IC4 = IC, DIP package, 20 pins [chip_label=IC]
  J1 = female pin header, 8 pins [form="♀ (female)"]
  J2 = female pin header, 8 pins [form="♀ (female)"]
  J3 = female pin header, 8 pins [form="♀ (female)"]
  J4 = female pin header, 8 pins [form="♀ (female)"]
  LEDS = IC, DIP package, 16 pins [chip_label=IC]
  R1 = Resistor [tolerance=±5% resistance=220 package="1206 [SMD]"]
  R2 = Resistor [tolerance=±5% resistance=220 package="1206 [SMD]"]
  R3 = Resistor [tolerance=±5% resistance=220 package="1206 [SMD]"]
  R4 = Resistor [tolerance=±5% resistance=220 package="1206 [SMD]"]
  R5 = Resistor [tolerance=±5% resistance=220 package="1206 [SMD]"]
  R6 = Resistor [tolerance=±5% resistance=220 package="1206 [SMD]"]
  R7 = Resistor [tolerance=±5% resistance=220 package="1206 [SMD]"]
  R8 = Resistor [tolerance=±5% resistance=220 package="1206 [SMD]"]
  LEDS1 = IC, DIP package, 16 pins [chip_label=IC]
  R9 = Resistor [tolerance=±5% resistance=220 package="1206 [SMD]"]
  R10 = Resistor [tolerance=±5% resistance=220 package="1206 [SMD]"]
  R11 = Resistor [tolerance=±5% resistance=220 package="1206 [SMD]"]
  R12 = Resistor [tolerance=±5% resistance=220 package="1206 [SMD]"]
  R13 = Resistor [tolerance=±5% resistance=220 package="1206 [SMD]"]
  R14 = Resistor [tolerance=±5% resistance=220 package="1206 [SMD]"]
  R15 = Resistor [tolerance=±5% resistance=220 package="1206 [SMD]"]
  R16 = Resistor [tolerance=±5% resistance=220 package="1206 [SMD]"]
  LEDS2 = IC, DIP package, 16 pins [chip_label=IC]
  R17 = Resistor [tolerance=±5% resistance=220 package="1206 [SMD]"]
  R18 = Resistor [tolerance=±5% resistance=220 package="1206 [SMD]"]
  R19 = Resistor [tolerance=±5% resistance=220 package="1206 [SMD]"]
  R20 = Resistor [tolerance=±5% resistance=220 package="1206 [SMD]"]
  R21 = Resistor [tolerance=±5% resistance=220 package="1206 [SMD]"]
  R22 = Resistor [tolerance=±5% resistance=220 package="1206 [SMD]"]
  R23 = Resistor [tolerance=±5% resistance=220 package="1206 [SMD]"]
  R24 = Resistor [tolerance=±5% resistance=220 package="1206 [SMD]"]
  LEDS3 = IC, DIP package, 16 pins [chip_label=IC]
  R25 = Resistor [tolerance=±5% resistance=220 package="1206 [SMD]"]
  R26 = Resistor [tolerance=±5% resistance=220 package="1206 [SMD]"]
  R27 = Resistor [tolerance=±5% resistance=220 package="1206 [SMD]"]
  R28 = Resistor [tolerance=±5% resistance=220 package="1206 [SMD]"]
  R29 = Resistor [tolerance=±5% resistance=220 package="1206 [SMD]"]
  R30 = Resistor [tolerance=±5% resistance=220 package="1206 [SMD]"]
  R31 = Resistor [tolerance=±5% resistance=220 package="1206 [SMD]"]
  R32 = Resistor [tolerance=±5% resistance=220 package="1206 [SMD]"]
  IC7 = IC, DIP package, 20 pins [chip_label=IC]
  J6 = female pin header, 8 pins [form="♀ (female)"]
  LEDS5 = IC, DIP package, 16 pins [chip_label=IC]
  R34 = Resistor [tolerance=±5% resistance=220 package="1206 [SMD]"]
  R35 = Resistor [tolerance=±5% resistance=220 package="1206 [SMD]"]
  R37 = Resistor [tolerance=±5% resistance=220 package="1206 [SMD]"]
  R38 = Resistor [tolerance=±5% resistance=220 package="1206 [SMD]"]
  R39 = Resistor [tolerance=±5% resistance=220 package="1206 [SMD]"]
  R48 = Resistor [tolerance=±5% resistance=220 package="1206 [SMD]"]
  R49 = Resistor [tolerance=±5% resistance=220 package="1206 [SMD]"]
  R51 = Resistor [tolerance=±5% resistance=220 package="1206 [SMD]"]
  IC8 = IC, DIP package, 20 pins [chip_label=IC]
  J7 = female pin header, 8 pins [form="♀ (female)"]
  LEDS6 = IC, DIP package, 16 pins [chip_label=IC]
  R52 = Resistor [tolerance=±5% resistance=220 package="1206 [SMD]"]
  R53 = Resistor [tolerance=±5% resistance=220 package="1206 [SMD]"]
  R54 = Resistor [tolerance=±5% resistance=220 package="1206 [SMD]"]
  R55 = Resistor [tolerance=±5% resistance=220 package="1206 [SMD]"]
  R56 = Resistor [tolerance=±5% resistance=220 package="1206 [SMD]"]
  R57 = Resistor [tolerance=±5% resistance=220 package="1206 [SMD]"]
  R58 = Resistor [tolerance=±5% resistance=220 package="1206 [SMD]"]
  R59 = Resistor [tolerance=±5% resistance=220 package="1206 [SMD]"]
  IC9 = IC, DIP package, 20 pins [chip_label=IC]
  J8 = female pin header, 8 pins [form="♀ (female)"]
  LEDS7 = IC, DIP package, 16 pins [chip_label=IC]
  R60 = Resistor [tolerance=±5% resistance=220 package="1206 [SMD]"]
  R61 = Resistor [tolerance=±5% resistance=220 package="1206 [SMD]"]
  R62 = Resistor [tolerance=±5% resistance=220 package="1206 [SMD]"]
  R63 = Resistor [tolerance=±5% resistance=220 package="1206 [SMD]"]
  R64 = Resistor [tolerance=±5% resistance=220 package="1206 [SMD]"]
  R65 = Resistor [tolerance=±5% resistance=220 package="1206 [SMD]"]
  R66 = Resistor [tolerance=±5% resistance=220 package="1206 [SMD]"]
  R67 = Resistor [tolerance=±5% resistance=220 package="1206 [SMD]"]
  J52 = female pin header, 2 pins [form="♀ (female)"]
  J53 = female pin header, 2 pins [form="♀ (female)"]
  J54 = female pin header, 3 pins [form="♀ (female)"]
  J55 = female pin header, 3 pins [form="♀ (female)"]
  J56 = female pin header, 3 pins [form="♀ (female)"]
  C1 = Electrolytic Capacitor [capacitance=1µF package="100 mil [THT, electrolytic]"]
  J57 = female pin header, 4 pins [form="♀ (female)"]  # not connected
  J58 = female pin header, 4 pins [form="♀ (female)"]  # not connected
  J59 = female pin header, 4 pins [form="♀ (female)"]  # not connected
  J60 = female pin header, 4 pins [form="♀ (female)"]  # not connected
  J61 = female pin header, 4 pins [form="♀ (female)"]  # not connected
  J62 = female pin header, 4 pins [form="♀ (female)"]  # not connected

nets:
  N1: IC1.pin1, IC1.pin10, IC1.pin19, IC2.pin1, IC2.pin10, IC2.pin19, IC3.pin1, IC3.pin10, IC3.pin19, IC4.pin1, IC4.pin10, IC4.pin19, IC7.pin1, IC7.pin10, IC7.pin19, IC8.pin1, IC8.pin10, IC8.pin19, IC9.pin1, IC9.pin10, IC9.pin19, J52.pin2, J53.pin2, J54.pin1, J55.pin1, J56.pin1, C1.-
  N2: IC1.pin2, LEDS.pin16
  N3: IC1.pin3, LEDS.pin15
  N4: IC1.pin4, LEDS.pin14
  N5: IC1.pin5, LEDS.pin13
  N6: IC1.pin6, LEDS.pin12
  N7: IC1.pin7, LEDS.pin11
  N8: IC1.pin8, LEDS.pin10
  N9: IC1.pin9, LEDS.pin9
  N10: IC1.pin11, J1.pin8
  N11: IC1.pin12, J1.pin7
  N12: IC1.pin13, J1.pin6
  N13: IC1.pin14, J1.pin5
  N14: IC1.pin15, J1.pin4
  N15: IC1.pin16, J1.pin3
  N16: IC1.pin17, J1.pin2
  N17: IC1.pin18, J1.pin1
  N18: IC1.pin20, IC2.pin20, IC3.pin20, IC4.pin20, IC7.pin20, IC8.pin20, IC9.pin20, J52.pin1, J53.pin1, J54.pin3, J55.pin3, J56.pin3, C1.+
  N19: IC2.pin2, LEDS1.pin16
  N20: IC2.pin3, LEDS1.pin15
  N21: IC2.pin4, LEDS1.pin14
  N22: IC2.pin5, LEDS1.pin13
  N23: IC2.pin6, LEDS1.pin12
  N24: IC2.pin7, LEDS1.pin11
  N25: IC2.pin8, LEDS1.pin10
  N26: IC2.pin9, LEDS1.pin9
  N27: IC2.pin11, J2.pin8
  N28: IC2.pin12, J2.pin7
  N29: IC2.pin13, J2.pin6
  N30: IC2.pin14, J2.pin5
  N31: IC2.pin15, J2.pin4
  N32: IC2.pin16, J2.pin3
  N33: IC2.pin17, J2.pin2
  N34: IC2.pin18, J2.pin1
  N35: IC3.pin2, LEDS2.pin16
  N36: IC3.pin3, LEDS2.pin15
  N37: IC3.pin4, LEDS2.pin14
  N38: IC3.pin5, LEDS2.pin13
  N39: IC3.pin6, LEDS2.pin12
  N40: IC3.pin7, LEDS2.pin11
  N41: IC3.pin8, LEDS2.pin10
  N42: IC3.pin9, LEDS2.pin9
  N43: IC3.pin11, J3.pin8
  N44: IC3.pin12, J3.pin7
  N45: IC3.pin13, J3.pin6
  N46: IC3.pin14, J3.pin5
  N47: IC3.pin15, J3.pin4
  N48: IC3.pin16, J3.pin3
  N49: IC3.pin17, J3.pin2
  N50: IC3.pin18, J3.pin1
  N51: IC4.pin2, LEDS3.pin16
  N52: IC4.pin3, LEDS3.pin15
  N53: IC4.pin4, LEDS3.pin14
  N54: IC4.pin5, LEDS3.pin13
  N55: IC4.pin6, LEDS3.pin12
  N56: IC4.pin7, LEDS3.pin11
  N57: IC4.pin8, LEDS3.pin10
  N58: IC4.pin9, LEDS3.pin9
  N59: IC4.pin11, J4.pin8
  N60: IC4.pin12, J4.pin7
  N61: IC4.pin13, J4.pin6
  N62: IC4.pin14, J4.pin5
  N63: IC4.pin15, J4.pin4
  N64: IC4.pin16, J4.pin3
  N65: IC4.pin17, J4.pin2
  N66: IC4.pin18, J4.pin1
  N67: LEDS.pin1, R1.Pin_1
  N68: LEDS.pin2, R2.Pin_1
  N69: LEDS.pin3, R3.Pin_1
  N70: LEDS.pin4, R4.Pin_1
  N71: LEDS.pin5, R5.Pin_1
  N72: LEDS.pin6, R6.Pin_1
  N73: LEDS.pin7, R7.Pin_1
  N74: LEDS.pin8, R8.Pin_1
  N75: R1.Pin_0, R2.Pin_0, R3.Pin_0, R4.Pin_0, R5.Pin_0, R6.Pin_0, R7.Pin_0, R8.Pin_0, R9.Pin_0, R10.Pin_0, R11.Pin_0, R12.Pin_0, R13.Pin_0, R14.Pin_0, R15.Pin_0, R16.Pin_0, R17.Pin_0, R18.Pin_0, R19.Pin_0, R20.Pin_0, R21.Pin_0, R22.Pin_0, R23.Pin_0, R24.Pin_0, R25.Pin_0, R26.Pin_0, R27.Pin_0, R28.Pin_0, R29.Pin_0, R30.Pin_0, R31.Pin_0, R32.Pin_0
  N76: LEDS1.pin1, R15.Pin_1
  N77: LEDS1.pin2, R16.Pin_1
  N78: LEDS1.pin3, R10.Pin_1
  N79: LEDS1.pin4, R11.Pin_1
  N80: LEDS1.pin5, R9.Pin_1
  N81: LEDS1.pin6, R12.Pin_1
  N82: LEDS1.pin7, R14.Pin_1
  N83: LEDS1.pin8, R13.Pin_1
  N84: LEDS2.pin1, R22.Pin_1
  N85: LEDS2.pin2, R20.Pin_1
  N86: LEDS2.pin3, R21.Pin_1
  N87: LEDS2.pin4, R18.Pin_1
  N88: LEDS2.pin5, R19.Pin_1
  N89: LEDS2.pin6, R17.Pin_1
  N90: LEDS2.pin7, R24.Pin_1
  N91: LEDS2.pin8, R23.Pin_1
  N92: LEDS3.pin1, R29.Pin_1
  N93: LEDS3.pin2, R30.Pin_1
  N94: LEDS3.pin3, R31.Pin_1
  N95: LEDS3.pin4, R26.Pin_1
  N96: LEDS3.pin5, R28.Pin_1
  N97: LEDS3.pin6, R32.Pin_1
  N98: LEDS3.pin7, R25.Pin_1
  N99: LEDS3.pin8, R27.Pin_1
  N100: IC7.pin2, LEDS5.pin16
  N101: IC7.pin3, LEDS5.pin15
  N102: IC7.pin4, LEDS5.pin14
  N103: IC7.pin5, LEDS5.pin13
  N104: IC7.pin6, LEDS5.pin12
  N105: IC7.pin7, LEDS5.pin11
  N106: IC7.pin8, LEDS5.pin10
  N107: IC7.pin9, LEDS5.pin9
  N108: IC7.pin11, J6.pin8
  N109: IC7.pin12, J6.pin7
  N110: IC7.pin13, J6.pin6
  N111: IC7.pin14, J6.pin5
  N112: IC7.pin15, J6.pin4
  N113: IC7.pin16, J6.pin3
  N114: IC7.pin17, J6.pin2
  N115: IC7.pin18, J6.pin1
  N116: LEDS5.pin1, R48.Pin_1
  N117: LEDS5.pin2, R49.Pin_1
  N118: LEDS5.pin3, R38.Pin_1
  N119: LEDS5.pin4, R39.Pin_1
  N120: LEDS5.pin5, R37.Pin_1
  N121: LEDS5.pin6, R35.Pin_1
  N122: LEDS5.pin7, R51.Pin_1
  N123: LEDS5.pin8, R34.Pin_1
  N124: R34.Pin_0, R35.Pin_0, R37.Pin_0, R38.Pin_0, R39.Pin_0, R48.Pin_0, R49.Pin_0, R51.Pin_0, J54.pin2
  N125: IC8.pin2, LEDS6.pin16
  N126: IC8.pin3, LEDS6.pin15
  N127: IC8.pin4, LEDS6.pin14
  N128: IC8.pin5, LEDS6.pin13
  N129: IC8.pin6, LEDS6.pin12
  N130: IC8.pin7, LEDS6.pin11
  N131: IC8.pin8, LEDS6.pin10
  N132: IC8.pin9, LEDS6.pin9
  N133: IC8.pin11, J7.pin8
  N134: IC8.pin12, J7.pin7
  N135: IC8.pin13, J7.pin6
  N136: IC8.pin14, J7.pin5
  N137: IC8.pin15, J7.pin4
  N138: IC8.pin16, J7.pin3
  N139: IC8.pin17, J7.pin2
  N140: IC8.pin18, J7.pin1
  N141: LEDS6.pin1, R58.Pin_1
  N142: LEDS6.pin2, R59.Pin_1
  N143: LEDS6.pin3, R53.Pin_1
  N144: LEDS6.pin4, R56.Pin_1
  N145: LEDS6.pin5, R57.Pin_1
  N146: LEDS6.pin6, R54.Pin_1
  N147: LEDS6.pin7, R52.Pin_1
  N148: LEDS6.pin8, R55.Pin_1
  N149: R52.Pin_0, R53.Pin_0, R54.Pin_0, R55.Pin_0, R56.Pin_0, R57.Pin_0, R58.Pin_0, R59.Pin_0, J55.pin2
  N150: IC9.pin2, LEDS7.pin16
  N151: IC9.pin3, LEDS7.pin15
  N152: IC9.pin4, LEDS7.pin14
  N153: IC9.pin5, LEDS7.pin13
  N154: IC9.pin6, LEDS7.pin12
  N155: IC9.pin7, LEDS7.pin11
  N156: IC9.pin8, LEDS7.pin10
  N157: IC9.pin9, LEDS7.pin9
  N158: IC9.pin11, J8.pin8
  N159: IC9.pin12, J8.pin7
  N160: IC9.pin13, J8.pin6
  N161: IC9.pin14, J8.pin5
  N162: IC9.pin15, J8.pin4
  N163: IC9.pin16, J8.pin3
  N164: IC9.pin17, J8.pin2
  N165: IC9.pin18, J8.pin1
  N166: LEDS7.pin1, R65.Pin_1
  N167: LEDS7.pin2, R61.Pin_1
  N168: LEDS7.pin3, R67.Pin_1
  N169: LEDS7.pin4, R64.Pin_1
  N170: LEDS7.pin5, R60.Pin_1
  N171: LEDS7.pin6, R62.Pin_1
  N172: LEDS7.pin7, R66.Pin_1
  N173: LEDS7.pin8, R63.Pin_1
  N174: R60.Pin_0, R61.Pin_0, R62.Pin_0, R63.Pin_0, R64.Pin_0, R65.Pin_0, R66.Pin_0, R67.Pin_0, J56.pin2

notes:
  -
  +
  BUS WRITE
  BUS READ
